// Logisim project CPU.circ as structural Verilog
module CPU (
  input  SELPC,
  input  SELADDR,
  input  STOREMEM
);

  wire control_1_instrn, control_1_loaddecir, control_1_loadir, control_1_loadpc, or_1_out;
  wire [5:0] ir_dec_1_opcode;
  wire [15:0] multiplexer_1_out, pc_1_out_4;
  wire [31:0] ir_1_instr0, ir_1_instr1, mem_1_data_2;

  PC pc_1 (.SELPC(SELPC), .LOADPC(control_1_loadpc), .out_4(pc_1_out_4));  // open: BRANCH
  IR ir_1 (
    .INSTRN(mem_1_data_2), .LOADIR(control_1_loadir), .INSTRN_2(control_1_instrn), .INSTR0(ir_1_instr0),
    .INSTR1(ir_1_instr1));
  Multiplexer #(.width(16)) multiplexer_1 (.in0(pc_1_out_4), .out(multiplexer_1_out), .sel(SELADDR));  // open: in1, en
  buf or_1 (or_1_out, control_1_loadir);  // OR_Gate
  IR_DEC ir_dec_1 (
    .INSTR0(ir_1_instr0), .INSTR1(ir_1_instr1), .LOADIRDEC(control_1_loaddecir), .OPCODE(ir_dec_1_opcode));  // open: IMM
  ALU alu_1 ();  // open: IN1, IN2, C, Z, N, OPCODE, Result
  MEM mem_1 (
    .ADDR(multiplexer_1_out), .STORE(STOREMEM), .LOAD(or_1_out), .DATA_2(mem_1_data_2),
    .LOADNEXT(control_1_instrn));  // open: DATA
  CONTROL control_1 (
    .OPCODE(ir_dec_1_opcode), .INSTRN(control_1_instrn), .LOADIR(control_1_loadir),
    .LOADPC(control_1_loadpc), .LOADDECIR(control_1_loaddecir));
  REG reg_1 ();  // open: REGADDR, STORE, REGSTR, REGVAL
endmodule

module ALU (
  input  [31:0] IN1,
  input  [31:0] IN2,
  input  [3:0] OPCODE,
  output C,
  output Z,
  output N,
  output [31:0] Result
);

  wire adder_1_cout, or_2_out, subtractor_1_bout;
  wire [31:0] adder_1_out, and_1_out, divider_1_out, divider_1_rem, multiplier_1_out, nand_1_out, nor_1_out,
       not_1_out, or_1_out, shifter_1_out, shifter_2_out, shifter_3_out, shifter_4_out, shifter_5_out,
       subtractor_1_out, xor_1_out;

  Adder #(.width(32)) adder_1 (.a(IN1), .b(IN2), .out(adder_1_out), .cout(adder_1_cout));  // open: cin
  Subtractor #(.width(32)) subtractor_1 (
    .a(IN1), .b(IN2), .out(subtractor_1_out), .bout(subtractor_1_bout));  // open: bin
  Multiplier #(.width(32)) multiplier_1 (.a(IN1), .b(IN2), .out(multiplier_1_out));  // open: cin, cout
  Divider #(.width(32)) divider_1 (.a(IN1), .b(IN2), .out(divider_1_out), .rem(divider_1_rem));  // open: upper
  assign and_1_out = IN1 & IN2;  // AND_Gate and_1, 32 bits wide
  assign or_1_out = IN1 | IN2;  // OR_Gate or_1, 32 bits wide
  assign xor_1_out = IN1 ^ IN2;  // XOR_Gate xor_1, 32 bits wide
  assign nand_1_out = ~(IN1 & IN2);  // NAND_Gate nand_1, 32 bits wide
  assign nor_1_out = ~(IN1 | IN2);  // NOR_Gate nor_1, 32 bits wide
  assign not_1_out = ~IN1;  // NOT_Gate not_1, 32 bits wide
  Shifter #(.width(32)) shifter_1 (.in(IN1), .\dist (IN2[4:0]), .out(shifter_1_out));
  Shifter #(.width(32), .shift("lr")) shifter_2 (.in(IN1), .\dist (IN2[4:0]), .out(shifter_2_out));
  Shifter #(.width(32), .shift("ar")) shifter_3 (.in(IN1), .\dist (IN2[4:0]), .out(shifter_3_out));
  Shifter #(.width(32), .shift("rl")) shifter_4 (.in(IN1), .\dist (IN2[4:0]), .out(shifter_4_out));
  Shifter #(.width(32), .shift("rr")) shifter_5 (.in(IN1), .\dist (IN2[4:0]), .out(shifter_5_out));
  Multiplexer #(.select(4), .width(32), .enable("false")) multiplexer_1 (
    .in0(adder_1_out), .in1(subtractor_1_out), .in2(multiplier_1_out), .in3(divider_1_out),
    .in4(divider_1_rem), .in5(and_1_out), .in6(or_1_out), .in7(xor_1_out), .in8(nand_1_out), .in9(nor_1_out),
    .in10(not_1_out), .in11(shifter_1_out), .in12(shifter_2_out), .in13(shifter_3_out), .in14(shifter_4_out),
    .in15(shifter_5_out), .out({N, Result[30:0]}), .sel(OPCODE));
  Multiplexer #(.select(4), .enable("false")) multiplexer_2 (
    .in0(adder_1_cout), .in1(subtractor_1_bout), .in2(1'b0), .in3(1'b0), .in4(1'b0), .in5(1'b0), .in6(1'b0),
    .in7(1'b0), .in8(1'b0), .in9(1'b0), .in10(1'b0), .in11(1'b0), .in12(1'b0), .in13(1'b0), .in14(1'b0),
    .in15(1'b0), .out(C), .sel(OPCODE));
  or or_2 (or_2_out, Result[0], Result[1], Result[2], Result[3], Result[4], Result[5], Result[6], Result[7], Result[8], Result[9], Result[10], Result[11], Result[12], Result[13], Result[14], Result[15], Result[17], Result[18], Result[19], Result[20], Result[21], Result[22], Result[23], Result[24], Result[25], Result[26], Result[27], Result[28], Result[29], Result[30], N, Result[16]);
  not not_2 (Z, or_2_out);

  assign Result[31] = N;
endmodule

module IR_DEC (
  input  [31:0] INSTR0,
  input  [31:0] INSTR1,
  input  LOADIRDEC,
  output [5:0] OPCODE,
  output [31:0] IMM
);

  wire clock_1_out;

  Clock clock_1 (.out(clock_1_out));
  Register #(.width(6)) OP1 (.D(INSTR0[5:0]), .en(LOADIRDEC), .Q(OPCODE), .clk(clock_1_out));  // open: clr
  Register #(.width(32)) u_IMM (.D(INSTR1), .en(LOADIRDEC), .Q(IMM), .clk(clock_1_out));  // open: clr
endmodule

module CONTROL (
  input  [5:0] OPCODE,
  output LOADIR,
  output INSTRN,
  output LOADPC,
  output LOADDECIR
);

  wire _1_out, _3_out, and_1_out, clock_1_out, demultiplexer_1_out1, demultiplexer_1_out3,
       demultiplexer_1_out4, demultiplexer_1_out5, demultiplexer_1_out6, demultiplexer_1_out7, undriven;
  wire [1:0] counter_1_q;
  wire [2:0] inc3_1_out_2, multiplexer_1_out, not_1_out, STATE_q;
  wire [15:0] rom_1_data;

  Clock clock_1 (.out(clock_1_out));
  INC3 inc3_1 (.in_1(STATE_q), .out_2(inc3_1_out_2));
  and and_1 (and_1_out, STATE_q[0], STATE_q[1], STATE_q[2]);
  Multiplexer #(.width(3)) multiplexer_1 (
    .in0(inc3_1_out_2), .in1(not_1_out), .out(multiplexer_1_out), .sel(and_1_out));  // open: en
  assign not_1_out = ~3'b111;  // NOT_Gate not_1, 3 bits wide
  Counter #(.width(2), .max('h3)) counter_1 (
    .count(undriven), .Q(counter_1_q), .clk(clock_1_out));  // open: load, D, carry, clr
  Register #(.width(3)) STATE (.D(multiplexer_1_out), .Q(STATE_q), .clk(_3_out));  // open: en, clr
  and _3 (_3_out, counter_1_q[0], counter_1_q[1]);
  // AND_Gate _2 has open pins: in0=counter_1_q[0], in1=counter_1_q[1], out=open
  and _1 (_1_out, counter_1_q[0], ~counter_1_q[1]);  // AND_Gate
  // AND_Gate _0 has open pins: in0=counter_1_q[0], in1=counter_1_q[1], out=open
  ROM #(.addrWidth(6), .dataWidth(16)) rom_1 (.addr(OPCODE), .data(rom_1_data));  // open: sel
  Demultiplexer #(.select(3)) demultiplexer_1 (
    .out0(LOADIR), .out1(demultiplexer_1_out1), .out2(LOADDECIR), .out3(demultiplexer_1_out3),
    .out4(demultiplexer_1_out4), .out5(demultiplexer_1_out5), .out6(demultiplexer_1_out6),
    .out7(demultiplexer_1_out7), .in(1'b1), .sel(STATE_q));  // open: en
  // Probe on demultiplexer_1_out4
  // Probe on demultiplexer_1_out5
  // Probe on demultiplexer_1_out6
  // Probe on demultiplexer_1_out7
  and and_2 (INSTRN, LOADIR, _1_out);
  and and_3 (LOADPC, _1_out, demultiplexer_1_out1);
  // Probe on demultiplexer_1_out3

  // Notes on the sheet:
  //   0: FETCH PC -> IR
  //   1: INCREMENT PC
  //   2: DECODE IR
endmodule

module REG (
  input  STORE,
  input  [3:0] REGADDR,
  input  [31:0] REGSTR,
  output [31:0] REGVAL
);

  wire clock_1_out, demultiplexer_1_out0, demultiplexer_1_out1, demultiplexer_1_out2, demultiplexer_1_out3,
       demultiplexer_1_out4, demultiplexer_1_out5, demultiplexer_1_out6, demultiplexer_1_out7,
       demultiplexer_1_out8, demultiplexer_1_out9;
  wire [31:0] register_1_q, register_2_q, register_3_q, register_4_q, register_5_q, register_6_q,
       register_7_q, register_8_q, register_9_q, register_10_q;

  Clock clock_1 (.out(clock_1_out));
  Demultiplexer #(.select(4)) demultiplexer_1 (
    .out0(demultiplexer_1_out0), .out1(demultiplexer_1_out1), .out2(demultiplexer_1_out2),
    .out3(demultiplexer_1_out3), .out4(demultiplexer_1_out4), .out5(demultiplexer_1_out5),
    .out6(demultiplexer_1_out6), .out7(demultiplexer_1_out7), .out8(demultiplexer_1_out8),
    .out9(demultiplexer_1_out9), .in(STORE), .sel(REGADDR));  // open: out10, out11, out12, out13, out14, out15, en
  Register #(.width(32)) register_1 (
    .D(REGSTR), .en(demultiplexer_1_out0), .Q(register_1_q), .clk(clock_1_out));  // open: clr
  Register #(.width(32)) register_2 (
    .D(REGSTR), .en(demultiplexer_1_out1), .Q(register_2_q), .clk(clock_1_out));  // open: clr
  Register #(.width(32)) register_3 (
    .D(REGSTR), .en(demultiplexer_1_out2), .Q(register_3_q), .clk(clock_1_out));  // open: clr
  Register #(.width(32)) register_4 (
    .D(REGSTR), .en(demultiplexer_1_out3), .Q(register_4_q), .clk(clock_1_out));  // open: clr
  Register #(.width(32)) register_5 (
    .D(REGSTR), .en(demultiplexer_1_out4), .Q(register_5_q), .clk(clock_1_out));  // open: clr
  Register #(.width(32)) register_6 (
    .D(REGSTR), .en(demultiplexer_1_out5), .Q(register_6_q), .clk(clock_1_out));  // open: clr
  Register #(.width(32)) register_7 (
    .D(REGSTR), .en(demultiplexer_1_out6), .Q(register_7_q), .clk(clock_1_out));  // open: clr
  Register #(.width(32)) register_8 (
    .D(REGSTR), .en(demultiplexer_1_out7), .Q(register_8_q), .clk(clock_1_out));  // open: clr
  Register #(.width(32)) register_9 (
    .D(REGSTR), .en(demultiplexer_1_out8), .Q(register_9_q), .clk(clock_1_out));  // open: clr
  Register #(.width(32)) register_10 (
    .D(REGSTR), .en(demultiplexer_1_out9), .Q(register_10_q), .clk(clock_1_out));  // open: clr
  Multiplexer #(.select(4), .width(32)) multiplexer_1 (
    .in0(register_1_q), .in1(register_2_q), .in2(register_3_q), .in3(register_4_q), .in4(register_5_q),
    .in5(register_6_q), .in6(register_7_q), .in7(register_8_q), .in8(register_9_q), .in9(register_10_q),
    .out(REGVAL), .sel(REGADDR));  // open: in10, in11, in12, in13, in14, in15, en
endmodule

module PC (
  input  [15:0] BRANCH,
  input  SELPC,
  input  LOADPC,
  output [15:0] out_4
);

  wire clock_1_out;
  wire [15:0] inc16_1_out_2, multiplexer_1_out;

  Clock clock_1 (.out(clock_1_out));
  INC16 inc16_1 (.in_1(out_4), .out_2(inc16_1_out_2));
  Multiplexer #(.width(16)) multiplexer_1 (
    .in0(inc16_1_out_2), .in1(BRANCH), .out(multiplexer_1_out), .sel(SELPC));  // open: en
  Register #(.width(16)) PC (.D(multiplexer_1_out), .en(LOADPC), .Q(out_4), .clk(clock_1_out));  // open: clr

  // Notes on the sheet:
  //   SELPC:
  //   0 -> PC + 1
  //   1 -> BRANCH
endmodule

module IR (
  input  [31:0] INSTRN,
  input  LOADIR,
  input  INSTRN_2,
  output [31:0] INSTR0,
  output [31:0] INSTR1
);

  wire and_1_out, and_2_out, clock_1_out;

  Clock clock_1 (.out(clock_1_out));
  and and_1 (and_1_out, LOADIR, ~INSTRN_2);  // AND_Gate
  and and_2 (and_2_out, LOADIR, INSTRN_2);
  Register #(.width(32)) INSTR (.D(INSTRN), .en(and_1_out), .Q(INSTR0), .clk(clock_1_out));  // open: clr
  Register #(.width(32)) IMM (.D(INSTRN), .en(and_2_out), .Q(INSTR1), .clk(clock_1_out));  // open: clr
endmodule

module MEM (
  input  [15:0] ADDR,
  input  [31:0] DATA,
  input  STORE,
  input  LOAD,
  input  LOADNEXT,
  output [31:0] DATA_2
);

  wire clock_1_out, or_1_out;
  wire [15:0] inc16_1_out_2, multiplexer_1_out;

  INC16 inc16_1 (.in_1(ADDR), .out_2(inc16_1_out_2));
  Multiplexer #(.width(16)) multiplexer_1 (
    .in0(ADDR), .in1(inc16_1_out_2), .out(multiplexer_1_out), .sel(LOADNEXT));  // open: en
  or or_1 (or_1_out, LOAD, LOADNEXT);
  Clock clock_1 (.out(clock_1_out));
  RAM #(.addrWidth(16), .dataWidth(32), .bus("separate")) ram_1 (
    .addr(multiplexer_1_out), .din(DATA), .data(DATA_2), .str(STORE), .clk(clock_1_out), .ld(or_1_out));  // open: sel, clr
endmodule

module INC3 (
  input  [2:0] in_1,
  output [2:0] out_2
);

  wire [2:0] bit_extender_1_out;

  assign bit_extender_1_out = {{2{1'b0}}, 1'b1};  // Bit_Extender bit_extender_1
  Adder #(.width(3)) adder_1 (.a(bit_extender_1_out), .b(in_1), .out(out_2));  // open: cin, cout
endmodule

module INC8 (
  input  [7:0] in_1,
  output [7:0] out_2
);

  wire [7:0] bit_extender_1_out;

  assign bit_extender_1_out = {{7{1'b0}}, 1'b1};  // Bit_Extender bit_extender_1
  Adder adder_1 (.a(bit_extender_1_out), .b(in_1), .out(out_2));  // open: cin, cout
endmodule

module INC16 (
  input  [15:0] in_1,
  output [15:0] out_2
);

  wire [15:0] bit_extender_1_out;

  assign bit_extender_1_out = {{15{1'b0}}, 1'b1};  // Bit_Extender bit_extender_1
  Adder #(.width(16)) adder_1 (.a(bit_extender_1_out), .b(in_1), .out(out_2));  // open: cin, cout
endmodule

module INC32 (
  input  [31:0] in_1,
  output [31:0] out_2
);

  wire [31:0] bit_extender_1_out;

  assign bit_extender_1_out = {{31{1'b0}}, 1'b1};  // Bit_Extender bit_extender_1
  Adder #(.width(32)) adder_1 (.a(bit_extender_1_out), .b(in_1), .out(out_2));  // open: cin, cout
endmodule

module BUFF (
  input  in_1,
  output out_2
);

  wire buffer_1_out, buffer_2_out, buffer_3_out, buffer_4_out, buffer_5_out, buffer_6_out, buffer_7_out,
       buffer_8_out, buffer_9_out, buffer_10_out, buffer_11_out, buffer_12_out, buffer_13_out, buffer_14_out,
       buffer_15_out, buffer_16_out, buffer_17_out, buffer_18_out, buffer_19_out, buffer_20_out,
       buffer_21_out, buffer_22_out;

  buf buffer_1 (buffer_1_out, buffer_4_out);
  buf buffer_2 (buffer_2_out, in_1);
  buf buffer_3 (buffer_3_out, buffer_2_out);
  buf buffer_4 (buffer_4_out, buffer_3_out);
  buf buffer_5 (buffer_5_out, buffer_1_out);
  buf buffer_6 (buffer_6_out, buffer_8_out);
  buf buffer_7 (buffer_7_out, buffer_5_out);
  buf buffer_8 (buffer_8_out, buffer_7_out);
  buf buffer_9 (buffer_9_out, buffer_10_out);
  buf buffer_10 (buffer_10_out, buffer_6_out);
  buf buffer_11 (buffer_11_out, buffer_12_out);
  buf buffer_12 (buffer_12_out, buffer_9_out);
  buf buffer_13 (buffer_13_out, buffer_11_out);
  buf buffer_14 (buffer_14_out, buffer_13_out);
  buf buffer_15 (buffer_15_out, buffer_14_out);
  buf buffer_16 (buffer_16_out, buffer_15_out);
  buf buffer_17 (buffer_17_out, buffer_16_out);
  buf buffer_18 (buffer_18_out, buffer_19_out);
  buf buffer_19 (buffer_19_out, buffer_17_out);
  buf buffer_20 (buffer_20_out, buffer_18_out);
  buf buffer_21 (buffer_21_out, buffer_22_out);
  buf buffer_22 (buffer_22_out, buffer_20_out);
  buf buffer_23 (out_2, buffer_21_out);
endmodule
