// Logisim project Computer Units.circ as structural Verilog
module CALCULATOR (
  input  in_1,
  input  in_2,
  input  in_3,
  input  INPUT_A,
  input  [7:0] in_5,
  input  [7:0] INPUT_B,
  output out_7,
  output out_8,
  output out_9,
  output [14:0] out_10
);

  wire _1_2_2_out, _1_2_3_out, _1_2_4_out, _1_2_5_out, _1_2_6_out, _1_2_7_out, _1_2_out, _1_2_out_2,
       _1_3_out, _1_4_2_out, _1_4_3_out, _1_4_4_out, _1_4_5_out, _1_4_6_out, _1_4_out, _1_4_out_2, _1_5_out,
       _1_6_out, _1_7_out, _1_8_2_out, _1_8_3_out, _1_8_4_out, _1_8_5_out, _1_8_out, _1_8_out_2, _1_16_2_out,
       _1_16_3_out, _1_16_4_out, _1_16_out, _1_32_2_out, _1_32_3_out, _1_32_out, _1_64_2_out, _1_64_out,
       _1_out, _2_2_out, _2_3_out, _2_4_out, _2_5_out, _2_6_out, _2_7_out, _2_out, _4_2_out, _4_3_out,
       _4_4_out, _4_5_out, _4_6_out, _4_out, _8_2_out, _8_3_out, _8_4_out, _8_5_out, _8_out, _16_2_out,
       _16_3_out, _16_4_out, _16_out, _32_2_out, _32_3_out, _32_out, _64_2_out, _64_out, _128_out,
       adder_1_out_17, adder_1_out_18, adder_1_out_19, adder_1_out_20, adder_1_out_21, adder_1_out_22,
       adder_1_out_23, adder_1_out_24, adder_1_out_25, and_1_out, and_2_out, and_3_out, and_4_out, and_5_out,
       and_6_out, and_7_out, and_8_out, and_9_out, and_10_out, and_11_out, and_12_out, and_13_out,
       and_14_out, and_15_out, and_16_out, and_17_out, and_18_out, and_19_out, and_20_out, and_21_out,
       and_22_out, and_23_out, and_24_out, and_25_out, and_26_out, and_27_out, and_28_out, and_29_out,
       and_30_out, and_31_out, and_32_out, and_33_out, and_34_out, and_35_out, and_36_out, and_37_out,
       and_38_out, and_39_out, and_40_out, and_41_out, and_42_out, and_43_out, and_44_out, and_45_out,
       and_46_out, and_47_out, and_48_out, and_49_out, and_50_out, and_51_out, and_52_out, and_53_out,
       and_54_out, and_55_out, and_56_out, and_57_out, and_58_out, and_59_out, and_60_out, and_61_out,
       and_62_out, and_63_out, and_64_out, bcd_to_7_segment_1_out_5, bcd_to_7_segment_1_out_6,
       bcd_to_7_segment_1_out_7, bcd_to_7_segment_1_out_8, bcd_to_7_segment_1_out_9,
       bcd_to_7_segment_1_out_10, bcd_to_7_segment_1_out_11, bcd_to_7_segment_2_out_5,
       bcd_to_7_segment_2_out_6, bcd_to_7_segment_2_out_7, bcd_to_7_segment_2_out_8,
       bcd_to_7_segment_2_out_9, bcd_to_7_segment_2_out_10, bcd_to_7_segment_2_out_11,
       bcd_to_7_segment_3_out_5, bcd_to_7_segment_3_out_6, bcd_to_7_segment_3_out_7,
       bcd_to_7_segment_3_out_8, bcd_to_7_segment_3_out_9, bcd_to_7_segment_3_out_10,
       bcd_to_7_segment_3_out_11, bcd_to_7_segment_4_out_5, bcd_to_7_segment_4_out_6,
       bcd_to_7_segment_4_out_7, bcd_to_7_segment_4_out_8, bcd_to_7_segment_4_out_9,
       bcd_to_7_segment_4_out_10, bcd_to_7_segment_4_out_11, bcd_to_7_segment_5_out_5,
       bcd_to_7_segment_5_out_6, bcd_to_7_segment_5_out_7, bcd_to_7_segment_5_out_8,
       bcd_to_7_segment_5_out_9, bcd_to_7_segment_5_out_10, bcd_to_7_segment_5_out_11,
       binary_bcd_9bit_1_out_10, binary_bcd_9bit_1_out_11, binary_bcd_9bit_1_out_12,
       binary_bcd_9bit_1_out_13, binary_bcd_9bit_1_out_14, binary_bcd_9bit_1_out_15,
       binary_bcd_9bit_1_out_16, binary_bcd_9bit_1_out_17, binary_bcd_9bit_1_out_18,
       binary_bcd_9bit_1_out_19, binary_bcd_9bit_1_out_20, binary_bcd_9bit_1_out_21,
       binary_bcd_16bit_1_out_17, binary_bcd_16bit_1_out_18, binary_bcd_16bit_1_out_19,
       binary_bcd_16bit_1_out_20, binary_bcd_16bit_1_out_21, binary_bcd_16bit_1_out_22,
       binary_bcd_16bit_1_out_23, binary_bcd_16bit_1_out_24, binary_bcd_16bit_1_out_25,
       binary_bcd_16bit_1_out_26, binary_bcd_16bit_1_out_27, binary_bcd_16bit_1_out_28,
       binary_bcd_16bit_1_out_29, binary_bcd_16bit_1_out_30, binary_bcd_16bit_1_out_31,
       binary_bcd_16bit_1_out_32, binary_bcd_16bit_1_out_33, binary_bcd_16bit_1_out_34,
       binary_bcd_16bit_1_out_35, binary_bcd_16bit_1_out_36, binary_bcd_decoder_1_out_9,
       binary_bcd_decoder_1_out_10, binary_bcd_decoder_1_out_11, binary_bcd_decoder_1_out_12,
       binary_bcd_decoder_1_out_13, binary_bcd_decoder_1_out_14, binary_bcd_decoder_1_out_15,
       binary_bcd_decoder_1_out_16, binary_bcd_decoder_1_out_17, binary_bcd_decoder_1_out_18,
       binary_bcd_decoder_1_out_19, full_adder_full_1_out_4, full_adder_full_1_out_5,
       full_adder_full_2_out_4, full_adder_full_2_out_5, full_adder_full_3_out_4, full_adder_full_3_out_5,
       full_adder_full_4_out_4, full_adder_full_4_out_5, full_adder_full_5_out_4, full_adder_full_5_out_5,
       full_adder_full_6_out_4, full_adder_full_6_out_5, full_adder_full_7_out_4, full_adder_full_7_out_5,
       full_adder_full_8_out_4, full_adder_full_8_out_5, full_adder_full_9_out_4, full_adder_full_9_out_5,
       full_adder_full_10_out_4, full_adder_full_10_out_5, full_adder_full_11_out_4,
       full_adder_full_11_out_5, full_adder_full_12_out_4, full_adder_full_12_out_5,
       full_adder_full_13_out_4, full_adder_full_13_out_5, full_adder_full_14_out_4,
       full_adder_full_14_out_5, full_adder_full_15_out_4, full_adder_full_15_out_5,
       full_adder_full_16_out_4, full_adder_full_16_out_5, full_adder_full_17_out_4,
       full_adder_full_17_out_5, full_adder_full_18_out_4, full_adder_full_18_out_5,
       full_adder_full_19_out_4, full_adder_full_19_out_5, full_adder_full_20_out_4,
       full_adder_full_20_out_5, full_adder_full_21_out_4, full_adder_full_21_out_5,
       full_adder_full_22_out_4, full_adder_full_22_out_5, full_adder_full_23_out_4,
       full_adder_full_23_out_5, full_adder_full_24_out_4, full_adder_full_24_out_5,
       full_adder_full_25_out_4, full_adder_full_25_out_5, full_adder_full_26_out_4,
       full_adder_full_26_out_5, full_adder_full_27_out_4, full_adder_full_27_out_5,
       full_adder_full_28_out_4, full_adder_full_28_out_5, full_adder_full_29_out_4,
       full_adder_full_29_out_5, full_adder_full_30_out_4, full_adder_full_30_out_5,
       full_adder_full_31_out_4, full_adder_full_31_out_5, full_adder_full_32_out_4,
       full_adder_full_32_out_5, full_adder_full_33_out_4, full_adder_full_33_out_5,
       full_adder_full_34_out_4, full_adder_full_34_out_5, full_adder_full_35_out_4,
       full_adder_full_35_out_5, full_adder_full_36_out_4, full_adder_full_36_out_5,
       full_adder_full_37_out_4, full_adder_full_37_out_5, full_adder_full_38_out_4,
       full_adder_full_38_out_5, full_adder_full_39_out_4, full_adder_full_39_out_5,
       full_adder_full_40_out_4, full_adder_full_40_out_5, full_adder_full_41_out_4,
       full_adder_full_41_out_5, full_adder_full_42_out_4, full_adder_full_42_out_5, half_adder_full_1_out_4,
       half_adder_full_2_out_4, half_adder_full_3_out_4, half_adder_full_4_out_4, half_adder_full_5_out_4,
       half_adder_full_6_out_4, half_adder_full_7_out_4, half_adder_full_8_out_4, half_adder_full_9_out_4,
       half_adder_full_10_out_3, half_adder_full_10_out_4, half_adder_full_11_out_4,
       half_adder_full_12_out_3, half_adder_full_12_out_4, half_adder_full_13_out_3,
       half_adder_full_13_out_4, half_adder_full_14_out_4, half_adder_full_15_out_3,
       half_adder_full_15_out_4, half_adder_full_16_out_3, half_adder_full_16_out_4,
       half_adder_full_17_out_3, half_adder_full_17_out_4, half_adder_full_18_out_4,
       half_adder_full_19_out_4, half_adder_full_20_out_3, half_adder_full_20_out_4,
       half_adder_full_21_out_3, half_adder_full_21_out_4, half_adder_full_22_out_3,
       half_adder_full_22_out_4, half_adder_full_23_out_3, half_adder_full_23_out_4,
       half_adder_full_24_out_3, half_adder_full_24_out_4, half_adder_full_25_out_3,
       half_adder_full_25_out_4, half_adder_full_26_out_3, half_adder_full_26_out_4,
       half_adder_full_27_out_3, half_adder_full_27_out_4, half_adder_full_28_out_3,
       half_adder_full_28_out_4, half_adder_full_30_out_3, half_adder_full_31_out_3,
       half_adder_full_32_out_3, half_adder_full_33_out_3, half_adder_full_34_out_3,
       half_adder_full_35_out_3, n1st_bit_pair_comparison_1_out_3, n1st_bit_pair_comparison_1_out_4,
       n8bit_multiplication_1__1, n8bit_multiplication_1__2, n8bit_multiplication_1__4,
       n8bit_multiplication_1__8, n8bit_multiplication_1__16, n8bit_multiplication_1__32,
       n8bit_multiplication_1__64, n8bit_multiplication_1__128, n8bit_multiplication_1__256,
       n8bit_multiplication_1__512, n8bit_multiplication_1__1024, n8bit_multiplication_1__2048,
       n8bit_multiplication_1__4096, n8bit_multiplication_1__8192, n8bit_multiplication_1__16384,
       n8bit_multiplication_1__32768, not_1_out, not_2_out, nth_bit_pair_comparison_1_out_5,
       nth_bit_pair_comparison_1_out_6, nth_bit_pair_comparison_2_out_5, nth_bit_pair_comparison_2_out_6,
       nth_bit_pair_comparison_3_out_5, nth_bit_pair_comparison_3_out_6, nth_bit_pair_comparison_4_out_5,
       nth_bit_pair_comparison_4_out_6, nth_bit_pair_comparison_5_out_5, nth_bit_pair_comparison_5_out_6,
       nth_bit_pair_comparison_6_out_5, nth_bit_pair_comparison_6_out_6, or_1_out, or_2_out, or_3_out,
       or_4_out, or_5_out, or_6_out, or_7_out, or_8_out, or_9_out, or_10_out, or_11_out, or_12_out,
       or_13_out, or_14_out, or_15_out, or_16_out, or_17_out, or_18_out, or_19_out, or_20_out, or_21_out,
       or_22_out, or_23_out, or_24_out, or_25_out, or_26_out, or_27_out, or_28_out, or_29_out, or_30_out,
       or_31_out, or_32_out, random_number_generator_1_out_1, random_number_generator_1_out_2,
       random_number_generator_1_out_3, random_number_generator_1_out_4, random_number_generator_1_out_5,
       random_number_generator_1_out_6, random_number_generator_1_out_7, random_number_generator_1_out_8,
       random_number_generator_1_out_9, random_number_generator_1_out_10, random_number_generator_1_out_11,
       random_number_generator_1_out_12, random_number_generator_1_out_13, random_number_generator_1_out_14,
       random_number_generator_1_out_15, random_number_generator_1_out_16, random_number_generator_1_out_17,
       random_number_generator_1_out_18, random_number_generator_1_out_19, random_number_generator_1_out_20,
       subtractor_1_out_17, subtractor_1_out_18, subtractor_1_out_19, subtractor_1_out_20,
       subtractor_1_out_21, subtractor_1_out_22, subtractor_1_out_23, subtractor_1_out_24,
       subtractor_1_out_25;

  Random_number_generator random_number_generator_1 (
    .out_1(random_number_generator_1_out_1), .out_2(random_number_generator_1_out_2),
    .out_3(random_number_generator_1_out_3), .out_4(random_number_generator_1_out_4),
    .out_5(random_number_generator_1_out_5), .out_6(random_number_generator_1_out_6),
    .out_7(random_number_generator_1_out_7), .out_8(random_number_generator_1_out_8),
    .out_9(random_number_generator_1_out_9), .out_10(random_number_generator_1_out_10),
    .out_11(random_number_generator_1_out_11), .out_12(random_number_generator_1_out_12),
    .out_13(random_number_generator_1_out_13), .out_14(random_number_generator_1_out_14),
    .out_15(random_number_generator_1_out_15), .out_16(random_number_generator_1_out_16),
    .out_17(random_number_generator_1_out_17), .out_18(random_number_generator_1_out_18),
    .out_19(random_number_generator_1_out_19), .out_20(random_number_generator_1_out_20));
  and and_1 (and_1_out, in_5[0], in_1);
  and and_2 (and_2_out, in_5[0], in_3);
  and and_3 (and_3_out, in_5[1], in_3);
  and and_4 (and_4_out, in_5[1], in_1);
  and and_5 (and_5_out, in_5[3], in_1);
  and and_6 (and_6_out, in_5[2], in_1);
  and and_7 (and_7_out, in_5[4], in_3);
  and and_8 (and_8_out, in_5[2], in_3);
  and and_9 (and_9_out, in_5[3], in_3);
  Binary_BCD_16bit binary_bcd_16bit_1 (
    .in_1(n8bit_multiplication_1__32768), .in_2(n8bit_multiplication_1__16384),
    .in_3(n8bit_multiplication_1__8192), .in_4(n8bit_multiplication_1__4096),
    .in_5(n8bit_multiplication_1__2048), .in_6(n8bit_multiplication_1__1024),
    .in_7(n8bit_multiplication_1__512), .in_8(n8bit_multiplication_1__256),
    .in_9(n8bit_multiplication_1__128), .in_10(n8bit_multiplication_1__64),
    .in_11(n8bit_multiplication_1__32), .in_12(n8bit_multiplication_1__16),
    .in_13(n8bit_multiplication_1__8), .in_14(n8bit_multiplication_1__4), .in_15(n8bit_multiplication_1__2),
    .in_16(n8bit_multiplication_1__1), .out_17(binary_bcd_16bit_1_out_17),
    .out_18(binary_bcd_16bit_1_out_18), .out_19(binary_bcd_16bit_1_out_19),
    .out_20(binary_bcd_16bit_1_out_20), .out_21(binary_bcd_16bit_1_out_21),
    .out_22(binary_bcd_16bit_1_out_22), .out_23(binary_bcd_16bit_1_out_23),
    .out_24(binary_bcd_16bit_1_out_24), .out_25(binary_bcd_16bit_1_out_25),
    .out_26(binary_bcd_16bit_1_out_26), .out_27(binary_bcd_16bit_1_out_27),
    .out_28(binary_bcd_16bit_1_out_28), .out_29(binary_bcd_16bit_1_out_29),
    .out_30(binary_bcd_16bit_1_out_30), .out_31(binary_bcd_16bit_1_out_31),
    .out_32(binary_bcd_16bit_1_out_32), .out_33(binary_bcd_16bit_1_out_33),
    .out_34(binary_bcd_16bit_1_out_34), .out_35(binary_bcd_16bit_1_out_35), .out_36(binary_bcd_16bit_1_out_36));
  _8bit_Multiplication u_8bit_multiplication_1 (
    .in_1(and_1_out), .in_2(and_4_out), .in_3(and_6_out), .in_4(and_5_out), .in_5(and_10_out),
    .in_6(and_11_out), .in_7(and_15_out), .in_8(and_14_out), .in_9(and_16_out), .in_10(and_19_out),
    .in_11(and_20_out), .in_12(and_18_out), .in_13(and_23_out), .in_14(and_22_out), .in_15(and_27_out),
    .in_16(and_26_out), ._1(n8bit_multiplication_1__1), ._2(n8bit_multiplication_1__2),
    ._4(n8bit_multiplication_1__4), ._8(n8bit_multiplication_1__8), ._16(n8bit_multiplication_1__16),
    ._32(n8bit_multiplication_1__32), ._64(n8bit_multiplication_1__64), ._128(n8bit_multiplication_1__128),
    ._256(n8bit_multiplication_1__256), ._512(n8bit_multiplication_1__512),
    ._1024(n8bit_multiplication_1__1024), ._2048(n8bit_multiplication_1__2048),
    ._4096(n8bit_multiplication_1__4096), ._8192(n8bit_multiplication_1__8192),
    ._16384(n8bit_multiplication_1__16384), ._32768(n8bit_multiplication_1__32768));
  and and_10 (and_10_out, in_5[4], in_1);
  and and_11 (and_11_out, in_5[5], in_1);
  and and_12 (and_12_out, in_5[5], in_3);
  and and_13 (and_13_out, in_5[6], in_3);
  and and_14 (and_14_out, in_5[7], in_1);
  and and_15 (and_15_out, in_5[6], in_1);
  and and_16 (and_16_out, INPUT_B[0], in_1);
  and and_17 (and_17_out, in_5[7], in_3);
  or or_1 (or_1_out, random_number_generator_1_out_1, binary_bcd_16bit_1_out_17);
  or or_2 (or_2_out, random_number_generator_1_out_2, binary_bcd_16bit_1_out_18);
  or or_3 (or_3_out, random_number_generator_1_out_3, binary_bcd_16bit_1_out_19);
  or or_4 (or_4_out, random_number_generator_1_out_4, binary_bcd_16bit_1_out_20);
  or or_5 (or_5_out, random_number_generator_1_out_5, binary_bcd_16bit_1_out_21);
  or or_6 (or_6_out, random_number_generator_1_out_6, binary_bcd_16bit_1_out_22);
  or or_7 (or_7_out, random_number_generator_1_out_7, binary_bcd_16bit_1_out_23);
  or or_8 (or_8_out, random_number_generator_1_out_8, binary_bcd_16bit_1_out_24);
  or or_9 (or_9_out, binary_bcd_16bit_1_out_25, random_number_generator_1_out_9);
  or or_10 (or_10_out, binary_bcd_16bit_1_out_26, random_number_generator_1_out_10);
  or or_11 (or_11_out, binary_bcd_16bit_1_out_27, random_number_generator_1_out_11);
  or or_12 (or_12_out, binary_bcd_16bit_1_out_28, random_number_generator_1_out_12);
  or or_13 (or_13_out, binary_bcd_16bit_1_out_29, random_number_generator_1_out_13);
  or or_14 (or_14_out, binary_bcd_16bit_1_out_30, random_number_generator_1_out_14);
  and and_18 (and_18_out, INPUT_B[3], in_1);
  and and_19 (and_19_out, INPUT_B[1], in_1);
  and and_20 (and_20_out, INPUT_B[2], in_1);
  and and_21 (and_21_out, INPUT_B[0], in_3);
  or or_15 (or_15_out, binary_bcd_16bit_1_out_31, random_number_generator_1_out_15);
  or or_16 (or_16_out, binary_bcd_16bit_1_out_32, random_number_generator_1_out_16);
  or or_17 (or_17_out, binary_bcd_16bit_1_out_33, random_number_generator_1_out_17);
  and and_22 (and_22_out, INPUT_B[5], in_1);
  and and_23 (and_23_out, INPUT_B[4], in_1);
  and and_24 (and_24_out, INPUT_B[1], in_3);
  and and_25 (and_25_out, INPUT_B[2], in_3);
  Half_adder_full half_adder_full_1 (
    .in_1(_1_64_out), .in_2(_1_64_2_out), .out_3(out_10[1]), .out_4(half_adder_full_1_out_4));
  and _1 (_1_out, and_17_out, and_33_out);
  and _1_2 (_1_2_out, and_13_out, and_33_out);
  or or_18 (or_18_out, binary_bcd_16bit_1_out_34, random_number_generator_1_out_18);
  or or_19 (or_19_out, binary_bcd_16bit_1_out_35, random_number_generator_1_out_19);
  or or_20 (or_20_out, binary_bcd_16bit_1_out_36, random_number_generator_1_out_20);
  and and_26 (and_26_out, INPUT_B[7], in_1);
  and and_27 (and_27_out, INPUT_B[6], in_1);
  and and_28 (and_28_out, INPUT_B[5], in_3);
  and and_29 (and_29_out, INPUT_B[3], in_3);
  and and_30 (and_30_out, INPUT_B[4], in_3);
  Half_adder_full half_adder_full_2 (
    .in_1(full_adder_full_1_out_4), .in_2(_1_32_3_out), .out_3(out_10[2]), .out_4(half_adder_full_2_out_4));
  Full_adder_full full_adder_full_1 (
    .in_1(half_adder_full_1_out_4), .in_2(_1_32_out), .in_3(_1_32_2_out), .out_4(full_adder_full_1_out_4),
    .out_5(full_adder_full_1_out_5));
  and _1_8 (_1_8_out, and_7_out, and_33_out);
  and _1_16 (_1_16_out, and_9_out, and_33_out);
  and _1_4 (_1_4_out, and_12_out, and_33_out);
  Binary_BCD_9bit binary_bcd_9bit_1 (
    .in_1(adder_1_out_17), .in_2(adder_1_out_18), .in_3(adder_1_out_19), .in_4(adder_1_out_20),
    .in_5(adder_1_out_21), .in_6(adder_1_out_22), .in_7(adder_1_out_23), .in_8(adder_1_out_24),
    .in_9(adder_1_out_25), .out_10(binary_bcd_9bit_1_out_10), .out_11(binary_bcd_9bit_1_out_11),
    .out_12(binary_bcd_9bit_1_out_12), .out_13(binary_bcd_9bit_1_out_13), .out_14(binary_bcd_9bit_1_out_14),
    .out_15(binary_bcd_9bit_1_out_15), .out_16(binary_bcd_9bit_1_out_16), .out_17(binary_bcd_9bit_1_out_17),
    .out_18(binary_bcd_9bit_1_out_18), .out_19(binary_bcd_9bit_1_out_19), .out_20(binary_bcd_9bit_1_out_20),
    .out_21(binary_bcd_9bit_1_out_21));
  Adder adder_1 (
    .in_1(and_31_out), .in_2(and_34_out), .in_3(and_35_out), .in_4(and_36_out), .in_5(and_37_out),
    .in_6(and_39_out), .in_7(and_38_out), .in_8(and_40_out), .in_9(and_41_out), .in_10(and_42_out),
    .in_11(and_43_out), .in_12(and_44_out), .in_13(and_45_out), .in_14(and_47_out), .in_15(and_46_out),
    .in_16(and_48_out), .out_17(adder_1_out_17), .out_18(adder_1_out_18), .out_19(adder_1_out_19),
    .out_20(adder_1_out_20), .out_21(adder_1_out_21), .out_22(adder_1_out_22), .out_23(adder_1_out_23),
    .out_24(adder_1_out_24), .out_25(adder_1_out_25));
  and and_31 (and_31_out, in_2, in_5[0]);
  and and_32 (and_32_out, INPUT_B[6], in_3);
  and and_33 (and_33_out, INPUT_B[7], in_3);
  Half_adder_full half_adder_full_3 (
    .in_1(full_adder_full_2_out_4), .in_2(_1_8_5_out), .out_3(out_10[4]), .out_4(half_adder_full_3_out_4));
  Full_adder_full full_adder_full_2 (
    .in_1(full_adder_full_3_out_4), .in_2(half_adder_full_4_out_4), .in_3(_1_8_4_out),
    .out_4(full_adder_full_2_out_4), .out_5(full_adder_full_2_out_5));
  Half_adder_full half_adder_full_4 (
    .in_1(full_adder_full_4_out_4), .in_2(_1_16_4_out), .out_3(out_10[3]), .out_4(half_adder_full_4_out_4));
  Full_adder_full full_adder_full_3 (
    .in_1(full_adder_full_5_out_4), .in_2(full_adder_full_4_out_5), .in_3(_1_8_3_out),
    .out_4(full_adder_full_3_out_4), .out_5(full_adder_full_3_out_5));
  Full_adder_full full_adder_full_4 (
    .in_1(half_adder_full_2_out_4), .in_2(full_adder_full_6_out_4), .in_3(_1_16_3_out),
    .out_4(full_adder_full_4_out_4), .out_5(full_adder_full_4_out_5));
  Full_adder_full full_adder_full_5 (
    .in_1(full_adder_full_6_out_5), .in_2(_1_8_2_out), .in_3(_1_8_out), .out_4(full_adder_full_5_out_4),
    .out_5(full_adder_full_5_out_5));
  Full_adder_full full_adder_full_6 (
    .in_1(full_adder_full_1_out_5), .in_2(_1_16_2_out), .in_3(_1_16_out), .out_4(full_adder_full_6_out_4),
    .out_5(full_adder_full_6_out_5));
  and _1_32 (_1_32_out, and_8_out, and_33_out);
  and _1_128 (out_10[0], and_2_out, and_33_out);
  and _1_64 (_1_64_out, and_3_out, and_33_out);
  and and_34 (and_34_out, in_2, in_5[1]);
  and and_35 (and_35_out, in_2, in_5[2]);
  and and_36 (and_36_out, in_2, in_5[3]);
  Half_adder_full half_adder_full_5 (
    .in_1(full_adder_full_7_out_4), .in_2(_1_4_6_out), .out_3(out_10[5]), .out_4(half_adder_full_5_out_4));
  Full_adder_full full_adder_full_7 (
    .in_1(half_adder_full_3_out_4), .in_2(full_adder_full_8_out_4), .in_3(_1_4_5_out),
    .out_4(full_adder_full_7_out_4), .out_5(full_adder_full_7_out_5));
  Full_adder_full full_adder_full_8 (
    .in_1(full_adder_full_9_out_4), .in_2(full_adder_full_2_out_5), .in_3(_1_4_4_out),
    .out_4(full_adder_full_8_out_4), .out_5(full_adder_full_8_out_5));
  Full_adder_full full_adder_full_9 (
    .in_1(full_adder_full_10_out_4), .in_2(full_adder_full_3_out_5), .in_3(_1_4_3_out),
    .out_4(full_adder_full_9_out_4), .out_5(full_adder_full_9_out_5));
  Full_adder_full full_adder_full_10 (
    .in_1(full_adder_full_5_out_5), .in_2(_1_4_out), .in_3(_1_4_2_out), .out_4(full_adder_full_10_out_4),
    .out_5(full_adder_full_10_out_5));
  and _1_2_dup2 (_1_2_out_2, and_13_out, and_32_out);
  and _2 (_2_out, and_17_out, and_32_out);
  and and_37 (and_37_out, in_2, in_5[4]);
  and and_38 (and_38_out, in_2, in_5[6]);
  and and_39 (and_39_out, in_2, in_5[5]);
  Half_adder_full half_adder_full_6 (
    .in_1(full_adder_full_11_out_4), .in_2(_1_2_7_out), .out_3(out_10[6]), .out_4(half_adder_full_6_out_4));
  Full_adder_full full_adder_full_11 (
    .in_1(full_adder_full_12_out_4), .in_2(half_adder_full_5_out_4), .in_3(_1_2_6_out),
    .out_4(full_adder_full_11_out_4), .out_5(full_adder_full_11_out_5));
  Full_adder_full full_adder_full_12 (
    .in_1(full_adder_full_13_out_4), .in_2(full_adder_full_7_out_5), .in_3(_1_2_5_out),
    .out_4(full_adder_full_12_out_4), .out_5(full_adder_full_12_out_5));
  Full_adder_full full_adder_full_13 (
    .in_1(full_adder_full_14_out_4), .in_2(full_adder_full_8_out_5), .in_3(_1_2_4_out),
    .out_4(full_adder_full_13_out_4), .out_5(full_adder_full_13_out_5));
  Full_adder_full full_adder_full_14 (
    .in_1(full_adder_full_15_out_4), .in_2(full_adder_full_9_out_5), .in_3(_1_2_3_out),
    .out_4(full_adder_full_14_out_4), .out_5(full_adder_full_14_out_5));
  Full_adder_full full_adder_full_15 (
    .in_1(full_adder_full_10_out_5), .in_2(_1_2_out), .in_3(_1_2_2_out), .out_4(full_adder_full_15_out_4),
    .out_5(full_adder_full_15_out_5));
  and _1_4_2 (_1_4_2_out, and_7_out, and_32_out);
  and _1_2_2 (_1_2_2_out, and_12_out, and_32_out);
  and _1_8_2 (_1_8_2_out, and_9_out, and_32_out);
  and and_40 (and_40_out, in_2, in_5[7]);
  and and_41 (and_41_out, in_2, INPUT_B[0]);
  Half_adder_full half_adder_full_7 (
    .in_1(full_adder_full_16_out_4), .in_2(_1_8_out_2), .out_3(out_10[7]), .out_4(half_adder_full_7_out_4));
  Full_adder_full full_adder_full_16 (
    .in_1(half_adder_full_6_out_4), .in_2(full_adder_full_17_out_4), .in_3(_1_7_out),
    .out_4(full_adder_full_16_out_4), .out_5(full_adder_full_16_out_5));
  Full_adder_full full_adder_full_17 (
    .in_1(full_adder_full_11_out_5), .in_2(full_adder_full_18_out_4), .in_3(_1_6_out),
    .out_4(full_adder_full_17_out_4), .out_5(full_adder_full_17_out_5));
  Full_adder_full full_adder_full_18 (
    .in_1(full_adder_full_12_out_5), .in_2(full_adder_full_19_out_4), .in_3(_1_5_out),
    .out_4(full_adder_full_18_out_4), .out_5(full_adder_full_18_out_5));
  Full_adder_full full_adder_full_19 (
    .in_1(full_adder_full_13_out_5), .in_2(full_adder_full_20_out_4), .in_3(_1_4_out_2),
    .out_4(full_adder_full_19_out_4), .out_5(full_adder_full_19_out_5));
  Full_adder_full full_adder_full_20 (
    .in_1(full_adder_full_14_out_5), .in_2(full_adder_full_21_out_4), .in_3(_1_3_out),
    .out_4(full_adder_full_20_out_4), .out_5(full_adder_full_20_out_5));
  Full_adder_full full_adder_full_21 (
    .in_1(full_adder_full_15_out_5), .in_2(_1_out), .in_3(_1_2_out_2), .out_4(full_adder_full_21_out_4),
    .out_5(full_adder_full_21_out_5));
  and _1_64_2 (_1_64_2_out, and_2_out, and_32_out);
  and _1_32_2 (_1_32_2_out, and_3_out, and_32_out);
  and _1_16_2 (_1_16_2_out, and_8_out, and_32_out);
  and and_42 (and_42_out, in_2, INPUT_B[1]);
  and and_43 (and_43_out, in_2, INPUT_B[2]);
  and and_44 (and_44_out, in_2, INPUT_B[3]);
  and _4 (_4_out, and_17_out, and_28_out);
  and _2_2 (_2_2_out, and_13_out, and_28_out);
  or or_21 (or_21_out, or_9_out, binary_bcd_9bit_1_out_10);
  or or_22 (or_22_out, or_10_out, binary_bcd_decoder_1_out_9, binary_bcd_9bit_1_out_11);
  or or_23 (or_23_out, or_11_out, binary_bcd_decoder_1_out_10, binary_bcd_9bit_1_out_12);
  or or_24 (or_24_out, or_12_out, binary_bcd_decoder_1_out_11, binary_bcd_9bit_1_out_13);
  or or_25 (or_25_out, binary_bcd_9bit_1_out_14, binary_bcd_decoder_1_out_12, or_13_out);
  or or_26 (or_26_out, binary_bcd_9bit_1_out_15, binary_bcd_decoder_1_out_13, or_14_out);
  or or_27 (or_27_out, binary_bcd_9bit_1_out_16, binary_bcd_decoder_1_out_14, or_15_out);
  or or_28 (or_28_out, binary_bcd_9bit_1_out_17, binary_bcd_decoder_1_out_15, or_16_out);
  or or_29 (or_29_out, binary_bcd_9bit_1_out_18, or_17_out, binary_bcd_decoder_1_out_16);
  or or_30 (or_30_out, binary_bcd_9bit_1_out_19, binary_bcd_decoder_1_out_17, or_18_out);
  or or_31 (or_31_out, binary_bcd_9bit_1_out_20, or_19_out, binary_bcd_decoder_1_out_18);
  or or_32 (or_32_out, or_20_out, binary_bcd_decoder_1_out_19, binary_bcd_9bit_1_out_21);
  and and_45 (and_45_out, in_2, INPUT_B[4]);
  and and_46 (and_46_out, in_2, INPUT_B[6]);
  and and_47 (and_47_out, in_2, INPUT_B[5]);
  Half_adder_full half_adder_full_8 (
    .in_1(full_adder_full_22_out_4), .in_2(half_adder_full_7_out_4), .out_3(out_10[8]),
    .out_4(half_adder_full_8_out_4));
  Full_adder_full full_adder_full_22 (
    .in_1(full_adder_full_23_out_4), .in_2(full_adder_full_16_out_5), .in_3(_2_7_out),
    .out_4(full_adder_full_22_out_4), .out_5(full_adder_full_22_out_5));
  Full_adder_full full_adder_full_23 (
    .in_1(full_adder_full_24_out_4), .in_2(full_adder_full_17_out_5), .in_3(_2_6_out),
    .out_4(full_adder_full_23_out_4), .out_5(full_adder_full_23_out_5));
  Full_adder_full full_adder_full_24 (
    .in_1(full_adder_full_25_out_4), .in_2(full_adder_full_18_out_5), .in_3(_2_5_out),
    .out_4(full_adder_full_24_out_4), .out_5(full_adder_full_24_out_5));
  Full_adder_full full_adder_full_25 (
    .in_1(full_adder_full_26_out_4), .in_2(full_adder_full_19_out_5), .in_3(_2_4_out),
    .out_4(full_adder_full_25_out_4), .out_5(full_adder_full_25_out_5));
  Full_adder_full full_adder_full_26 (
    .in_1(full_adder_full_27_out_4), .in_2(full_adder_full_20_out_5), .in_3(_2_3_out),
    .out_4(full_adder_full_26_out_4), .out_5(full_adder_full_26_out_5));
  Full_adder_full full_adder_full_27 (
    .in_1(full_adder_full_21_out_5), .in_2(_2_out), .in_3(_2_2_out), .out_4(full_adder_full_27_out_4),
    .out_5(full_adder_full_27_out_5));
  and _1_4_3 (_1_4_3_out, and_9_out, and_28_out);
  and _1_2_3 (_1_2_3_out, and_7_out, and_28_out);
  and _1_3 (_1_3_out, and_12_out, and_28_out);
  and and_48 (and_48_out, in_2, INPUT_B[7]);
  and and_49 (and_49_out, INPUT_A, in_5[0]);
  Half_adder_full half_adder_full_9 (
    .in_1(half_adder_full_8_out_4), .in_2(half_adder_full_10_out_3), .out_3(out_10[9]),
    .out_4(half_adder_full_9_out_4));
  Half_adder_full half_adder_full_10 (
    .in_1(full_adder_full_22_out_5), .in_2(full_adder_full_28_out_4), .out_3(half_adder_full_10_out_3),
    .out_4(half_adder_full_10_out_4));
  Full_adder_full full_adder_full_28 (
    .in_1(full_adder_full_23_out_5), .in_2(full_adder_full_29_out_4), .in_3(_4_6_out),
    .out_4(full_adder_full_28_out_4), .out_5(full_adder_full_28_out_5));
  Full_adder_full full_adder_full_29 (
    .in_1(full_adder_full_24_out_5), .in_2(full_adder_full_30_out_4), .in_3(_4_5_out),
    .out_4(full_adder_full_29_out_4), .out_5(full_adder_full_29_out_5));
  Full_adder_full full_adder_full_30 (
    .in_1(full_adder_full_25_out_5), .in_2(full_adder_full_31_out_4), .in_3(_4_4_out),
    .out_4(full_adder_full_30_out_4), .out_5(full_adder_full_30_out_5));
  Full_adder_full full_adder_full_31 (
    .in_1(full_adder_full_26_out_5), .in_2(full_adder_full_32_out_4), .in_3(_4_3_out),
    .out_4(full_adder_full_31_out_4), .out_5(full_adder_full_31_out_5));
  Full_adder_full full_adder_full_32 (
    .in_1(full_adder_full_27_out_5), .in_2(_4_out), .in_3(_4_2_out), .out_4(full_adder_full_32_out_4),
    .out_5(full_adder_full_32_out_5));
  and _1_16_3 (_1_16_3_out, and_3_out, and_28_out);
  and _1_8_3 (_1_8_3_out, and_8_out, and_28_out);
  and _1_32_3 (_1_32_3_out, and_2_out, and_28_out);
  and and_50 (and_50_out, INPUT_A, in_5[3]);
  and and_51 (and_51_out, INPUT_A, in_5[2]);
  and and_52 (and_52_out, INPUT_A, in_5[1]);
  Half_adder_full half_adder_full_11 (
    .in_1(half_adder_full_12_out_3), .in_2(half_adder_full_9_out_4), .out_3(out_10[10]),
    .out_4(half_adder_full_11_out_4));
  Half_adder_full half_adder_full_12 (
    .in_1(half_adder_full_13_out_3), .in_2(half_adder_full_10_out_4), .out_3(half_adder_full_12_out_3),
    .out_4(half_adder_full_12_out_4));
  Half_adder_full half_adder_full_13 (
    .in_1(full_adder_full_33_out_4), .in_2(full_adder_full_28_out_5), .out_3(half_adder_full_13_out_3),
    .out_4(half_adder_full_13_out_4));
  Full_adder_full full_adder_full_33 (
    .in_1(full_adder_full_34_out_4), .in_2(full_adder_full_29_out_5), .in_3(_8_5_out),
    .out_4(full_adder_full_33_out_4), .out_5(full_adder_full_33_out_5));
  Full_adder_full full_adder_full_34 (
    .in_1(full_adder_full_35_out_4), .in_2(full_adder_full_30_out_5), .in_3(_8_4_out),
    .out_4(full_adder_full_34_out_4), .out_5(full_adder_full_34_out_5));
  Full_adder_full full_adder_full_35 (
    .in_1(full_adder_full_36_out_4), .in_2(full_adder_full_31_out_5), .in_3(_8_3_out),
    .out_4(full_adder_full_35_out_4), .out_5(full_adder_full_35_out_5));
  Full_adder_full full_adder_full_36 (
    .in_1(full_adder_full_32_out_5), .in_2(_8_out), .in_3(_8_2_out), .out_4(full_adder_full_36_out_4),
    .out_5(full_adder_full_36_out_5));
  and _4_2 (_4_2_out, and_13_out, and_30_out);
  and _8 (_8_out, and_17_out, and_30_out);
  Binary_BCD_Decoder binary_bcd_decoder_1 (
    .in_1(subtractor_1_out_17), .in_2(subtractor_1_out_18), .in_3(subtractor_1_out_19),
    .in_4(subtractor_1_out_20), .in_5(subtractor_1_out_21), .in_6(subtractor_1_out_22),
    .in_7(subtractor_1_out_23), .in_8(subtractor_1_out_24), .out_9(binary_bcd_decoder_1_out_9),
    .out_10(binary_bcd_decoder_1_out_10), .out_11(binary_bcd_decoder_1_out_11),
    .out_12(binary_bcd_decoder_1_out_12), .out_13(binary_bcd_decoder_1_out_13),
    .out_14(binary_bcd_decoder_1_out_14), .out_15(binary_bcd_decoder_1_out_15),
    .out_16(binary_bcd_decoder_1_out_16), .out_17(binary_bcd_decoder_1_out_17),
    .out_18(binary_bcd_decoder_1_out_18), .out_19(binary_bcd_decoder_1_out_19));
  Subtractor subtractor_1 (
    .in_1(and_49_out), .in_2(and_52_out), .in_3(and_51_out), .in_4(and_50_out), .in_5(and_55_out),
    .in_6(and_54_out), .in_7(and_53_out), .in_8(and_56_out), .in_9(and_57_out), .in_10(and_60_out),
    .in_11(and_59_out), .in_12(and_58_out), .in_13(and_62_out), .in_14(and_61_out), .in_15(and_63_out),
    .in_16(and_64_out), .out_17(subtractor_1_out_17), .out_18(subtractor_1_out_18),
    .out_19(subtractor_1_out_19), .out_20(subtractor_1_out_20), .out_21(subtractor_1_out_21),
    .out_22(subtractor_1_out_22), .out_23(subtractor_1_out_23), .out_24(subtractor_1_out_24),
    .out_25(subtractor_1_out_25));
  and and_53 (and_53_out, INPUT_A, in_5[6]);
  and and_54 (and_54_out, INPUT_A, in_5[5]);
  and and_55 (and_55_out, INPUT_A, in_5[4]);
  _1st_bit_pair_comparison u_1st_bit_pair_comparison_1 (
    .in_1(in_5[0]), .in_2(INPUT_B[0]), .out_3(n1st_bit_pair_comparison_1_out_3),
    .out_4(n1st_bit_pair_comparison_1_out_4));
  Half_adder_full half_adder_full_14 (
    .in_1(half_adder_full_15_out_3), .in_2(half_adder_full_11_out_4), .out_3(out_10[11]),
    .out_4(half_adder_full_14_out_4));
  Half_adder_full half_adder_full_15 (
    .in_1(half_adder_full_16_out_3), .in_2(half_adder_full_12_out_4), .out_3(half_adder_full_15_out_3),
    .out_4(half_adder_full_15_out_4));
  Half_adder_full half_adder_full_16 (
    .in_1(half_adder_full_17_out_3), .in_2(half_adder_full_13_out_4), .out_3(half_adder_full_16_out_3),
    .out_4(half_adder_full_16_out_4));
  Half_adder_full half_adder_full_17 (
    .in_1(full_adder_full_37_out_4), .in_2(full_adder_full_33_out_5), .out_3(half_adder_full_17_out_3),
    .out_4(half_adder_full_17_out_4));
  Full_adder_full full_adder_full_37 (
    .in_1(full_adder_full_38_out_4), .in_2(full_adder_full_34_out_5), .in_3(_16_4_out),
    .out_4(full_adder_full_37_out_4), .out_5(full_adder_full_37_out_5));
  Full_adder_full full_adder_full_38 (
    .in_1(full_adder_full_39_out_4), .in_2(full_adder_full_35_out_5), .in_3(_16_3_out),
    .out_4(full_adder_full_38_out_4), .out_5(full_adder_full_38_out_5));
  Full_adder_full full_adder_full_39 (
    .in_1(full_adder_full_36_out_5), .in_2(_16_out), .in_3(_16_2_out), .out_4(full_adder_full_39_out_4),
    .out_5(full_adder_full_39_out_5));
  and _1_4_dup2 (_1_4_out_2, and_7_out, and_30_out);
  and _1_2_4 (_1_2_4_out, and_9_out, and_30_out);
  and _2_3 (_2_3_out, and_12_out, and_30_out);
  and and_56 (and_56_out, INPUT_A, in_5[7]);
  and and_57 (and_57_out, INPUT_A, INPUT_B[0]);
  nth_bit_pair_comparison nth_bit_pair_comparison_1 (
    .in_1(in_5[1]), .in_2(n1st_bit_pair_comparison_1_out_3), .in_3(n1st_bit_pair_comparison_1_out_4),
    .in_4(INPUT_B[1]), .out_5(nth_bit_pair_comparison_1_out_5), .out_6(nth_bit_pair_comparison_1_out_6));
  Half_adder_full half_adder_full_18 (
    .in_1(half_adder_full_20_out_3), .in_2(half_adder_full_19_out_4), .out_3(out_10[13]),
    .out_4(half_adder_full_18_out_4));
  Half_adder_full half_adder_full_19 (
    .in_1(half_adder_full_21_out_3), .in_2(half_adder_full_14_out_4), .out_3(out_10[12]),
    .out_4(half_adder_full_19_out_4));
  Half_adder_full half_adder_full_20 (
    .in_1(half_adder_full_22_out_3), .in_2(half_adder_full_21_out_4), .out_3(half_adder_full_20_out_3),
    .out_4(half_adder_full_20_out_4));
  Half_adder_full half_adder_full_21 (
    .in_1(half_adder_full_23_out_3), .in_2(half_adder_full_15_out_4), .out_3(half_adder_full_21_out_3),
    .out_4(half_adder_full_21_out_4));
  Half_adder_full half_adder_full_22 (
    .in_1(half_adder_full_24_out_3), .in_2(half_adder_full_23_out_4), .out_3(half_adder_full_22_out_3),
    .out_4(half_adder_full_22_out_4));
  Half_adder_full half_adder_full_23 (
    .in_1(half_adder_full_25_out_3), .in_2(half_adder_full_16_out_4), .out_3(half_adder_full_23_out_3),
    .out_4(half_adder_full_23_out_4));
  Half_adder_full half_adder_full_24 (
    .in_1(half_adder_full_26_out_3), .in_2(half_adder_full_25_out_4), .out_3(half_adder_full_24_out_3),
    .out_4(half_adder_full_24_out_4));
  Half_adder_full half_adder_full_25 (
    .in_1(half_adder_full_27_out_3), .in_2(half_adder_full_17_out_4), .out_3(half_adder_full_25_out_3),
    .out_4(half_adder_full_25_out_4));
  Half_adder_full half_adder_full_26 (
    .in_1(half_adder_full_28_out_3), .in_2(half_adder_full_27_out_4), .out_3(half_adder_full_26_out_3),
    .out_4(half_adder_full_26_out_4));
  Half_adder_full half_adder_full_27 (
    .in_1(full_adder_full_40_out_4), .in_2(full_adder_full_37_out_5), .out_3(half_adder_full_27_out_3),
    .out_4(half_adder_full_27_out_4));
  Half_adder_full half_adder_full_28 (
    .in_1(full_adder_full_41_out_4), .in_2(full_adder_full_40_out_5), .out_3(half_adder_full_28_out_3),
    .out_4(half_adder_full_28_out_4));
  Full_adder_full full_adder_full_40 (
    .in_1(full_adder_full_42_out_4), .in_2(full_adder_full_38_out_5), .in_3(_32_3_out),
    .out_4(full_adder_full_40_out_4), .out_5(full_adder_full_40_out_5));
  Full_adder_full full_adder_full_41 (
    .in_1(full_adder_full_42_out_5), .in_2(_64_out), .in_3(_64_2_out), .out_4(full_adder_full_41_out_4),
    .out_5(full_adder_full_41_out_5));
  Full_adder_full full_adder_full_42 (
    .in_1(full_adder_full_39_out_5), .in_2(_32_out), .in_3(_32_2_out), .out_4(full_adder_full_42_out_4),
    .out_5(full_adder_full_42_out_5));
  and _1_4_4 (_1_4_4_out, and_8_out, and_30_out);
  and _1_8_4 (_1_8_4_out, and_3_out, and_30_out);
  and _1_16_4 (_1_16_4_out, and_2_out, and_30_out);
  and and_58 (and_58_out, INPUT_A, INPUT_B[3]);
  and and_59 (and_59_out, INPUT_A, INPUT_B[2]);
  and and_60 (and_60_out, INPUT_A, INPUT_B[1]);
  nth_bit_pair_comparison nth_bit_pair_comparison_2 (
    .in_1(in_5[3]), .in_2(nth_bit_pair_comparison_3_out_5), .in_3(nth_bit_pair_comparison_3_out_6),
    .in_4(INPUT_B[3]), .out_5(nth_bit_pair_comparison_2_out_5), .out_6(nth_bit_pair_comparison_2_out_6));
  nth_bit_pair_comparison nth_bit_pair_comparison_3 (
    .in_1(in_5[2]), .in_2(nth_bit_pair_comparison_1_out_5), .in_3(nth_bit_pair_comparison_1_out_6),
    .in_4(INPUT_B[2]), .out_5(nth_bit_pair_comparison_3_out_5), .out_6(nth_bit_pair_comparison_3_out_6));
  Half_adder_full half_adder_full_29 (
    .in_1(half_adder_full_30_out_3), .in_2(half_adder_full_18_out_4), .out_3(out_10[14]));  // open: out_4
  Half_adder_full half_adder_full_30 (
    .in_1(half_adder_full_31_out_3), .in_2(half_adder_full_20_out_4), .out_3(half_adder_full_30_out_3));  // open: out_4
  Half_adder_full half_adder_full_31 (
    .in_1(half_adder_full_32_out_3), .in_2(half_adder_full_22_out_4), .out_3(half_adder_full_31_out_3));  // open: out_4
  Half_adder_full half_adder_full_32 (
    .in_1(half_adder_full_33_out_3), .in_2(half_adder_full_24_out_4), .out_3(half_adder_full_32_out_3));  // open: out_4
  Half_adder_full half_adder_full_33 (
    .in_1(half_adder_full_34_out_3), .in_2(half_adder_full_26_out_4), .out_3(half_adder_full_33_out_3));  // open: out_4
  Half_adder_full half_adder_full_34 (
    .in_1(half_adder_full_35_out_3), .in_2(half_adder_full_28_out_4), .out_3(half_adder_full_34_out_3));  // open: out_4
  Half_adder_full half_adder_full_35 (
    .in_1(full_adder_full_41_out_5), .in_2(_128_out), .out_3(half_adder_full_35_out_3));  // open: out_4
  and _16 (_16_out, and_17_out, and_29_out);
  and _8_2 (_8_2_out, and_13_out, and_29_out);
  and and_61 (and_61_out, INPUT_A, INPUT_B[5]);
  and and_62 (and_62_out, INPUT_A, INPUT_B[4]);
  and and_63 (and_63_out, INPUT_A, INPUT_B[6]);
  nth_bit_pair_comparison nth_bit_pair_comparison_4 (
    .in_1(in_5[4]), .in_2(nth_bit_pair_comparison_2_out_5), .in_3(nth_bit_pair_comparison_2_out_6),
    .in_4(INPUT_B[4]), .out_5(nth_bit_pair_comparison_4_out_5), .out_6(nth_bit_pair_comparison_4_out_6));
  and _4_3 (_4_3_out, and_12_out, and_29_out);
  and _2_4 (_2_4_out, and_7_out, and_29_out);
  and _1_5 (_1_5_out, and_9_out, and_29_out);
  BCD_to_7_Segment bcd_to_7_segment_1 (
    .in_1(or_4_out), .in_2(or_3_out), .in_3(or_2_out), .in_4(or_1_out), .out_5(bcd_to_7_segment_1_out_5),
    .out_6(bcd_to_7_segment_1_out_6), .out_7(bcd_to_7_segment_1_out_7), .out_8(bcd_to_7_segment_1_out_8),
    .out_9(bcd_to_7_segment_1_out_9), .out_10(bcd_to_7_segment_1_out_10), .out_11(bcd_to_7_segment_1_out_11));
  BCD_to_7_Segment bcd_to_7_segment_2 (
    .in_1(or_8_out), .in_2(or_7_out), .in_3(or_6_out), .in_4(or_5_out), .out_5(bcd_to_7_segment_2_out_5),
    .out_6(bcd_to_7_segment_2_out_6), .out_7(bcd_to_7_segment_2_out_7), .out_8(bcd_to_7_segment_2_out_8),
    .out_9(bcd_to_7_segment_2_out_9), .out_10(bcd_to_7_segment_2_out_10), .out_11(bcd_to_7_segment_2_out_11));
  BCD_to_7_Segment bcd_to_7_segment_3 (
    .in_1(or_24_out), .in_2(or_23_out), .in_3(or_22_out), .in_4(or_21_out), .out_5(bcd_to_7_segment_3_out_5),
    .out_6(bcd_to_7_segment_3_out_6), .out_7(bcd_to_7_segment_3_out_7), .out_8(bcd_to_7_segment_3_out_8),
    .out_9(bcd_to_7_segment_3_out_9), .out_10(bcd_to_7_segment_3_out_10), .out_11(bcd_to_7_segment_3_out_11));
  BCD_to_7_Segment bcd_to_7_segment_4 (
    .in_1(or_28_out), .in_2(or_27_out), .in_3(or_26_out), .in_4(or_25_out), .out_5(bcd_to_7_segment_4_out_5),
    .out_6(bcd_to_7_segment_4_out_6), .out_7(bcd_to_7_segment_4_out_7), .out_8(bcd_to_7_segment_4_out_8),
    .out_9(bcd_to_7_segment_4_out_9), .out_10(bcd_to_7_segment_4_out_10), .out_11(bcd_to_7_segment_4_out_11));
  BCD_to_7_Segment bcd_to_7_segment_5 (
    .in_1(or_32_out), .in_2(or_31_out), .in_3(or_30_out), .in_4(or_29_out), .out_5(bcd_to_7_segment_5_out_5),
    .out_6(bcd_to_7_segment_5_out_6), .out_7(bcd_to_7_segment_5_out_7), .out_8(bcd_to_7_segment_5_out_8),
    .out_9(bcd_to_7_segment_5_out_9), .out_10(bcd_to_7_segment_5_out_10), .out_11(bcd_to_7_segment_5_out_11));
  and and_64 (and_64_out, INPUT_A, INPUT_B[7]);
  _7_Segment_Display u_7_segment_display_1 (.g(subtractor_1_out_25));  // open: f, a, b, e, d, c, dp
  nth_bit_pair_comparison nth_bit_pair_comparison_5 (
    .in_1(in_5[5]), .in_2(nth_bit_pair_comparison_4_out_5), .in_3(nth_bit_pair_comparison_4_out_6),
    .in_4(INPUT_B[5]), .out_5(nth_bit_pair_comparison_5_out_5), .out_6(nth_bit_pair_comparison_5_out_6));
  nth_bit_pair_comparison nth_bit_pair_comparison_6 (
    .in_1(in_5[6]), .in_2(nth_bit_pair_comparison_5_out_5), .in_3(nth_bit_pair_comparison_5_out_6),
    .in_4(INPUT_B[6]), .out_5(nth_bit_pair_comparison_6_out_5), .out_6(nth_bit_pair_comparison_6_out_6));
  and _1_4_5 (_1_4_5_out, and_3_out, and_29_out);
  and _1_2_5 (_1_2_5_out, and_8_out, and_29_out);
  and _1_8_5 (_1_8_5_out, and_2_out, and_29_out);
  _7_Segment_Display u_7_segment_display_2 (
    .g(bcd_to_7_segment_1_out_11), .f(bcd_to_7_segment_1_out_8), .a(bcd_to_7_segment_1_out_7),
    .b(bcd_to_7_segment_1_out_5), .e(bcd_to_7_segment_1_out_9), .d(bcd_to_7_segment_1_out_10),
    .c(bcd_to_7_segment_1_out_6));  // open: dp
  nth_bit_pair_comparison nth_bit_pair_comparison_7 (
    .in_1(in_5[7]), .in_2(nth_bit_pair_comparison_6_out_5), .in_3(nth_bit_pair_comparison_6_out_6),
    .in_4(INPUT_B[7]), .out_5(out_7), .out_6(out_9));
  and _16_2 (_16_2_out, and_13_out, and_25_out);
  and _32 (_32_out, and_17_out, and_25_out);
  _7_Segment_Display u_7_segment_display_3 (
    .g(bcd_to_7_segment_2_out_11), .f(bcd_to_7_segment_2_out_8), .a(bcd_to_7_segment_2_out_7),
    .b(bcd_to_7_segment_2_out_5), .e(bcd_to_7_segment_2_out_9), .d(bcd_to_7_segment_2_out_10),
    .c(bcd_to_7_segment_2_out_6));  // open: dp
  and _2_5 (_2_5_out, and_9_out, and_25_out);
  and _8_3 (_8_3_out, and_12_out, and_25_out);
  and _4_4 (_4_4_out, and_7_out, and_25_out);
  _7_Segment_Display u_7_segment_display_4 (
    .g(bcd_to_7_segment_3_out_11), .f(bcd_to_7_segment_3_out_8), .a(bcd_to_7_segment_3_out_7),
    .b(bcd_to_7_segment_3_out_5), .e(bcd_to_7_segment_3_out_9), .d(bcd_to_7_segment_3_out_10),
    .c(bcd_to_7_segment_3_out_6));  // open: dp
  and and_65 (out_8, not_1_out, not_2_out);
  not not_1 (not_1_out, out_7);
  not not_2 (not_2_out, out_9);
  and _1_4_6 (_1_4_6_out, and_2_out, and_25_out);
  and _1_2_6 (_1_2_6_out, and_3_out, and_25_out);
  and _1_6 (_1_6_out, and_8_out, and_25_out);
  _7_Segment_Display u_7_segment_display_5 (
    .g(bcd_to_7_segment_4_out_11), .f(bcd_to_7_segment_4_out_8), .a(bcd_to_7_segment_4_out_7),
    .b(bcd_to_7_segment_4_out_5), .e(bcd_to_7_segment_4_out_9), .d(bcd_to_7_segment_4_out_10),
    .c(bcd_to_7_segment_4_out_6));  // open: dp
  and _32_2 (_32_2_out, and_13_out, and_24_out);
  and _64 (_64_out, and_17_out, and_24_out);
  _7_Segment_Display u_7_segment_display_6 (
    .g(bcd_to_7_segment_5_out_11), .f(bcd_to_7_segment_5_out_8), .a(bcd_to_7_segment_5_out_7),
    .b(bcd_to_7_segment_5_out_5), .e(bcd_to_7_segment_5_out_9), .d(bcd_to_7_segment_5_out_10),
    .c(bcd_to_7_segment_5_out_6));  // open: dp
  and _4_5 (_4_5_out, and_9_out, and_24_out);
  and _8_4 (_8_4_out, and_7_out, and_24_out);
  and _16_3 (_16_3_out, and_12_out, and_24_out);
  and _1_7 (_1_7_out, and_3_out, and_24_out);
  and _1_2_7 (_1_2_7_out, and_2_out, and_24_out);
  and _2_6 (_2_6_out, and_8_out, and_24_out);
  and _128 (_128_out, and_17_out, and_21_out);
  and _64_2 (_64_2_out, and_13_out, and_21_out);
  and _32_3 (_32_3_out, and_12_out, and_21_out);
  and _16_4 (_16_4_out, and_7_out, and_21_out);
  and _8_5 (_8_5_out, and_9_out, and_21_out);
  and _1_8_dup2 (_1_8_out_2, and_2_out, and_21_out);
  and _4_6 (_4_6_out, and_8_out, and_21_out);
  and _2_7 (_2_7_out, and_3_out, and_21_out);

  // Notes on the sheet:
  //   /
  //   **
  //   DESIGNED BY FRASER PRICE
  //   DESIGN/BUID TIME < 1 WEEK
  //   CALCULATOR V.2- FIRST LOGIC PROJECT
  //   DIVISION OUTPUT
  //   *SEE RIGHT FOR VALUES
  //   *DIVISION OUTPUT BELOW:
  //   128,  64,  32,  16,  8,  4,  2,
  //   **INPUT VALUES BELOW:
  //   128,  64,  32,  16,  8,  4,  2,  1
  //   A IS LARGER THAN B
  //   CAN ONLY DIVIDE BY BINARY NUMBERS
  //   RANDOM NUMBER GENERATOR WILL CHOSE A RANDOM INTEGER BETWEEN 0 AND 65,534
  //   SIMULATION MUST BE RESET BEFORE GOING FROM RAN TO CALC
  //   1,  0.5,  0.25,  0.125,  0.0625,  0.03125,  0.015625,  0.0078125
  //   A AND B ARE EQUAL
  //   IN DESCENDING ORDER (TOP ROW LEFT TO RIGHT, FOLLOWED BY BOTTOM ROW LEFT TO RIGHT)
  //   FOR RANDOM NUMBER GENERATOR, PRESS "CTRL" + "K" (TO START PROCESS) AND "CTRL" + "K" AGAIN (TO CHOOSE VALUE)
  //   B IS LARGER THAN A
endmodule

module Subtractor (
  input  in_1,
  input  in_2,
  input  in_3,
  input  in_4,
  input  in_5,
  input  in_6,
  input  in_7,
  input  in_8,
  input  in_9,
  input  in_10,
  input  in_11,
  input  in_12,
  input  in_13,
  input  in_14,
  input  in_15,
  input  in_16,
  output out_17,
  output out_18,
  output out_19,
  output out_20,
  output out_21,
  output out_22,
  output out_23,
  output out_24,
  output out_25
);

  wire and_1_out, and_2_out, and_3_out, and_4_out, and_5_out, and_6_out, and_7_out, and_8_out, and_9_out,
       and_10_out, and_11_out, and_12_out, and_13_out, and_14_out, and_15_out, and_16_out,
       full_adder_1_out_4, full_adder_1_out_5, full_adder_2_out_4, full_adder_2_out_5, full_adder_3_out_4,
       full_adder_3_out_5, full_adder_4_out_4, full_adder_4_out_5, full_adder_5_out_4, full_adder_5_out_5,
       full_adder_6_out_4, full_adder_6_out_5, full_adder_7_out_4, full_adder_7_out_5, full_adder_8_out_4,
       full_adder_8_out_5, half_adder_1_out_3, half_adder_1_out_4, half_adder_2_out_4, half_adder_3_out_3,
       half_adder_3_out_4, half_adder_4_out_3, half_adder_4_out_4, half_adder_5_out_3, half_adder_5_out_4,
       half_adder_6_out_3, half_adder_6_out_4, half_adder_7_out_3, half_adder_7_out_4, half_adder_8_out_3,
       half_adder_8_out_4, not_1_out, not_2_out, not_3_out, not_4_out, not_5_out, not_6_out, not_7_out,
       not_8_out, not_9_out, not_10_out, not_12_out, not_13_out, not_14_out, not_15_out, not_16_out,
       not_17_out;

  not not_1 (not_1_out, in_9);
  not not_2 (not_2_out, in_10);
  not not_3 (not_3_out, in_11);
  not not_4 (not_4_out, in_12);
  not not_5 (not_5_out, in_13);
  not not_6 (not_6_out, in_14);
  not not_7 (not_7_out, in_15);
  not not_8 (not_8_out, in_16);
  or or_1 (out_17, and_3_out, half_adder_2_out_4);
  or or_2 (out_18, and_6_out, half_adder_1_out_4);
  Half_adder half_adder_1 (
    .in_1(not_9_out), .in_2(half_adder_3_out_3), .out_3(half_adder_1_out_3), .out_4(half_adder_1_out_4));
  Half_adder half_adder_2 (.in_1(not_10_out), .in_2(half_adder_1_out_3), .out_4(half_adder_2_out_4));  // open: out_3
  not not_9 (not_9_out, and_1_out);
  not not_10 (not_10_out, and_2_out);
  and and_1 (and_1_out, full_adder_2_out_5, out_25);
  and and_2 (and_2_out, full_adder_1_out_5, out_25);
  not not_11 (out_25, full_adder_1_out_4);
  and and_3 (and_3_out, full_adder_1_out_5, full_adder_1_out_4);
  Full_adder full_adder_1 (
    .in_1(not_8_out), .in_2(in_8), .in_3(full_adder_2_out_4), .out_4(full_adder_1_out_4),
    .out_5(full_adder_1_out_5));
  Full_adder full_adder_2 (
    .in_1(not_7_out), .in_2(in_7), .in_3(full_adder_3_out_4), .out_4(full_adder_2_out_4),
    .out_5(full_adder_2_out_5));
  or or_3 (out_19, and_5_out, half_adder_3_out_4);
  Half_adder half_adder_3 (
    .in_1(not_12_out), .in_2(half_adder_4_out_3), .out_3(half_adder_3_out_3), .out_4(half_adder_3_out_4));
  not not_12 (not_12_out, and_4_out);
  and and_4 (and_4_out, full_adder_3_out_5, out_25);
  and and_5 (and_5_out, full_adder_3_out_5, full_adder_1_out_4);
  and and_6 (and_6_out, full_adder_2_out_5, full_adder_1_out_4);
  Full_adder full_adder_3 (
    .in_1(not_6_out), .in_2(in_6), .in_3(full_adder_5_out_4), .out_4(full_adder_3_out_4),
    .out_5(full_adder_3_out_5));
  or or_4 (out_21, and_12_out, half_adder_5_out_4);
  or or_5 (out_20, and_9_out, half_adder_4_out_4);
  Half_adder half_adder_4 (
    .in_1(not_13_out), .in_2(half_adder_5_out_3), .out_3(half_adder_4_out_3), .out_4(half_adder_4_out_4));
  Half_adder half_adder_5 (
    .in_1(not_14_out), .in_2(half_adder_6_out_3), .out_3(half_adder_5_out_3), .out_4(half_adder_5_out_4));
  not not_13 (not_13_out, and_8_out);
  not not_14 (not_14_out, and_7_out);
  and and_7 (and_7_out, full_adder_4_out_5, out_25);
  and and_8 (and_8_out, full_adder_5_out_5, out_25);
  and and_9 (and_9_out, full_adder_5_out_5, full_adder_1_out_4);
  Full_adder full_adder_4 (
    .in_1(not_4_out), .in_2(in_4), .in_3(full_adder_7_out_4), .out_4(full_adder_4_out_4),
    .out_5(full_adder_4_out_5));
  Full_adder full_adder_5 (
    .in_1(not_5_out), .in_2(in_5), .in_3(full_adder_4_out_4), .out_4(full_adder_5_out_4),
    .out_5(full_adder_5_out_5));
  or or_6 (out_22, and_13_out, half_adder_6_out_4);
  or or_7 (out_23, and_15_out, half_adder_7_out_4);
  Half_adder half_adder_6 (
    .in_1(not_16_out), .in_2(half_adder_7_out_3), .out_3(half_adder_6_out_3), .out_4(half_adder_6_out_4));
  Half_adder half_adder_7 (
    .in_1(not_15_out), .in_2(half_adder_8_out_3), .out_3(half_adder_7_out_3), .out_4(half_adder_7_out_4));
  not not_15 (not_15_out, and_10_out);
  not not_16 (not_16_out, and_11_out);
  and and_10 (and_10_out, full_adder_6_out_5, out_25);
  and and_11 (and_11_out, full_adder_7_out_5, out_25);
  and and_12 (and_12_out, full_adder_4_out_5, full_adder_1_out_4);
  and and_13 (and_13_out, full_adder_7_out_5, full_adder_1_out_4);
  Full_adder full_adder_6 (
    .in_1(not_2_out), .in_2(in_2), .in_3(full_adder_8_out_4), .out_4(full_adder_6_out_4),
    .out_5(full_adder_6_out_5));
  Full_adder full_adder_7 (
    .in_1(not_3_out), .in_2(in_3), .in_3(full_adder_6_out_4), .out_4(full_adder_7_out_4),
    .out_5(full_adder_7_out_5));
  or or_8 (out_24, and_16_out, half_adder_8_out_4);
  Half_adder half_adder_8 (.in_1(not_17_out), .in_2(1'b1), .out_3(half_adder_8_out_3), .out_4(half_adder_8_out_4));
  not not_17 (not_17_out, and_14_out);
  and and_14 (and_14_out, full_adder_8_out_5, out_25);
  and and_15 (and_15_out, full_adder_6_out_5, full_adder_1_out_4);
  and and_16 (and_16_out, full_adder_8_out_5, full_adder_1_out_4);
  Full_adder full_adder_8 (
    .in_1(in_1), .in_2(not_1_out), .in_3(1'b1), .out_4(full_adder_8_out_4), .out_5(full_adder_8_out_5));
endmodule

module Adder (
  input  in_1,
  input  in_2,
  input  in_3,
  input  in_4,
  input  in_5,
  input  in_6,
  input  in_7,
  input  in_8,
  input  in_9,
  input  in_10,
  input  in_11,
  input  in_12,
  input  in_13,
  input  in_14,
  input  in_15,
  input  in_16,
  output out_17,
  output out_18,
  output out_19,
  output out_20,
  output out_21,
  output out_22,
  output out_23,
  output out_24,
  output out_25
);

  wire full_adder_1_out_4, full_adder_3_out_4, full_adder_4_out_4, full_adder_5_out_4, full_adder_6_out_4,
       full_adder_7_out_4, half_adder_1_out_3;

  Full_adder full_adder_1 (
    .in_1(in_15), .in_2(in_7), .in_3(full_adder_3_out_4), .out_4(full_adder_1_out_4), .out_5(out_19));
  Full_adder full_adder_2 (.in_1(in_16), .in_2(in_8), .in_3(full_adder_1_out_4), .out_4(out_17), .out_5(out_18));
  Full_adder full_adder_3 (
    .in_1(in_14), .in_2(in_6), .in_3(full_adder_5_out_4), .out_4(full_adder_3_out_4), .out_5(out_20));
  Full_adder full_adder_4 (
    .in_1(in_12), .in_2(in_4), .in_3(full_adder_6_out_4), .out_4(full_adder_4_out_4), .out_5(out_22));
  Full_adder full_adder_5 (
    .in_1(in_13), .in_2(in_5), .in_3(full_adder_4_out_4), .out_4(full_adder_5_out_4), .out_5(out_21));
  Full_adder full_adder_6 (
    .in_1(in_11), .in_2(in_3), .in_3(full_adder_7_out_4), .out_4(full_adder_6_out_4), .out_5(out_23));
  Full_adder full_adder_7 (
    .in_1(in_10), .in_2(in_2), .in_3(half_adder_1_out_3), .out_4(full_adder_7_out_4), .out_5(out_24));
  Half_adder half_adder_1 (.in_1(in_1), .in_2(in_9), .out_3(half_adder_1_out_3), .out_4(out_25));
endmodule

module Full_adder (
  input  in_1,
  input  in_2,
  input  in_3,
  output out_4,
  output out_5
);

  wire half_adder_1_out_3, half_adder_1_out_4, half_adder_2_out_3;

  or or_1 (out_4, half_adder_1_out_3, half_adder_2_out_3);
  Half_adder half_adder_1 (.in_1(in_3), .in_2(in_2), .out_3(half_adder_1_out_3), .out_4(half_adder_1_out_4));
  Half_adder half_adder_2 (.in_1(half_adder_1_out_4), .in_2(in_1), .out_3(half_adder_2_out_3), .out_4(out_5));
endmodule

module Half_adder (
  input  in_1,
  input  in_2,
  output out_3,
  output out_4
);

  and and_1 (out_3, in_2, in_1);
  xor xor_1 (out_4, in_1, in_2);
endmodule

module Full_adder_full (
  input  in_1,
  input  in_2,
  input  in_3,
  output out_4,
  output out_5
);

  wire and_1_out, and_2_out, xor_2_out;

  xor xor_1 (out_4, in_1, xor_2_out);
  and and_1 (and_1_out, in_1, xor_2_out);
  xor xor_2 (xor_2_out, in_2, in_3);
  and and_2 (and_2_out, in_2, in_3);
  or or_1 (out_5, and_1_out, and_2_out);
endmodule

module Half_adder_full (
  input  in_1,
  input  in_2,
  output out_3,
  output out_4
);

  xor xor_1 (out_3, in_1, in_2);
  and and_1 (out_4, in_1, in_2);
endmodule

module Multiplication2 (
  input  _1,
  input  _2,
  input  _4,
  input  _8,
  input  _16,
  input  _1_2,
  input  _2_2,
  input  _4_2,
  input  _8_2,
  input  _16_2,
  output _1_3,
  output _2_3,
  output _4_3,
  output _8_3,
  output _16_3,
  output _32,
  output _64,
  output _128,
  output _256,
  output _512
);

  wire _2_2_out, _2_out, _4_2_out, _4_3_out, _4_out, _8_2_out, _8_3_out, _8_4_out, _8_out, _16_2_out,
       _16_3_out, _16_4_out, _16_5_out, _16_out, _32_2_out, _32_3_out, _32_4_out, _32_out, _64_2_out,
       _64_3_out, _64_out, _128_2_out, _128_out, _256_out, and_1_out, and_2_out, and_3_out, and_4_out,
       and_5_out, and_6_out, and_7_out, and_8_out, and_9_out, and_10_out, and_11_out, and_12_out, and_13_out,
       and_14_out, and_15_out, and_16_out, and_17_out, and_18_out, and_19_out, and_20_out, and_21_out,
       and_22_out, and_23_out, and_24_out, and_25_out, and_26_out, and_27_out, and_28_out, and_29_out,
       and_30_out, and_31_out, and_32_out, and_33_out, and_34_out, and_35_out, and_36_out, and_37_out,
       and_38_out, or_1_out, or_2_out, or_3_out, or_4_out, or_5_out, or_6_out, or_7_out, or_8_out, or_9_out,
       or_10_out, or_11_out, or_12_out, or_14_out, or_15_out, xor_3_out, xor_4_out, xor_6_out, xor_7_out,
       xor_8_out, xor_9_out, xor_11_out, xor_12_out, xor_13_out, xor_14_out, xor_15_out, xor_16_out,
       xor_18_out, xor_19_out, xor_20_out, xor_21_out, xor_22_out, xor_23_out, xor_25_out, xor_26_out,
       xor_27_out, xor_28_out, xor_29_out, xor_31_out, xor_32_out, xor_33_out, xor_34_out, xor_35_out,
       xor_36_out, xor_38_out;

  xor xor_1 (_2_3, _2_out, _2_2_out);
  and u__2 (_2_out, _1, _2_2);
  and u__4 (_4_out, _1, _4_2);
  and u__1 (_1_3, _1, _1_2);
  and and_1 (and_1_out, _2_out, _2_2_out);
  and u__16 (_16_out, _1, _16_2);
  and u__8 (_8_out, _1, _8_2);
  xor xor_2 (_4_3, xor_3_out, _4_3_out);
  xor xor_3 (xor_3_out, and_1_out, xor_4_out);
  xor xor_4 (xor_4_out, _4_out, _4_2_out);
  and u__4_2 (_4_2_out, _2, _2_2);
  and u__2_2 (_2_2_out, _2, _1_2);
  and u__8_2 (_8_2_out, _2, _4_2);
  and and_2 (and_2_out, xor_3_out, _4_3_out);
  and and_3 (and_3_out, and_1_out, xor_4_out);
  and and_4 (and_4_out, _4_out, _4_2_out);
  and u__16_2 (_16_2_out, _2, _8_2);
  and u__32 (_32_out, _2, _16_2);
  and u__4_3 (_4_3_out, _4, _1_2);
  or or_1 (or_1_out, and_3_out, and_4_out);
  and u__8_3 (_8_3_out, _4, _2_2);
  and u__16_3 (_16_3_out, _4, _4_2);
  xor xor_5 (_8_3, xor_6_out, _8_4_out);
  xor xor_6 (xor_6_out, and_2_out, xor_7_out);
  and and_5 (and_5_out, and_2_out, xor_7_out);
  xor xor_7 (xor_7_out, xor_8_out, _8_3_out);
  and and_6 (and_6_out, xor_8_out, _8_3_out);
  xor xor_8 (xor_8_out, or_1_out, xor_9_out);
  and and_7 (and_7_out, or_1_out, xor_9_out);
  xor xor_9 (xor_9_out, _8_out, _8_2_out);
  and and_8 (and_8_out, _8_out, _8_2_out);
  and _32_2 (_32_2_out, _4, _8_2);
  and u__64 (_64_out, _4, _16_2);
  and _8_4 (_8_4_out, _8, _1_2);
  and and_9 (and_9_out, xor_6_out, _8_4_out);
  or or_2 (or_2_out, and_5_out, and_6_out);
  or or_3 (or_3_out, and_7_out, and_8_out);
  and _64_2 (_64_2_out, _8, _8_2);
  and _16_4 (_16_4_out, _8, _2_2);
  and _32_3 (_32_3_out, _8, _4_2);
  xor xor_10 (_16_3, xor_11_out, _16_5_out);
  xor xor_11 (xor_11_out, and_9_out, xor_12_out);
  xor xor_12 (xor_12_out, xor_13_out, _16_4_out);
  xor xor_13 (xor_13_out, or_2_out, xor_14_out);
  xor xor_14 (xor_14_out, xor_15_out, _16_3_out);
  xor xor_15 (xor_15_out, or_3_out, xor_16_out);
  xor xor_16 (xor_16_out, _16_out, _16_2_out);
  and _16_5 (_16_5_out, _16, _1_2);
  and u__128 (_128_out, _8, _16_2);
  and and_10 (and_10_out, and_9_out, xor_12_out);
  and and_11 (and_11_out, xor_13_out, _16_4_out);
  and and_12 (and_12_out, or_2_out, xor_14_out);
  and and_13 (and_13_out, xor_15_out, _16_3_out);
  and and_14 (and_14_out, or_3_out, xor_16_out);
  and and_15 (and_15_out, _16_out, _16_2_out);
  and _128_2 (_128_2_out, _16, _8_2);
  and _32_4 (_32_4_out, _16, _2_2);
  and _64_3 (_64_3_out, _16, _4_2);
  and and_16 (and_16_out, xor_11_out, _16_5_out);
  or or_4 (or_4_out, and_10_out, and_11_out);
  or or_5 (or_5_out, and_12_out, and_13_out);
  or or_6 (or_6_out, and_14_out, and_15_out);
  and u__256 (_256_out, _16, _16_2);
  xor xor_17 (_32, and_16_out, xor_18_out);
  xor xor_18 (xor_18_out, or_4_out, xor_19_out);
  xor xor_19 (xor_19_out, xor_20_out, _32_4_out);
  xor xor_20 (xor_20_out, or_5_out, xor_21_out);
  xor xor_21 (xor_21_out, xor_22_out, _32_3_out);
  xor xor_22 (xor_22_out, or_6_out, xor_23_out);
  xor xor_23 (xor_23_out, _32_out, _32_2_out);
  and and_17 (and_17_out, and_16_out, xor_18_out);
  and and_18 (and_18_out, or_4_out, xor_19_out);
  or or_7 (or_7_out, and_18_out, and_19_out);
  and and_19 (and_19_out, xor_20_out, _32_4_out);
  and and_20 (and_20_out, or_5_out, xor_21_out);
  or or_8 (or_8_out, and_20_out, and_21_out);
  and and_21 (and_21_out, xor_22_out, _32_3_out);
  and and_22 (and_22_out, or_6_out, xor_23_out);
  or or_9 (or_9_out, and_22_out, and_23_out);
  and and_23 (and_23_out, _32_out, _32_2_out);
  xor xor_24 (_64, xor_25_out, and_17_out);
  xor xor_25 (xor_25_out, xor_26_out, or_7_out);
  xor xor_26 (xor_26_out, or_8_out, xor_27_out);
  and and_24 (and_24_out, or_8_out, xor_27_out);
  xor xor_27 (xor_27_out, xor_28_out, _64_3_out);
  and and_25 (and_25_out, xor_28_out, _64_3_out);
  xor xor_28 (xor_28_out, or_9_out, xor_29_out);
  and and_26 (and_26_out, or_9_out, xor_29_out);
  xor xor_29 (xor_29_out, _64_out, _64_2_out);
  and and_27 (and_27_out, _64_out, _64_2_out);
  and and_28 (and_28_out, xor_25_out, and_17_out);
  and and_29 (and_29_out, xor_26_out, or_7_out);
  or or_10 (or_10_out, and_24_out, and_25_out);
  or or_11 (or_11_out, and_26_out, and_27_out);
  xor xor_30 (_128, xor_31_out, and_28_out);
  xor xor_31 (xor_31_out, xor_32_out, and_29_out);
  xor xor_32 (xor_32_out, xor_33_out, or_10_out);
  xor xor_33 (xor_33_out, or_11_out, xor_34_out);
  xor xor_34 (xor_34_out, _128_out, _128_2_out);
  and and_30 (and_30_out, xor_33_out, or_10_out);
  and and_31 (and_31_out, or_11_out, xor_34_out);
  and and_32 (and_32_out, _128_out, _128_2_out);
  and and_33 (and_33_out, xor_31_out, and_28_out);
  and and_34 (and_34_out, xor_32_out, and_29_out);
  xor xor_35 (xor_35_out, xor_36_out, and_30_out);
  xor xor_36 (xor_36_out, or_12_out, _256_out);
  or or_12 (or_12_out, and_31_out, and_32_out);
  xor xor_37 (_256, xor_38_out, and_33_out);
  xor xor_38 (xor_38_out, xor_35_out, and_34_out);
  and and_35 (and_35_out, xor_38_out, and_33_out);
  and and_36 (and_36_out, xor_35_out, and_34_out);
  and and_37 (and_37_out, xor_36_out, and_30_out);
  and and_38 (and_38_out, or_12_out, _256_out);
  or or_13 (_512, and_35_out, or_14_out);
  or or_14 (or_14_out, and_36_out, or_15_out);
  or or_15 (or_15_out, and_37_out, and_38_out);
endmodule

module _8bit_Multiplication (
  input  in_1,
  input  in_2,
  input  in_3,
  input  in_4,
  input  in_5,
  input  in_6,
  input  in_7,
  input  in_8,
  input  in_9,
  input  in_10,
  input  in_11,
  input  in_12,
  input  in_13,
  input  in_14,
  input  in_15,
  input  in_16,
  output _1,
  output _2,
  output _4,
  output _8,
  output _16,
  output _32,
  output _64,
  output _128,
  output _256,
  output _512,
  output _1024,
  output _2048,
  output _4096,
  output _8192,
  output _16384,
  output _32768
);

  wire _2_2_out, _2_out, _4_2_out, _4_3_out, _4_out, _8_2_out, _8_3_out, _8_4_out, _8_out, _16_2_out,
       _16_3_out, _16_4_out, _16_5_out, _16_out, _32_2_out, _32_3_out, _32_4_out, _32_5_out, _32_6_out,
       _32_out, _64_2_out, _64_3_out, _64_4_out, _64_5_out, _64_6_out, _64_7_out, _64_out, _128_2_out,
       _128_3_out, _128_4_out, _128_5_out, _128_6_out, _128_7_out, _128_8_out, _128_out, _256_2_out,
       _256_3_out, _256_4_out, _256_5_out, _256_6_out, _256_7_out, _256_out, _512_2_out, _512_3_out,
       _512_4_out, _512_5_out, _512_6_out, _512_out, _1024_2_out, _1024_3_out, _1024_4_out, _1024_5_out,
       _1024_out, _2048_2_out, _2048_3_out, _2048_4_out, _2048_out, _4096_2_out, _4096_3_out, _4096_out,
       _8192_2_out, _8192_out, and_1_out, full_adder_full_1_out_4, full_adder_full_1_out_5,
       full_adder_full_2_out_4, full_adder_full_2_out_5, full_adder_full_3_out_4, full_adder_full_3_out_5,
       full_adder_full_4_out_4, full_adder_full_4_out_5, full_adder_full_5_out_4, full_adder_full_5_out_5,
       full_adder_full_6_out_4, full_adder_full_6_out_5, full_adder_full_7_out_4, full_adder_full_7_out_5,
       full_adder_full_8_out_4, full_adder_full_8_out_5, full_adder_full_9_out_4, full_adder_full_9_out_5,
       full_adder_full_10_out_4, full_adder_full_10_out_5, full_adder_full_11_out_4,
       full_adder_full_11_out_5, full_adder_full_12_out_4, full_adder_full_12_out_5,
       full_adder_full_13_out_4, full_adder_full_13_out_5, full_adder_full_14_out_4,
       full_adder_full_14_out_5, full_adder_full_15_out_4, full_adder_full_15_out_5,
       full_adder_full_16_out_4, full_adder_full_16_out_5, full_adder_full_17_out_4,
       full_adder_full_17_out_5, full_adder_full_18_out_4, full_adder_full_18_out_5,
       full_adder_full_19_out_4, full_adder_full_19_out_5, full_adder_full_20_out_4,
       full_adder_full_20_out_5, full_adder_full_21_out_4, full_adder_full_21_out_5,
       full_adder_full_22_out_4, full_adder_full_22_out_5, full_adder_full_23_out_4,
       full_adder_full_23_out_5, full_adder_full_24_out_4, full_adder_full_24_out_5,
       full_adder_full_25_out_4, full_adder_full_25_out_5, full_adder_full_26_out_4,
       full_adder_full_26_out_5, full_adder_full_27_out_4, full_adder_full_27_out_5,
       full_adder_full_28_out_4, full_adder_full_28_out_5, full_adder_full_29_out_4,
       full_adder_full_29_out_5, full_adder_full_30_out_4, full_adder_full_30_out_5,
       full_adder_full_31_out_4, full_adder_full_31_out_5, full_adder_full_32_out_4,
       full_adder_full_32_out_5, full_adder_full_33_out_4, full_adder_full_33_out_5,
       full_adder_full_34_out_4, full_adder_full_34_out_5, full_adder_full_35_out_4,
       full_adder_full_35_out_5, full_adder_full_36_out_4, full_adder_full_36_out_5,
       full_adder_full_37_out_4, full_adder_full_37_out_5, full_adder_full_38_out_4,
       full_adder_full_38_out_5, full_adder_full_39_out_4, full_adder_full_39_out_5,
       full_adder_full_40_out_4, full_adder_full_40_out_5, full_adder_full_41_out_4,
       full_adder_full_41_out_5, full_adder_full_42_out_4, full_adder_full_42_out_5, half_adder_full_1_out_4,
       half_adder_full_2_out_4, half_adder_full_3_out_4, half_adder_full_4_out_4, half_adder_full_5_out_4,
       half_adder_full_6_out_4, half_adder_full_7_out_4, half_adder_full_8_out_4, half_adder_full_9_out_4,
       half_adder_full_10_out_3, half_adder_full_10_out_4, half_adder_full_11_out_4,
       half_adder_full_12_out_3, half_adder_full_12_out_4, half_adder_full_13_out_3,
       half_adder_full_13_out_4, half_adder_full_14_out_4, half_adder_full_15_out_3,
       half_adder_full_15_out_4, half_adder_full_16_out_3, half_adder_full_16_out_4,
       half_adder_full_17_out_3, half_adder_full_17_out_4, half_adder_full_18_out_4,
       half_adder_full_19_out_3, half_adder_full_19_out_4, half_adder_full_20_out_3,
       half_adder_full_20_out_4, half_adder_full_21_out_3, half_adder_full_21_out_4,
       half_adder_full_22_out_3, half_adder_full_22_out_4, half_adder_full_23_out_4,
       half_adder_full_24_out_4, half_adder_full_25_out_3, half_adder_full_25_out_4,
       half_adder_full_26_out_3, half_adder_full_26_out_4, half_adder_full_27_out_3,
       half_adder_full_27_out_4, half_adder_full_28_out_3, half_adder_full_28_out_4,
       half_adder_full_29_out_3, half_adder_full_29_out_4, half_adder_full_30_out_3,
       half_adder_full_30_out_4, half_adder_full_31_out_3, half_adder_full_31_out_4,
       half_adder_full_32_out_3, half_adder_full_32_out_4, half_adder_full_33_out_3,
       half_adder_full_33_out_4, half_adder_full_34_out_3, half_adder_full_34_out_4,
       half_adder_full_35_out_3, half_adder_full_35_out_4, or_2_out, or_3_out, or_4_out, or_5_out, or_6_out;

  Half_adder_full half_adder_full_1 (.in_1(_2_out), .in_2(_2_2_out), .out_3(_2), .out_4(half_adder_full_1_out_4));
  and u__1 (_1, in_1, in_9);
  and u__2 (_2_out, in_2, in_9);
  Half_adder_full half_adder_full_2 (
    .in_1(full_adder_full_1_out_4), .in_2(_4_3_out), .out_3(_4), .out_4(half_adder_full_2_out_4));
  Full_adder_full full_adder_full_1 (
    .in_1(_4_out), .in_2(_4_2_out), .in_3(half_adder_full_1_out_4), .out_4(full_adder_full_1_out_4),
    .out_5(full_adder_full_1_out_5));
  and u__8 (_8_out, in_4, in_9);
  and u__4 (_4_out, in_3, in_9);
  and u__16 (_16_out, in_5, in_9);
  Half_adder_full half_adder_full_3 (
    .in_1(full_adder_full_2_out_4), .in_2(_16_5_out), .out_3(_16), .out_4(half_adder_full_3_out_4));
  Full_adder_full full_adder_full_2 (
    .in_1(full_adder_full_3_out_4), .in_2(half_adder_full_4_out_4), .in_3(_16_4_out),
    .out_4(full_adder_full_2_out_4), .out_5(full_adder_full_2_out_5));
  Half_adder_full half_adder_full_4 (
    .in_1(full_adder_full_4_out_4), .in_2(_8_4_out), .out_3(_8), .out_4(half_adder_full_4_out_4));
  Full_adder_full full_adder_full_3 (
    .in_1(full_adder_full_5_out_4), .in_2(full_adder_full_4_out_5), .in_3(_16_3_out),
    .out_4(full_adder_full_3_out_4), .out_5(full_adder_full_3_out_5));
  Full_adder_full full_adder_full_4 (
    .in_1(half_adder_full_2_out_4), .in_2(full_adder_full_6_out_4), .in_3(_8_3_out),
    .out_4(full_adder_full_4_out_4), .out_5(full_adder_full_4_out_5));
  Full_adder_full full_adder_full_5 (
    .in_1(full_adder_full_6_out_5), .in_2(_16_out), .in_3(_16_2_out), .out_4(full_adder_full_5_out_4),
    .out_5(full_adder_full_5_out_5));
  Full_adder_full full_adder_full_6 (
    .in_1(_8_out), .in_2(_8_2_out), .in_3(full_adder_full_1_out_5), .out_4(full_adder_full_6_out_4),
    .out_5(full_adder_full_6_out_5));
  and u__64 (_64_out, in_7, in_9);
  and u__32 (_32_out, in_6, in_9);
  Half_adder_full half_adder_full_5 (
    .in_1(full_adder_full_7_out_4), .in_2(_32_6_out), .out_3(_32), .out_4(half_adder_full_5_out_4));
  Full_adder_full full_adder_full_7 (
    .in_1(half_adder_full_3_out_4), .in_2(full_adder_full_8_out_4), .in_3(_32_5_out),
    .out_4(full_adder_full_7_out_4), .out_5(full_adder_full_7_out_5));
  Full_adder_full full_adder_full_8 (
    .in_1(full_adder_full_9_out_4), .in_2(full_adder_full_2_out_5), .in_3(_32_4_out),
    .out_4(full_adder_full_8_out_4), .out_5(full_adder_full_8_out_5));
  Full_adder_full full_adder_full_9 (
    .in_1(full_adder_full_10_out_4), .in_2(full_adder_full_3_out_5), .in_3(_32_3_out),
    .out_4(full_adder_full_9_out_4), .out_5(full_adder_full_9_out_5));
  Full_adder_full full_adder_full_10 (
    .in_1(full_adder_full_5_out_5), .in_2(_32_out), .in_3(_32_2_out), .out_4(full_adder_full_10_out_4),
    .out_5(full_adder_full_10_out_5));
  and _2_2 (_2_2_out, in_1, in_10);
  and _4_2 (_4_2_out, in_2, in_10);
  and u__128 (_128_out, in_8, in_9);
  Half_adder_full half_adder_full_6 (
    .in_1(full_adder_full_11_out_4), .in_2(_64_7_out), .out_3(_64), .out_4(half_adder_full_6_out_4));
  Full_adder_full full_adder_full_11 (
    .in_1(full_adder_full_12_out_4), .in_2(half_adder_full_5_out_4), .in_3(_64_6_out),
    .out_4(full_adder_full_11_out_4), .out_5(full_adder_full_11_out_5));
  Full_adder_full full_adder_full_12 (
    .in_1(full_adder_full_13_out_4), .in_2(full_adder_full_7_out_5), .in_3(_64_5_out),
    .out_4(full_adder_full_12_out_4), .out_5(full_adder_full_12_out_5));
  Full_adder_full full_adder_full_13 (
    .in_1(full_adder_full_14_out_4), .in_2(full_adder_full_8_out_5), .in_3(_64_4_out),
    .out_4(full_adder_full_13_out_4), .out_5(full_adder_full_13_out_5));
  Full_adder_full full_adder_full_14 (
    .in_1(full_adder_full_15_out_4), .in_2(full_adder_full_9_out_5), .in_3(_64_3_out),
    .out_4(full_adder_full_14_out_4), .out_5(full_adder_full_14_out_5));
  Full_adder_full full_adder_full_15 (
    .in_1(full_adder_full_10_out_5), .in_2(_64_out), .in_3(_64_2_out), .out_4(full_adder_full_15_out_4),
    .out_5(full_adder_full_15_out_5));
  and _8_2 (_8_2_out, in_3, in_10);
  and _32_2 (_32_2_out, in_5, in_10);
  and _16_2 (_16_2_out, in_4, in_10);
  and _128_2 (_128_2_out, in_7, in_10);
  and _64_2 (_64_2_out, in_6, in_10);
  Half_adder_full half_adder_full_7 (
    .in_1(full_adder_full_16_out_4), .in_2(_128_8_out), .out_3(_128), .out_4(half_adder_full_7_out_4));
  Full_adder_full full_adder_full_16 (
    .in_1(half_adder_full_6_out_4), .in_2(full_adder_full_17_out_4), .in_3(_128_7_out),
    .out_4(full_adder_full_16_out_4), .out_5(full_adder_full_16_out_5));
  Full_adder_full full_adder_full_17 (
    .in_1(full_adder_full_11_out_5), .in_2(full_adder_full_18_out_4), .in_3(_128_6_out),
    .out_4(full_adder_full_17_out_4), .out_5(full_adder_full_17_out_5));
  Full_adder_full full_adder_full_18 (
    .in_1(full_adder_full_12_out_5), .in_2(full_adder_full_19_out_4), .in_3(_128_5_out),
    .out_4(full_adder_full_18_out_4), .out_5(full_adder_full_18_out_5));
  Full_adder_full full_adder_full_19 (
    .in_1(full_adder_full_13_out_5), .in_2(full_adder_full_20_out_4), .in_3(_128_4_out),
    .out_4(full_adder_full_19_out_4), .out_5(full_adder_full_19_out_5));
  Full_adder_full full_adder_full_20 (
    .in_1(full_adder_full_14_out_5), .in_2(full_adder_full_21_out_4), .in_3(_128_3_out),
    .out_4(full_adder_full_20_out_4), .out_5(full_adder_full_20_out_5));
  Full_adder_full full_adder_full_21 (
    .in_1(full_adder_full_15_out_5), .in_2(_128_out), .in_3(_128_2_out), .out_4(full_adder_full_21_out_4),
    .out_5(full_adder_full_21_out_5));
  and _4_3 (_4_3_out, in_1, in_11);
  and u__256 (_256_out, in_8, in_10);
  and _8_3 (_8_3_out, in_2, in_11);
  Half_adder_full half_adder_full_8 (
    .in_1(full_adder_full_22_out_4), .in_2(half_adder_full_7_out_4), .out_3(_256),
    .out_4(half_adder_full_8_out_4));
  Full_adder_full full_adder_full_22 (
    .in_1(full_adder_full_23_out_4), .in_2(full_adder_full_16_out_5), .in_3(_256_7_out),
    .out_4(full_adder_full_22_out_4), .out_5(full_adder_full_22_out_5));
  Full_adder_full full_adder_full_23 (
    .in_1(full_adder_full_24_out_4), .in_2(full_adder_full_17_out_5), .in_3(_256_6_out),
    .out_4(full_adder_full_23_out_4), .out_5(full_adder_full_23_out_5));
  Full_adder_full full_adder_full_24 (
    .in_1(full_adder_full_25_out_4), .in_2(full_adder_full_18_out_5), .in_3(_256_5_out),
    .out_4(full_adder_full_24_out_4), .out_5(full_adder_full_24_out_5));
  Full_adder_full full_adder_full_25 (
    .in_1(full_adder_full_26_out_4), .in_2(full_adder_full_19_out_5), .in_3(_256_4_out),
    .out_4(full_adder_full_25_out_4), .out_5(full_adder_full_25_out_5));
  Full_adder_full full_adder_full_26 (
    .in_1(full_adder_full_27_out_4), .in_2(full_adder_full_20_out_5), .in_3(_256_3_out),
    .out_4(full_adder_full_26_out_4), .out_5(full_adder_full_26_out_5));
  Full_adder_full full_adder_full_27 (
    .in_1(full_adder_full_21_out_5), .in_2(_256_out), .in_3(_256_2_out), .out_4(full_adder_full_27_out_4),
    .out_5(full_adder_full_27_out_5));
  and _32_3 (_32_3_out, in_4, in_11);
  and _16_3 (_16_3_out, in_3, in_11);
  and _64_3 (_64_3_out, in_5, in_11);
  Half_adder_full half_adder_full_9 (
    .in_1(half_adder_full_8_out_4), .in_2(half_adder_full_10_out_3), .out_3(_512),
    .out_4(half_adder_full_9_out_4));
  Half_adder_full half_adder_full_10 (
    .in_1(full_adder_full_22_out_5), .in_2(full_adder_full_28_out_4), .out_3(half_adder_full_10_out_3),
    .out_4(half_adder_full_10_out_4));
  Full_adder_full full_adder_full_28 (
    .in_1(full_adder_full_23_out_5), .in_2(full_adder_full_29_out_4), .in_3(_512_6_out),
    .out_4(full_adder_full_28_out_4), .out_5(full_adder_full_28_out_5));
  Full_adder_full full_adder_full_29 (
    .in_1(full_adder_full_24_out_5), .in_2(full_adder_full_30_out_4), .in_3(_512_5_out),
    .out_4(full_adder_full_29_out_4), .out_5(full_adder_full_29_out_5));
  Full_adder_full full_adder_full_30 (
    .in_1(full_adder_full_25_out_5), .in_2(full_adder_full_31_out_4), .in_3(_512_4_out),
    .out_4(full_adder_full_30_out_4), .out_5(full_adder_full_30_out_5));
  Full_adder_full full_adder_full_31 (
    .in_1(full_adder_full_26_out_5), .in_2(full_adder_full_32_out_4), .in_3(_512_3_out),
    .out_4(full_adder_full_31_out_4), .out_5(full_adder_full_31_out_5));
  Full_adder_full full_adder_full_32 (
    .in_1(full_adder_full_27_out_5), .in_2(_512_out), .in_3(_512_2_out), .out_4(full_adder_full_32_out_4),
    .out_5(full_adder_full_32_out_5));
  and _256_2 (_256_2_out, in_7, in_11);
  and _128_3 (_128_3_out, in_6, in_11);
  Half_adder_full half_adder_full_11 (
    .in_1(half_adder_full_12_out_3), .in_2(half_adder_full_9_out_4), .out_3(_1024),
    .out_4(half_adder_full_11_out_4));
  Half_adder_full half_adder_full_12 (
    .in_1(half_adder_full_13_out_3), .in_2(half_adder_full_10_out_4), .out_3(half_adder_full_12_out_3),
    .out_4(half_adder_full_12_out_4));
  Half_adder_full half_adder_full_13 (
    .in_1(full_adder_full_33_out_4), .in_2(full_adder_full_28_out_5), .out_3(half_adder_full_13_out_3),
    .out_4(half_adder_full_13_out_4));
  Full_adder_full full_adder_full_33 (
    .in_1(full_adder_full_34_out_4), .in_2(full_adder_full_29_out_5), .in_3(_1024_5_out),
    .out_4(full_adder_full_33_out_4), .out_5(full_adder_full_33_out_5));
  Full_adder_full full_adder_full_34 (
    .in_1(full_adder_full_35_out_4), .in_2(full_adder_full_30_out_5), .in_3(_1024_4_out),
    .out_4(full_adder_full_34_out_4), .out_5(full_adder_full_34_out_5));
  Full_adder_full full_adder_full_35 (
    .in_1(full_adder_full_36_out_4), .in_2(full_adder_full_31_out_5), .in_3(_1024_3_out),
    .out_4(full_adder_full_35_out_4), .out_5(full_adder_full_35_out_5));
  Full_adder_full full_adder_full_36 (
    .in_1(full_adder_full_32_out_5), .in_2(_1024_out), .in_3(_1024_2_out), .out_4(full_adder_full_36_out_4),
    .out_5(full_adder_full_36_out_5));
  and _16_4 (_16_4_out, in_2, in_12);
  and _8_4 (_8_4_out, in_1, in_12);
  and u__512 (_512_out, in_8, in_11);
  Half_adder_full half_adder_full_14 (
    .in_1(half_adder_full_15_out_3), .in_2(half_adder_full_11_out_4), .out_3(_2048),
    .out_4(half_adder_full_14_out_4));
  Half_adder_full half_adder_full_15 (
    .in_1(half_adder_full_16_out_3), .in_2(half_adder_full_12_out_4), .out_3(half_adder_full_15_out_3),
    .out_4(half_adder_full_15_out_4));
  Half_adder_full half_adder_full_16 (
    .in_1(half_adder_full_17_out_3), .in_2(half_adder_full_13_out_4), .out_3(half_adder_full_16_out_3),
    .out_4(half_adder_full_16_out_4));
  Half_adder_full half_adder_full_17 (
    .in_1(full_adder_full_37_out_4), .in_2(full_adder_full_33_out_5), .out_3(half_adder_full_17_out_3),
    .out_4(half_adder_full_17_out_4));
  Full_adder_full full_adder_full_37 (
    .in_1(full_adder_full_38_out_4), .in_2(full_adder_full_34_out_5), .in_3(_2048_4_out),
    .out_4(full_adder_full_37_out_4), .out_5(full_adder_full_37_out_5));
  Full_adder_full full_adder_full_38 (
    .in_1(full_adder_full_39_out_4), .in_2(full_adder_full_35_out_5), .in_3(_2048_3_out),
    .out_4(full_adder_full_38_out_4), .out_5(full_adder_full_38_out_5));
  Full_adder_full full_adder_full_39 (
    .in_1(full_adder_full_36_out_5), .in_2(_2048_out), .in_3(_2048_2_out), .out_4(full_adder_full_39_out_4),
    .out_5(full_adder_full_39_out_5));
  and _128_4 (_128_4_out, in_5, in_12);
  and _64_4 (_64_4_out, in_4, in_12);
  and _32_4 (_32_4_out, in_3, in_12);
  Half_adder_full half_adder_full_18 (
    .in_1(half_adder_full_19_out_3), .in_2(half_adder_full_14_out_4), .out_3(_4096),
    .out_4(half_adder_full_18_out_4));
  Half_adder_full half_adder_full_19 (
    .in_1(half_adder_full_20_out_3), .in_2(half_adder_full_15_out_4), .out_3(half_adder_full_19_out_3),
    .out_4(half_adder_full_19_out_4));
  Half_adder_full half_adder_full_20 (
    .in_1(half_adder_full_21_out_3), .in_2(half_adder_full_16_out_4), .out_3(half_adder_full_20_out_3),
    .out_4(half_adder_full_20_out_4));
  Half_adder_full half_adder_full_21 (
    .in_1(half_adder_full_22_out_3), .in_2(half_adder_full_17_out_4), .out_3(half_adder_full_21_out_3),
    .out_4(half_adder_full_21_out_4));
  Half_adder_full half_adder_full_22 (
    .in_1(full_adder_full_40_out_4), .in_2(full_adder_full_37_out_5), .out_3(half_adder_full_22_out_3),
    .out_4(half_adder_full_22_out_4));
  Full_adder_full full_adder_full_40 (
    .in_1(full_adder_full_41_out_4), .in_2(full_adder_full_38_out_5), .in_3(_4096_3_out),
    .out_4(full_adder_full_40_out_4), .out_5(full_adder_full_40_out_5));
  Full_adder_full full_adder_full_41 (
    .in_1(full_adder_full_39_out_5), .in_2(_4096_out), .in_3(_4096_2_out), .out_4(full_adder_full_41_out_4),
    .out_5(full_adder_full_41_out_5));
  and _512_2 (_512_2_out, in_7, in_12);
  and _256_3 (_256_3_out, in_6, in_12);
  Half_adder_full half_adder_full_23 (
    .in_1(half_adder_full_25_out_3), .in_2(half_adder_full_24_out_4), .out_3(_16384),
    .out_4(half_adder_full_23_out_4));
  Half_adder_full half_adder_full_24 (
    .in_1(half_adder_full_26_out_3), .in_2(half_adder_full_18_out_4), .out_3(_8192),
    .out_4(half_adder_full_24_out_4));
  Half_adder_full half_adder_full_25 (
    .in_1(half_adder_full_27_out_3), .in_2(half_adder_full_26_out_4), .out_3(half_adder_full_25_out_3),
    .out_4(half_adder_full_25_out_4));
  Half_adder_full half_adder_full_26 (
    .in_1(half_adder_full_28_out_3), .in_2(half_adder_full_19_out_4), .out_3(half_adder_full_26_out_3),
    .out_4(half_adder_full_26_out_4));
  Half_adder_full half_adder_full_27 (
    .in_1(half_adder_full_29_out_3), .in_2(half_adder_full_28_out_4), .out_3(half_adder_full_27_out_3),
    .out_4(half_adder_full_27_out_4));
  Half_adder_full half_adder_full_28 (
    .in_1(half_adder_full_30_out_3), .in_2(half_adder_full_20_out_4), .out_3(half_adder_full_28_out_3),
    .out_4(half_adder_full_28_out_4));
  Half_adder_full half_adder_full_29 (
    .in_1(half_adder_full_31_out_3), .in_2(half_adder_full_30_out_4), .out_3(half_adder_full_29_out_3),
    .out_4(half_adder_full_29_out_4));
  Half_adder_full half_adder_full_30 (
    .in_1(half_adder_full_32_out_3), .in_2(half_adder_full_21_out_4), .out_3(half_adder_full_30_out_3),
    .out_4(half_adder_full_30_out_4));
  Half_adder_full half_adder_full_31 (
    .in_1(half_adder_full_33_out_3), .in_2(half_adder_full_32_out_4), .out_3(half_adder_full_31_out_3),
    .out_4(half_adder_full_31_out_4));
  Half_adder_full half_adder_full_32 (
    .in_1(half_adder_full_34_out_3), .in_2(half_adder_full_22_out_4), .out_3(half_adder_full_32_out_3),
    .out_4(half_adder_full_32_out_4));
  Half_adder_full half_adder_full_33 (
    .in_1(half_adder_full_35_out_3), .in_2(half_adder_full_34_out_4), .out_3(half_adder_full_33_out_3),
    .out_4(half_adder_full_33_out_4));
  Half_adder_full half_adder_full_34 (
    .in_1(full_adder_full_42_out_4), .in_2(full_adder_full_40_out_5), .out_3(half_adder_full_34_out_3),
    .out_4(half_adder_full_34_out_4));
  Half_adder_full half_adder_full_35 (
    .in_1(full_adder_full_42_out_5), .in_2(and_1_out), .out_3(half_adder_full_35_out_3),
    .out_4(half_adder_full_35_out_4));
  Full_adder_full full_adder_full_42 (
    .in_1(full_adder_full_41_out_5), .in_2(_8192_out), .in_3(_8192_2_out), .out_4(full_adder_full_42_out_4),
    .out_5(full_adder_full_42_out_5));
  and _32_5 (_32_5_out, in_2, in_13);
  and _16_5 (_16_5_out, in_1, in_13);
  and u__1024 (_1024_out, in_8, in_12);
  or or_1 (_32768, or_2_out, half_adder_full_23_out_4);
  or or_2 (or_2_out, half_adder_full_25_out_4, or_3_out);
  or or_3 (or_3_out, or_4_out, half_adder_full_27_out_4);
  or or_4 (or_4_out, half_adder_full_29_out_4, or_5_out);
  or or_5 (or_5_out, or_6_out, half_adder_full_31_out_4);
  or or_6 (or_6_out, half_adder_full_35_out_4, half_adder_full_33_out_4);
  and _256_4 (_256_4_out, in_5, in_13);
  and _128_5 (_128_5_out, in_4, in_13);
  and _64_5 (_64_5_out, in_3, in_13);
  and _512_3 (_512_3_out, in_6, in_13);
  and _1024_2 (_1024_2_out, in_7, in_13);
  and u__2048 (_2048_out, in_8, in_13);
  and _64_6 (_64_6_out, in_2, in_14);
  and _32_6 (_32_6_out, in_1, in_14);
  and _128_6 (_128_6_out, in_3, in_14);
  and _512_4 (_512_4_out, in_5, in_14);
  and _256_5 (_256_5_out, in_4, in_14);
  and _2048_2 (_2048_2_out, in_7, in_14);
  and _1024_3 (_1024_3_out, in_6, in_14);
  and u__4096 (_4096_out, in_8, in_14);
  and _64_7 (_64_7_out, in_1, in_15);
  and _128_7 (_128_7_out, in_2, in_15);
  and _256_6 (_256_6_out, in_3, in_15);
  and _1024_4 (_1024_4_out, in_5, in_15);
  and _512_5 (_512_5_out, in_4, in_15);
  and _2048_3 (_2048_3_out, in_6, in_15);
  and _4096_2 (_4096_2_out, in_7, in_15);
  and u__8192 (_8192_out, in_8, in_15);
  and _256_7 (_256_7_out, in_2, in_16);
  and _128_8 (_128_8_out, in_1, in_16);
  and _2048_4 (_2048_4_out, in_5, in_16);
  and _1024_5 (_1024_5_out, in_4, in_16);
  and _512_6 (_512_6_out, in_3, in_16);
  and _4096_3 (_4096_3_out, in_6, in_16);
  and _8192_2 (_8192_2_out, in_7, in_16);
  and and_1 (and_1_out, in_8, in_16);

  // Notes on the sheet:
  //   16384
endmodule

module Division2 (
  input  _1,
  input  _2,
  input  _4,
  input  _8,
  input  _16,
  input  _1_2,
  input  _2_2,
  input  _4_2,
  input  _8_2,
  input  _16_2
);

  wire _1_2_2_out, _1_2_3_out, _1_2_4_out, _1_2_out, _1_2_out_2, _1_3_out, _1_4_2_out, _1_4_3_out, _1_4_out,
       _1_4_out_2, _1_5_out, _1_8_2_out, _1_8_out, _1_16_out, _1_out, _2_2_out, _2_3_out, _2_4_out, _2_out,
       _4_2_out, _4_3_out, _4_out, _8_2_out, _8_out, _16_out, and_1_out, and_2_out, and_3_out, and_4_out,
       and_5_out, and_6_out, and_7_out, and_8_out, and_9_out, and_10_out, and_11_out, and_12_out, and_13_out,
       and_14_out, and_15_out, and_16_out, and_17_out, and_18_out, and_19_out, and_20_out, and_21_out,
       and_22_out, and_23_out, and_24_out, and_25_out, and_26_out, and_27_out, and_28_out, and_29_out,
       and_30_out, and_31_out, and_32_out, and_33_out, and_34_out, or_1_out, or_2_out, or_3_out, or_4_out,
       or_5_out, or_6_out, or_7_out, or_8_out, or_9_out, or_10_out, or_11_out, or_12_out, xor_1_out,
       xor_2_out, xor_3_out, xor_4_out, xor_5_out, xor_6_out, xor_7_out, xor_8_out, xor_9_out, xor_10_out,
       xor_11_out, xor_12_out, xor_13_out, xor_14_out, xor_15_out, xor_16_out, xor_17_out, xor_18_out,
       xor_19_out, xor_20_out, xor_21_out, xor_22_out, xor_23_out, xor_24_out, xor_25_out, xor_26_out,
       xor_27_out, xor_28_out, xor_29_out, xor_30_out, xor_31_out, xor_32_out, xor_33_out, xor_34_out,
       xor_35_out, xor_36_out, xor_37_out, xor_38_out;

  xor xor_1 (xor_1_out, _1_8_out, _1_8_2_out);
  and u__1_2 (_1_2_out_2, _1, _2_2);
  and u__1 (_1_out, _1, _1_2);
  and and_1 (and_1_out, _1_8_out, _1_8_2_out);
  and _1_8 (_1_8_out, _1, _8_2);
  and _1_4 (_1_4_out, _1, _4_2);
  and _1_16 (_1_16_out, _1, _16_2);
  xor xor_2 (xor_2_out, xor_3_out, _1_4_3_out);
  xor xor_3 (xor_3_out, and_1_out, xor_4_out);
  and and_2 (and_2_out, and_1_out, xor_4_out);
  xor xor_4 (xor_4_out, _1_4_out, _1_4_2_out);
  and and_3 (and_3_out, _1_4_out, _1_4_2_out);
  and _1_2_2 (_1_2_2_out, _2, _4_2);
  and u__2 (_2_out, _2, _1_2);
  and u__1_2_dup2 (_1_2_out, _2, _2_2);
  and and_4 (and_4_out, xor_3_out, _1_4_3_out);
  or or_1 (or_1_out, and_2_out, and_3_out);
  and _1_8_2 (_1_8_2_out, _2, _16_2);
  and _1_4_2 (_1_4_2_out, _2, _8_2);
  xor xor_5 (xor_5_out, xor_6_out, _1_2_4_out);
  xor xor_6 (xor_6_out, and_4_out, xor_7_out);
  xor xor_7 (xor_7_out, xor_8_out, _1_2_3_out);
  xor xor_8 (xor_8_out, or_1_out, xor_9_out);
  xor xor_9 (xor_9_out, _1_2_out_2, _1_2_2_out);
  and u__2_2 (_2_2_out, _4, _2_2);
  and u__4 (_4_out, _4, _1_2);
  and _1_3 (_1_3_out, _4, _4_2);
  and and_5 (and_5_out, xor_6_out, _1_2_4_out);
  and and_6 (and_6_out, and_4_out, xor_7_out);
  and and_7 (and_7_out, xor_8_out, _1_2_3_out);
  and and_8 (and_8_out, or_1_out, xor_9_out);
  or or_2 (or_2_out, and_8_out, and_9_out);
  and and_9 (and_9_out, _1_2_out_2, _1_2_2_out);
  and _1_2_3 (_1_2_3_out, _4, _8_2);
  and _1_4_3 (_1_4_3_out, _4, _16_2);
  and u__8 (_8_out, _8, _1_2);
  xor xor_10 (xor_10_out, or_3_out, xor_11_out);
  or or_3 (or_3_out, and_6_out, and_7_out);
  xor xor_11 (xor_11_out, xor_12_out, _1_3_out);
  xor xor_12 (xor_12_out, or_2_out, xor_13_out);
  xor xor_13 (xor_13_out, _1_out, _1_2_out);
  and _2_3 (_2_3_out, _8, _4_2);
  and u__4_2 (_4_2_out, _8, _2_2);
  xor xor_14 (xor_14_out, xor_15_out, _1_5_out);
  xor xor_15 (xor_15_out, and_5_out, xor_16_out);
  and and_10 (and_10_out, and_5_out, xor_16_out);
  xor xor_16 (xor_16_out, xor_10_out, _1_4_out_2);
  and and_11 (and_11_out, xor_10_out, _1_4_out_2);
  and and_12 (and_12_out, or_3_out, xor_11_out);
  and and_13 (and_13_out, xor_12_out, _1_3_out);
  and and_14 (and_14_out, or_2_out, xor_13_out);
  and and_15 (and_15_out, _1_out, _1_2_out);
  and _1_4_dup2 (_1_4_out_2, _8, _8_2);
  and u__16 (_16_out, _16, _1_2);
  and _1_2_4 (_1_2_4_out, _8, _16_2);
  and and_16 (and_16_out, xor_15_out, _1_5_out);
  or or_4 (or_4_out, and_10_out, and_11_out);
  or or_5 (or_5_out, and_12_out, and_13_out);
  or or_6 (or_6_out, and_14_out, and_15_out);
  and _2_4 (_2_4_out, _16, _8_2);
  and u__8_2 (_8_2_out, _16, _2_2);
  and _4_3 (_4_3_out, _16, _4_2);
  xor xor_17 (xor_17_out, xor_18_out, and_16_out);
  xor xor_18 (xor_18_out, or_4_out, xor_19_out);
  xor xor_19 (xor_19_out, xor_20_out, _2_4_out);
  xor xor_20 (xor_20_out, or_5_out, xor_21_out);
  xor xor_21 (xor_21_out, xor_22_out, _2_3_out);
  xor xor_22 (xor_22_out, or_6_out, xor_23_out);
  xor xor_23 (xor_23_out, _2_out, _2_2_out);
  and _1_5 (_1_5_out, _16, _16_2);
  and and_17 (and_17_out, or_4_out, xor_19_out);
  and and_18 (and_18_out, xor_20_out, _2_4_out);
  and and_19 (and_19_out, or_5_out, xor_21_out);
  and and_20 (and_20_out, xor_22_out, _2_3_out);
  and and_21 (and_21_out, or_6_out, xor_23_out);
  or or_7 (or_7_out, and_21_out, and_22_out);
  and and_22 (and_22_out, _2_out, _2_2_out);
  and and_23 (and_23_out, xor_18_out, and_16_out);
  or or_8 (or_8_out, and_17_out, and_18_out);
  xor xor_24 (xor_24_out, or_9_out, xor_25_out);
  or or_9 (or_9_out, and_19_out, and_20_out);
  xor xor_25 (xor_25_out, xor_26_out, _4_3_out);
  xor xor_26 (xor_26_out, or_7_out, xor_27_out);
  xor xor_27 (xor_27_out, _4_out, _4_2_out);
  xor xor_28 (xor_28_out, xor_29_out, and_23_out);
  xor xor_29 (xor_29_out, xor_24_out, or_8_out);
  and and_24 (and_24_out, or_9_out, xor_25_out);
  and and_25 (and_25_out, xor_26_out, _4_3_out);
  and and_26 (and_26_out, or_7_out, xor_27_out);
  and and_27 (and_27_out, _4_out, _4_2_out);
  and and_28 (and_28_out, xor_29_out, and_23_out);
  and and_29 (and_29_out, xor_24_out, or_8_out);
  or or_10 (or_10_out, and_24_out, and_25_out);
  or or_11 (or_11_out, and_26_out, and_27_out);
  xor xor_30 (xor_30_out, xor_31_out, and_28_out);
  xor xor_31 (xor_31_out, xor_32_out, and_29_out);
  xor xor_32 (xor_32_out, xor_33_out, or_10_out);
  xor xor_33 (xor_33_out, or_11_out, xor_34_out);
  xor xor_34 (xor_34_out, _8_out, _8_2_out);
  and and_30 (and_30_out, xor_32_out, and_29_out);
  and and_31 (and_31_out, xor_33_out, or_10_out);
  and and_32 (and_32_out, or_11_out, xor_34_out);
  or or_12 (or_12_out, and_32_out, and_33_out);
  and and_33 (and_33_out, _8_out, _8_2_out);
  xor xor_35 (xor_35_out, xor_36_out, and_34_out);
  and and_34 (and_34_out, xor_31_out, and_28_out);
  xor xor_36 (xor_36_out, xor_37_out, and_30_out);
  xor xor_37 (xor_37_out, xor_38_out, and_31_out);
  xor xor_38 (xor_38_out, or_12_out, _16_out);
  // AND_Gate and_35 has open pins: in2=xor_37_out, in3=and_30_out, out=open
  // AND_Gate and_36 has open pins: in2=or_12_out, in3=_16_out, out=open
  // AND_Gate and_37 has open pins: in2=xor_36_out, in3=and_34_out, out=open
  // AND_Gate and_38 has open pins: in2=xor_38_out, in3=and_31_out, out=open
endmodule
module _8bit_division (
  input  in_1,
  input  in_2,
  input  in_3,
  input  y,
  input  in_5,
  input  in_6,
  input  in_7,
  input  in_8,
  input  in_9,
  input  in_10,
  input  x,
  input  in_12,
  input  in_13,
  input  in_14,
  input  in_15,
  input  in_16,
  output _0_0078125,
  output _0_03125,
  output out_19,
  output _0_125,
  output out_21,
  output out_22,
  output _0_5,
  output _1,
  output _2,
  output _4,
  output _8,
  output _16,
  output _32,
  output _64,
  output _128
);

  wire _1_2_2_out, _1_2_3_out, _1_2_4_out, _1_2_5_out, _1_2_6_out, _1_2_7_out, _1_2_out, _1_2_out_2,
       _1_3_out, _1_4_2_out, _1_4_3_out, _1_4_4_out, _1_4_5_out, _1_4_6_out, _1_4_out, _1_4_out_2, _1_5_out,
       _1_6_out, _1_7_out, _1_8_2_out, _1_8_3_out, _1_8_4_out, _1_8_5_out, _1_8_out, _1_8_out_2, _1_16_2_out,
       _1_16_3_out, _1_16_4_out, _1_16_out, _1_32_2_out, _1_32_3_out, _1_32_out, _1_64_2_out, _1_64_out,
       _1_out, _2_2_out, _2_3_out, _2_4_out, _2_5_out, _2_6_out, _2_7_out, _2_out, _4_2_out, _4_3_out,
       _4_4_out, _4_5_out, _4_6_out, _4_out, _8_2_out, _8_3_out, _8_4_out, _8_5_out, _8_out, _16_2_out,
       _16_3_out, _16_4_out, _16_out, _32_2_out, _32_3_out, _32_out, _64_2_out, _64_out, _128_out,
       full_adder_full_1_out_4, full_adder_full_1_out_5, full_adder_full_2_out_4, full_adder_full_2_out_5,
       full_adder_full_3_out_4, full_adder_full_3_out_5, full_adder_full_4_out_4, full_adder_full_4_out_5,
       full_adder_full_5_out_4, full_adder_full_5_out_5, full_adder_full_6_out_4, full_adder_full_6_out_5,
       full_adder_full_7_out_4, full_adder_full_7_out_5, full_adder_full_8_out_4, full_adder_full_8_out_5,
       full_adder_full_9_out_4, full_adder_full_9_out_5, full_adder_full_10_out_4, full_adder_full_10_out_5,
       full_adder_full_11_out_4, full_adder_full_11_out_5, full_adder_full_12_out_4,
       full_adder_full_12_out_5, full_adder_full_13_out_4, full_adder_full_13_out_5,
       full_adder_full_14_out_4, full_adder_full_14_out_5, full_adder_full_15_out_4,
       full_adder_full_15_out_5, full_adder_full_16_out_4, full_adder_full_16_out_5,
       full_adder_full_17_out_4, full_adder_full_17_out_5, full_adder_full_18_out_4,
       full_adder_full_18_out_5, full_adder_full_19_out_4, full_adder_full_19_out_5,
       full_adder_full_20_out_4, full_adder_full_20_out_5, full_adder_full_21_out_4,
       full_adder_full_21_out_5, full_adder_full_22_out_4, full_adder_full_22_out_5,
       full_adder_full_23_out_4, full_adder_full_23_out_5, full_adder_full_24_out_4,
       full_adder_full_24_out_5, full_adder_full_25_out_4, full_adder_full_25_out_5,
       full_adder_full_26_out_4, full_adder_full_26_out_5, full_adder_full_27_out_4,
       full_adder_full_27_out_5, full_adder_full_28_out_4, full_adder_full_28_out_5,
       full_adder_full_29_out_4, full_adder_full_29_out_5, full_adder_full_30_out_4,
       full_adder_full_30_out_5, full_adder_full_31_out_4, full_adder_full_31_out_5,
       full_adder_full_32_out_4, full_adder_full_32_out_5, full_adder_full_33_out_4,
       full_adder_full_33_out_5, full_adder_full_34_out_4, full_adder_full_34_out_5,
       full_adder_full_35_out_4, full_adder_full_35_out_5, full_adder_full_36_out_4,
       full_adder_full_36_out_5, full_adder_full_37_out_4, full_adder_full_37_out_5,
       full_adder_full_38_out_4, full_adder_full_38_out_5, full_adder_full_39_out_4,
       full_adder_full_39_out_5, full_adder_full_40_out_4, full_adder_full_40_out_5,
       full_adder_full_41_out_4, full_adder_full_41_out_5, full_adder_full_42_out_4,
       full_adder_full_42_out_5, half_adder_full_1_out_4, half_adder_full_2_out_4, half_adder_full_3_out_4,
       half_adder_full_4_out_4, half_adder_full_5_out_4, half_adder_full_6_out_4, half_adder_full_7_out_4,
       half_adder_full_8_out_4, half_adder_full_9_out_4, half_adder_full_10_out_3, half_adder_full_10_out_4,
       half_adder_full_11_out_4, half_adder_full_12_out_3, half_adder_full_12_out_4,
       half_adder_full_13_out_3, half_adder_full_13_out_4, half_adder_full_14_out_4,
       half_adder_full_15_out_3, half_adder_full_15_out_4, half_adder_full_16_out_3,
       half_adder_full_16_out_4, half_adder_full_17_out_3, half_adder_full_17_out_4,
       half_adder_full_18_out_4, half_adder_full_19_out_3, half_adder_full_19_out_4,
       half_adder_full_20_out_3, half_adder_full_20_out_4, half_adder_full_21_out_3,
       half_adder_full_21_out_4, half_adder_full_22_out_3, half_adder_full_22_out_4,
       half_adder_full_24_out_4, half_adder_full_25_out_3, half_adder_full_26_out_3,
       half_adder_full_26_out_4, half_adder_full_27_out_3, half_adder_full_28_out_3,
       half_adder_full_28_out_4, half_adder_full_29_out_3, half_adder_full_30_out_3,
       half_adder_full_30_out_4, half_adder_full_31_out_3, half_adder_full_32_out_3,
       half_adder_full_32_out_4, half_adder_full_33_out_3, half_adder_full_34_out_3,
       half_adder_full_34_out_4, half_adder_full_35_out_3;

  Half_adder_full half_adder_full_1 (
    .in_1(_1_64_out), .in_2(_1_64_2_out), .out_3(_0_03125), .out_4(half_adder_full_1_out_4));
  and _1_2 (_1_2_out, in_2, in_9);
  and u__1 (_1_out, in_1, in_9);
  Half_adder_full half_adder_full_2 (
    .in_1(full_adder_full_1_out_4), .in_2(_1_32_3_out), .out_3(out_19), .out_4(half_adder_full_2_out_4));
  Full_adder_full full_adder_full_1 (
    .in_1(half_adder_full_1_out_4), .in_2(_1_32_out), .in_3(_1_32_2_out), .out_4(full_adder_full_1_out_4),
    .out_5(full_adder_full_1_out_5));
  and _1_8 (_1_8_out, y, in_9);
  and _1_4 (_1_4_out, in_3, in_9);
  and _1_16 (_1_16_out, in_5, in_9);
  Half_adder_full half_adder_full_3 (
    .in_1(full_adder_full_2_out_4), .in_2(_1_8_5_out), .out_3(out_21), .out_4(half_adder_full_3_out_4));
  Full_adder_full full_adder_full_2 (
    .in_1(full_adder_full_3_out_4), .in_2(half_adder_full_4_out_4), .in_3(_1_8_4_out),
    .out_4(full_adder_full_2_out_4), .out_5(full_adder_full_2_out_5));
  Half_adder_full half_adder_full_4 (
    .in_1(full_adder_full_4_out_4), .in_2(_1_16_4_out), .out_3(_0_125), .out_4(half_adder_full_4_out_4));
  Full_adder_full full_adder_full_3 (
    .in_1(full_adder_full_5_out_4), .in_2(full_adder_full_4_out_5), .in_3(_1_8_3_out),
    .out_4(full_adder_full_3_out_4), .out_5(full_adder_full_3_out_5));
  Full_adder_full full_adder_full_4 (
    .in_1(half_adder_full_2_out_4), .in_2(full_adder_full_6_out_4), .in_3(_1_16_3_out),
    .out_4(full_adder_full_4_out_4), .out_5(full_adder_full_4_out_5));
  Full_adder_full full_adder_full_5 (
    .in_1(full_adder_full_6_out_5), .in_2(_1_8_2_out), .in_3(_1_8_out), .out_4(full_adder_full_5_out_4),
    .out_5(full_adder_full_5_out_5));
  Full_adder_full full_adder_full_6 (
    .in_1(full_adder_full_1_out_5), .in_2(_1_16_2_out), .in_3(_1_16_out), .out_4(full_adder_full_6_out_4),
    .out_5(full_adder_full_6_out_5));
  and _1_64 (_1_64_out, in_7, in_9);
  and _1_32 (_1_32_out, in_6, in_9);
  Half_adder_full half_adder_full_5 (
    .in_1(full_adder_full_7_out_4), .in_2(_1_4_6_out), .out_3(out_22), .out_4(half_adder_full_5_out_4));
  Full_adder_full full_adder_full_7 (
    .in_1(half_adder_full_3_out_4), .in_2(full_adder_full_8_out_4), .in_3(_1_4_5_out),
    .out_4(full_adder_full_7_out_4), .out_5(full_adder_full_7_out_5));
  Full_adder_full full_adder_full_8 (
    .in_1(full_adder_full_9_out_4), .in_2(full_adder_full_2_out_5), .in_3(_1_4_4_out),
    .out_4(full_adder_full_8_out_4), .out_5(full_adder_full_8_out_5));
  Full_adder_full full_adder_full_9 (
    .in_1(full_adder_full_10_out_4), .in_2(full_adder_full_3_out_5), .in_3(_1_4_3_out),
    .out_4(full_adder_full_9_out_4), .out_5(full_adder_full_9_out_5));
  Full_adder_full full_adder_full_10 (
    .in_1(full_adder_full_5_out_5), .in_2(_1_4_out), .in_3(_1_4_2_out), .out_4(full_adder_full_10_out_4),
    .out_5(full_adder_full_10_out_5));
  and u__2 (_2_out, in_1, in_10);
  and _1_2_dup2 (_1_2_out_2, in_2, in_10);
  and _1_128 (_0_0078125, in_8, in_9);
  Half_adder_full half_adder_full_6 (
    .in_1(full_adder_full_11_out_4), .in_2(_1_2_7_out), .out_3(_0_5), .out_4(half_adder_full_6_out_4));
  Full_adder_full full_adder_full_11 (
    .in_1(full_adder_full_12_out_4), .in_2(half_adder_full_5_out_4), .in_3(_1_2_6_out),
    .out_4(full_adder_full_11_out_4), .out_5(full_adder_full_11_out_5));
  Full_adder_full full_adder_full_12 (
    .in_1(full_adder_full_13_out_4), .in_2(full_adder_full_7_out_5), .in_3(_1_2_5_out),
    .out_4(full_adder_full_12_out_4), .out_5(full_adder_full_12_out_5));
  Full_adder_full full_adder_full_13 (
    .in_1(full_adder_full_14_out_4), .in_2(full_adder_full_8_out_5), .in_3(_1_2_4_out),
    .out_4(full_adder_full_13_out_4), .out_5(full_adder_full_13_out_5));
  Full_adder_full full_adder_full_14 (
    .in_1(full_adder_full_15_out_4), .in_2(full_adder_full_9_out_5), .in_3(_1_2_3_out),
    .out_4(full_adder_full_14_out_4), .out_5(full_adder_full_14_out_5));
  Full_adder_full full_adder_full_15 (
    .in_1(full_adder_full_10_out_5), .in_2(_1_2_out), .in_3(_1_2_2_out), .out_4(full_adder_full_15_out_4),
    .out_5(full_adder_full_15_out_5));
  and _1_2_2 (_1_2_2_out, in_3, in_10);
  and _1_4_2 (_1_4_2_out, y, in_10);
  and _1_8_2 (_1_8_2_out, in_5, in_10);
  and _1_32_2 (_1_32_2_out, in_7, in_10);
  and _1_16_2 (_1_16_2_out, in_6, in_10);
  Half_adder_full half_adder_full_7 (
    .in_1(full_adder_full_16_out_4), .in_2(_1_8_out_2), .out_3(_1), .out_4(half_adder_full_7_out_4));
  Full_adder_full full_adder_full_16 (
    .in_1(half_adder_full_6_out_4), .in_2(full_adder_full_17_out_4), .in_3(_1_7_out),
    .out_4(full_adder_full_16_out_4), .out_5(full_adder_full_16_out_5));
  Full_adder_full full_adder_full_17 (
    .in_1(full_adder_full_11_out_5), .in_2(full_adder_full_18_out_4), .in_3(_1_6_out),
    .out_4(full_adder_full_17_out_4), .out_5(full_adder_full_17_out_5));
  Full_adder_full full_adder_full_18 (
    .in_1(full_adder_full_12_out_5), .in_2(full_adder_full_19_out_4), .in_3(_1_5_out),
    .out_4(full_adder_full_18_out_4), .out_5(full_adder_full_18_out_5));
  Full_adder_full full_adder_full_19 (
    .in_1(full_adder_full_13_out_5), .in_2(full_adder_full_20_out_4), .in_3(_1_4_out_2),
    .out_4(full_adder_full_19_out_4), .out_5(full_adder_full_19_out_5));
  Full_adder_full full_adder_full_20 (
    .in_1(full_adder_full_14_out_5), .in_2(full_adder_full_21_out_4), .in_3(_1_3_out),
    .out_4(full_adder_full_20_out_4), .out_5(full_adder_full_20_out_5));
  Full_adder_full full_adder_full_21 (
    .in_1(full_adder_full_15_out_5), .in_2(_1_out), .in_3(_1_2_out_2), .out_4(full_adder_full_21_out_4),
    .out_5(full_adder_full_21_out_5));
  and _2_2 (_2_2_out, in_2, x);
  and _1_64_2 (_1_64_2_out, in_8, in_10);
  and u__4 (_4_out, in_1, x);
  Half_adder_full half_adder_full_8 (
    .in_1(full_adder_full_22_out_4), .in_2(half_adder_full_7_out_4), .out_3(_2),
    .out_4(half_adder_full_8_out_4));
  Full_adder_full full_adder_full_22 (
    .in_1(full_adder_full_23_out_4), .in_2(full_adder_full_16_out_5), .in_3(_2_7_out),
    .out_4(full_adder_full_22_out_4), .out_5(full_adder_full_22_out_5));
  Full_adder_full full_adder_full_23 (
    .in_1(full_adder_full_24_out_4), .in_2(full_adder_full_17_out_5), .in_3(_2_6_out),
    .out_4(full_adder_full_23_out_4), .out_5(full_adder_full_23_out_5));
  Full_adder_full full_adder_full_24 (
    .in_1(full_adder_full_25_out_4), .in_2(full_adder_full_18_out_5), .in_3(_2_5_out),
    .out_4(full_adder_full_24_out_4), .out_5(full_adder_full_24_out_5));
  Full_adder_full full_adder_full_25 (
    .in_1(full_adder_full_26_out_4), .in_2(full_adder_full_19_out_5), .in_3(_2_4_out),
    .out_4(full_adder_full_25_out_4), .out_5(full_adder_full_25_out_5));
  Full_adder_full full_adder_full_26 (
    .in_1(full_adder_full_27_out_4), .in_2(full_adder_full_20_out_5), .in_3(_2_3_out),
    .out_4(full_adder_full_26_out_4), .out_5(full_adder_full_26_out_5));
  Full_adder_full full_adder_full_27 (
    .in_1(full_adder_full_21_out_5), .in_2(_2_out), .in_3(_2_2_out), .out_4(full_adder_full_27_out_4),
    .out_5(full_adder_full_27_out_5));
  and _1_4_3 (_1_4_3_out, in_5, x);
  and _1_3 (_1_3_out, in_3, x);
  and _1_2_3 (_1_2_3_out, y, x);
  Half_adder_full half_adder_full_9 (
    .in_1(half_adder_full_8_out_4), .in_2(half_adder_full_10_out_3), .out_3(_4),
    .out_4(half_adder_full_9_out_4));
  Half_adder_full half_adder_full_10 (
    .in_1(full_adder_full_22_out_5), .in_2(full_adder_full_28_out_4), .out_3(half_adder_full_10_out_3),
    .out_4(half_adder_full_10_out_4));
  Full_adder_full full_adder_full_28 (
    .in_1(full_adder_full_23_out_5), .in_2(full_adder_full_29_out_4), .in_3(_4_6_out),
    .out_4(full_adder_full_28_out_4), .out_5(full_adder_full_28_out_5));
  Full_adder_full full_adder_full_29 (
    .in_1(full_adder_full_24_out_5), .in_2(full_adder_full_30_out_4), .in_3(_4_5_out),
    .out_4(full_adder_full_29_out_4), .out_5(full_adder_full_29_out_5));
  Full_adder_full full_adder_full_30 (
    .in_1(full_adder_full_25_out_5), .in_2(full_adder_full_31_out_4), .in_3(_4_4_out),
    .out_4(full_adder_full_30_out_4), .out_5(full_adder_full_30_out_5));
  Full_adder_full full_adder_full_31 (
    .in_1(full_adder_full_26_out_5), .in_2(full_adder_full_32_out_4), .in_3(_4_3_out),
    .out_4(full_adder_full_31_out_4), .out_5(full_adder_full_31_out_5));
  Full_adder_full full_adder_full_32 (
    .in_1(full_adder_full_27_out_5), .in_2(_4_out), .in_3(_4_2_out), .out_4(full_adder_full_32_out_4),
    .out_5(full_adder_full_32_out_5));
  and _1_16_3 (_1_16_3_out, in_7, x);
  and _1_8_3 (_1_8_3_out, in_6, x);
  Half_adder_full half_adder_full_11 (
    .in_1(half_adder_full_12_out_3), .in_2(half_adder_full_9_out_4), .out_3(_8),
    .out_4(half_adder_full_11_out_4));
  Half_adder_full half_adder_full_12 (
    .in_1(half_adder_full_13_out_3), .in_2(half_adder_full_10_out_4), .out_3(half_adder_full_12_out_3),
    .out_4(half_adder_full_12_out_4));
  Half_adder_full half_adder_full_13 (
    .in_1(full_adder_full_33_out_4), .in_2(full_adder_full_28_out_5), .out_3(half_adder_full_13_out_3),
    .out_4(half_adder_full_13_out_4));
  Full_adder_full full_adder_full_33 (
    .in_1(full_adder_full_34_out_4), .in_2(full_adder_full_29_out_5), .in_3(_8_5_out),
    .out_4(full_adder_full_33_out_4), .out_5(full_adder_full_33_out_5));
  Full_adder_full full_adder_full_34 (
    .in_1(full_adder_full_35_out_4), .in_2(full_adder_full_30_out_5), .in_3(_8_4_out),
    .out_4(full_adder_full_34_out_4), .out_5(full_adder_full_34_out_5));
  Full_adder_full full_adder_full_35 (
    .in_1(full_adder_full_36_out_4), .in_2(full_adder_full_31_out_5), .in_3(_8_3_out),
    .out_4(full_adder_full_35_out_4), .out_5(full_adder_full_35_out_5));
  Full_adder_full full_adder_full_36 (
    .in_1(full_adder_full_32_out_5), .in_2(_8_out), .in_3(_8_2_out), .out_4(full_adder_full_36_out_4),
    .out_5(full_adder_full_36_out_5));
  and _1_32_3 (_1_32_3_out, in_8, x);
  and _4_2 (_4_2_out, in_2, in_12);
  and u__8 (_8_out, in_1, in_12);
  Half_adder_full half_adder_full_14 (
    .in_1(half_adder_full_15_out_3), .in_2(half_adder_full_11_out_4), .out_3(_16),
    .out_4(half_adder_full_14_out_4));
  Half_adder_full half_adder_full_15 (
    .in_1(half_adder_full_16_out_3), .in_2(half_adder_full_12_out_4), .out_3(half_adder_full_15_out_3),
    .out_4(half_adder_full_15_out_4));
  Half_adder_full half_adder_full_16 (
    .in_1(half_adder_full_17_out_3), .in_2(half_adder_full_13_out_4), .out_3(half_adder_full_16_out_3),
    .out_4(half_adder_full_16_out_4));
  Half_adder_full half_adder_full_17 (
    .in_1(full_adder_full_37_out_4), .in_2(full_adder_full_33_out_5), .out_3(half_adder_full_17_out_3),
    .out_4(half_adder_full_17_out_4));
  Full_adder_full full_adder_full_37 (
    .in_1(full_adder_full_38_out_4), .in_2(full_adder_full_34_out_5), .in_3(_16_4_out),
    .out_4(full_adder_full_37_out_4), .out_5(full_adder_full_37_out_5));
  Full_adder_full full_adder_full_38 (
    .in_1(full_adder_full_39_out_4), .in_2(full_adder_full_35_out_5), .in_3(_16_3_out),
    .out_4(full_adder_full_38_out_4), .out_5(full_adder_full_38_out_5));
  Full_adder_full full_adder_full_39 (
    .in_1(full_adder_full_36_out_5), .in_2(_16_out), .in_3(_16_2_out), .out_4(full_adder_full_39_out_4),
    .out_5(full_adder_full_39_out_5));
  and _1_2_4 (_1_2_4_out, in_5, in_12);
  and _1_4_dup2 (_1_4_out_2, y, in_12);
  and _2_3 (_2_3_out, in_3, in_12);
  Half_adder_full half_adder_full_18 (
    .in_1(half_adder_full_19_out_3), .in_2(half_adder_full_14_out_4), .out_3(_32),
    .out_4(half_adder_full_18_out_4));
  Half_adder_full half_adder_full_19 (
    .in_1(half_adder_full_20_out_3), .in_2(half_adder_full_15_out_4), .out_3(half_adder_full_19_out_3),
    .out_4(half_adder_full_19_out_4));
  Half_adder_full half_adder_full_20 (
    .in_1(half_adder_full_21_out_3), .in_2(half_adder_full_16_out_4), .out_3(half_adder_full_20_out_3),
    .out_4(half_adder_full_20_out_4));
  Half_adder_full half_adder_full_21 (
    .in_1(half_adder_full_22_out_3), .in_2(half_adder_full_17_out_4), .out_3(half_adder_full_21_out_3),
    .out_4(half_adder_full_21_out_4));
  Half_adder_full half_adder_full_22 (
    .in_1(full_adder_full_40_out_4), .in_2(full_adder_full_37_out_5), .out_3(half_adder_full_22_out_3),
    .out_4(half_adder_full_22_out_4));
  Full_adder_full full_adder_full_40 (
    .in_1(full_adder_full_41_out_4), .in_2(full_adder_full_38_out_5), .in_3(_32_3_out),
    .out_4(full_adder_full_40_out_4), .out_5(full_adder_full_40_out_5));
  Full_adder_full full_adder_full_41 (
    .in_1(full_adder_full_39_out_5), .in_2(_32_out), .in_3(_32_2_out), .out_4(full_adder_full_41_out_4),
    .out_5(full_adder_full_41_out_5));
  and _1_8_4 (_1_8_4_out, in_7, in_12);
  and _1_4_4 (_1_4_4_out, in_6, in_12);
  Half_adder_full half_adder_full_23 (
    .in_1(half_adder_full_25_out_3), .in_2(half_adder_full_24_out_4), .out_3(_128));  // open: out_4
  Half_adder_full half_adder_full_24 (
    .in_1(half_adder_full_26_out_3), .in_2(half_adder_full_18_out_4), .out_3(_64),
    .out_4(half_adder_full_24_out_4));
  Half_adder_full half_adder_full_25 (
    .in_1(half_adder_full_27_out_3), .in_2(half_adder_full_26_out_4), .out_3(half_adder_full_25_out_3));  // open: out_4
  Half_adder_full half_adder_full_26 (
    .in_1(half_adder_full_28_out_3), .in_2(half_adder_full_19_out_4), .out_3(half_adder_full_26_out_3),
    .out_4(half_adder_full_26_out_4));
  Half_adder_full half_adder_full_27 (
    .in_1(half_adder_full_29_out_3), .in_2(half_adder_full_28_out_4), .out_3(half_adder_full_27_out_3));  // open: out_4
  Half_adder_full half_adder_full_28 (
    .in_1(half_adder_full_30_out_3), .in_2(half_adder_full_20_out_4), .out_3(half_adder_full_28_out_3),
    .out_4(half_adder_full_28_out_4));
  Half_adder_full half_adder_full_29 (
    .in_1(half_adder_full_31_out_3), .in_2(half_adder_full_30_out_4), .out_3(half_adder_full_29_out_3));  // open: out_4
  Half_adder_full half_adder_full_30 (
    .in_1(half_adder_full_32_out_3), .in_2(half_adder_full_21_out_4), .out_3(half_adder_full_30_out_3),
    .out_4(half_adder_full_30_out_4));
  Half_adder_full half_adder_full_31 (
    .in_1(half_adder_full_33_out_3), .in_2(half_adder_full_32_out_4), .out_3(half_adder_full_31_out_3));  // open: out_4
  Half_adder_full half_adder_full_32 (
    .in_1(half_adder_full_34_out_3), .in_2(half_adder_full_22_out_4), .out_3(half_adder_full_32_out_3),
    .out_4(half_adder_full_32_out_4));
  Half_adder_full half_adder_full_33 (
    .in_1(half_adder_full_35_out_3), .in_2(half_adder_full_34_out_4), .out_3(half_adder_full_33_out_3));  // open: out_4
  Half_adder_full half_adder_full_34 (
    .in_1(full_adder_full_42_out_4), .in_2(full_adder_full_40_out_5), .out_3(half_adder_full_34_out_3),
    .out_4(half_adder_full_34_out_4));
  Half_adder_full half_adder_full_35 (
    .in_1(full_adder_full_42_out_5), .in_2(_128_out), .out_3(half_adder_full_35_out_3));  // open: out_4
  Full_adder_full full_adder_full_42 (
    .in_1(full_adder_full_41_out_5), .in_2(_64_out), .in_3(_64_2_out), .out_4(full_adder_full_42_out_4),
    .out_5(full_adder_full_42_out_5));
  and _8_2 (_8_2_out, in_2, in_13);
  and _1_16_4 (_1_16_4_out, in_8, in_12);
  and u__16 (_16_out, in_1, in_13);
  and _4_3 (_4_3_out, in_3, in_13);
  and _2_4 (_2_4_out, y, in_13);
  and _1_5 (_1_5_out, in_5, in_13);
  and _1_2_5 (_1_2_5_out, in_6, in_13);
  and _1_4_5 (_1_4_5_out, in_7, in_13);
  and _16_2 (_16_2_out, in_2, in_14);
  and _1_8_5 (_1_8_5_out, in_8, in_13);
  and u__32 (_32_out, in_1, in_14);
  and _8_3 (_8_3_out, in_3, in_14);
  and _4_4 (_4_4_out, y, in_14);
  and _2_5 (_2_5_out, in_5, in_14);
  and _1_2_6 (_1_2_6_out, in_7, in_14);
  and _1_6 (_1_6_out, in_6, in_14);
  and _1_4_6 (_1_4_6_out, in_8, in_14);
  and _32_2 (_32_2_out, in_2, in_15);
  and u__64 (_64_out, in_1, in_15);
  and _8_4 (_8_4_out, y, in_15);
  and _4_5 (_4_5_out, in_5, in_15);
  and _16_3 (_16_3_out, in_3, in_15);
  and _1_7 (_1_7_out, in_7, in_15);
  and _2_6 (_2_6_out, in_6, in_15);
  and _1_2_7 (_1_2_7_out, in_8, in_15);
  and _64_2 (_64_2_out, in_2, in_16);
  and u__128 (_128_out, in_1, in_16);
  and _8_5 (_8_5_out, in_5, in_16);
  and _16_4 (_16_4_out, y, in_16);
  and _32_3 (_32_3_out, in_3, in_16);
  and _4_6 (_4_6_out, in_6, in_16);
  and _2_7 (_2_7_out, in_7, in_16);
  and _1_8_dup2 (_1_8_out_2, in_8, in_16);

  // Notes on the sheet:
  //   0.015625
  //   0.0625
  //   CAN ONLY DIVIDE BY BINARY NUMBERS
  //   answer is x/y
  //   0.25
endmodule

module Double_Dabble (
  input  in_1,
  input  in_2,
  input  in_3,
  input  in_4,
  output out_5,
  output out_6,
  output out_7,
  output out_8
);

  wire _0_out, _1_out, _2_out, _3_out, _4_out, _5_out, _6_out, _7_out, _8_out, _9_out, not_1_out, not_2_out,
       not_3_out, not_4_out, not_5_out, not_6_out, not_7_out, not_8_out, not_9_out, not_10_out, not_11_out,
       not_12_out, not_13_out, not_14_out, not_15_out, not_16_out, not_17_out, not_18_out, not_19_out,
       not_20_out, not_21_out, not_22_out, not_23_out, not_25_out, not_26_out, or_1_out, or_2_out;

  not not_1 (not_1_out, in_4);
  not not_2 (not_2_out, in_2);
  not not_3 (not_3_out, in_3);
  and _0 (_0_out, not_1_out, not_3_out, not_2_out, not_5_out);
  not not_4 (not_4_out, in_3);
  not not_5 (not_5_out, in_1);
  not not_6 (not_6_out, in_4);
  not not_7 (not_7_out, in_2);
  not not_8 (not_8_out, in_4);
  not not_9 (not_9_out, in_3);
  and _1 (_1_out, not_8_out, not_9_out, not_7_out, in_1);
  not not_10 (not_10_out, in_4);
  not not_11 (not_11_out, in_1);
  not not_12 (not_12_out, in_3);
  and _2 (_2_out, not_6_out, not_4_out, in_2, not_11_out);
  and _3 (_3_out, not_10_out, not_12_out, in_2, in_1);
  or or_1 (or_1_out, _0_out, _1_out, _2_out, _3_out, _4_out);
  not not_13 (not_13_out, in_2);
  not not_14 (not_14_out, in_4);
  not not_15 (not_15_out, in_1);
  and _4 (_4_out, not_14_out, in_3, not_13_out, not_15_out);
  not not_16 (not_16_out, in_2);
  not not_17 (not_17_out, in_4);
  and _5 (_5_out, not_17_out, in_3, not_16_out, in_1);
  not not_18 (not_18_out, in_1);
  not not_19 (not_19_out, in_4);
  not not_20 (not_20_out, in_4);
  and _6 (_6_out, not_19_out, in_3, in_2, not_18_out);
  or or_2 (or_2_out, _5_out, _6_out, _7_out, _8_out, _9_out);
  not not_21 (not_21_out, in_2);
  not not_22 (not_22_out, in_3);
  not not_23 (not_23_out, in_1);
  and _8 (_8_out, in_4, not_22_out, not_21_out, not_23_out);
  and _7 (_7_out, not_20_out, in_3, in_2, in_1);
  not not_24 (or_1_out, or_2_out);
  Add_3 add_3_1 (
    .in_1(or_1_out), .in_2(in_4), .in_3(in_3), .in_4(in_2), .in_5(in_1), .out_6(out_8), .out_7(out_7),
    .out_8(out_6), .out_9(out_5));
  not not_25 (not_25_out, in_3);
  not not_26 (not_26_out, in_2);
  and _9 (_9_out, in_4, not_25_out, not_26_out, in_1);
endmodule

module Add_3 (
  input  in_1,
  input  in_2,
  input  in_3,
  input  in_4,
  input  in_5,
  output out_6,
  output out_7,
  output out_8,
  output out_9
);

  wire and_1_out, and_2_out, and_3_out, and_5_out, and_6_out, and_7_out, not_1_out, not_2_out, or_1_out,
       xor_4_out;

  xor xor_1 (out_6, in_2, and_5_out);
  xor xor_2 (out_7, in_3, or_1_out);
  xor xor_3 (out_8, and_6_out, xor_4_out);
  and and_1 (and_1_out, and_6_out, xor_4_out);
  xor xor_4 (xor_4_out, in_4, and_7_out);
  and and_2 (and_2_out, in_4, and_7_out);
  xor xor_5 (out_9, in_5, and_3_out);
  and and_3 (and_3_out, not_1_out, 1'b1);
  not not_1 (not_1_out, in_1);
  // AND_Gate and_4 has open pins: in2=in_2, in3=and_5_out, out=open
  and and_5 (and_5_out, in_3, or_1_out);
  or or_1 (or_1_out, and_1_out, and_2_out);
  and and_6 (and_6_out, in_5, and_3_out);
  and and_7 (and_7_out, not_2_out, 1'b1);
  not not_2 (not_2_out, in_1);
endmodule

module Binary_BCD_Decoder (
  input  in_1,
  input  in_2,
  input  in_3,
  input  in_4,
  input  in_5,
  input  in_6,
  input  in_7,
  input  in_8,
  output out_9,
  output out_10,
  output out_11,
  output out_12,
  output out_13,
  output out_14,
  output out_15,
  output out_16,
  output out_17,
  output out_18,
  output out_19
);

  wire double_dabble_1_out_5, double_dabble_1_out_6, double_dabble_1_out_7, double_dabble_1_out_8,
       double_dabble_2_out_5, double_dabble_2_out_6, double_dabble_2_out_7, double_dabble_2_out_8,
       double_dabble_3_out_5, double_dabble_3_out_6, double_dabble_3_out_7, double_dabble_3_out_8,
       double_dabble_4_out_5, double_dabble_4_out_6, double_dabble_4_out_7, double_dabble_4_out_8,
       double_dabble_5_out_5, double_dabble_5_out_6, double_dabble_5_out_7, double_dabble_6_out_5,
       double_dabble_6_out_6, double_dabble_6_out_7, double_dabble_8_out_5, double_dabble_8_out_6,
       double_dabble_8_out_7, double_dabble_8_out_8, double_dabble_9_out_5, double_dabble_9_out_6,
       double_dabble_9_out_7, double_dabble_9_out_8, not_1_out, not_2_out, not_3_out;

  not not_1 (not_1_out, 1'b1);
  not not_2 (not_2_out, 1'b1);
  not not_3 (not_3_out, 1'b1);
  Double_Dabble double_dabble_1 (
    .in_1(in_1), .in_2(not_2_out), .in_3(not_3_out), .in_4(not_1_out), .out_5(double_dabble_1_out_5),
    .out_6(double_dabble_1_out_6), .out_7(double_dabble_1_out_7), .out_8(double_dabble_1_out_8));
  Double_Dabble double_dabble_2 (
    .in_1(in_2), .in_2(double_dabble_1_out_5), .in_3(double_dabble_1_out_6), .in_4(double_dabble_1_out_7),
    .out_5(double_dabble_2_out_5), .out_6(double_dabble_2_out_6), .out_7(double_dabble_2_out_7),
    .out_8(double_dabble_2_out_8));
  Double_Dabble double_dabble_3 (
    .in_1(in_3), .in_2(double_dabble_2_out_5), .in_3(double_dabble_2_out_6), .in_4(double_dabble_2_out_7),
    .out_5(double_dabble_3_out_5), .out_6(double_dabble_3_out_6), .out_7(double_dabble_3_out_7),
    .out_8(double_dabble_3_out_8));
  Double_Dabble double_dabble_4 (
    .in_1(in_4), .in_2(double_dabble_3_out_5), .in_3(double_dabble_3_out_6), .in_4(double_dabble_3_out_7),
    .out_5(double_dabble_4_out_5), .out_6(double_dabble_4_out_6), .out_7(double_dabble_4_out_7),
    .out_8(double_dabble_4_out_8));
  Double_Dabble double_dabble_5 (
    .in_1(double_dabble_4_out_8), .in_2(double_dabble_3_out_8), .in_3(double_dabble_2_out_8),
    .in_4(double_dabble_1_out_8), .out_5(double_dabble_5_out_5), .out_6(double_dabble_5_out_6),
    .out_7(double_dabble_5_out_7), .out_8(out_9));
  Double_Dabble double_dabble_6 (
    .in_1(double_dabble_8_out_8), .in_2(double_dabble_5_out_5), .in_3(double_dabble_5_out_6),
    .in_4(double_dabble_5_out_7), .out_5(double_dabble_6_out_5), .out_6(double_dabble_6_out_6),
    .out_7(double_dabble_6_out_7), .out_8(out_10));
  Double_Dabble double_dabble_7 (
    .in_1(double_dabble_9_out_8), .in_2(double_dabble_6_out_5), .in_3(double_dabble_6_out_6),
    .in_4(double_dabble_6_out_7), .out_5(out_14), .out_6(out_13), .out_7(out_12), .out_8(out_11));
  Double_Dabble double_dabble_8 (
    .in_1(in_5), .in_2(double_dabble_4_out_5), .in_3(double_dabble_4_out_6), .in_4(double_dabble_4_out_7),
    .out_5(double_dabble_8_out_5), .out_6(double_dabble_8_out_6), .out_7(double_dabble_8_out_7),
    .out_8(double_dabble_8_out_8));
  Double_Dabble double_dabble_9 (
    .in_1(in_6), .in_2(double_dabble_8_out_5), .in_3(double_dabble_8_out_6), .in_4(double_dabble_8_out_7),
    .out_5(double_dabble_9_out_5), .out_6(double_dabble_9_out_6), .out_7(double_dabble_9_out_7),
    .out_8(double_dabble_9_out_8));
  Double_Dabble double_dabble_10 (
    .in_1(in_7), .in_2(double_dabble_9_out_5), .in_3(double_dabble_9_out_6), .in_4(double_dabble_9_out_7),
    .out_5(out_18), .out_6(out_17), .out_7(out_16), .out_8(out_15));

  assign out_19 = in_8;
endmodule

module Binary_BCD_16bit (
  input  in_1,
  input  in_2,
  input  in_3,
  input  in_4,
  input  in_5,
  input  in_6,
  input  in_7,
  input  in_8,
  input  in_9,
  input  in_10,
  input  in_11,
  input  in_12,
  input  in_13,
  input  in_14,
  input  in_15,
  input  in_16,
  output out_17,
  output out_18,
  output out_19,
  output out_20,
  output out_21,
  output out_22,
  output out_23,
  output out_24,
  output out_25,
  output out_26,
  output out_27,
  output out_28,
  output out_29,
  output out_30,
  output out_31,
  output out_32,
  output out_33,
  output out_34,
  output out_35,
  output out_36
);

  wire double_dabble_1_out_5, double_dabble_1_out_6, double_dabble_1_out_7, double_dabble_1_out_8,
       double_dabble_2_out_5, double_dabble_2_out_6, double_dabble_2_out_7, double_dabble_2_out_8,
       double_dabble_3_out_5, double_dabble_3_out_6, double_dabble_3_out_7, double_dabble_3_out_8,
       double_dabble_4_out_5, double_dabble_4_out_6, double_dabble_4_out_7, double_dabble_4_out_8,
       double_dabble_5_out_5, double_dabble_5_out_6, double_dabble_5_out_7, double_dabble_5_out_8,
       double_dabble_6_out_5, double_dabble_6_out_6, double_dabble_6_out_7, double_dabble_6_out_8,
       double_dabble_7_out_5, double_dabble_7_out_6, double_dabble_7_out_7, double_dabble_7_out_8,
       double_dabble_8_out_5, double_dabble_8_out_6, double_dabble_8_out_7, double_dabble_8_out_8,
       double_dabble_9_out_5, double_dabble_9_out_6, double_dabble_9_out_7, double_dabble_9_out_8,
       double_dabble_10_out_5, double_dabble_10_out_6, double_dabble_10_out_7, double_dabble_10_out_8,
       double_dabble_11_out_5, double_dabble_11_out_6, double_dabble_11_out_7, double_dabble_11_out_8,
       double_dabble_12_out_5, double_dabble_12_out_6, double_dabble_12_out_7, double_dabble_12_out_8,
       double_dabble_13_out_5, double_dabble_13_out_6, double_dabble_13_out_7, double_dabble_13_out_8,
       double_dabble_14_out_5, double_dabble_14_out_6, double_dabble_14_out_7, double_dabble_14_out_8,
       double_dabble_15_out_5, double_dabble_15_out_6, double_dabble_15_out_7, double_dabble_15_out_8,
       double_dabble_16_out_5, double_dabble_16_out_6, double_dabble_16_out_7, double_dabble_16_out_8,
       double_dabble_17_out_5, double_dabble_17_out_6, double_dabble_17_out_7, double_dabble_17_out_8,
       double_dabble_18_out_5, double_dabble_18_out_6, double_dabble_18_out_7, double_dabble_18_out_8,
       double_dabble_19_out_5, double_dabble_19_out_6, double_dabble_19_out_7, double_dabble_20_out_5,
       double_dabble_20_out_6, double_dabble_20_out_7, double_dabble_20_out_8, double_dabble_21_out_5,
       double_dabble_21_out_6, double_dabble_21_out_7, double_dabble_22_out_5, double_dabble_22_out_6,
       double_dabble_22_out_7, double_dabble_22_out_8, double_dabble_25_out_5, double_dabble_25_out_6,
       double_dabble_25_out_7, double_dabble_25_out_8, double_dabble_26_out_5, double_dabble_26_out_6,
       double_dabble_26_out_7, double_dabble_26_out_8, double_dabble_27_out_5, double_dabble_27_out_6,
       double_dabble_27_out_7, double_dabble_27_out_8, double_dabble_28_out_5, double_dabble_28_out_6,
       double_dabble_28_out_7, double_dabble_28_out_8, double_dabble_29_out_5, double_dabble_29_out_6,
       double_dabble_29_out_7, double_dabble_29_out_8, double_dabble_30_out_5, double_dabble_30_out_6,
       double_dabble_30_out_7, double_dabble_30_out_8, double_dabble_31_out_5, double_dabble_31_out_6,
       double_dabble_31_out_7, double_dabble_31_out_8, double_dabble_32_out_5, double_dabble_32_out_6,
       double_dabble_32_out_7, double_dabble_32_out_8, double_dabble_33_out_5, double_dabble_33_out_6,
       double_dabble_33_out_7, double_dabble_33_out_8, double_dabble_34_out_5, double_dabble_34_out_6,
       double_dabble_34_out_7, double_dabble_34_out_8, not_2_out, not_3_out, not_4_out;

  not not_1 (out_17, 1'b1);
  not not_2 (not_2_out, 1'b1);
  not not_3 (not_3_out, 1'b1);
  not not_4 (not_4_out, 1'b1);
  Double_Dabble double_dabble_1 (
    .in_1(in_1), .in_2(not_4_out), .in_3(not_2_out), .in_4(not_3_out), .out_5(double_dabble_1_out_5),
    .out_6(double_dabble_1_out_6), .out_7(double_dabble_1_out_7), .out_8(double_dabble_1_out_8));
  Double_Dabble double_dabble_2 (
    .in_1(in_2), .in_2(double_dabble_1_out_5), .in_3(double_dabble_1_out_6), .in_4(double_dabble_1_out_7),
    .out_5(double_dabble_2_out_5), .out_6(double_dabble_2_out_6), .out_7(double_dabble_2_out_7),
    .out_8(double_dabble_2_out_8));
  Double_Dabble double_dabble_3 (
    .in_1(in_3), .in_2(double_dabble_2_out_5), .in_3(double_dabble_2_out_6), .in_4(double_dabble_2_out_7),
    .out_5(double_dabble_3_out_5), .out_6(double_dabble_3_out_6), .out_7(double_dabble_3_out_7),
    .out_8(double_dabble_3_out_8));
  Double_Dabble double_dabble_4 (
    .in_1(in_4), .in_2(double_dabble_3_out_5), .in_3(double_dabble_3_out_6), .in_4(double_dabble_3_out_7),
    .out_5(double_dabble_4_out_5), .out_6(double_dabble_4_out_6), .out_7(double_dabble_4_out_7),
    .out_8(double_dabble_4_out_8));
  Double_Dabble double_dabble_5 (
    .in_1(double_dabble_4_out_8), .in_2(double_dabble_3_out_8), .in_3(double_dabble_2_out_8),
    .in_4(double_dabble_1_out_8), .out_5(double_dabble_5_out_5), .out_6(double_dabble_5_out_6),
    .out_7(double_dabble_5_out_7), .out_8(double_dabble_5_out_8));
  Double_Dabble double_dabble_6 (
    .in_1(in_5), .in_2(double_dabble_4_out_5), .in_3(double_dabble_4_out_6), .in_4(double_dabble_4_out_7),
    .out_5(double_dabble_6_out_5), .out_6(double_dabble_6_out_6), .out_7(double_dabble_6_out_7),
    .out_8(double_dabble_6_out_8));
  Double_Dabble double_dabble_7 (
    .in_1(in_6), .in_2(double_dabble_6_out_5), .in_3(double_dabble_6_out_6), .in_4(double_dabble_6_out_7),
    .out_5(double_dabble_7_out_5), .out_6(double_dabble_7_out_6), .out_7(double_dabble_7_out_7),
    .out_8(double_dabble_7_out_8));
  Double_Dabble double_dabble_8 (
    .in_1(double_dabble_6_out_8), .in_2(double_dabble_5_out_5), .in_3(double_dabble_5_out_6),
    .in_4(double_dabble_5_out_7), .out_5(double_dabble_8_out_5), .out_6(double_dabble_8_out_6),
    .out_7(double_dabble_8_out_7), .out_8(double_dabble_8_out_8));
  Double_Dabble double_dabble_9 (
    .in_1(double_dabble_7_out_8), .in_2(double_dabble_8_out_5), .in_3(double_dabble_8_out_6),
    .in_4(double_dabble_8_out_7), .out_5(double_dabble_9_out_5), .out_6(double_dabble_9_out_6),
    .out_7(double_dabble_9_out_7), .out_8(double_dabble_9_out_8));
  Double_Dabble double_dabble_10 (
    .in_1(in_7), .in_2(double_dabble_7_out_5), .in_3(double_dabble_7_out_6), .in_4(double_dabble_7_out_7),
    .out_5(double_dabble_10_out_5), .out_6(double_dabble_10_out_6), .out_7(double_dabble_10_out_7),
    .out_8(double_dabble_10_out_8));
  Double_Dabble double_dabble_11 (
    .in_1(double_dabble_10_out_8), .in_2(double_dabble_9_out_5), .in_3(double_dabble_9_out_6),
    .in_4(double_dabble_9_out_7), .out_5(double_dabble_11_out_5), .out_6(double_dabble_11_out_6),
    .out_7(double_dabble_11_out_7), .out_8(double_dabble_11_out_8));
  Double_Dabble double_dabble_12 (
    .in_1(double_dabble_25_out_8), .in_2(double_dabble_11_out_5), .in_3(double_dabble_11_out_6),
    .in_4(double_dabble_11_out_7), .out_5(double_dabble_12_out_5), .out_6(double_dabble_12_out_6),
    .out_7(double_dabble_12_out_7), .out_8(double_dabble_12_out_8));
  Double_Dabble double_dabble_13 (
    .in_1(double_dabble_11_out_8), .in_2(double_dabble_9_out_8), .in_3(double_dabble_8_out_8),
    .in_4(double_dabble_5_out_8), .out_5(double_dabble_13_out_5), .out_6(double_dabble_13_out_6),
    .out_7(double_dabble_13_out_7), .out_8(double_dabble_13_out_8));
  Double_Dabble double_dabble_14 (
    .in_1(double_dabble_26_out_8), .in_2(double_dabble_12_out_5), .in_3(double_dabble_12_out_6),
    .in_4(double_dabble_12_out_7), .out_5(double_dabble_14_out_5), .out_6(double_dabble_14_out_6),
    .out_7(double_dabble_14_out_7), .out_8(double_dabble_14_out_8));
  Double_Dabble double_dabble_15 (
    .in_1(double_dabble_12_out_8), .in_2(double_dabble_13_out_5), .in_3(double_dabble_13_out_6),
    .in_4(double_dabble_13_out_7), .out_5(double_dabble_15_out_5), .out_6(double_dabble_15_out_6),
    .out_7(double_dabble_15_out_7), .out_8(double_dabble_15_out_8));
  Double_Dabble double_dabble_16 (
    .in_1(double_dabble_14_out_8), .in_2(double_dabble_15_out_5), .in_3(double_dabble_15_out_6),
    .in_4(double_dabble_15_out_7), .out_5(double_dabble_16_out_5), .out_6(double_dabble_16_out_6),
    .out_7(double_dabble_16_out_7), .out_8(double_dabble_16_out_8));
  Double_Dabble double_dabble_17 (
    .in_1(double_dabble_27_out_8), .in_2(double_dabble_14_out_5), .in_3(double_dabble_14_out_6),
    .in_4(double_dabble_14_out_7), .out_5(double_dabble_17_out_5), .out_6(double_dabble_17_out_6),
    .out_7(double_dabble_17_out_7), .out_8(double_dabble_17_out_8));
  Double_Dabble double_dabble_18 (
    .in_1(double_dabble_17_out_8), .in_2(double_dabble_16_out_5), .in_3(double_dabble_16_out_6),
    .in_4(double_dabble_16_out_7), .out_5(double_dabble_18_out_5), .out_6(double_dabble_18_out_6),
    .out_7(double_dabble_18_out_7), .out_8(double_dabble_18_out_8));
  Double_Dabble double_dabble_19 (
    .in_1(double_dabble_18_out_8), .in_2(double_dabble_16_out_8), .in_3(double_dabble_15_out_8),
    .in_4(double_dabble_13_out_8), .out_5(double_dabble_19_out_5), .out_6(double_dabble_19_out_6),
    .out_7(double_dabble_19_out_7), .out_8(out_18));
  Double_Dabble double_dabble_20 (
    .in_1(double_dabble_29_out_8), .in_2(double_dabble_18_out_5), .in_3(double_dabble_18_out_6),
    .in_4(double_dabble_18_out_7), .out_5(double_dabble_20_out_5), .out_6(double_dabble_20_out_6),
    .out_7(double_dabble_20_out_7), .out_8(double_dabble_20_out_8));
  Double_Dabble double_dabble_21 (
    .in_1(double_dabble_20_out_8), .in_2(double_dabble_19_out_5), .in_3(double_dabble_19_out_6),
    .in_4(double_dabble_19_out_7), .out_5(double_dabble_21_out_5), .out_6(double_dabble_21_out_6),
    .out_7(double_dabble_21_out_7), .out_8(out_19));
  Double_Dabble double_dabble_22 (
    .in_1(double_dabble_32_out_8), .in_2(double_dabble_20_out_5), .in_3(double_dabble_20_out_6),
    .in_4(double_dabble_20_out_7), .out_5(double_dabble_22_out_5), .out_6(double_dabble_22_out_6),
    .out_7(double_dabble_22_out_7), .out_8(double_dabble_22_out_8));
  Double_Dabble double_dabble_23 (
    .in_1(double_dabble_34_out_8), .in_2(double_dabble_22_out_5), .in_3(double_dabble_22_out_6),
    .in_4(double_dabble_22_out_7), .out_5(out_27), .out_6(out_26), .out_7(out_25), .out_8(out_24));
  Double_Dabble double_dabble_24 (
    .in_1(double_dabble_22_out_8), .in_2(double_dabble_21_out_5), .in_3(double_dabble_21_out_6),
    .in_4(double_dabble_21_out_7), .out_5(out_23), .out_6(out_22), .out_7(out_21), .out_8(out_20));
  Double_Dabble double_dabble_25 (
    .in_1(in_8), .in_2(double_dabble_10_out_5), .in_3(double_dabble_10_out_6), .in_4(double_dabble_10_out_7),
    .out_5(double_dabble_25_out_5), .out_6(double_dabble_25_out_6), .out_7(double_dabble_25_out_7),
    .out_8(double_dabble_25_out_8));
  Double_Dabble double_dabble_26 (
    .in_1(in_9), .in_2(double_dabble_25_out_5), .in_3(double_dabble_25_out_6), .in_4(double_dabble_25_out_7),
    .out_5(double_dabble_26_out_5), .out_6(double_dabble_26_out_6), .out_7(double_dabble_26_out_7),
    .out_8(double_dabble_26_out_8));
  Double_Dabble double_dabble_27 (
    .in_1(in_10), .in_2(double_dabble_26_out_5), .in_3(double_dabble_26_out_6),
    .in_4(double_dabble_26_out_7), .out_5(double_dabble_27_out_5), .out_6(double_dabble_27_out_6),
    .out_7(double_dabble_27_out_7), .out_8(double_dabble_27_out_8));
  Double_Dabble double_dabble_28 (
    .in_1(in_11), .in_2(double_dabble_27_out_5), .in_3(double_dabble_27_out_6),
    .in_4(double_dabble_27_out_7), .out_5(double_dabble_28_out_5), .out_6(double_dabble_28_out_6),
    .out_7(double_dabble_28_out_7), .out_8(double_dabble_28_out_8));
  Double_Dabble double_dabble_29 (
    .in_1(double_dabble_28_out_8), .in_2(double_dabble_17_out_5), .in_3(double_dabble_17_out_6),
    .in_4(double_dabble_17_out_7), .out_5(double_dabble_29_out_5), .out_6(double_dabble_29_out_6),
    .out_7(double_dabble_29_out_7), .out_8(double_dabble_29_out_8));
  Double_Dabble double_dabble_30 (
    .in_1(in_12), .in_2(double_dabble_28_out_5), .in_3(double_dabble_28_out_6),
    .in_4(double_dabble_28_out_7), .out_5(double_dabble_30_out_5), .out_6(double_dabble_30_out_6),
    .out_7(double_dabble_30_out_7), .out_8(double_dabble_30_out_8));
  Double_Dabble double_dabble_31 (
    .in_1(in_13), .in_2(double_dabble_30_out_5), .in_3(double_dabble_30_out_6),
    .in_4(double_dabble_30_out_7), .out_5(double_dabble_31_out_5), .out_6(double_dabble_31_out_6),
    .out_7(double_dabble_31_out_7), .out_8(double_dabble_31_out_8));
  Double_Dabble double_dabble_32 (
    .in_1(double_dabble_30_out_8), .in_2(double_dabble_29_out_5), .in_3(double_dabble_29_out_6),
    .in_4(double_dabble_29_out_7), .out_5(double_dabble_32_out_5), .out_6(double_dabble_32_out_6),
    .out_7(double_dabble_32_out_7), .out_8(double_dabble_32_out_8));
  Double_Dabble double_dabble_33 (
    .in_1(in_14), .in_2(double_dabble_31_out_5), .in_3(double_dabble_31_out_6),
    .in_4(double_dabble_31_out_7), .out_5(double_dabble_33_out_5), .out_6(double_dabble_33_out_6),
    .out_7(double_dabble_33_out_7), .out_8(double_dabble_33_out_8));
  Double_Dabble double_dabble_34 (
    .in_1(double_dabble_31_out_8), .in_2(double_dabble_32_out_5), .in_3(double_dabble_32_out_6),
    .in_4(double_dabble_32_out_7), .out_5(double_dabble_34_out_5), .out_6(double_dabble_34_out_6),
    .out_7(double_dabble_34_out_7), .out_8(double_dabble_34_out_8));
  Double_Dabble double_dabble_35 (
    .in_1(in_15), .in_2(double_dabble_33_out_5), .in_3(double_dabble_33_out_6),
    .in_4(double_dabble_33_out_7), .out_5(out_35), .out_6(out_34), .out_7(out_33), .out_8(out_32));
  Double_Dabble double_dabble_36 (
    .in_1(double_dabble_33_out_8), .in_2(double_dabble_34_out_5), .in_3(double_dabble_34_out_6),
    .in_4(double_dabble_34_out_7), .out_5(out_31), .out_6(out_30), .out_7(out_29), .out_8(out_28));

  assign out_36 = in_16;
endmodule

module Binary_BCD_9bit (
  input  in_1,
  input  in_2,
  input  in_3,
  input  in_4,
  input  in_5,
  input  in_6,
  input  in_7,
  input  in_8,
  input  in_9,
  output out_10,
  output out_11,
  output out_12,
  output out_13,
  output out_14,
  output out_15,
  output out_16,
  output out_17,
  output out_18,
  output out_19,
  output out_20,
  output out_21
);

  wire double_dabble_1_out_5, double_dabble_1_out_6, double_dabble_1_out_7, double_dabble_1_out_8,
       double_dabble_2_out_5, double_dabble_2_out_6, double_dabble_2_out_7, double_dabble_2_out_8,
       double_dabble_3_out_5, double_dabble_3_out_6, double_dabble_3_out_7, double_dabble_3_out_8,
       double_dabble_4_out_5, double_dabble_4_out_6, double_dabble_4_out_7, double_dabble_4_out_8,
       double_dabble_5_out_5, double_dabble_5_out_6, double_dabble_5_out_7, double_dabble_6_out_5,
       double_dabble_6_out_6, double_dabble_6_out_7, double_dabble_7_out_5, double_dabble_7_out_6,
       double_dabble_7_out_7, double_dabble_9_out_5, double_dabble_9_out_6, double_dabble_9_out_7,
       double_dabble_9_out_8, double_dabble_10_out_5, double_dabble_10_out_6, double_dabble_10_out_7,
       double_dabble_10_out_8, double_dabble_11_out_5, double_dabble_11_out_6, double_dabble_11_out_7,
       double_dabble_11_out_8, not_1_out, not_2_out, not_3_out;

  not not_1 (not_1_out, 1'b1);
  not not_2 (not_2_out, 1'b1);
  not not_3 (not_3_out, 1'b1);
  Double_Dabble double_dabble_1 (
    .in_1(in_1), .in_2(not_1_out), .in_3(not_3_out), .in_4(not_2_out), .out_5(double_dabble_1_out_5),
    .out_6(double_dabble_1_out_6), .out_7(double_dabble_1_out_7), .out_8(double_dabble_1_out_8));
  Double_Dabble double_dabble_2 (
    .in_1(in_2), .in_2(double_dabble_1_out_5), .in_3(double_dabble_1_out_6), .in_4(double_dabble_1_out_7),
    .out_5(double_dabble_2_out_5), .out_6(double_dabble_2_out_6), .out_7(double_dabble_2_out_7),
    .out_8(double_dabble_2_out_8));
  Double_Dabble double_dabble_3 (
    .in_1(in_3), .in_2(double_dabble_2_out_5), .in_3(double_dabble_2_out_6), .in_4(double_dabble_2_out_7),
    .out_5(double_dabble_3_out_5), .out_6(double_dabble_3_out_6), .out_7(double_dabble_3_out_7),
    .out_8(double_dabble_3_out_8));
  Double_Dabble double_dabble_4 (
    .in_1(in_4), .in_2(double_dabble_3_out_5), .in_3(double_dabble_3_out_6), .in_4(double_dabble_3_out_7),
    .out_5(double_dabble_4_out_5), .out_6(double_dabble_4_out_6), .out_7(double_dabble_4_out_7),
    .out_8(double_dabble_4_out_8));
  Double_Dabble double_dabble_5 (
    .in_1(double_dabble_4_out_8), .in_2(double_dabble_3_out_8), .in_3(double_dabble_2_out_8),
    .in_4(double_dabble_1_out_8), .out_5(double_dabble_5_out_5), .out_6(double_dabble_5_out_6),
    .out_7(double_dabble_5_out_7), .out_8(out_10));
  Double_Dabble double_dabble_6 (
    .in_1(double_dabble_9_out_8), .in_2(double_dabble_5_out_5), .in_3(double_dabble_5_out_6),
    .in_4(double_dabble_5_out_7), .out_5(double_dabble_6_out_5), .out_6(double_dabble_6_out_6),
    .out_7(double_dabble_6_out_7), .out_8(out_11));
  Double_Dabble double_dabble_7 (
    .in_1(double_dabble_10_out_8), .in_2(double_dabble_6_out_5), .in_3(double_dabble_6_out_6),
    .in_4(double_dabble_6_out_7), .out_5(double_dabble_7_out_5), .out_6(double_dabble_7_out_6),
    .out_7(double_dabble_7_out_7), .out_8(out_12));
  Double_Dabble double_dabble_8 (
    .in_1(double_dabble_11_out_8), .in_2(double_dabble_7_out_5), .in_3(double_dabble_7_out_6),
    .in_4(double_dabble_7_out_7), .out_5(out_16), .out_6(out_15), .out_7(out_14), .out_8(out_13));
  Double_Dabble double_dabble_9 (
    .in_1(in_5), .in_2(double_dabble_4_out_5), .in_3(double_dabble_4_out_6), .in_4(double_dabble_4_out_7),
    .out_5(double_dabble_9_out_5), .out_6(double_dabble_9_out_6), .out_7(double_dabble_9_out_7),
    .out_8(double_dabble_9_out_8));
  Double_Dabble double_dabble_10 (
    .in_1(in_6), .in_2(double_dabble_9_out_5), .in_3(double_dabble_9_out_6), .in_4(double_dabble_9_out_7),
    .out_5(double_dabble_10_out_5), .out_6(double_dabble_10_out_6), .out_7(double_dabble_10_out_7),
    .out_8(double_dabble_10_out_8));
  Double_Dabble double_dabble_11 (
    .in_1(in_7), .in_2(double_dabble_10_out_5), .in_3(double_dabble_10_out_6), .in_4(double_dabble_10_out_7),
    .out_5(double_dabble_11_out_5), .out_6(double_dabble_11_out_6), .out_7(double_dabble_11_out_7),
    .out_8(double_dabble_11_out_8));
  Double_Dabble double_dabble_12 (
    .in_1(in_8), .in_2(double_dabble_11_out_5), .in_3(double_dabble_11_out_6), .in_4(double_dabble_11_out_7),
    .out_5(out_20), .out_6(out_19), .out_7(out_18), .out_8(out_17));

  assign out_21 = in_9;
endmodule

module BCD_to_7_Segment (
  input  in_1,
  input  in_2,
  input  in_3,
  input  in_4,
  output out_5,
  output out_6,
  output out_7,
  output out_8,
  output out_9,
  output out_10,
  output out_11
);

  wire and_1_out, and_2_out, and_3_out, and_4_out, and_5_out, and_6_out, and_7_out, and_8_out, and_9_out,
       and_10_out, not_1_out, not_2_out, not_3_out, not_4_out, not_5_out, not_6_out, not_7_out, not_8_out,
       not_9_out, not_10_out, not_11_out, not_12_out, not_13_out, not_14_out, not_15_out, not_16_out,
       not_17_out, not_18_out, not_19_out, not_20_out, not_21_out, not_22_out, not_23_out, not_24_out,
       not_25_out;

  not not_1 (not_1_out, in_1);
  not not_2 (not_2_out, in_2);
  not not_3 (not_3_out, in_3);
  not not_4 (not_4_out, in_4);
  not not_5 (not_5_out, in_2);
  not not_6 (not_6_out, in_3);
  not not_7 (not_7_out, in_4);
  not not_8 (not_8_out, in_1);
  not not_9 (not_9_out, in_3);
  not not_10 (not_10_out, in_4);
  not not_11 (not_11_out, in_3);
  not not_12 (not_12_out, in_4);
  not not_13 (not_13_out, in_1);
  not not_14 (not_14_out, in_2);
  not not_15 (not_15_out, in_4);
  not not_16 (not_16_out, in_2);
  not not_17 (not_17_out, in_4);
  not not_18 (not_18_out, in_1);
  not not_19 (not_19_out, in_4);
  not not_20 (not_20_out, in_4);
  not not_21 (not_21_out, in_1);
  not not_22 (not_22_out, in_2);
  not not_23 (not_23_out, in_3);
  not not_24 (not_24_out, in_2);
  not not_25 (not_25_out, in_3);
  and and_1 (and_1_out, not_1_out, not_2_out, not_3_out, not_4_out);
  and and_2 (and_2_out, in_1, not_5_out, not_6_out, not_7_out);
  and and_3 (and_3_out, not_8_out, in_2, not_9_out, not_10_out);
  and and_4 (and_4_out, in_1, in_2, not_11_out, not_12_out);
  and and_5 (and_5_out, not_13_out, not_14_out, in_3, not_15_out);
  and and_6 (and_6_out, in_1, not_16_out, in_3, not_17_out);
  and and_7 (and_7_out, not_18_out, in_2, in_3, not_19_out);
  and and_8 (and_8_out, in_1, in_2, in_3, not_20_out);
  and and_9 (and_9_out, not_21_out, not_22_out, not_23_out, in_4);
  and and_10 (and_10_out, in_1, not_24_out, not_25_out, in_4);
  or or_1 (out_5, and_2_out, and_3_out, and_4_out, and_5_out, and_8_out, and_9_out, and_10_out, and_1_out);
  or or_2 (out_6, and_2_out, and_1_out, and_8_out, and_9_out, and_10_out, and_7_out, and_6_out, and_5_out, and_4_out);
  or or_3 (out_7, and_3_out, and_4_out, and_6_out, and_7_out, and_8_out, and_9_out, and_10_out, and_1_out);
  or or_4 (out_8, and_5_out, and_6_out, and_7_out, and_9_out, and_10_out, and_1_out);
  or or_5 (out_9, and_3_out, and_7_out, and_9_out, and_1_out);
  or or_6 (out_10, and_3_out, and_4_out, and_6_out, and_1_out, and_7_out, and_9_out, and_10_out);
  or or_7 (out_11, and_3_out, and_4_out, and_5_out, and_10_out, and_6_out, and_9_out, and_7_out);
endmodule

module Random_number_generator (
  output out_1,
  output out_2,
  output out_3,
  output out_4,
  output out_5,
  output out_6,
  output out_7,
  output out_8,
  output out_9,
  output out_10,
  output out_11,
  output out_12,
  output out_13,
  output out_14,
  output out_15,
  output out_16,
  output out_17,
  output out_18,
  output out_19,
  output out_20
);

  wire clock_1_out, clock_2_out, clock_3_out, clock_4_out, clock_5_out, clock_6_out, clock_7_out,
       clock_8_out, clock_9_out, clock_10_out, clock_11_out, clock_12_out, clock_13_out, clock_14_out,
       clock_15_out, clock_16_out;

  Clock #(.highDuration(59), .lowDuration(59)) clock_1 (.out(clock_1_out));
  Clock #(.highDuration(2), .lowDuration(2)) clock_2 (.out(clock_2_out));
  Clock #(.highDuration(5), .lowDuration(5)) clock_3 (.out(clock_3_out));
  Clock #(.highDuration(11), .lowDuration(11)) clock_4 (.out(clock_4_out));
  Clock #(.highDuration(7), .lowDuration(7)) clock_5 (.out(clock_5_out));
  Clock #(.highDuration(17), .lowDuration(17)) clock_6 (.out(clock_6_out));
  Clock #(.highDuration(13), .lowDuration(13)) clock_7 (.out(clock_7_out));
  Clock #(.highDuration(19), .lowDuration(19)) clock_8 (.out(clock_8_out));
  Clock #(.highDuration(23), .lowDuration(23)) clock_9 (.out(clock_9_out));
  Clock #(.highDuration(31), .lowDuration(31)) clock_10 (.out(clock_10_out));
  Clock #(.highDuration(29), .lowDuration(29)) clock_11 (.out(clock_11_out));
  Binary_BCD_16bit binary_bcd_16bit_1 (
    .in_1(clock_16_out), .in_2(clock_14_out), .in_3(clock_15_out), .in_4(clock_13_out), .in_5(clock_12_out),
    .in_6(clock_10_out), .in_7(clock_11_out), .in_8(clock_9_out), .in_9(clock_8_out), .in_10(clock_6_out),
    .in_11(clock_7_out), .in_12(clock_4_out), .in_13(clock_5_out), .in_14(clock_3_out), .in_15(clock_2_out),
    .in_16(clock_1_out), .out_17(out_1), .out_18(out_2), .out_19(out_3), .out_20(out_4), .out_21(out_5),
    .out_22(out_6), .out_23(out_7), .out_24(out_8), .out_25(out_9), .out_26(out_10), .out_27(out_11),
    .out_28(out_12), .out_29(out_13), .out_30(out_14), .out_31(out_15), .out_32(out_16), .out_33(out_17),
    .out_34(out_18), .out_35(out_19), .out_36(out_20));
  Clock #(.highDuration(3), .lowDuration(3)) clock_12 (.out(clock_12_out));
  Clock #(.highDuration(41), .lowDuration(41)) clock_13 (.out(clock_13_out));
  Clock #(.highDuration(47), .lowDuration(47)) clock_14 (.out(clock_14_out));
  Clock #(.highDuration(43), .lowDuration(43)) clock_15 (.out(clock_15_out));
  Clock #(.highDuration(53), .lowDuration(53)) clock_16 (.out(clock_16_out));
endmodule

module BCD_output_comparison (
  input  A,
  input  in_2,
  input  in_3,
  input  in_4,
  input  in_5,
  input  B,
  input  in_7,
  input  in_8,
  output YES,
  output SAME,
  output NO
);

  wire and_1_out, and_2_out, and_3_out, and_4_out, and_5_out, and_6_out, and_7_out, and_8_out, and_9_out,
       and_10_out, and_11_out, and_12_out, and_13_out, and_14_out, and_15_out, and_16_out, and_17_out,
       and_18_out, and_19_out, and_20_out, and_22_out, and_23_out, and_24_out, and_25_out, and_26_out,
       and_27_out, and_28_out, and_29_out, and_30_out, and_33_out, and_34_out, and_35_out, and_36_out,
       and_37_out, and_38_out, and_39_out, and_40_out, and_44_out, and_45_out, and_46_out, and_47_out,
       and_48_out, and_49_out, and_50_out, and_55_out, and_56_out, and_57_out, and_58_out, and_59_out,
       and_60_out, and_66_out, and_67_out, and_68_out, and_69_out, and_70_out, and_77_out, and_78_out,
       and_79_out, and_80_out, and_88_out, and_89_out, and_90_out, and_99_out, and_100_out, and_110_out,
       not_1_out, not_2_out, not_3_out, not_4_out, not_5_out, not_6_out, not_7_out, not_8_out, not_9_out,
       not_10_out, not_11_out, not_12_out, not_13_out, not_14_out, not_15_out, not_16_out, not_17_out,
       not_18_out, not_19_out, not_20_out, not_21_out, not_22_out, not_23_out, not_24_out, not_25_out,
       not_26_out, not_27_out, not_28_out, not_29_out, not_30_out, not_31_out, not_32_out, not_33_out,
       not_34_out, not_35_out, not_36_out, not_37_out, not_38_out, not_39_out, not_40_out, not_41_out,
       not_42_out, not_43_out, not_44_out, not_45_out, not_46_out, not_47_out, not_48_out, not_49_out,
       not_50_out, not_51_out, not_52_out, not_53_out, not_54_out, not_55_out, not_56_out, not_57_out,
       not_58_out, not_59_out, not_60_out, not_61_out, not_62_out, not_63_out, not_64_out, not_65_out,
       not_66_out, not_67_out, not_68_out, not_69_out, not_70_out, not_71_out, not_72_out, not_73_out,
       not_74_out, not_75_out, not_76_out, not_77_out, not_78_out, not_79_out, not_80_out, not_81_out,
       not_82_out, not_83_out, not_84_out, not_85_out, not_86_out, not_87_out, not_88_out, not_89_out,
       not_90_out, not_91_out, not_92_out, not_93_out, not_94_out, not_95_out, not_96_out, not_97_out,
       not_98_out, not_99_out, not_100_out, not_101_out, not_102_out, not_103_out, not_104_out, not_105_out,
       not_106_out, not_107_out, not_108_out, not_109_out, not_110_out, not_111_out, not_112_out,
       not_113_out, not_114_out, not_115_out, not_116_out, not_117_out, not_118_out, not_119_out,
       not_120_out, not_121_out, not_122_out, not_123_out, not_124_out, not_125_out, not_126_out,
       not_127_out, not_128_out, not_129_out, not_130_out, not_131_out, not_132_out, not_133_out,
       not_134_out, not_135_out, not_136_out, not_137_out, not_138_out, not_139_out, not_140_out,
       not_141_out, not_142_out, not_143_out, not_144_out, not_145_out, not_146_out, not_147_out,
       not_148_out, not_149_out, not_150_out, not_151_out, not_152_out, not_153_out, not_154_out,
       not_155_out, not_156_out, not_157_out, not_158_out, not_159_out, not_160_out, not_161_out,
       not_162_out, not_163_out, not_164_out, not_165_out, not_166_out, not_167_out, not_168_out,
       not_169_out, not_170_out, not_171_out, not_172_out, not_173_out, not_174_out, not_175_out,
       not_176_out, not_177_out, not_178_out, not_179_out, not_180_out, not_181_out, not_182_out,
       not_183_out, not_184_out, not_185_out, not_186_out, not_187_out, not_188_out, not_189_out,
       not_190_out, not_191_out, not_192_out, not_193_out, not_194_out, not_195_out, not_196_out,
       not_197_out, not_198_out, not_199_out, not_200_out, not_201_out, not_202_out, not_203_out,
       not_204_out, not_205_out, not_206_out, not_207_out, not_208_out, not_209_out, not_210_out,
       not_211_out, not_212_out, not_213_out, not_214_out, not_215_out, not_216_out, not_217_out,
       not_218_out, not_219_out, not_220_out, not_221_out, not_222_out, not_223_out, not_224_out,
       not_225_out, not_226_out, not_227_out, not_228_out, not_229_out, not_230_out, not_231_out,
       not_232_out, not_233_out, not_234_out, not_235_out, not_236_out, not_237_out, not_238_out,
       not_239_out, not_240_out, not_241_out, not_242_out, not_243_out, not_244_out, not_245_out,
       not_246_out, not_247_out, not_248_out, not_249_out, not_250_out, not_251_out, not_252_out,
       not_253_out, not_254_out, not_255_out, not_256_out, not_257_out, not_258_out, not_259_out,
       not_260_out, not_261_out, not_262_out, not_263_out, not_264_out, not_265_out, not_266_out,
       not_267_out, not_268_out, not_269_out, not_270_out, not_271_out, not_272_out, not_273_out,
       not_274_out, not_275_out, not_276_out, not_277_out, or_3_out;

  not not_1 (not_1_out, in_5);
  not not_2 (not_2_out, B);
  not not_3 (not_3_out, in_7);
  not not_4 (not_4_out, in_8);
  not not_5 (not_5_out, B);
  not not_6 (not_6_out, in_7);
  not not_7 (not_7_out, in_8);
  not not_8 (not_8_out, in_5);
  not not_9 (not_9_out, in_7);
  not not_10 (not_10_out, in_8);
  not not_11 (not_11_out, in_7);
  not not_12 (not_12_out, in_8);
  not not_13 (not_13_out, in_5);
  not not_14 (not_14_out, B);
  not not_15 (not_15_out, in_8);
  not not_16 (not_16_out, B);
  not not_17 (not_17_out, in_8);
  not not_18 (not_18_out, in_5);
  not not_19 (not_19_out, in_8);
  not not_20 (not_20_out, in_8);
  not not_21 (not_21_out, in_5);
  not not_22 (not_22_out, B);
  not not_23 (not_23_out, in_7);
  not not_24 (not_24_out, B);
  not not_25 (not_25_out, in_7);
  and and_1 (and_1_out, not_1_out, not_2_out, not_3_out, not_4_out);
  and and_2 (and_2_out, in_5, not_5_out, not_6_out, not_7_out);
  and and_3 (and_3_out, not_8_out, B, not_9_out, not_10_out);
  and and_4 (and_4_out, in_5, B, not_11_out, not_12_out);
  and and_5 (and_5_out, not_13_out, not_14_out, in_7, not_15_out);
  and and_6 (and_6_out, in_5, not_16_out, in_7, not_17_out);
  and and_7 (and_7_out, not_18_out, B, in_7, not_19_out);
  and and_8 (and_8_out, in_5, B, in_7, not_20_out);
  and and_9 (and_9_out, not_21_out, not_22_out, not_23_out, in_8);
  and and_10 (and_10_out, in_5, not_24_out, not_25_out, in_8);
  not not_26 (not_26_out, A);
  not not_27 (not_27_out, in_2);
  and and_11 (and_11_out, not_26_out, not_27_out, and_1_out, not_28_out, not_29_out);
  not not_28 (not_28_out, in_3);
  not not_29 (not_29_out, in_4);
  not not_30 (not_30_out, in_2);
  and and_12 (and_12_out, A, not_30_out, and_1_out, not_31_out, not_32_out);
  not not_31 (not_31_out, in_3);
  not not_32 (not_32_out, in_4);
  not not_33 (not_33_out, A);
  and and_13 (and_13_out, not_33_out, in_2, and_1_out, not_34_out, not_35_out);
  not not_34 (not_34_out, in_3);
  not not_35 (not_35_out, in_4);
  and and_14 (and_14_out, A, in_2, and_1_out, not_36_out, not_37_out);
  not not_36 (not_36_out, in_3);
  not not_37 (not_37_out, in_4);
  not not_38 (not_38_out, A);
  not not_39 (not_39_out, in_2);
  and and_15 (and_15_out, not_38_out, not_39_out, and_1_out, in_3, not_40_out);
  not not_40 (not_40_out, in_4);
  not not_41 (not_41_out, in_2);
  and and_16 (and_16_out, A, not_41_out, and_1_out, in_3, not_42_out);
  not not_42 (not_42_out, in_4);
  not not_43 (not_43_out, A);
  and and_17 (and_17_out, not_43_out, in_2, and_1_out, in_3, not_44_out);
  not not_44 (not_44_out, in_4);
  and and_18 (and_18_out, A, in_2, and_1_out, in_3, not_45_out);
  not not_45 (not_45_out, in_4);
  not not_46 (not_46_out, A);
  not not_47 (not_47_out, in_2);
  and and_19 (and_19_out, not_46_out, not_47_out, and_1_out, not_48_out, in_4);
  not not_48 (not_48_out, in_3);
  not not_49 (not_49_out, in_2);
  and and_20 (and_20_out, A, not_49_out, and_1_out, not_50_out, in_4);
  not not_50 (not_50_out, in_3);
  not not_51 (not_51_out, A);
  not not_52 (not_52_out, in_2);
  // AND_Gate and_21 has open pins: in0=not_51_out, in1=not_52_out, in2=and_2_out, in3=not_53_out, in4=not_54_out, out=open
  not not_53 (not_53_out, in_3);
  not not_54 (not_54_out, in_4);
  not not_55 (not_55_out, in_2);
  and and_22 (and_22_out, A, not_55_out, and_2_out, not_56_out, not_57_out);
  not not_56 (not_56_out, in_3);
  not not_57 (not_57_out, in_4);
  not not_58 (not_58_out, A);
  and and_23 (and_23_out, not_58_out, in_2, and_2_out, not_59_out, not_60_out);
  not not_59 (not_59_out, in_3);
  not not_60 (not_60_out, in_4);
  and and_24 (and_24_out, A, in_2, and_2_out, not_61_out, not_62_out);
  not not_61 (not_61_out, in_3);
  not not_62 (not_62_out, in_4);
  not not_63 (not_63_out, A);
  not not_64 (not_64_out, in_2);
  and and_25 (and_25_out, not_63_out, not_64_out, and_2_out, in_3, not_65_out);
  not not_65 (not_65_out, in_4);
  not not_66 (not_66_out, in_2);
  and and_26 (and_26_out, A, not_66_out, and_2_out, in_3, not_67_out);
  not not_67 (not_67_out, in_4);
  not not_68 (not_68_out, A);
  and and_27 (and_27_out, not_68_out, in_2, and_2_out, in_3, not_69_out);
  not not_69 (not_69_out, in_4);
  and and_28 (and_28_out, A, in_2, and_2_out, in_3, not_70_out);
  not not_70 (not_70_out, in_4);
  not not_71 (not_71_out, A);
  not not_72 (not_72_out, in_2);
  and and_29 (and_29_out, not_71_out, not_72_out, and_2_out, not_73_out, in_4);
  not not_73 (not_73_out, in_3);
  not not_74 (not_74_out, in_2);
  and and_30 (and_30_out, A, not_74_out, and_2_out, not_75_out, in_4);
  not not_75 (not_75_out, in_3);
  not not_76 (not_76_out, A);
  not not_77 (not_77_out, in_2);
  // AND_Gate and_31 has open pins: in0=not_76_out, in1=not_77_out, in2=and_3_out, in3=not_78_out, in4=not_79_out, out=open
  not not_78 (not_78_out, in_3);
  not not_79 (not_79_out, in_4);
  not not_80 (not_80_out, in_2);
  // AND_Gate and_32 has open pins: in0=A, in1=not_80_out, in2=and_3_out, in3=not_81_out, in4=not_82_out, out=open
  not not_81 (not_81_out, in_3);
  not not_82 (not_82_out, in_4);
  not not_83 (not_83_out, A);
  and and_33 (and_33_out, not_83_out, in_2, and_3_out, not_84_out, not_85_out);
  not not_84 (not_84_out, in_3);
  not not_85 (not_85_out, in_4);
  and and_34 (and_34_out, A, in_2, and_3_out, not_86_out, not_87_out);
  not not_86 (not_86_out, in_3);
  not not_87 (not_87_out, in_4);
  not not_88 (not_88_out, A);
  not not_89 (not_89_out, in_2);
  and and_35 (and_35_out, not_88_out, not_89_out, and_3_out, in_3, not_90_out);
  not not_90 (not_90_out, in_4);
  not not_91 (not_91_out, in_2);
  and and_36 (and_36_out, A, not_91_out, and_3_out, in_3, not_92_out);
  not not_92 (not_92_out, in_4);
  not not_93 (not_93_out, A);
  and and_37 (and_37_out, not_93_out, in_2, and_3_out, in_3, not_94_out);
  not not_94 (not_94_out, in_4);
  and and_38 (and_38_out, A, in_2, and_3_out, in_3, not_95_out);
  not not_95 (not_95_out, in_4);
  not not_96 (not_96_out, A);
  not not_97 (not_97_out, in_2);
  and and_39 (and_39_out, not_96_out, not_97_out, and_3_out, not_98_out, in_4);
  not not_98 (not_98_out, in_3);
  not not_99 (not_99_out, in_2);
  and and_40 (and_40_out, A, not_99_out, and_3_out, not_100_out, in_4);
  not not_100 (not_100_out, in_3);
  not not_101 (not_101_out, A);
  not not_102 (not_102_out, in_2);
  // AND_Gate and_41 has open pins: in0=not_101_out, in1=not_102_out, in2=and_4_out, in3=not_103_out, in4=not_104_out, out=open
  not not_103 (not_103_out, in_3);
  not not_104 (not_104_out, in_4);
  not not_105 (not_105_out, in_2);
  // AND_Gate and_42 has open pins: in0=A, in1=not_105_out, in2=and_4_out, in3=not_106_out, in4=not_107_out, out=open
  not not_106 (not_106_out, in_3);
  not not_107 (not_107_out, in_4);
  not not_108 (not_108_out, A);
  // AND_Gate and_43 has open pins: in0=not_108_out, in1=in_2, in2=and_4_out, in3=not_109_out, in4=not_110_out, out=open
  not not_109 (not_109_out, in_3);
  not not_110 (not_110_out, in_4);
  and and_44 (and_44_out, A, in_2, and_4_out, not_111_out, not_112_out);
  not not_111 (not_111_out, in_3);
  not not_112 (not_112_out, in_4);
  not not_113 (not_113_out, A);
  not not_114 (not_114_out, in_2);
  and and_45 (and_45_out, not_113_out, not_114_out, and_4_out, in_3, not_115_out);
  not not_115 (not_115_out, in_4);
  not not_116 (not_116_out, in_2);
  and and_46 (and_46_out, A, not_116_out, and_4_out, in_3, not_117_out);
  not not_117 (not_117_out, in_4);
  not not_118 (not_118_out, A);
  and and_47 (and_47_out, not_118_out, in_2, and_4_out, in_3, not_119_out);
  not not_119 (not_119_out, in_4);
  and and_48 (and_48_out, A, in_2, and_4_out, in_3, not_120_out);
  not not_120 (not_120_out, in_4);
  not not_121 (not_121_out, A);
  not not_122 (not_122_out, in_2);
  and and_49 (and_49_out, not_121_out, not_122_out, and_4_out, not_123_out, in_4);
  not not_123 (not_123_out, in_3);
  not not_124 (not_124_out, in_2);
  and and_50 (and_50_out, A, not_124_out, and_4_out, not_125_out, in_4);
  not not_125 (not_125_out, in_3);
  not not_126 (not_126_out, A);
  not not_127 (not_127_out, in_2);
  // AND_Gate and_51 has open pins: in0=not_126_out, in1=not_127_out, in2=and_5_out, in3=not_128_out, in4=not_129_out, out=open
  not not_128 (not_128_out, in_3);
  not not_129 (not_129_out, in_4);
  not not_130 (not_130_out, in_2);
  // AND_Gate and_52 has open pins: in0=A, in1=not_130_out, in2=and_5_out, in3=not_131_out, in4=not_132_out, out=open
  not not_131 (not_131_out, in_3);
  not not_132 (not_132_out, in_4);
  not not_133 (not_133_out, A);
  // AND_Gate and_53 has open pins: in0=not_133_out, in1=in_2, in2=and_5_out, in3=not_134_out, in4=not_135_out, out=open
  not not_134 (not_134_out, in_3);
  not not_135 (not_135_out, in_4);
  // AND_Gate and_54 has open pins: in0=A, in1=in_2, in2=and_5_out, in3=not_136_out, in4=not_137_out, out=open
  not not_136 (not_136_out, in_3);
  not not_137 (not_137_out, in_4);
  not not_138 (not_138_out, A);
  not not_139 (not_139_out, in_2);
  and and_55 (and_55_out, not_138_out, not_139_out, and_5_out, in_3, not_140_out);
  not not_140 (not_140_out, in_4);
  not not_141 (not_141_out, in_2);
  and and_56 (and_56_out, A, not_141_out, and_5_out, in_3, not_142_out);
  not not_142 (not_142_out, in_4);
  not not_143 (not_143_out, A);
  and and_57 (and_57_out, not_143_out, in_2, and_5_out, in_3, not_144_out);
  not not_144 (not_144_out, in_4);
  and and_58 (and_58_out, A, in_2, and_5_out, in_3, not_145_out);
  not not_145 (not_145_out, in_4);
  not not_146 (not_146_out, A);
  not not_147 (not_147_out, in_2);
  and and_59 (and_59_out, not_146_out, not_147_out, and_5_out, not_148_out, in_4);
  not not_148 (not_148_out, in_3);
  not not_149 (not_149_out, in_2);
  and and_60 (and_60_out, A, not_149_out, and_5_out, not_150_out, in_4);
  not not_150 (not_150_out, in_3);
  not not_151 (not_151_out, A);
  not not_152 (not_152_out, in_2);
  // AND_Gate and_61 has open pins: in0=not_151_out, in1=not_152_out, in2=and_6_out, in3=not_153_out, in4=not_154_out, out=open
  not not_153 (not_153_out, in_3);
  not not_154 (not_154_out, in_4);
  not not_155 (not_155_out, in_2);
  // AND_Gate and_62 has open pins: in0=A, in1=not_155_out, in2=and_6_out, in3=not_156_out, in4=not_157_out, out=open
  not not_156 (not_156_out, in_3);
  not not_157 (not_157_out, in_4);
  not not_158 (not_158_out, A);
  // AND_Gate and_63 has open pins: in0=not_158_out, in1=in_2, in2=and_6_out, in3=not_159_out, in4=not_160_out, out=open
  not not_159 (not_159_out, in_3);
  not not_160 (not_160_out, in_4);
  // AND_Gate and_64 has open pins: in0=A, in1=in_2, in2=and_6_out, in3=not_161_out, in4=not_162_out, out=open
  not not_161 (not_161_out, in_3);
  not not_162 (not_162_out, in_4);
  not not_163 (not_163_out, A);
  not not_164 (not_164_out, in_2);
  // AND_Gate and_65 has open pins: in0=not_163_out, in1=not_164_out, in2=and_6_out, in3=in_3, in4=not_165_out, out=open
  not not_165 (not_165_out, in_4);
  not not_166 (not_166_out, in_2);
  and and_66 (and_66_out, A, not_166_out, and_6_out, in_3, not_167_out);
  not not_167 (not_167_out, in_4);
  not not_168 (not_168_out, A);
  and and_67 (and_67_out, not_168_out, in_2, and_6_out, in_3, not_169_out);
  not not_169 (not_169_out, in_4);
  and and_68 (and_68_out, A, in_2, and_6_out, in_3, not_170_out);
  not not_170 (not_170_out, in_4);
  not not_171 (not_171_out, A);
  not not_172 (not_172_out, in_2);
  and and_69 (and_69_out, not_171_out, not_172_out, and_6_out, not_173_out, in_4);
  not not_173 (not_173_out, in_3);
  not not_174 (not_174_out, in_2);
  and and_70 (and_70_out, A, not_174_out, and_6_out, not_175_out, in_4);
  not not_175 (not_175_out, in_3);
  not not_176 (not_176_out, A);
  not not_177 (not_177_out, in_2);
  // AND_Gate and_71 has open pins: in0=not_176_out, in1=not_177_out, in2=and_7_out, in3=not_178_out, in4=not_179_out, out=open
  not not_178 (not_178_out, in_3);
  not not_179 (not_179_out, in_4);
  not not_180 (not_180_out, in_2);
  // AND_Gate and_72 has open pins: in0=A, in1=not_180_out, in2=and_7_out, in3=not_181_out, in4=not_182_out, out=open
  not not_181 (not_181_out, in_3);
  not not_182 (not_182_out, in_4);
  not not_183 (not_183_out, A);
  // AND_Gate and_73 has open pins: in0=not_183_out, in1=in_2, in2=and_7_out, in3=not_184_out, in4=not_185_out, out=open
  not not_184 (not_184_out, in_3);
  not not_185 (not_185_out, in_4);
  // AND_Gate and_74 has open pins: in0=A, in1=in_2, in2=and_7_out, in3=not_186_out, in4=not_187_out, out=open
  not not_186 (not_186_out, in_3);
  not not_187 (not_187_out, in_4);
  not not_188 (not_188_out, A);
  not not_189 (not_189_out, in_2);
  // AND_Gate and_75 has open pins: in0=not_188_out, in1=not_189_out, in2=and_7_out, in3=in_3, in4=not_190_out, out=open
  not not_190 (not_190_out, in_4);
  not not_191 (not_191_out, in_2);
  // AND_Gate and_76 has open pins: in0=A, in1=not_191_out, in2=and_7_out, in3=in_3, in4=not_192_out, out=open
  not not_192 (not_192_out, in_4);
  not not_193 (not_193_out, A);
  and and_77 (and_77_out, not_193_out, in_2, and_7_out, in_3, not_194_out);
  not not_194 (not_194_out, in_4);
  and and_78 (and_78_out, A, in_2, and_7_out, in_3, not_195_out);
  not not_195 (not_195_out, in_4);
  not not_196 (not_196_out, A);
  not not_197 (not_197_out, in_2);
  and and_79 (and_79_out, not_196_out, not_197_out, and_7_out, not_198_out, in_4);
  not not_198 (not_198_out, in_3);
  not not_199 (not_199_out, in_2);
  and and_80 (and_80_out, A, not_199_out, and_7_out, not_200_out, in_4);
  not not_200 (not_200_out, in_3);
  not not_201 (not_201_out, A);
  not not_202 (not_202_out, in_2);
  // AND_Gate and_81 has open pins: in0=not_201_out, in1=not_202_out, in2=and_8_out, in3=not_203_out, in4=not_204_out, out=open
  not not_203 (not_203_out, in_3);
  not not_204 (not_204_out, in_4);
  not not_205 (not_205_out, in_2);
  // AND_Gate and_82 has open pins: in0=A, in1=not_205_out, in2=and_8_out, in3=not_206_out, in4=not_207_out, out=open
  not not_206 (not_206_out, in_3);
  not not_207 (not_207_out, in_4);
  not not_208 (not_208_out, A);
  // AND_Gate and_83 has open pins: in0=not_208_out, in1=in_2, in2=and_8_out, in3=not_209_out, in4=not_210_out, out=open
  not not_209 (not_209_out, in_3);
  not not_210 (not_210_out, in_4);
  // AND_Gate and_84 has open pins: in0=A, in1=in_2, in2=and_8_out, in3=not_211_out, in4=not_212_out, out=open
  not not_211 (not_211_out, in_3);
  not not_212 (not_212_out, in_4);
  not not_213 (not_213_out, A);
  not not_214 (not_214_out, in_2);
  // AND_Gate and_85 has open pins: in0=not_213_out, in1=not_214_out, in2=and_8_out, in3=in_3, in4=not_215_out, out=open
  not not_215 (not_215_out, in_4);
  not not_216 (not_216_out, in_2);
  // AND_Gate and_86 has open pins: in0=A, in1=not_216_out, in2=and_8_out, in3=in_3, in4=not_217_out, out=open
  not not_217 (not_217_out, in_4);
  not not_218 (not_218_out, A);
  // AND_Gate and_87 has open pins: in0=not_218_out, in1=in_2, in2=and_8_out, in3=in_3, in4=not_219_out, out=open
  not not_219 (not_219_out, in_4);
  and and_88 (and_88_out, A, in_2, and_8_out, in_3, not_220_out);
  not not_220 (not_220_out, in_4);
  not not_221 (not_221_out, A);
  not not_222 (not_222_out, in_2);
  and and_89 (and_89_out, not_221_out, not_222_out, and_8_out, not_223_out, in_4);
  not not_223 (not_223_out, in_3);
  not not_224 (not_224_out, in_2);
  and and_90 (and_90_out, A, not_224_out, and_8_out, not_225_out, in_4);
  not not_225 (not_225_out, in_3);
  not not_226 (not_226_out, A);
  not not_227 (not_227_out, in_2);
  // AND_Gate and_91 has open pins: in0=not_226_out, in1=not_227_out, in2=and_9_out, in3=not_228_out, in4=not_229_out, out=open
  not not_228 (not_228_out, in_3);
  not not_229 (not_229_out, in_4);
  not not_230 (not_230_out, in_2);
  // AND_Gate and_92 has open pins: in0=A, in1=not_230_out, in2=and_9_out, in3=not_231_out, in4=not_232_out, out=open
  not not_231 (not_231_out, in_3);
  not not_232 (not_232_out, in_4);
  not not_233 (not_233_out, A);
  // AND_Gate and_93 has open pins: in0=not_233_out, in1=in_2, in2=and_9_out, in3=not_234_out, in4=not_235_out, out=open
  not not_234 (not_234_out, in_3);
  not not_235 (not_235_out, in_4);
  // AND_Gate and_94 has open pins: in0=A, in1=in_2, in2=and_9_out, in3=not_236_out, in4=not_237_out, out=open
  not not_236 (not_236_out, in_3);
  not not_237 (not_237_out, in_4);
  not not_238 (not_238_out, A);
  not not_239 (not_239_out, in_2);
  // AND_Gate and_95 has open pins: in0=not_238_out, in1=not_239_out, in2=and_9_out, in3=in_3, in4=not_240_out, out=open
  not not_240 (not_240_out, in_4);
  not not_241 (not_241_out, in_2);
  // AND_Gate and_96 has open pins: in0=A, in1=not_241_out, in2=and_9_out, in3=in_3, in4=not_242_out, out=open
  not not_242 (not_242_out, in_4);
  not not_243 (not_243_out, A);
  // AND_Gate and_97 has open pins: in0=not_243_out, in1=in_2, in2=and_9_out, in3=in_3, in4=not_244_out, out=open
  not not_244 (not_244_out, in_4);
  // AND_Gate and_98 has open pins: in0=A, in1=in_2, in2=and_9_out, in3=in_3, in4=not_245_out, out=open
  not not_245 (not_245_out, in_4);
  not not_246 (not_246_out, A);
  not not_247 (not_247_out, in_2);
  and and_99 (and_99_out, not_246_out, not_247_out, and_9_out, not_248_out, in_4);
  not not_248 (not_248_out, in_3);
  not not_249 (not_249_out, in_2);
  and and_100 (and_100_out, A, not_249_out, and_9_out, not_250_out, in_4);
  not not_250 (not_250_out, in_3);
  not not_251 (not_251_out, A);
  not not_252 (not_252_out, in_2);
  // AND_Gate and_101 has open pins: in0=not_251_out, in1=not_252_out, in2=and_10_out, in3=not_253_out, in4=not_254_out, out=open
  not not_253 (not_253_out, in_3);
  not not_254 (not_254_out, in_4);
  not not_255 (not_255_out, in_2);
  // AND_Gate and_102 has open pins: in0=A, in1=not_255_out, in2=and_10_out, in3=not_256_out, in4=not_257_out, out=open
  not not_256 (not_256_out, in_3);
  not not_257 (not_257_out, in_4);
  not not_258 (not_258_out, A);
  // AND_Gate and_103 has open pins: in0=not_258_out, in1=in_2, in2=and_10_out, in3=not_259_out, in4=not_260_out, out=open
  not not_259 (not_259_out, in_3);
  not not_260 (not_260_out, in_4);
  // AND_Gate and_104 has open pins: in0=A, in1=in_2, in2=and_10_out, in3=not_261_out, in4=not_262_out, out=open
  not not_261 (not_261_out, in_3);
  not not_262 (not_262_out, in_4);
  not not_263 (not_263_out, A);
  not not_264 (not_264_out, in_2);
  // AND_Gate and_105 has open pins: in0=not_263_out, in1=not_264_out, in2=and_10_out, in3=in_3, in4=not_265_out, out=open
  not not_265 (not_265_out, in_4);
  not not_266 (not_266_out, in_2);
  // AND_Gate and_106 has open pins: in0=A, in1=not_266_out, in2=and_10_out, in3=in_3, in4=not_267_out, out=open
  not not_267 (not_267_out, in_4);
  not not_268 (not_268_out, A);
  // AND_Gate and_107 has open pins: in0=not_268_out, in1=in_2, in2=and_10_out, in3=in_3, in4=not_269_out, out=open
  not not_269 (not_269_out, in_4);
  // AND_Gate and_108 has open pins: in0=A, in1=in_2, in2=and_10_out, in3=in_3, in4=not_270_out, out=open
  not not_270 (not_270_out, in_4);
  not not_271 (not_271_out, A);
  not not_272 (not_272_out, in_2);
  // AND_Gate and_109 has open pins: in0=not_271_out, in1=not_272_out, in2=and_10_out, in3=not_273_out, in4=in_4, out=open
  not not_273 (not_273_out, in_3);
  not not_274 (not_274_out, in_2);
  and and_110 (and_110_out, A, not_274_out, and_10_out, not_275_out, in_4);
  not not_275 (not_275_out, in_3);
  or or_1 (YES, and_12_out, and_13_out, and_14_out, and_15_out, and_20_out, and_16_out, and_17_out, and_18_out, and_19_out, and_23_out, and_24_out, and_25_out, and_26_out, and_27_out, and_28_out, and_29_out, and_30_out, and_34_out, and_35_out, and_36_out, and_37_out, and_38_out, and_39_out, and_40_out, or_3_out);
  or or_2 (SAME, and_11_out, and_22_out, and_33_out, and_44_out, and_55_out, and_66_out, and_88_out, and_99_out, and_77_out, and_110_out);
  not not_276 (not_276_out, SAME);
  and and_111 (NO, not_276_out, not_277_out);
  not not_277 (not_277_out, YES);
  or or_3 (or_3_out, and_45_out, and_46_out, and_47_out, and_48_out, and_49_out, and_50_out, and_56_out, and_57_out, and_58_out, and_59_out, and_60_out, and_67_out, and_68_out, and_69_out, and_70_out, and_78_out, and_79_out, and_80_out, and_89_out, and_90_out, and_100_out);

  // Notes on the sheet:
  //   Q: Is A larger than B?
  //   ATTEMPT 1 (FAILED)
endmodule

module Binary_comparison (
  input  in_1,
  input  in_2,
  input  in_3,
  input  in_4,
  input  in_5,
  input  in_6,
  output out_7,
  output out_8
);

  wire and_1_out, and_2_out, and_3_out, and_4_out, and_5_out, and_6_out, and_7_out, and_8_out, and_9_out,
       and_10_out, not_1_out, not_2_out, not_3_out, not_4_out, not_5_out, not_6_out, not_7_out, not_8_out,
       not_9_out, not_10_out, not_11_out, not_12_out, not_13_out, not_14_out, or_1_out, or_2_out, xor_1_out,
       xor_2_out, xor_3_out, xor_4_out, xor_5_out, xor_6_out;

  xor xor_1 (xor_1_out, in_3, in_4);
  xor xor_2 (xor_2_out, in_3, in_4);
  and and_1 (and_1_out, xor_1_out, not_1_out);
  not not_1 (not_1_out, in_4);
  not not_2 (not_2_out, in_3);
  and and_2 (and_2_out, not_2_out, xor_2_out);
  xor xor_3 (xor_3_out, in_1, in_5);
  xor xor_4 (xor_4_out, in_1, in_5);
  and and_3 (and_3_out, xor_3_out, not_3_out);
  not not_3 (not_3_out, in_5);
  not not_4 (not_4_out, in_1);
  and and_4 (and_4_out, not_4_out, xor_4_out);
  not not_5 (not_5_out, and_3_out);
  not not_6 (not_6_out, and_4_out);
  not not_7 (not_7_out, and_3_out);
  not not_8 (not_8_out, and_4_out);
  and and_5 (and_5_out, not_5_out, not_6_out, and_1_out);
  and and_6 (and_6_out, and_2_out, not_7_out, not_8_out);
  or or_1 (or_1_out, and_3_out, and_5_out);
  or or_2 (or_2_out, and_6_out, and_4_out);
  xor xor_5 (xor_5_out, in_2, in_6);
  xor xor_6 (xor_6_out, in_2, in_6);
  and and_7 (and_7_out, xor_5_out, not_9_out);
  not not_9 (not_9_out, in_6);
  not not_10 (not_10_out, in_2);
  and and_8 (and_8_out, not_10_out, xor_6_out);
  not not_11 (not_11_out, and_7_out);
  not not_12 (not_12_out, and_8_out);
  not not_13 (not_13_out, and_7_out);
  not not_14 (not_14_out, and_8_out);
  and and_9 (and_9_out, not_11_out, not_12_out, or_1_out);
  and and_10 (and_10_out, or_2_out, not_13_out, not_14_out);
  or or_3 (out_7, and_7_out, and_9_out);
  or or_4 (out_8, and_10_out, and_8_out);

  // Notes on the sheet:
  //   ATTEMPT 2 (SUCCESS)
  //   ETC...
endmodule

module _1st_bit_pair_comparison (
  input  in_1,
  input  in_2,
  output out_3,
  output out_4
);

  wire not_1_out, not_2_out, xor_1_out, xor_2_out;

  xor xor_1 (xor_1_out, in_1, in_2);
  xor xor_2 (xor_2_out, in_1, in_2);
  and and_1 (out_3, xor_1_out, not_1_out);
  not not_1 (not_1_out, in_2);
  not not_2 (not_2_out, in_1);
  and and_2 (out_4, not_2_out, xor_2_out);
endmodule

module nth_bit_pair_comparison (
  input  in_1,
  input  in_2,
  input  in_3,
  input  in_4,
  output out_5,
  output out_6
);

  wire and_1_out, and_2_out, and_3_out, and_4_out, not_1_out, not_2_out, not_3_out, not_4_out, not_5_out,
       not_6_out, xor_1_out, xor_2_out;

  xor xor_1 (xor_1_out, in_1, in_4);
  xor xor_2 (xor_2_out, in_1, in_4);
  and and_1 (and_1_out, xor_1_out, not_1_out);
  not not_1 (not_1_out, in_4);
  not not_2 (not_2_out, in_1);
  and and_2 (and_2_out, not_2_out, xor_2_out);
  not not_3 (not_3_out, and_1_out);
  not not_4 (not_4_out, and_2_out);
  not not_5 (not_5_out, and_1_out);
  not not_6 (not_6_out, and_2_out);
  and and_3 (and_3_out, not_3_out, not_4_out, in_2);
  and and_4 (and_4_out, in_3, not_5_out, not_6_out);
  or or_1 (out_5, and_1_out, and_3_out);
  or or_2 (out_6, and_4_out, and_2_out);
endmodule

module JK_Flip_flop (
  input  in_1,
  input  in_2,
  input  in_3,
  input  in_4,
  output out_5,
  output out_6
);

  wire nand_1_out, nand_2_out, nand_3_out, nand_4_out, nand_5_out, nand_6_out, not_1_out, or_1_out;

  or or_1 (or_1_out, in_1, nand_4_out);
  nand nand_1 (nand_1_out, in_2, out_6, in_3);
  nand nand_2 (nand_2_out, in_3, in_4, out_5);
  nand nand_3 (nand_3_out, or_1_out, nand_1_out);
  nand nand_4 (nand_4_out, nand_2_out, nand_3_out);
  not not_1 (not_1_out, in_3);
  nand nand_5 (nand_5_out, not_1_out, nand_3_out);
  nand nand_6 (nand_6_out, not_1_out, nand_4_out);
  nand nand_7 (out_5, out_6, nand_5_out);
  nand nand_8 (out_6, nand_6_out, out_5);
endmodule

module Full_Adder (
  input  in_1,
  input  in_2,
  input  in_3,
  output out_4,
  output out_5
);

  wire and_1_out, and_2_out, xor_2_out;

  xor xor_1 (out_4, in_1, xor_2_out);
  xor xor_2 (xor_2_out, in_3, in_2);
  and and_1 (and_1_out, in_1, xor_2_out);
  and and_2 (and_2_out, in_2, in_3);
  or or_1 (out_5, and_1_out, and_2_out);
endmodule

module Half_Adder (
  input  in_1,
  input  in_2,
  output out_3,
  output out_4
);

  and and_1 (out_4, in_1, in_2);
  xor xor_1 (out_3, in_1, in_2);
endmodule

module _1_bit_Memory (
  input  in_1,
  input  in_2,
  output out_3
);

  S_R_Flip_Flop #(.trigger("high")) s_r_ff_1 (
    .S(in_1), .clk(1'b1), .R(in_2), .Q(out_3), .reset(in_2));  // open: Qn, preset, en
endmodule

module Memory_2 (
  input  Ignite_Reset,
  output [7:0] out_2
);

  wire clock_1_out, jk_flip_flop_1_out_5, jk_flip_flop_1_out_6, jk_flip_flop_2_out_5, jk_flip_flop_2_out_6,
       jk_flip_flop_3_out_5, jk_flip_flop_3_out_6, jk_flip_flop_4_out_5, jk_flip_flop_4_out_6,
       jk_flip_flop_5_out_5, jk_flip_flop_5_out_6, jk_flip_flop_6_out_5, jk_flip_flop_6_out_6,
       jk_flip_flop_7_out_5, jk_flip_flop_7_out_6, jk_flip_flop_8_out_6;

  Clock clock_1 (.out(clock_1_out));
  JK_Flip_flop jk_flip_flop_1 (
    .in_1(Ignite_Reset), .in_2(1'b1), .in_3(clock_1_out), .in_4(1'b1), .out_5(jk_flip_flop_1_out_5),
    .out_6(jk_flip_flop_1_out_6));
  not not_1 (out_2[7], jk_flip_flop_8_out_6);
  JK_Flip_flop jk_flip_flop_2 (
    .in_1(Ignite_Reset), .in_2(1'b1), .in_3(jk_flip_flop_1_out_5), .in_4(1'b1), .out_5(jk_flip_flop_2_out_5),
    .out_6(jk_flip_flop_2_out_6));
  not not_2 (out_2[4], jk_flip_flop_5_out_6);
  not not_3 (out_2[6], jk_flip_flop_7_out_6);
  not not_4 (out_2[5], jk_flip_flop_6_out_6);
  not not_5 (out_2[3], jk_flip_flop_4_out_6);
  not not_6 (out_2[2], jk_flip_flop_3_out_6);
  JK_Flip_flop jk_flip_flop_3 (
    .in_1(Ignite_Reset), .in_2(1'b1), .in_3(jk_flip_flop_2_out_5), .in_4(1'b1), .out_5(jk_flip_flop_3_out_5),
    .out_6(jk_flip_flop_3_out_6));
  not not_7 (out_2[1], jk_flip_flop_2_out_6);
  not not_8 (out_2[0], jk_flip_flop_1_out_6);
  JK_Flip_flop jk_flip_flop_4 (
    .in_1(Ignite_Reset), .in_2(1'b1), .in_3(jk_flip_flop_3_out_5), .in_4(1'b1), .out_5(jk_flip_flop_4_out_5),
    .out_6(jk_flip_flop_4_out_6));
  JK_Flip_flop jk_flip_flop_5 (
    .in_1(Ignite_Reset), .in_2(1'b1), .in_3(jk_flip_flop_4_out_5), .in_4(1'b1), .out_5(jk_flip_flop_5_out_5),
    .out_6(jk_flip_flop_5_out_6));
  JK_Flip_flop jk_flip_flop_6 (
    .in_1(Ignite_Reset), .in_2(1'b1), .in_3(jk_flip_flop_5_out_5), .in_4(1'b1), .out_5(jk_flip_flop_6_out_5),
    .out_6(jk_flip_flop_6_out_6));
  JK_Flip_flop jk_flip_flop_7 (
    .in_1(Ignite_Reset), .in_2(1'b1), .in_3(jk_flip_flop_6_out_5), .in_4(1'b1), .out_5(jk_flip_flop_7_out_5),
    .out_6(jk_flip_flop_7_out_6));
  JK_Flip_flop jk_flip_flop_8 (
    .in_1(Ignite_Reset), .in_2(1'b1), .in_3(jk_flip_flop_7_out_5), .in_4(1'b1), .out_6(jk_flip_flop_8_out_6));  // open: out_5
endmodule

module Counter (
  input  IGNITE_RESET,
  output [7:0] out_2
);

  Memory_2 memory_2_1 (.Ignite_Reset(IGNITE_RESET), .out_2(out_2));
endmodule

module Keyboard_to_TTY__clock__counter (
);

  wire _0_out, _1_out, _2_out, _3_out, _4_out, _5_out, _6_out, _7_out, _8_out, _9_out, A_out, B_out,
       button_1_out, button_2_out, button_3_out, button_4_out, button_5_out, button_6_out, button_7_out,
       C_out, D_out, E_out, F_out, G_out, H_out, I_out, j_k_ff_1_q, J_out, K_out, keyboard_counter_1_out_69,
       L_out, M_out, N_out, O_out, P_out, Q_out, R_out, S_out, T_out, U_out, V_out, W_out, X_out, Y_out,
       Z_out;
  wire [6:0] keyboard_counter_1_out_68;

  Button _1 (.out(_1_out));
  Button Q (.out(Q_out));
  Button _2 (.out(_2_out));
  Button _3 (.out(_3_out));
  Button _4 (.out(_4_out));
  Button E (.out(E_out));
  Button W (.out(W_out));
  Button D (.out(D_out));
  Button S (.out(S_out));
  Button A (.out(A_out));
  Button Z (.out(Z_out));
  Button X (.out(X_out));
  Button button_1 (.out(button_1_out));
  Button button_2 (.out(button_2_out));
  Button _5 (.out(_5_out));
  Button _6 (.out(_6_out));
  Button Y (.out(Y_out));
  Button T (.out(T_out));
  Button R (.out(R_out));
  Button F (.out(F_out));
  Button H (.out(H_out));
  Button G (.out(G_out));
  Button B (.out(B_out));
  Button C (.out(C_out));
  Button V (.out(V_out));
  Button button_3 (.out(button_3_out));
  Keyboard_counter keyboard_counter_1 (
    .Ignite_Reset(button_6_out), .in_2(B_out), .in_3(C_out), .in_4(D_out), .in_5(E_out), .in_6(F_out),
    .in_7(G_out), .in_8(H_out), .in_9(I_out), .in_10(J_out), .K(K_out), .in_12(L_out), .in_13(M_out),
    .in_14(N_out), .in_15(O_out), .in_16(P_out), .in_17(Q_out), .in_18(R_out), .in_19(S_out), .in_20(T_out),
    .in_21(U_out), .in_22(V_out), .in_23(W_out), .in_24(X_out), .in_25(Y_out), .in_26(Z_out), .in_27(A_out),
    .in_28(button_3_out), .in_29(button_4_out), .in_30(j_k_ff_1_q), .in_31(A_out), .in_32(B_out),
    .in_33(C_out), .in_34(D_out), .in_35(E_out), .in_36(F_out), .in_37(G_out), .in_38(H_out), .in_39(I_out),
    .in_40(J_out), .in_41(K_out), .in_42(L_out), .in_43(M_out), .in_44(N_out), .in_45(O_out), .in_46(P_out),
    .in_47(Q_out), .in_48(R_out), .in_49(S_out), .in_50(T_out), .in_51(U_out), .in_52(V_out), .in_53(W_out),
    .in_54(X_out), .in_55(Y_out), .in_56(Z_out), .in_57(_0_out), .in_58(_1_out), .in_59(_2_out),
    .in_60(_3_out), .in_61(_4_out), .in_62(_5_out), .in_63(_6_out), .in_64(_7_out), .in_65(_8_out),
    .in_66(_9_out), .in_67(button_5_out), .out_68(keyboard_counter_1_out_68),
    .out_69(keyboard_counter_1_out_69));
  Button _9 (.out(_9_out));
  Button _7 (.out(_7_out));
  Button _8 (.out(_8_out));
  Button O (.out(O_out));
  Button I (.out(I_out));
  Button U (.out(U_out));
  Button J (.out(J_out));
  Button K (.out(K_out));
  Button M (.out(M_out));
  Button N (.out(N_out));
  Button _0 (.out(_0_out));
  Button P (.out(P_out));
  Button button_4 (.out(button_4_out));
  Button L (.out(L_out));
  Button button_5 (.out(button_5_out));
  Button button_6 (.out(button_6_out));
  Button button_7 (.out(button_7_out));
  J_K_Flip_Flop j_k_ff_1 (
    .J(1'b1), .clk(button_1_out), .K(1'b1), .Q(j_k_ff_1_q), .reset(button_6_out));  // open: Qn, preset, en
  TTY tty_1 (.data(keyboard_counter_1_out_68), .clk(keyboard_counter_1_out_69), .clr(button_2_out));  // open: we
  _1_bit_Memory u_1_bit_memory_1 (.in_1(button_7_out));  // open: in_2, out_3

  // Notes on the sheet:
  //   SHIFT LOCK
  //   CLEAR ALL
  //   SPACE
  //   BUTTON --> TTY
  //   DELETE
  //   ENTER
  //   IGNITE / RESET
  //   Designed/built by Fraser Price (±4 hours)
  //   Non-homemade JK and SR flip flops were not used
  //   BEST FREQUENCY = 256 / 512kHz
  //   COMMAND LOCK
  //   KEYBOARD BUTTONS CANNOT BE HELD OR CIRCUIT WILL OSCILLATE
  //   due to problems with calculation speed and errors with clock ticks- I do however have designs for both
endmodule
module Keyboard_counter (
  input  Ignite_Reset,
  input  in_2,
  input  in_3,
  input  in_4,
  input  in_5,
  input  in_6,
  input  in_7,
  input  in_8,
  input  in_9,
  input  in_10,
  input  K,
  input  in_12,
  input  in_13,
  input  in_14,
  input  in_15,
  input  in_16,
  input  in_17,
  input  in_18,
  input  in_19,
  input  in_20,
  input  in_21,
  input  in_22,
  input  in_23,
  input  in_24,
  input  in_25,
  input  in_26,
  input  in_27,
  input  in_28,
  input  in_29,
  input  in_30,
  input  in_31,
  input  in_32,
  input  in_33,
  input  in_34,
  input  in_35,
  input  in_36,
  input  in_37,
  input  in_38,
  input  in_39,
  input  in_40,
  input  in_41,
  input  in_42,
  input  in_43,
  input  in_44,
  input  in_45,
  input  in_46,
  input  in_47,
  input  in_48,
  input  in_49,
  input  in_50,
  input  in_51,
  input  in_52,
  input  in_53,
  input  in_54,
  input  in_55,
  input  in_56,
  input  in_57,
  input  in_58,
  input  in_59,
  input  in_60,
  input  in_61,
  input  in_62,
  input  in_63,
  input  in_64,
  input  in_65,
  input  in_66,
  input  in_67,
  output [6:0] out_68,
  output out_69
);

  wire _0_out, _1_out, _2_out, _3_out, _4_out, _5_out, _6_out, _7_out, _8_out, _9_out, A_2_out, A_out,
       and_2_out, and_3_out, and_4_out, and_5_out, and_6_out, and_7_out, and_8_out, and_9_out, and_10_out,
       and_11_out, and_12_out, and_13_out, and_14_out, and_15_out, and_16_out, and_17_out, and_18_out,
       and_19_out, and_20_out, and_21_out, and_22_out, and_23_out, and_24_out, and_25_out, and_26_out,
       and_27_out, and_28_out, and_29_out, and_30_out, and_31_out, and_32_out, and_33_out, and_34_out,
       and_35_out, and_36_out, and_37_out, and_38_out, and_39_out, and_40_out, and_41_out, and_42_out,
       and_43_out, and_44_out, and_45_out, and_46_out, and_47_out, and_48_out, and_49_out, and_50_out,
       and_51_out, and_52_out, and_53_out, and_54_out, and_55_out, and_56_out, and_57_out, and_58_out,
       and_59_out, and_60_out, and_61_out, and_62_out, and_63_out, and_64_out, and_65_out, and_66_out,
       and_out, B_2_out, B_out, C_2_out, C_out, clock_1_out, D_2_out, D_out, DEL_out, E_2_out, E_out,
       ENT_out, F_2_out, F_out, G_2_out, G_out, H_2_out, H_out, I_2_out, I_out, J_2_out, J_3_out, j_k_ff_1_q,
       j_k_ff_1_qn, j_k_ff_2_q, j_k_ff_2_qn, j_k_ff_3_q, j_k_ff_3_qn, j_k_ff_4_q, j_k_ff_4_qn, j_k_ff_5_q,
       j_k_ff_5_qn, j_k_ff_6_q, j_k_ff_6_qn, j_k_ff_7_qn, J_out, K_out, L_2_out, L_out, M_2_out, M_out,
       n1_bit_memory_1_out_3, n1_bit_memory_2_out_3, n1_bit_memory_3_out_3, n1_bit_memory_4_out_3,
       n1_bit_memory_5_out_3, n1_bit_memory_6_out_3, n1_bit_memory_7_out_3, n1_bit_memory_8_out_3,
       n1_bit_memory_9_out_3, n1_bit_memory_10_out_3, n1_bit_memory_11_out_3, n1_bit_memory_12_out_3,
       n1_bit_memory_13_out_3, n1_bit_memory_14_out_3, n1_bit_memory_15_out_3, n1_bit_memory_16_out_3,
       n1_bit_memory_17_out_3, n1_bit_memory_18_out_3, n1_bit_memory_19_out_3, n1_bit_memory_20_out_3,
       n1_bit_memory_21_out_3, n1_bit_memory_22_out_3, n1_bit_memory_23_out_3, n1_bit_memory_24_out_3,
       n1_bit_memory_25_out_3, n1_bit_memory_26_out_3, n1_bit_memory_27_out_3, n1_bit_memory_28_out_3,
       n1_bit_memory_29_out_3, n1_bit_memory_30_out_3, n1_bit_memory_31_out_3, n1_bit_memory_32_out_3,
       n1_bit_memory_33_out_3, n1_bit_memory_34_out_3, n1_bit_memory_35_out_3, n1_bit_memory_36_out_3,
       n1_bit_memory_37_out_3, n1_bit_memory_38_out_3, n1_bit_memory_39_out_3, n1_bit_memory_40_out_3,
       n1_bit_memory_41_out_3, n1_bit_memory_42_out_3, n1_bit_memory_43_out_3, n1_bit_memory_44_out_3,
       n1_bit_memory_45_out_3, n1_bit_memory_46_out_3, n1_bit_memory_47_out_3, n1_bit_memory_48_out_3,
       n1_bit_memory_49_out_3, n1_bit_memory_50_out_3, n1_bit_memory_51_out_3, n1_bit_memory_52_out_3,
       n1_bit_memory_53_out_3, n1_bit_memory_54_out_3, n1_bit_memory_55_out_3, n1_bit_memory_56_out_3,
       n1_bit_memory_57_out_3, n1_bit_memory_58_out_3, n1_bit_memory_59_out_3, n1_bit_memory_60_out_3,
       n1_bit_memory_61_out_3, n1_bit_memory_62_out_3, n1_bit_memory_63_out_3, n1_bit_memory_64_out_3,
       n1_bit_memory_65_out_3, N_2_out, N_out, not_8_out, not_9_out, not_10_out, not_11_out, not_12_out,
       not_13_out, not_14_out, not_15_out, not_16_out, not_17_out, not_18_out, not_19_out, not_20_out,
       not_21_out, not_22_out, not_23_out, not_24_out, not_25_out, not_26_out, not_27_out, not_28_out,
       not_29_out, not_30_out, not_31_out, not_32_out, not_33_out, not_34_out, not_35_out, not_36_out,
       not_37_out, not_38_out, not_39_out, not_40_out, not_41_out, not_42_out, not_43_out, not_44_out,
       not_45_out, not_46_out, not_47_out, not_48_out, not_49_out, not_50_out, not_51_out, not_52_out,
       not_53_out, not_54_out, not_55_out, not_56_out, not_57_out, not_58_out, not_59_out, not_60_out,
       not_61_out, not_62_out, not_63_out, not_64_out, not_65_out, not_66_out, not_67_out, not_68_out,
       not_69_out, not_70_out, not_71_out, not_72_out, not_73_out, not_74_out, not_75_out, not_76_out,
       not_77_out, not_78_out, not_79_out, not_80_out, not_81_out, not_82_out, not_83_out, not_84_out,
       not_85_out, not_86_out, not_87_out, not_88_out, not_89_out, not_90_out, not_91_out, not_92_out,
       not_93_out, not_94_out, not_95_out, not_96_out, not_97_out, not_98_out, not_101_out, not_102_out,
       not_103_out, not_104_out, not_105_out, not_106_out, not_107_out, not_108_out, not_109_out,
       not_110_out, not_111_out, not_112_out, not_113_out, not_114_out, not_115_out, not_116_out,
       not_117_out, not_118_out, not_119_out, not_120_out, not_121_out, not_122_out, not_123_out,
       not_124_out, not_125_out, not_126_out, not_127_out, not_128_out, not_129_out, not_130_out,
       not_131_out, not_132_out, not_133_out, not_134_out, not_135_out, not_136_out, not_137_out,
       not_138_out, not_139_out, not_140_out, not_141_out, not_142_out, not_143_out, not_144_out,
       not_145_out, not_146_out, not_147_out, not_148_out, not_149_out, not_150_out, not_151_out,
       not_152_out, not_153_out, not_154_out, not_155_out, not_156_out, not_157_out, not_158_out,
       not_159_out, not_160_out, not_161_out, not_162_out, not_163_out, not_164_out, not_165_out,
       not_166_out, not_167_out, not_168_out, not_169_out, not_170_out, not_171_out, not_172_out,
       not_173_out, not_174_out, not_175_out, not_176_out, not_177_out, not_178_out, not_179_out,
       not_180_out, not_181_out, not_182_out, not_183_out, not_184_out, not_185_out, not_186_out,
       not_187_out, not_188_out, not_189_out, not_190_out, not_191_out, not_192_out, not_193_out,
       not_194_out, not_195_out, not_196_out, not_197_out, not_198_out, not_199_out, not_200_out,
       not_201_out, not_202_out, not_203_out, not_204_out, not_205_out, not_206_out, not_207_out,
       not_208_out, not_209_out, not_210_out, not_211_out, not_212_out, not_213_out, not_214_out,
       not_215_out, not_216_out, not_217_out, not_218_out, not_219_out, not_220_out, not_221_out,
       not_222_out, not_223_out, not_224_out, not_225_out, not_226_out, not_227_out, not_228_out, O_2_out,
       O_out, or_1_out, or_2_out, or_3_out, P_2_out, P_out, Q_2_out, Q_out, R_2_out, R_out, S_2_out, S_out,
       T_2_out, T_out, U_2_out, U_out, V_2_out, V_out, W_2_out, W_out, X_2_out, X_out, Y_2_out, Y_out,
       Z_2_out, Z_out;

  Clock clock_1 (.out(clock_1_out));
  not not_1 (out_68[6], j_k_ff_7_qn);
  J_K_Flip_Flop j_k_ff_1 (
    .J(1'b1), .clk(clock_1_out), .K(1'b1), .Q(j_k_ff_1_q), .Qn(j_k_ff_1_qn), .reset(Ignite_Reset));  // open: preset, en
  not not_2 (out_68[5], j_k_ff_6_qn);
  J_K_Flip_Flop j_k_ff_2 (
    .J(1'b1), .clk(j_k_ff_1_q), .K(1'b1), .Q(j_k_ff_2_q), .Qn(j_k_ff_2_qn), .reset(Ignite_Reset));  // open: preset, en
  not not_3 (out_68[4], j_k_ff_5_qn);
  not not_4 (out_68[3], j_k_ff_4_qn);
  not not_5 (out_68[2], j_k_ff_3_qn);
  J_K_Flip_Flop j_k_ff_3 (
    .J(1'b1), .clk(j_k_ff_2_q), .K(1'b1), .Q(j_k_ff_3_q), .Qn(j_k_ff_3_qn), .reset(Ignite_Reset));  // open: preset, en
  not not_6 (out_68[1], j_k_ff_2_qn);
  J_K_Flip_Flop j_k_ff_4 (
    .J(1'b1), .clk(j_k_ff_3_q), .K(1'b1), .Q(j_k_ff_4_q), .Qn(j_k_ff_4_qn), .reset(Ignite_Reset));  // open: preset, en
  not not_7 (out_68[0], j_k_ff_1_qn);
  not not_8 (not_8_out, out_68[0]);
  not not_9 (not_9_out, out_68[2]);
  not not_10 (not_10_out, out_68[3]);
  and B (B_out, not_8_out, out_68[1], not_9_out, not_10_out, not_11_out, not_12_out, out_68[6]);
  not not_11 (not_11_out, out_68[4]);
  not not_12 (not_12_out, out_68[5]);
  not not_13 (not_13_out, out_68[2]);
  and C (C_out, out_68[0], out_68[1], not_13_out, not_14_out, not_15_out, not_16_out, out_68[6]);
  not not_14 (not_14_out, out_68[3]);
  not not_15 (not_15_out, out_68[4]);
  not not_16 (not_16_out, out_68[5]);
  not not_17 (not_17_out, out_68[0]);
  not not_18 (not_18_out, out_68[1]);
  not not_19 (not_19_out, out_68[3]);
  and D (D_out, not_17_out, not_18_out, out_68[2], not_19_out, not_20_out, not_21_out, out_68[6]);
  not not_20 (not_20_out, out_68[4]);
  not not_21 (not_21_out, out_68[5]);
  not not_22 (not_22_out, out_68[1]);
  and E (E_out, out_68[0], not_22_out, out_68[2], not_23_out, not_24_out, not_25_out, out_68[6]);
  not not_23 (not_23_out, out_68[3]);
  not not_24 (not_24_out, out_68[4]);
  not not_25 (not_25_out, out_68[5]);
  not not_26 (not_26_out, out_68[0]);
  and F (F_out, not_26_out, out_68[1], out_68[2], not_27_out, not_28_out, not_29_out, out_68[6]);
  not not_27 (not_27_out, out_68[3]);
  not not_28 (not_28_out, out_68[4]);
  not not_29 (not_29_out, out_68[5]);
  and G (G_out, out_68[0], out_68[1], out_68[2], not_30_out, not_31_out, not_32_out, out_68[6]);
  not not_30 (not_30_out, out_68[3]);
  not not_31 (not_31_out, out_68[4]);
  not not_32 (not_32_out, out_68[5]);
  not not_33 (not_33_out, out_68[0]);
  not not_34 (not_34_out, out_68[1]);
  not not_35 (not_35_out, out_68[2]);
  and H (H_out, not_33_out, not_34_out, not_35_out, out_68[3], not_36_out, not_37_out, out_68[6]);
  not not_36 (not_36_out, out_68[4]);
  not not_37 (not_37_out, out_68[5]);
  not not_38 (not_38_out, out_68[1]);
  not not_39 (not_39_out, out_68[2]);
  and I (I_out, out_68[0], not_38_out, not_39_out, out_68[3], not_40_out, not_41_out, out_68[6]);
  not not_40 (not_40_out, out_68[4]);
  not not_41 (not_41_out, out_68[5]);
  not not_42 (not_42_out, out_68[0]);
  not not_43 (not_43_out, out_68[2]);
  and J (J_out, not_42_out, out_68[1], not_43_out, out_68[3], not_44_out, not_45_out, out_68[6]);
  not not_44 (not_44_out, out_68[4]);
  not not_45 (not_45_out, out_68[5]);
  not not_46 (not_46_out, out_68[2]);
  and J_2 (J_2_out, out_68[0], out_68[1], not_46_out, out_68[3], not_47_out, not_48_out, out_68[6]);
  not not_47 (not_47_out, out_68[4]);
  not not_48 (not_48_out, out_68[5]);
  not not_49 (not_49_out, out_68[0]);
  not not_50 (not_50_out, out_68[1]);
  and L (L_out, not_49_out, not_50_out, out_68[2], out_68[3], not_51_out, not_52_out, out_68[6]);
  not not_51 (not_51_out, out_68[4]);
  not not_52 (not_52_out, out_68[5]);
  not not_53 (not_53_out, out_68[1]);
  and M (M_out, out_68[0], not_53_out, out_68[2], out_68[3], not_54_out, not_55_out, out_68[6]);
  not not_54 (not_54_out, out_68[4]);
  not not_55 (not_55_out, out_68[5]);
  not not_56 (not_56_out, out_68[0]);
  and N (N_out, not_56_out, out_68[1], out_68[2], out_68[3], not_57_out, not_58_out, out_68[6]);
  not not_57 (not_57_out, out_68[4]);
  not not_58 (not_58_out, out_68[5]);
  and O (O_out, out_68[0], out_68[1], out_68[2], out_68[3], not_59_out, not_60_out, out_68[6]);
  not not_59 (not_59_out, out_68[4]);
  not not_60 (not_60_out, out_68[5]);
  not not_61 (not_61_out, out_68[0]);
  not not_62 (not_62_out, out_68[1]);
  not not_63 (not_63_out, out_68[2]);
  and P (P_out, not_61_out, not_62_out, not_63_out, not_64_out, out_68[4], not_65_out, out_68[6]);
  not not_64 (not_64_out, out_68[3]);
  not not_65 (not_65_out, out_68[5]);
  not not_66 (not_66_out, out_68[1]);
  not not_67 (not_67_out, out_68[2]);
  not not_68 (not_68_out, out_68[3]);
  and Q (Q_out, out_68[0], not_66_out, not_67_out, not_68_out, out_68[4], not_69_out, out_68[6]);
  not not_69 (not_69_out, out_68[5]);
  not not_70 (not_70_out, out_68[0]);
  not not_71 (not_71_out, out_68[2]);
  and R (R_out, not_70_out, out_68[1], not_71_out, not_72_out, out_68[4], not_73_out, out_68[6]);
  not not_72 (not_72_out, out_68[3]);
  not not_73 (not_73_out, out_68[5]);
  not not_74 (not_74_out, out_68[2]);
  and S (S_out, out_68[0], out_68[1], not_74_out, not_75_out, out_68[4], not_76_out, out_68[6]);
  not not_75 (not_75_out, out_68[3]);
  not not_76 (not_76_out, out_68[5]);
  not not_77 (not_77_out, out_68[0]);
  not not_78 (not_78_out, out_68[1]);
  not not_79 (not_79_out, out_68[3]);
  and T (T_out, not_77_out, not_78_out, out_68[2], not_79_out, out_68[4], not_80_out, out_68[6]);
  not not_80 (not_80_out, out_68[5]);
  not not_81 (not_81_out, out_68[1]);
  not not_82 (not_82_out, out_68[3]);
  and U (U_out, out_68[0], not_81_out, out_68[2], not_82_out, out_68[4], not_83_out, out_68[6]);
  not not_83 (not_83_out, out_68[5]);
  not not_84 (not_84_out, out_68[0]);
  not not_85 (not_85_out, out_68[3]);
  and V (V_out, not_84_out, out_68[1], out_68[2], not_85_out, out_68[4], not_86_out, out_68[6]);
  not not_86 (not_86_out, out_68[5]);
  and W (W_out, out_68[0], out_68[1], out_68[2], not_87_out, out_68[4], not_88_out, out_68[6]);
  not not_87 (not_87_out, out_68[3]);
  not not_88 (not_88_out, out_68[5]);
  not not_89 (not_89_out, out_68[0]);
  not not_90 (not_90_out, out_68[1]);
  not not_91 (not_91_out, out_68[2]);
  and X (X_out, not_89_out, not_90_out, not_91_out, out_68[3], out_68[4], not_92_out, out_68[6]);
  not not_92 (not_92_out, out_68[5]);
  not not_93 (not_93_out, out_68[1]);
  not not_94 (not_94_out, out_68[2]);
  and Y (Y_out, out_68[0], not_93_out, not_94_out, out_68[3], out_68[4], not_95_out, out_68[6]);
  not not_95 (not_95_out, out_68[5]);
  not not_96 (not_96_out, out_68[0]);
  not not_97 (not_97_out, out_68[2]);
  and Z (Z_out, not_96_out, out_68[1], not_97_out, out_68[3], out_68[4], not_98_out, out_68[6]);
  not not_98 (not_98_out, out_68[5]);
  // NOT_Gate not_99 has open pins: in=out_68[2], out=open
  // NOT_Gate not_100 has open pins: in=out_68[5], out=open
  not not_101 (not_101_out, out_68[1]);
  not not_102 (not_102_out, out_68[2]);
  not not_103 (not_103_out, out_68[3]);
  and A (A_out, out_68[0], not_101_out, not_102_out, not_103_out, not_104_out, not_105_out, out_68[6]);
  not not_104 (not_104_out, out_68[4]);
  not not_105 (not_105_out, out_68[5]);
  not not_106 (not_106_out, out_68[0]);
  not not_107 (not_107_out, out_68[1]);
  not not_108 (not_108_out, out_68[2]);
  not not_109 (not_109_out, out_68[3]);
  and \and  (and_out, not_106_out, not_107_out, not_108_out, not_109_out, not_110_out, out_68[5], not_111_out);
  not not_110 (not_110_out, out_68[4]);
  not not_111 (not_111_out, out_68[6]);
  not not_112 (not_112_out, out_68[0]);
  not not_113 (not_113_out, out_68[1]);
  not not_114 (not_114_out, out_68[2]);
  and DEL (DEL_out, not_112_out, not_113_out, not_114_out, out_68[3], not_115_out, not_116_out, not_117_out);
  not not_115 (not_115_out, out_68[4]);
  not not_116 (not_116_out, out_68[5]);
  not not_117 (not_117_out, out_68[6]);
  not not_118 (not_118_out, out_68[1]);
  not not_119 (not_119_out, out_68[2]);
  and A_2 (A_2_out, out_68[0], not_118_out, not_119_out, not_120_out, not_121_out, out_68[5], out_68[6]);
  not not_120 (not_120_out, out_68[3]);
  not not_121 (not_121_out, out_68[4]);
  not not_122 (not_122_out, out_68[0]);
  not not_123 (not_123_out, out_68[2]);
  not not_124 (not_124_out, out_68[3]);
  and B_2 (B_2_out, not_122_out, out_68[1], not_123_out, not_124_out, not_125_out, out_68[5], out_68[6]);
  not not_125 (not_125_out, out_68[4]);
  not not_126 (not_126_out, out_68[2]);
  not not_127 (not_127_out, out_68[3]);
  and C_2 (C_2_out, out_68[0], out_68[1], not_126_out, not_127_out, not_128_out, out_68[5], out_68[6]);
  not not_128 (not_128_out, out_68[4]);
  not not_129 (not_129_out, out_68[0]);
  not not_130 (not_130_out, out_68[1]);
  not not_131 (not_131_out, out_68[3]);
  and D_2 (D_2_out, not_129_out, not_130_out, out_68[2], not_131_out, not_132_out, out_68[5], out_68[6]);
  not not_132 (not_132_out, out_68[4]);
  not not_133 (not_133_out, out_68[1]);
  not not_134 (not_134_out, out_68[3]);
  and E_2 (E_2_out, out_68[0], not_133_out, out_68[2], not_134_out, not_135_out, out_68[5], out_68[6]);
  not not_135 (not_135_out, out_68[4]);
  not not_136 (not_136_out, out_68[0]);
  not not_137 (not_137_out, out_68[3]);
  and F_2 (F_2_out, not_136_out, out_68[1], out_68[2], not_137_out, not_138_out, out_68[5], out_68[6]);
  not not_138 (not_138_out, out_68[4]);
  not not_139 (not_139_out, out_68[3]);
  and G_2 (G_2_out, out_68[0], out_68[1], out_68[2], not_139_out, not_140_out, out_68[5], out_68[6]);
  not not_140 (not_140_out, out_68[4]);
  not not_141 (not_141_out, out_68[0]);
  not not_142 (not_142_out, out_68[1]);
  not not_143 (not_143_out, out_68[2]);
  and H_2 (H_2_out, not_141_out, not_142_out, not_143_out, out_68[3], not_144_out, out_68[5], out_68[6]);
  not not_144 (not_144_out, out_68[4]);
  not not_145 (not_145_out, out_68[1]);
  not not_146 (not_146_out, out_68[2]);
  and I_2 (I_2_out, out_68[0], not_145_out, not_146_out, out_68[3], not_147_out, out_68[5], out_68[6]);
  not not_147 (not_147_out, out_68[4]);
  not not_148 (not_148_out, out_68[0]);
  not not_149 (not_149_out, out_68[2]);
  and J_3 (J_3_out, not_148_out, out_68[1], not_149_out, out_68[3], not_150_out, out_68[5], out_68[6]);
  not not_150 (not_150_out, out_68[4]);
  not not_151 (not_151_out, out_68[2]);
  and u_K (K_out, out_68[0], out_68[1], not_151_out, out_68[3], not_152_out, out_68[5], out_68[6]);
  not not_152 (not_152_out, out_68[4]);
  not not_153 (not_153_out, out_68[0]);
  not not_154 (not_154_out, out_68[1]);
  and L_2 (L_2_out, not_153_out, not_154_out, out_68[2], out_68[3], not_155_out, out_68[5], out_68[6]);
  not not_155 (not_155_out, out_68[4]);
  not not_156 (not_156_out, out_68[1]);
  and M_2 (M_2_out, out_68[0], not_156_out, out_68[2], out_68[3], not_157_out, out_68[5], out_68[6]);
  not not_157 (not_157_out, out_68[4]);
  not not_158 (not_158_out, out_68[0]);
  and N_2 (N_2_out, not_158_out, out_68[1], out_68[2], out_68[3], not_159_out, out_68[5], out_68[6]);
  not not_159 (not_159_out, out_68[4]);
  and O_2 (O_2_out, out_68[0], out_68[1], out_68[2], out_68[3], not_160_out, out_68[5], out_68[6]);
  not not_160 (not_160_out, out_68[4]);
  not not_161 (not_161_out, out_68[0]);
  not not_162 (not_162_out, out_68[1]);
  not not_163 (not_163_out, out_68[2]);
  and P_2 (P_2_out, not_161_out, not_162_out, not_163_out, not_164_out, out_68[4], out_68[5], out_68[6]);
  not not_164 (not_164_out, out_68[3]);
  not not_165 (not_165_out, out_68[1]);
  not not_166 (not_166_out, out_68[2]);
  and Q_2 (Q_2_out, out_68[0], not_165_out, not_166_out, not_167_out, out_68[4], out_68[5], out_68[6]);
  not not_167 (not_167_out, out_68[3]);
  not not_168 (not_168_out, out_68[0]);
  not not_169 (not_169_out, out_68[2]);
  and R_2 (R_2_out, not_168_out, out_68[1], not_169_out, not_170_out, out_68[4], out_68[5], out_68[6]);
  not not_170 (not_170_out, out_68[3]);
  not not_171 (not_171_out, out_68[2]);
  and S_2 (S_2_out, out_68[0], out_68[1], not_171_out, not_172_out, out_68[4], out_68[5], out_68[6]);
  not not_172 (not_172_out, out_68[3]);
  not not_173 (not_173_out, out_68[0]);
  not not_174 (not_174_out, out_68[1]);
  and T_2 (T_2_out, not_173_out, not_174_out, out_68[2], not_175_out, out_68[4], out_68[5], out_68[6]);
  not not_175 (not_175_out, out_68[3]);
  not not_176 (not_176_out, out_68[1]);
  and U_2 (U_2_out, out_68[0], not_176_out, out_68[2], not_177_out, out_68[4], out_68[5], out_68[6]);
  not not_177 (not_177_out, out_68[3]);
  not not_178 (not_178_out, out_68[0]);
  not not_179 (not_179_out, out_68[3]);
  and V_2 (V_2_out, not_178_out, out_68[1], out_68[2], not_179_out, out_68[4], out_68[5], out_68[6]);
  not not_180 (not_180_out, out_68[3]);
  and W_2 (W_2_out, out_68[0], out_68[1], out_68[2], not_180_out, out_68[4], out_68[5], out_68[6]);
  not not_181 (not_181_out, out_68[0]);
  not not_182 (not_182_out, out_68[1]);
  not not_183 (not_183_out, out_68[2]);
  and X_2 (X_2_out, not_181_out, not_182_out, not_183_out, out_68[3], out_68[4], out_68[5], out_68[6]);
  not not_184 (not_184_out, out_68[1]);
  not not_185 (not_185_out, out_68[2]);
  and Y_2 (Y_2_out, out_68[0], not_184_out, not_185_out, out_68[3], out_68[4], out_68[5], out_68[6]);
  not not_186 (not_186_out, out_68[0]);
  not not_187 (not_187_out, out_68[2]);
  and Z_2 (Z_2_out, not_186_out, out_68[1], not_187_out, out_68[3], out_68[4], out_68[5], out_68[6]);
  not not_188 (not_188_out, out_68[0]);
  not not_189 (not_189_out, out_68[1]);
  not not_190 (not_190_out, out_68[2]);
  and _0 (_0_out, not_188_out, not_189_out, not_190_out, not_191_out, out_68[4], out_68[5], not_192_out);
  not not_191 (not_191_out, out_68[3]);
  not not_192 (not_192_out, out_68[6]);
  not not_193 (not_193_out, out_68[1]);
  not not_194 (not_194_out, out_68[2]);
  not not_195 (not_195_out, out_68[3]);
  and _1 (_1_out, out_68[0], not_193_out, not_194_out, not_195_out, out_68[4], out_68[5], not_196_out);
  not not_196 (not_196_out, out_68[6]);
  not not_197 (not_197_out, out_68[0]);
  not not_198 (not_198_out, out_68[2]);
  not not_199 (not_199_out, out_68[3]);
  and _2 (_2_out, not_197_out, out_68[1], not_198_out, not_199_out, out_68[4], out_68[5], not_200_out);
  not not_200 (not_200_out, out_68[6]);
  not not_201 (not_201_out, out_68[2]);
  and _3 (_3_out, out_68[0], out_68[1], not_201_out, not_202_out, out_68[4], out_68[5], not_203_out);
  not not_202 (not_202_out, out_68[3]);
  not not_203 (not_203_out, out_68[6]);
  not not_204 (not_204_out, out_68[0]);
  not not_205 (not_205_out, out_68[1]);
  not not_206 (not_206_out, out_68[3]);
  and _4 (_4_out, not_204_out, not_205_out, out_68[2], not_206_out, out_68[4], out_68[5], not_207_out);
  not not_207 (not_207_out, out_68[6]);
  not not_208 (not_208_out, out_68[1]);
  not not_209 (not_209_out, out_68[3]);
  and _5 (_5_out, out_68[0], not_208_out, out_68[2], not_209_out, out_68[4], out_68[5], not_210_out);
  not not_210 (not_210_out, out_68[6]);
  not not_211 (not_211_out, out_68[0]);
  and _6 (_6_out, not_211_out, out_68[1], out_68[2], not_212_out, out_68[4], out_68[5], not_213_out);
  not not_212 (not_212_out, out_68[3]);
  not not_213 (not_213_out, out_68[6]);
  and _7 (_7_out, out_68[0], out_68[1], out_68[2], not_214_out, out_68[4], out_68[5], not_215_out);
  not not_214 (not_214_out, out_68[3]);
  not not_215 (not_215_out, out_68[6]);
  not not_216 (not_216_out, out_68[0]);
  not not_217 (not_217_out, out_68[1]);
  not not_218 (not_218_out, out_68[2]);
  and _8 (_8_out, not_216_out, not_217_out, not_218_out, out_68[3], out_68[4], out_68[5], not_219_out);
  not not_219 (not_219_out, out_68[6]);
  not not_220 (not_220_out, out_68[1]);
  not not_221 (not_221_out, out_68[2]);
  and _9 (_9_out, out_68[0], not_220_out, not_221_out, out_68[3], out_68[4], out_68[5], not_222_out);
  not not_222 (not_222_out, out_68[6]);
  not not_223 (not_223_out, out_68[0]);
  not not_224 (not_224_out, out_68[2]);
  and ENT (ENT_out, not_223_out, out_68[1], not_224_out, out_68[3], not_225_out, not_226_out, not_227_out);
  not not_225 (not_225_out, out_68[4]);
  not not_226 (not_226_out, out_68[5]);
  not not_227 (not_227_out, out_68[6]);
  _1_bit_Memory u_1_bit_memory_1 (.in_1(in_2), .in_2(or_2_out), .out_3(n1_bit_memory_1_out_3));
  _1_bit_Memory u_1_bit_memory_2 (.in_1(in_3), .in_2(or_2_out), .out_3(n1_bit_memory_2_out_3));
  _1_bit_Memory u_1_bit_memory_3 (.in_1(in_4), .in_2(or_2_out), .out_3(n1_bit_memory_3_out_3));
  _1_bit_Memory u_1_bit_memory_4 (.in_1(in_5), .in_2(or_2_out), .out_3(n1_bit_memory_4_out_3));
  _1_bit_Memory u_1_bit_memory_5 (.in_1(in_6), .in_2(or_2_out), .out_3(n1_bit_memory_5_out_3));
  _1_bit_Memory u_1_bit_memory_6 (.in_1(in_7), .in_2(or_2_out), .out_3(n1_bit_memory_6_out_3));
  _1_bit_Memory u_1_bit_memory_7 (.in_1(in_8), .in_2(or_2_out), .out_3(n1_bit_memory_7_out_3));
  _1_bit_Memory u_1_bit_memory_8 (.in_1(in_9), .in_2(or_2_out), .out_3(n1_bit_memory_8_out_3));
  _1_bit_Memory u_1_bit_memory_9 (.in_1(in_10), .in_2(or_2_out), .out_3(n1_bit_memory_9_out_3));
  _1_bit_Memory u_1_bit_memory_10 (.in_1(K), .in_2(or_2_out), .out_3(n1_bit_memory_10_out_3));
  _1_bit_Memory u_1_bit_memory_11 (.in_1(in_12), .in_2(or_2_out), .out_3(n1_bit_memory_11_out_3));
  _1_bit_Memory u_1_bit_memory_12 (.in_1(in_13), .in_2(or_2_out), .out_3(n1_bit_memory_12_out_3));
  _1_bit_Memory u_1_bit_memory_13 (.in_1(in_14), .in_2(or_2_out), .out_3(n1_bit_memory_13_out_3));
  _1_bit_Memory u_1_bit_memory_14 (.in_1(in_15), .in_2(or_2_out), .out_3(n1_bit_memory_14_out_3));
  _1_bit_Memory u_1_bit_memory_15 (.in_1(in_16), .in_2(or_2_out), .out_3(n1_bit_memory_15_out_3));
  _1_bit_Memory u_1_bit_memory_16 (.in_1(in_17), .in_2(or_2_out), .out_3(n1_bit_memory_16_out_3));
  _1_bit_Memory u_1_bit_memory_17 (.in_1(in_18), .in_2(or_2_out), .out_3(n1_bit_memory_17_out_3));
  _1_bit_Memory u_1_bit_memory_18 (.in_1(in_19), .in_2(or_2_out), .out_3(n1_bit_memory_18_out_3));
  _1_bit_Memory u_1_bit_memory_19 (.in_1(in_20), .in_2(or_2_out), .out_3(n1_bit_memory_19_out_3));
  _1_bit_Memory u_1_bit_memory_20 (.in_1(in_21), .in_2(or_2_out), .out_3(n1_bit_memory_20_out_3));
  _1_bit_Memory u_1_bit_memory_21 (.in_1(in_22), .in_2(or_2_out), .out_3(n1_bit_memory_21_out_3));
  _1_bit_Memory u_1_bit_memory_22 (.in_1(in_23), .in_2(or_2_out), .out_3(n1_bit_memory_22_out_3));
  _1_bit_Memory u_1_bit_memory_23 (.in_1(in_24), .in_2(or_2_out), .out_3(n1_bit_memory_23_out_3));
  _1_bit_Memory u_1_bit_memory_24 (.in_1(in_25), .in_2(or_2_out), .out_3(n1_bit_memory_24_out_3));
  _1_bit_Memory u_1_bit_memory_25 (.in_1(in_26), .in_2(or_2_out), .out_3(n1_bit_memory_25_out_3));
  _1_bit_Memory u_1_bit_memory_26 (.in_1(in_27), .in_2(or_2_out), .out_3(n1_bit_memory_26_out_3));
  _1_bit_Memory u_1_bit_memory_27 (.in_1(in_28), .in_2(or_2_out), .out_3(n1_bit_memory_27_out_3));
  _1_bit_Memory u_1_bit_memory_28 (.in_1(in_29), .in_2(or_2_out), .out_3(n1_bit_memory_28_out_3));
  not not_228 (not_228_out, in_30);
  _1_bit_Memory u_1_bit_memory_29 (.in_1(in_31), .in_2(or_2_out), .out_3(n1_bit_memory_29_out_3));
  _1_bit_Memory u_1_bit_memory_30 (.in_1(in_32), .in_2(or_2_out), .out_3(n1_bit_memory_30_out_3));
  _1_bit_Memory u_1_bit_memory_31 (.in_1(in_33), .in_2(or_2_out), .out_3(n1_bit_memory_31_out_3));
  _1_bit_Memory u_1_bit_memory_32 (.in_1(in_34), .in_2(or_2_out), .out_3(n1_bit_memory_32_out_3));
  _1_bit_Memory u_1_bit_memory_33 (.in_1(in_35), .in_2(or_2_out), .out_3(n1_bit_memory_33_out_3));
  _1_bit_Memory u_1_bit_memory_34 (.in_1(in_36), .in_2(or_2_out), .out_3(n1_bit_memory_34_out_3));
  _1_bit_Memory u_1_bit_memory_35 (.in_1(in_37), .in_2(or_2_out), .out_3(n1_bit_memory_35_out_3));
  _1_bit_Memory u_1_bit_memory_36 (.in_1(in_38), .in_2(or_2_out), .out_3(n1_bit_memory_36_out_3));
  _1_bit_Memory u_1_bit_memory_37 (.in_1(in_39), .in_2(or_2_out), .out_3(n1_bit_memory_37_out_3));
  _1_bit_Memory u_1_bit_memory_38 (.in_1(in_40), .in_2(or_2_out), .out_3(n1_bit_memory_38_out_3));
  _1_bit_Memory u_1_bit_memory_39 (.in_1(in_41), .in_2(or_2_out), .out_3(n1_bit_memory_39_out_3));
  _1_bit_Memory u_1_bit_memory_40 (.in_1(in_42), .in_2(or_2_out), .out_3(n1_bit_memory_40_out_3));
  _1_bit_Memory u_1_bit_memory_41 (.in_1(in_43), .in_2(or_2_out), .out_3(n1_bit_memory_41_out_3));
  _1_bit_Memory u_1_bit_memory_42 (.in_1(in_44), .in_2(or_2_out), .out_3(n1_bit_memory_42_out_3));
  _1_bit_Memory u_1_bit_memory_43 (.in_1(in_45), .in_2(or_2_out), .out_3(n1_bit_memory_43_out_3));
  _1_bit_Memory u_1_bit_memory_44 (.in_1(in_46), .in_2(or_2_out), .out_3(n1_bit_memory_44_out_3));
  _1_bit_Memory u_1_bit_memory_45 (.in_1(in_47), .in_2(or_2_out), .out_3(n1_bit_memory_45_out_3));
  _1_bit_Memory u_1_bit_memory_46 (.in_1(in_48), .in_2(or_2_out), .out_3(n1_bit_memory_46_out_3));
  _1_bit_Memory u_1_bit_memory_47 (.in_1(in_49), .in_2(or_2_out), .out_3(n1_bit_memory_47_out_3));
  _1_bit_Memory u_1_bit_memory_48 (.in_1(in_50), .in_2(or_2_out), .out_3(n1_bit_memory_48_out_3));
  _1_bit_Memory u_1_bit_memory_49 (.in_1(in_51), .in_2(or_2_out), .out_3(n1_bit_memory_49_out_3));
  _1_bit_Memory u_1_bit_memory_50 (.in_1(in_52), .in_2(or_2_out), .out_3(n1_bit_memory_50_out_3));
  _1_bit_Memory u_1_bit_memory_51 (.in_1(in_53), .in_2(or_2_out), .out_3(n1_bit_memory_51_out_3));
  _1_bit_Memory u_1_bit_memory_52 (.in_1(in_54), .in_2(or_2_out), .out_3(n1_bit_memory_52_out_3));
  _1_bit_Memory u_1_bit_memory_53 (.in_1(in_55), .in_2(or_2_out), .out_3(n1_bit_memory_53_out_3));
  _1_bit_Memory u_1_bit_memory_54 (.in_1(in_56), .in_2(or_2_out), .out_3(n1_bit_memory_54_out_3));
  _1_bit_Memory u_1_bit_memory_55 (.in_1(in_57), .in_2(or_2_out), .out_3(n1_bit_memory_55_out_3));
  _1_bit_Memory u_1_bit_memory_56 (.in_1(in_58), .in_2(or_2_out), .out_3(n1_bit_memory_56_out_3));
  _1_bit_Memory u_1_bit_memory_57 (.in_1(in_59), .in_2(or_2_out), .out_3(n1_bit_memory_57_out_3));
  _1_bit_Memory u_1_bit_memory_58 (.in_1(in_60), .in_2(or_2_out), .out_3(n1_bit_memory_58_out_3));
  _1_bit_Memory u_1_bit_memory_59 (.in_1(in_61), .in_2(or_2_out), .out_3(n1_bit_memory_59_out_3));
  _1_bit_Memory u_1_bit_memory_60 (.in_1(in_62), .in_2(or_2_out), .out_3(n1_bit_memory_60_out_3));
  _1_bit_Memory u_1_bit_memory_61 (.in_1(in_63), .in_2(or_2_out), .out_3(n1_bit_memory_61_out_3));
  _1_bit_Memory u_1_bit_memory_62 (.in_1(in_64), .in_2(or_2_out), .out_3(n1_bit_memory_62_out_3));
  _1_bit_Memory u_1_bit_memory_63 (.in_1(in_65), .in_2(or_2_out), .out_3(n1_bit_memory_63_out_3));
  _1_bit_Memory u_1_bit_memory_64 (.in_1(in_66), .in_2(or_2_out), .out_3(n1_bit_memory_64_out_3));
  _1_bit_Memory u_1_bit_memory_65 (.in_1(in_67), .in_2(or_2_out), .out_3(n1_bit_memory_65_out_3));
  J_K_Flip_Flop j_k_ff_5 (
    .J(1'b1), .clk(j_k_ff_4_q), .K(1'b1), .Q(j_k_ff_5_q), .Qn(j_k_ff_5_qn), .reset(Ignite_Reset));  // open: preset, en
  and and_2 (and_2_out, B_out, in_30, n1_bit_memory_1_out_3);
  and and_3 (and_3_out, C_out, in_30, n1_bit_memory_2_out_3);
  and and_4 (and_4_out, D_out, in_30, n1_bit_memory_3_out_3);
  and and_5 (and_5_out, E_out, in_30, n1_bit_memory_4_out_3);
  and and_6 (and_6_out, F_out, in_30, n1_bit_memory_5_out_3);
  and and_7 (and_7_out, G_out, in_30, n1_bit_memory_6_out_3);
  and and_8 (and_8_out, H_out, in_30, n1_bit_memory_7_out_3);
  and and_9 (and_9_out, I_out, in_30, n1_bit_memory_8_out_3);
  and and_10 (and_10_out, J_out, in_30, n1_bit_memory_9_out_3);
  and and_11 (and_11_out, J_2_out, in_30, n1_bit_memory_10_out_3);
  and and_12 (and_12_out, L_out, in_30, n1_bit_memory_11_out_3);
  and and_13 (and_13_out, M_out, in_30, n1_bit_memory_12_out_3);
  and and_14 (and_14_out, N_out, in_30, n1_bit_memory_13_out_3);
  and and_15 (and_15_out, O_out, in_30, n1_bit_memory_14_out_3);
  and and_16 (and_16_out, P_out, in_30, n1_bit_memory_15_out_3);
  and and_17 (and_17_out, Q_out, in_30, n1_bit_memory_16_out_3);
  and and_18 (and_18_out, R_out, in_30, n1_bit_memory_17_out_3);
  and and_19 (and_19_out, S_out, in_30, n1_bit_memory_18_out_3);
  and and_20 (and_20_out, T_out, in_30, n1_bit_memory_19_out_3);
  and and_21 (and_21_out, U_out, in_30, n1_bit_memory_20_out_3);
  and and_22 (and_22_out, V_out, in_30, n1_bit_memory_21_out_3);
  and and_23 (and_23_out, W_out, in_30, n1_bit_memory_22_out_3);
  and and_24 (and_24_out, X_out, in_30, n1_bit_memory_23_out_3);
  and and_25 (and_25_out, Y_out, in_30, n1_bit_memory_24_out_3);
  and and_26 (and_26_out, Z_out, in_30, n1_bit_memory_25_out_3);
  and and_27 (and_27_out, A_out, in_30, n1_bit_memory_26_out_3);
  and and_28 (and_28_out, and_out, n1_bit_memory_27_out_3);
  and and_29 (and_29_out, DEL_out, n1_bit_memory_28_out_3);
  and and_30 (and_30_out, A_2_out, not_228_out, n1_bit_memory_29_out_3);
  and and_31 (and_31_out, B_2_out, not_228_out, n1_bit_memory_30_out_3);
  and and_32 (and_32_out, C_2_out, not_228_out, n1_bit_memory_31_out_3);
  and and_33 (and_33_out, D_2_out, not_228_out, n1_bit_memory_32_out_3);
  and and_34 (and_34_out, E_2_out, not_228_out, n1_bit_memory_33_out_3);
  and and_35 (and_35_out, F_2_out, not_228_out, n1_bit_memory_34_out_3);
  and and_36 (and_36_out, G_2_out, not_228_out, n1_bit_memory_35_out_3);
  and and_37 (and_37_out, H_2_out, not_228_out, n1_bit_memory_36_out_3);
  and and_38 (and_38_out, I_2_out, not_228_out, n1_bit_memory_37_out_3);
  and and_39 (and_39_out, J_3_out, not_228_out, n1_bit_memory_38_out_3);
  and and_40 (and_40_out, K_out, not_228_out, n1_bit_memory_39_out_3);
  and and_41 (and_41_out, L_2_out, not_228_out, n1_bit_memory_40_out_3);
  and and_42 (and_42_out, M_2_out, not_228_out, n1_bit_memory_41_out_3);
  and and_43 (and_43_out, N_2_out, not_228_out, n1_bit_memory_42_out_3);
  and and_44 (and_44_out, O_2_out, not_228_out, n1_bit_memory_43_out_3);
  and and_45 (and_45_out, P_2_out, not_228_out, n1_bit_memory_44_out_3);
  and and_46 (and_46_out, Q_2_out, not_228_out, n1_bit_memory_45_out_3);
  and and_47 (and_47_out, R_2_out, not_228_out, n1_bit_memory_46_out_3);
  and and_48 (and_48_out, S_2_out, not_228_out, n1_bit_memory_47_out_3);
  and and_49 (and_49_out, T_2_out, not_228_out, n1_bit_memory_48_out_3);
  and and_50 (and_50_out, U_2_out, not_228_out, n1_bit_memory_49_out_3);
  and and_51 (and_51_out, V_2_out, not_228_out, n1_bit_memory_50_out_3);
  and and_52 (and_52_out, W_2_out, not_228_out, n1_bit_memory_51_out_3);
  and and_53 (and_53_out, X_2_out, not_228_out, n1_bit_memory_52_out_3);
  and and_54 (and_54_out, Y_2_out, not_228_out, n1_bit_memory_53_out_3);
  and and_55 (and_55_out, Z_2_out, not_228_out, n1_bit_memory_54_out_3);
  and and_56 (and_56_out, _0_out, n1_bit_memory_55_out_3);
  and and_57 (and_57_out, _1_out, n1_bit_memory_56_out_3);
  and and_58 (and_58_out, _2_out, n1_bit_memory_57_out_3);
  and and_59 (and_59_out, _3_out, n1_bit_memory_58_out_3);
  and and_60 (and_60_out, _4_out, n1_bit_memory_59_out_3);
  and and_61 (and_61_out, _5_out, n1_bit_memory_60_out_3);
  and and_62 (and_62_out, _6_out, n1_bit_memory_61_out_3);
  and and_63 (and_63_out, _7_out, n1_bit_memory_62_out_3);
  and and_64 (and_64_out, _8_out, n1_bit_memory_63_out_3);
  and and_65 (and_65_out, _9_out, n1_bit_memory_64_out_3);
  and and_66 (and_66_out, ENT_out, n1_bit_memory_65_out_3);
  J_K_Flip_Flop j_k_ff_6 (
    .J(1'b1), .clk(j_k_ff_5_q), .K(1'b1), .Q(j_k_ff_6_q), .Qn(j_k_ff_6_qn), .reset(Ignite_Reset));  // open: preset, en
  J_K_Flip_Flop j_k_ff_7 (
    .J(1'b1), .clk(j_k_ff_6_q), .K(1'b1), .Qn(j_k_ff_7_qn), .reset(Ignite_Reset));  // open: Q, preset, en
  or or_1 (or_1_out, and_2_out, and_3_out, and_4_out, and_5_out, and_6_out, and_7_out, and_8_out, and_9_out, and_10_out, and_11_out, and_12_out, and_13_out, and_14_out, and_15_out, and_16_out, and_17_out, and_18_out, and_19_out, and_20_out, and_21_out, and_22_out, and_23_out, and_24_out, and_25_out, and_26_out, and_27_out);
  or or_2 (or_2_out, Ignite_Reset, out_69);
  or or_3 (or_3_out, or_1_out, and_28_out, and_29_out, and_30_out, and_31_out, and_32_out, and_33_out, and_34_out, and_35_out, and_36_out, and_37_out, and_38_out, and_39_out, and_40_out, and_41_out, and_42_out, and_43_out, and_44_out, and_45_out, and_46_out, and_47_out, and_48_out, and_49_out, and_50_out, and_51_out, and_52_out, and_53_out, and_54_out, and_55_out);
  or or_4 (out_69, and_60_out, or_3_out, and_56_out, and_57_out, and_58_out, and_59_out, and_61_out, and_62_out, and_63_out, and_64_out, and_65_out, and_66_out);
endmodule

module _1_bit_Memory_falling_edge (
  input  in_1,
  input  in_2,
  output out_3
);

  wire n1_bit_memory_1_out_3;

  _1_bit_Memory u_1_bit_memory_1 (.in_1(in_1), .in_2(out_3), .out_3(n1_bit_memory_1_out_3));
  S_R_Flip_Flop #(.trigger("falling")) s_r_ff_1 (
    .S(n1_bit_memory_1_out_3), .clk(in_1), .R(in_2), .Q(out_3), .reset(in_2));  // open: Qn, preset, en
endmodule

module _3_Letter_Command (
  input  CMD,
  input  EQL,
  input  in_3,
  input  in_4,
  input  in_5,
  output out_6
);

  wire and_1_out, and_2_out, and_3_out, and_4_out, and_5_out, and_6_out, n1_bit_memory_1_out_3,
       n1_bit_memory_2_out_3, n1_bit_memory_3_out_3, n1_bit_memory_4_out_3, n1_bit_memory_5_out_3;

  _1_bit_Memory u_1_bit_memory_1 (.in_1(in_3), .in_2(EQL), .out_3(n1_bit_memory_1_out_3));
  _1_bit_Memory u_1_bit_memory_2 (.in_1(in_4), .in_2(EQL), .out_3(n1_bit_memory_2_out_3));
  and and_1 (and_1_out, n1_bit_memory_1_out_3, in_4);
  and and_2 (and_2_out, n1_bit_memory_1_out_3, n1_bit_memory_2_out_3, in_5);
  and and_3 (and_3_out, CMD, in_3);
  and and_4 (and_4_out, CMD, and_1_out);
  and and_5 (and_5_out, CMD, and_2_out);
  _1_bit_Memory u_1_bit_memory_3 (.in_1(and_3_out), .in_2(EQL), .out_3(n1_bit_memory_3_out_3));
  _1_bit_Memory u_1_bit_memory_4 (.in_1(and_4_out), .in_2(EQL), .out_3(n1_bit_memory_4_out_3));
  _1_bit_Memory u_1_bit_memory_5 (.in_1(and_5_out), .in_2(EQL), .out_3(n1_bit_memory_5_out_3));
  and and_6 (and_6_out, n1_bit_memory_3_out_3, n1_bit_memory_4_out_3, n1_bit_memory_5_out_3);
  _1_bit_Memory u_1_bit_memory_6 (.in_1(and_6_out), .in_2(EQL), .out_3(out_6));
endmodule

module Double_letter_CMD (
  input  CMD,
  input  EQL,
  input  in_3,
  input  in_4,
  output out_5
);

  wire and_1_out, and_2_out, and_3_out, and_4_out, and_5_out, and_6_out, n1_bit_memory_1_out_3,
       n1_bit_memory_2_out_3, n1_bit_memory_3_out_3, n1_bit_memory_falling_edge_1_out_3, or_1_out;

  _1_bit_Memory_falling_edge u_1_bit_memory_falling_edge_1 (
    .in_1(in_4), .in_2(or_1_out), .out_3(n1_bit_memory_falling_edge_1_out_3));
  or or_1 (or_1_out, and_4_out, EQL);
  and and_1 (and_1_out, n1_bit_memory_falling_edge_1_out_3, in_4);
  and and_2 (and_2_out, CMD, in_3);
  and and_3 (and_3_out, CMD, n1_bit_memory_falling_edge_1_out_3);
  and and_4 (and_4_out, CMD, and_1_out);
  _1_bit_Memory u_1_bit_memory_1 (.in_1(and_2_out), .in_2(EQL), .out_3(n1_bit_memory_1_out_3));
  _1_bit_Memory u_1_bit_memory_2 (.in_1(and_3_out), .in_2(EQL), .out_3(n1_bit_memory_2_out_3));
  _1_bit_Memory u_1_bit_memory_3 (.in_1(and_4_out), .in_2(EQL), .out_3(n1_bit_memory_3_out_3));
  and and_5 (and_5_out, n1_bit_memory_1_out_3, n1_bit_memory_2_out_3);
  and and_6 (and_6_out, and_5_out, n1_bit_memory_3_out_3);
  _1_bit_Memory u_1_bit_memory_4 (.in_1(and_6_out), .in_2(EQL), .out_3(out_5));
endmodule

module Equals (
  input  CMD,
  input  in_2,
  input  in_3,
  input  in_4,
  input  RESET,
  output out_6
);

  wire and_1_out, and_2_out, and_3_out, and_4_out, and_5_out, and_6_out, n1_bit_memory_1_out_3,
       n1_bit_memory_2_out_3, n1_bit_memory_3_out_3, n1_bit_memory_4_out_3, n1_bit_memory_5_out_3, or_1_out;

  _1_bit_Memory u_1_bit_memory_1 (.in_1(in_2), .in_2(or_1_out), .out_3(n1_bit_memory_1_out_3));
  _1_bit_Memory u_1_bit_memory_2 (.in_1(in_3), .in_2(or_1_out), .out_3(n1_bit_memory_2_out_3));
  and and_1 (and_1_out, n1_bit_memory_1_out_3, in_3);
  and and_2 (and_2_out, n1_bit_memory_1_out_3, n1_bit_memory_2_out_3, in_4);
  and and_3 (and_3_out, CMD, in_2);
  and and_4 (and_4_out, CMD, and_1_out);
  and and_5 (and_5_out, CMD, and_2_out);
  _1_bit_Memory u_1_bit_memory_3 (.in_1(and_3_out), .in_2(or_1_out), .out_3(n1_bit_memory_3_out_3));
  _1_bit_Memory u_1_bit_memory_4 (.in_1(and_4_out), .in_2(or_1_out), .out_3(n1_bit_memory_4_out_3));
  _1_bit_Memory u_1_bit_memory_5 (.in_1(and_5_out), .in_2(or_1_out), .out_3(n1_bit_memory_5_out_3));
  and and_6 (and_6_out, n1_bit_memory_3_out_3, n1_bit_memory_4_out_3, n1_bit_memory_5_out_3);
  _1_bit_Memory u_1_bit_memory_6 (.in_1(and_6_out), .in_2(or_1_out), .out_3(out_6));
  or or_1 (or_1_out, out_6, RESET);
endmodule

module Keyboard_Commands (
  input  RESET,
  input  EQL_RESET,
  input  A,
  input  B,
  input  D,
  input  E,
  input  I,
  input  L,
  input  M,
  input  Q,
  input  S,
  input  U,
  input  V,
  input  CMD,
  output out_15,
  output out_16,
  output out_17,
  output out_18,
  output out_19
);

  wire or_1_out;

  Double_letter_CMD ADD (.CMD(CMD), .EQL(or_1_out), .in_3(A), .in_4(D), .out_5(out_15));
  _3_Letter_Command SUB (.CMD(CMD), .EQL(or_1_out), .in_3(S), .in_4(U), .in_5(B), .out_6(out_16));
  _3_Letter_Command MUL (.CMD(CMD), .EQL(or_1_out), .in_3(M), .in_4(U), .in_5(L), .out_6(out_17));
  _3_Letter_Command DIV (.CMD(CMD), .EQL(or_1_out), .in_3(D), .in_4(I), .in_5(V), .out_6(out_18));
  Equals EQL (.CMD(CMD), .in_2(E), .in_3(Q), .in_4(L), .RESET(EQL_RESET), .out_6(out_19));
  or or_1 (or_1_out, out_19, RESET);
endmodule

module _16bit_Adder (
  input  in_1,
  input  in_2,
  input  in_3,
  input  in_4,
  input  in_5,
  input  in_6,
  input  in_7,
  input  in_8,
  input  in_9,
  input  in_10,
  input  in_11,
  input  in_12,
  input  in_13,
  input  in_14,
  input  in_15,
  input  in_16,
  input  in_17,
  input  in_18,
  input  in_19,
  input  in_20,
  input  in_21,
  input  in_22,
  input  in_23,
  input  in_24,
  input  in_25,
  input  in_26,
  input  in_27,
  input  in_28,
  input  in_29,
  input  in_30,
  input  in_31,
  input  in_32,
  output out_33,
  output out_34,
  output out_35,
  output out_36,
  output out_37,
  output out_38,
  output out_39,
  output out_40,
  output out_41,
  output out_42,
  output out_43,
  output out_44,
  output out_45,
  output out_46,
  output out_47,
  output out_48,
  output out_49
);

  wire adder_2_cout, adder_3_cout, adder_4_cout, adder_5_cout, adder_6_cout, adder_7_cout, adder_8_cout,
       adder_9_cout, adder_10_cout, adder_11_cout, adder_12_cout, adder_13_cout, adder_14_cout,
       adder_15_cout, adder_16_cout;

  Adder_part #(.width(1)) adder_1 (.a(in_32), .b(in_16), .out(out_34), .cin(adder_2_cout), .cout(out_33));
  Adder_part #(.width(1)) adder_2 (.a(in_31), .b(in_15), .out(out_35), .cin(adder_3_cout), .cout(adder_2_cout));
  Adder_part #(.width(1)) adder_3 (.a(in_30), .b(in_14), .out(out_36), .cin(adder_4_cout), .cout(adder_3_cout));
  Adder_part #(.width(1)) adder_4 (.a(in_29), .b(in_13), .out(out_37), .cin(adder_5_cout), .cout(adder_4_cout));
  Adder_part #(.width(1)) adder_5 (.a(in_28), .b(in_12), .out(out_38), .cin(adder_6_cout), .cout(adder_5_cout));
  Adder_part #(.width(1)) adder_6 (.a(in_27), .b(in_11), .out(out_39), .cin(adder_7_cout), .cout(adder_6_cout));
  Adder_part #(.width(1)) adder_7 (.a(in_26), .b(in_10), .out(out_40), .cin(adder_8_cout), .cout(adder_7_cout));
  Adder_part #(.width(1)) adder_8 (.a(in_25), .b(in_9), .out(out_41), .cin(adder_9_cout), .cout(adder_8_cout));
  Adder_part #(.width(1)) adder_9 (.a(in_24), .b(in_8), .out(out_42), .cin(adder_10_cout), .cout(adder_9_cout));
  Adder_part #(.width(1)) adder_10 (.a(in_23), .b(in_7), .out(out_43), .cin(adder_11_cout), .cout(adder_10_cout));
  Adder_part #(.width(1)) adder_11 (.a(in_22), .b(in_6), .out(out_44), .cin(adder_12_cout), .cout(adder_11_cout));
  Adder_part #(.width(1)) adder_12 (.a(in_21), .b(in_5), .out(out_45), .cin(adder_13_cout), .cout(adder_12_cout));
  Adder_part #(.width(1)) adder_13 (.a(in_20), .b(in_4), .out(out_46), .cin(adder_14_cout), .cout(adder_13_cout));
  Adder_part #(.width(1)) adder_14 (.a(in_19), .b(in_3), .out(out_47), .cin(adder_15_cout), .cout(adder_14_cout));
  Adder_part #(.width(1)) adder_15 (.a(in_18), .b(in_2), .out(out_48), .cin(adder_16_cout), .cout(adder_15_cout));
  Adder_part #(.width(1)) adder_16 (.a(in_17), .b(in_1), .out(out_49), .cout(adder_16_cout));  // open: cin
endmodule

module _17bit_Adder (
  input  in_1,
  input  in_2,
  input  in_3,
  input  in_4,
  input  in_5,
  input  in_6,
  input  in_7,
  input  in_8,
  input  in_9,
  input  in_10,
  input  in_11,
  input  in_12,
  input  in_13,
  input  in_14,
  input  in_15,
  input  in_16,
  input  in_17,
  input  in_18,
  input  in_19,
  input  in_20,
  input  in_21,
  input  in_22,
  input  in_23,
  input  in_24,
  input  in_25,
  input  in_26,
  input  in_27,
  input  in_28,
  input  in_29,
  input  in_30,
  input  in_31,
  input  in_32,
  input  in_33,
  input  in_34,
  output out_35,
  output out_36,
  output out_37,
  output out_38,
  output out_39,
  output out_40,
  output out_41,
  output out_42,
  output out_43,
  output out_44,
  output out_45,
  output out_46,
  output out_47,
  output out_48,
  output out_49,
  output out_50,
  output out_51,
  output out_52
);

  wire adder_2_cout, adder_3_cout, adder_4_cout, adder_5_cout, adder_6_cout, adder_7_cout, adder_8_cout,
       adder_9_cout, adder_10_cout, adder_11_cout, adder_12_cout, adder_13_cout, adder_14_cout,
       adder_15_cout, adder_16_cout, adder_17_cout;

  Adder_part #(.width(1)) adder_1 (.a(in_34), .b(in_17), .out(out_36), .cin(adder_2_cout), .cout(out_35));
  Adder_part #(.width(1)) adder_2 (.a(in_33), .b(in_16), .out(out_37), .cin(adder_3_cout), .cout(adder_2_cout));
  Adder_part #(.width(1)) adder_3 (.a(in_32), .b(in_15), .out(out_38), .cin(adder_4_cout), .cout(adder_3_cout));
  Adder_part #(.width(1)) adder_4 (.a(in_31), .b(in_14), .out(out_39), .cin(adder_5_cout), .cout(adder_4_cout));
  Adder_part #(.width(1)) adder_5 (.a(in_30), .b(in_13), .out(out_40), .cin(adder_6_cout), .cout(adder_5_cout));
  Adder_part #(.width(1)) adder_6 (.a(in_29), .b(in_12), .out(out_41), .cin(adder_7_cout), .cout(adder_6_cout));
  Adder_part #(.width(1)) adder_7 (.a(in_28), .b(in_11), .out(out_42), .cin(adder_8_cout), .cout(adder_7_cout));
  Adder_part #(.width(1)) adder_8 (.a(in_27), .b(in_10), .out(out_43), .cin(adder_9_cout), .cout(adder_8_cout));
  Adder_part #(.width(1)) adder_9 (.a(in_26), .b(in_9), .out(out_44), .cin(adder_10_cout), .cout(adder_9_cout));
  Adder_part #(.width(1)) adder_10 (.a(in_25), .b(in_8), .out(out_45), .cin(adder_11_cout), .cout(adder_10_cout));
  Adder_part #(.width(1)) adder_11 (.a(in_24), .b(in_7), .out(out_46), .cin(adder_12_cout), .cout(adder_11_cout));
  Adder_part #(.width(1)) adder_12 (.a(in_23), .b(in_6), .out(out_47), .cin(adder_13_cout), .cout(adder_12_cout));
  Adder_part #(.width(1)) adder_13 (.a(in_22), .b(in_5), .out(out_48), .cin(adder_14_cout), .cout(adder_13_cout));
  Adder_part #(.width(1)) adder_14 (.a(in_21), .b(in_4), .out(out_49), .cin(adder_15_cout), .cout(adder_14_cout));
  Adder_part #(.width(1)) adder_15 (.a(in_20), .b(in_3), .out(out_50), .cin(adder_16_cout), .cout(adder_15_cout));
  Adder_part #(.width(1)) adder_16 (.a(in_19), .b(in_2), .out(out_51), .cin(adder_17_cout), .cout(adder_16_cout));
  Adder_part #(.width(1)) adder_17 (.a(in_18), .b(in_1), .out(out_52), .cout(adder_17_cout));  // open: cin
endmodule

module _18bit_Adder (
  input  in_1,
  input  in_2,
  input  in_3,
  input  in_4,
  input  in_5,
  input  in_6,
  input  in_7,
  input  in_8,
  input  in_9,
  input  in_10,
  input  in_11,
  input  in_12,
  input  in_13,
  input  in_14,
  input  in_15,
  input  in_16,
  input  in_17,
  input  in_18,
  input  in_19,
  input  in_20,
  input  in_21,
  input  in_22,
  input  in_23,
  input  in_24,
  input  in_25,
  input  in_26,
  input  in_27,
  input  in_28,
  input  in_29,
  input  in_30,
  input  in_31,
  input  in_32,
  input  in_33,
  input  in_34,
  input  in_35,
  input  in_36,
  output out_37,
  output out_38,
  output out_39,
  output out_40,
  output out_41,
  output out_42,
  output out_43,
  output out_44,
  output out_45,
  output out_46,
  output out_47,
  output out_48,
  output out_49,
  output out_50,
  output out_51,
  output out_52,
  output out_53,
  output out_54,
  output out_55
);

  wire adder_2_cout, adder_3_cout, adder_4_cout, adder_5_cout, adder_6_cout, adder_7_cout, adder_8_cout,
       adder_9_cout, adder_10_cout, adder_11_cout, adder_12_cout, adder_13_cout, adder_14_cout,
       adder_15_cout, adder_16_cout, adder_17_cout, adder_18_cout;

  Adder_part #(.width(1)) adder_1 (.a(in_36), .b(in_18), .out(out_38), .cin(adder_2_cout), .cout(out_37));
  Adder_part #(.width(1)) adder_2 (.a(in_35), .b(in_17), .out(out_39), .cin(adder_3_cout), .cout(adder_2_cout));
  Adder_part #(.width(1)) adder_3 (.a(in_34), .b(in_16), .out(out_40), .cin(adder_4_cout), .cout(adder_3_cout));
  Adder_part #(.width(1)) adder_4 (.a(in_33), .b(in_15), .out(out_41), .cin(adder_5_cout), .cout(adder_4_cout));
  Adder_part #(.width(1)) adder_5 (.a(in_32), .b(in_14), .out(out_42), .cin(adder_6_cout), .cout(adder_5_cout));
  Adder_part #(.width(1)) adder_6 (.a(in_31), .b(in_13), .out(out_43), .cin(adder_7_cout), .cout(adder_6_cout));
  Adder_part #(.width(1)) adder_7 (.a(in_30), .b(in_12), .out(out_44), .cin(adder_8_cout), .cout(adder_7_cout));
  Adder_part #(.width(1)) adder_8 (.a(in_29), .b(in_11), .out(out_45), .cin(adder_9_cout), .cout(adder_8_cout));
  Adder_part #(.width(1)) adder_9 (.a(in_28), .b(in_10), .out(out_46), .cin(adder_10_cout), .cout(adder_9_cout));
  Adder_part #(.width(1)) adder_10 (.a(in_27), .b(in_9), .out(out_47), .cin(adder_11_cout), .cout(adder_10_cout));
  Adder_part #(.width(1)) adder_11 (.a(in_26), .b(in_8), .out(out_48), .cin(adder_12_cout), .cout(adder_11_cout));
  Adder_part #(.width(1)) adder_12 (.a(in_25), .b(in_7), .out(out_49), .cin(adder_13_cout), .cout(adder_12_cout));
  Adder_part #(.width(1)) adder_13 (.a(in_24), .b(in_6), .out(out_50), .cin(adder_14_cout), .cout(adder_13_cout));
  Adder_part #(.width(1)) adder_14 (.a(in_23), .b(in_5), .out(out_51), .cin(adder_15_cout), .cout(adder_14_cout));
  Adder_part #(.width(1)) adder_15 (.a(in_22), .b(in_4), .out(out_52), .cin(adder_16_cout), .cout(adder_15_cout));
  Adder_part #(.width(1)) adder_16 (.a(in_21), .b(in_3), .out(out_53), .cin(adder_17_cout), .cout(adder_16_cout));
  Adder_part #(.width(1)) adder_17 (.a(in_20), .b(in_2), .out(out_54), .cin(adder_18_cout), .cout(adder_17_cout));
  Adder_part #(.width(1)) adder_18 (.a(in_19), .b(in_1), .out(out_55), .cout(adder_18_cout));  // open: cin
endmodule

module BCD_Binary_1 (
  input  _8,
  input  _4,
  input  _2,
  input  _1,
  output out_5,
  output out_6,
  output out_7,
  output out_8,
  output out_9,
  output out_10,
  output out_11,
  output out_12,
  output out_13,
  output out_14,
  output out_15,
  output out_16,
  output out_17,
  output out_18,
  output out_19,
  output out_20,
  output out_21,
  output out_22
);

  wire and_1_out, and_2_out, and_3_out, and_4_out, and_5_out, and_6_out, and_7_out, and_8_out, and_9_out,
       and_10_out, and_11_out, and_12_out, and_13_out, and_14_out, and_15_out, and_16_out, and_17_out,
       and_18_out, and_19_out, and_20_out, and_21_out, and_22_out, and_23_out, and_24_out, and_25_out,
       and_26_out, and_27_out, and_28_out, and_29_out, and_30_out, and_31_out, and_32_out, and_33_out,
       and_34_out, and_35_out, and_36_out, and_37_out, and_38_out, and_39_out, and_40_out, and_41_out,
       and_42_out, and_43_out, and_44_out, and_45_out, and_46_out, and_47_out, and_48_out, and_49_out,
       and_50_out, and_51_out, and_52_out, and_53_out, and_54_out, and_55_out, and_56_out, and_57_out,
       and_58_out, and_59_out, and_60_out, and_61_out, and_62_out, and_63_out, and_64_out, and_65_out,
       and_66_out, and_67_out, and_68_out, and_69_out, and_70_out, and_71_out, and_72_out, and_73_out,
       and_74_out, and_75_out, and_76_out, and_77_out, and_78_out, and_79_out, and_80_out, and_81_out,
       and_82_out, and_83_out, and_84_out, and_85_out, and_86_out, and_87_out, and_88_out, and_89_out,
       and_90_out, and_91_out, and_92_out, and_93_out, and_94_out, and_95_out, and_96_out, and_97_out,
       and_98_out, and_99_out, and_100_out, and_101_out, and_102_out, and_103_out, and_104_out, and_105_out,
       and_106_out, and_107_out, and_108_out, and_109_out, and_110_out, and_111_out, and_112_out,
       and_113_out, and_114_out, and_115_out, and_116_out, and_117_out, and_118_out, and_119_out,
       and_120_out, and_121_out, and_122_out, and_123_out, and_124_out, and_125_out, and_126_out,
       and_127_out, and_128_out, and_129_out, and_130_out, and_131_out, and_132_out, and_133_out,
       and_134_out, and_135_out, and_136_out, and_137_out, and_138_out, and_139_out, and_140_out,
       and_141_out, and_142_out, and_143_out, and_144_out, and_145_out, and_146_out, and_147_out,
       and_148_out, and_149_out, and_150_out, and_151_out, and_152_out, and_153_out, and_154_out,
       and_155_out, and_156_out, and_157_out, and_158_out, and_159_out, and_160_out, and_161_out,
       and_162_out, and_163_out, and_164_out, and_165_out, and_166_out, and_167_out, and_168_out,
       and_169_out, and_170_out, and_171_out, and_172_out, and_173_out, and_174_out, and_175_out,
       and_176_out, n17bit_adder_1_out_35, n17bit_adder_1_out_36, n17bit_adder_1_out_37,
       n17bit_adder_1_out_38, n17bit_adder_1_out_39, n17bit_adder_1_out_40, n17bit_adder_1_out_41,
       n17bit_adder_1_out_42, n17bit_adder_1_out_43, n17bit_adder_1_out_44, n17bit_adder_1_out_45,
       n17bit_adder_1_out_46, n17bit_adder_1_out_47, n17bit_adder_1_out_48, n17bit_adder_1_out_49,
       n17bit_adder_1_out_50, n17bit_adder_1_out_51, n17bit_adder_1_out_52, n17bit_adder_2_out_35,
       n17bit_adder_2_out_36, n17bit_adder_2_out_37, n17bit_adder_2_out_38, n17bit_adder_2_out_39,
       n17bit_adder_2_out_40, n17bit_adder_2_out_41, n17bit_adder_2_out_42, n17bit_adder_2_out_43,
       n17bit_adder_2_out_44, n17bit_adder_2_out_45, n17bit_adder_2_out_46, n17bit_adder_2_out_47,
       n17bit_adder_2_out_48, n17bit_adder_2_out_49, n17bit_adder_2_out_50, n17bit_adder_2_out_51,
       n17bit_adder_2_out_52, n17bit_adder_3_out_35, n17bit_adder_3_out_36, n17bit_adder_3_out_37,
       n17bit_adder_3_out_38, n17bit_adder_3_out_39, n17bit_adder_3_out_40, n17bit_adder_3_out_41,
       n17bit_adder_3_out_42, n17bit_adder_3_out_43, n17bit_adder_3_out_44, n17bit_adder_3_out_45,
       n17bit_adder_3_out_46, n17bit_adder_3_out_47, n17bit_adder_3_out_48, n17bit_adder_3_out_49,
       n17bit_adder_3_out_50, n17bit_adder_3_out_51, n17bit_adder_3_out_52, n17bit_adder_4_out_35,
       n17bit_adder_4_out_36, n17bit_adder_4_out_37, n17bit_adder_4_out_38, n17bit_adder_4_out_39,
       n17bit_adder_4_out_40, n17bit_adder_4_out_41, n17bit_adder_4_out_42, n17bit_adder_4_out_43,
       n17bit_adder_4_out_44, n17bit_adder_4_out_45, n17bit_adder_4_out_46, n17bit_adder_4_out_47,
       n17bit_adder_4_out_48, n17bit_adder_4_out_49, n17bit_adder_4_out_50, n17bit_adder_4_out_51,
       n17bit_adder_4_out_52, n17bit_adder_5_out_35, n17bit_adder_5_out_36, n17bit_adder_5_out_37,
       n17bit_adder_5_out_38, n17bit_adder_5_out_39, n17bit_adder_5_out_40, n17bit_adder_5_out_41,
       n17bit_adder_5_out_42, n17bit_adder_5_out_43, n17bit_adder_5_out_44, n17bit_adder_5_out_45,
       n17bit_adder_5_out_46, n17bit_adder_5_out_47, n17bit_adder_5_out_48, n17bit_adder_5_out_49,
       n17bit_adder_5_out_50, n17bit_adder_5_out_51, n17bit_adder_5_out_52, not_1_out, not_2_out, not_3_out,
       not_4_out, not_5_out, not_6_out, not_7_out, not_8_out, not_9_out, not_10_out, not_11_out, not_12_out,
       not_13_out, not_14_out, not_15_out, not_16_out, not_17_out, not_18_out, not_19_out, not_20_out,
       not_21_out, not_22_out, not_23_out, not_24_out, not_25_out, not_26_out, not_27_out, not_28_out,
       not_29_out, not_30_out, not_31_out, not_32_out, not_33_out, not_34_out, not_35_out, not_36_out,
       not_37_out, not_38_out, not_39_out, not_40_out, not_41_out, not_42_out, not_43_out, not_44_out,
       not_45_out, not_46_out, not_47_out, not_48_out, not_49_out, not_50_out, not_51_out, not_52_out,
       not_53_out, not_54_out, not_55_out, not_56_out, not_57_out, not_58_out, not_59_out, not_60_out,
       not_61_out, not_62_out, not_63_out, not_64_out, not_65_out, not_66_out, not_67_out, not_68_out,
       not_69_out, not_70_out, not_71_out, not_72_out, not_73_out, not_74_out;

  and and_1 (and_1_out, not_1_out, _8, not_17_out);
  and and_2 (and_2_out, not_1_out, _8, not_21_out);
  and and_3 (and_3_out, not_1_out, _8, not_16_out);
  and and_4 (and_4_out, not_1_out, _8, _8);
  and and_5 (and_5_out, not_1_out, _8, not_8_out);
  and and_6 (and_6_out, not_1_out, _8, not_18_out);
  and and_7 (and_7_out, not_1_out, _8, not_13_out);
  and and_8 (and_8_out, not_1_out, _8, not_12_out);
  and and_9 (and_9_out, not_1_out, _8, not_9_out);
  and and_10 (and_10_out, not_1_out, _8, not_14_out);
  and and_11 (and_11_out, not_1_out, _8, not_11_out);
  and and_12 (and_12_out, not_1_out, _8, not_10_out);
  and and_13 (and_13_out, not_1_out, _8, not_5_out);
  and and_14 (and_14_out, not_1_out, _8, not_15_out);
  and and_15 (and_15_out, not_1_out, _8, not_2_out);
  and and_16 (and_16_out, not_1_out, _8, not_3_out);
  and and_17 (and_17_out, not_1_out, _8, not_4_out);
  not not_1 (not_1_out, _1);
  not not_2 (not_2_out, _8);
  not not_3 (not_3_out, _8);
  not not_4 (not_4_out, _8);
  not not_5 (not_5_out, _8);
  and and_18 (and_18_out, n17bit_adder_1_out_52, _8, _1);
  not not_6 (not_6_out, _4);
  not not_7 (not_7_out, _1);
  not not_8 (not_8_out, _8);
  not not_9 (not_9_out, _8);
  not not_10 (not_10_out, _8);
  not not_11 (not_11_out, _8);
  not not_12 (not_12_out, _8);
  not not_13 (not_13_out, _8);
  not not_14 (not_14_out, _8);
  not not_15 (not_15_out, _8);
  and and_19 (and_19_out, n17bit_adder_1_out_49, _8, _1);
  and and_20 (and_20_out, n17bit_adder_1_out_50, _8, _1);
  and and_21 (and_21_out, n17bit_adder_1_out_51, _8, _1);
  not not_16 (not_16_out, _8);
  not not_17 (not_17_out, _8);
  not not_18 (not_18_out, _8);
  not not_19 (not_19_out, _4);
  not not_20 (not_20_out, _4);
  not not_21 (not_21_out, _8);
  and and_22 (and_22_out, n17bit_adder_1_out_47, _8, _1);
  and and_23 (and_23_out, n17bit_adder_1_out_46, _8, _1);
  and and_24 (and_24_out, n17bit_adder_1_out_48, _8, _1);
  and and_25 (and_25_out, n17bit_adder_2_out_52, _2, not_6_out, _1);
  or or_1 (out_5, and_107_out, and_176_out, and_42_out, and_53_out, and_102_out);
  not not_22 (not_22_out, _4);
  not not_23 (not_23_out, _4);
  not not_24 (not_24_out, _4);
  not not_25 (not_25_out, _4);
  not not_26 (not_26_out, _4);
  not not_27 (not_27_out, _4);
  not not_28 (not_28_out, _4);
  not not_29 (not_29_out, _4);
  _17bit_Adder u_17bit_adder_1 (
    .in_1(_1), .in_2(not_67_out), .in_3(not_66_out), .in_4(not_63_out), .in_5(not_60_out), .in_6(not_62_out),
    .in_7(not_64_out), .in_8(not_61_out), .in_9(not_65_out), .in_10(not_59_out), .in_11(not_58_out),
    .in_12(not_51_out), .in_13(not_57_out), .in_14(not_56_out), .in_15(not_52_out), .in_16(not_53_out),
    .in_17(not_54_out), .in_18(not_17_out), .in_19(not_16_out), .in_20(not_21_out), .in_21(_8),
    .in_22(not_18_out), .in_23(not_8_out), .in_24(not_12_out), .in_25(not_9_out), .in_26(not_13_out),
    .in_27(not_14_out), .in_28(not_11_out), .in_29(not_10_out), .in_30(not_15_out), .in_31(not_5_out),
    .in_32(not_2_out), .in_33(not_4_out), .in_34(not_3_out), .out_35(n17bit_adder_1_out_35),
    .out_36(n17bit_adder_1_out_36), .out_37(n17bit_adder_1_out_37), .out_38(n17bit_adder_1_out_38),
    .out_39(n17bit_adder_1_out_39), .out_40(n17bit_adder_1_out_40), .out_41(n17bit_adder_1_out_41),
    .out_42(n17bit_adder_1_out_42), .out_43(n17bit_adder_1_out_43), .out_44(n17bit_adder_1_out_44),
    .out_45(n17bit_adder_1_out_45), .out_46(n17bit_adder_1_out_46), .out_47(n17bit_adder_1_out_47),
    .out_48(n17bit_adder_1_out_48), .out_49(n17bit_adder_1_out_49), .out_50(n17bit_adder_1_out_50),
    .out_51(n17bit_adder_1_out_51), .out_52(n17bit_adder_1_out_52));
  and and_26 (and_26_out, n17bit_adder_1_out_45, _8, _1);
  and and_27 (and_27_out, n17bit_adder_1_out_44, _8, _1);
  and and_28 (and_28_out, n17bit_adder_2_out_51, _2, not_6_out, _1);
  not not_30 (not_30_out, _4);
  not not_31 (not_31_out, _4);
  not not_32 (not_32_out, _4);
  not not_33 (not_33_out, _4);
  not not_34 (not_34_out, _4);
  not not_35 (not_35_out, _4);
  and and_29 (and_29_out, n17bit_adder_1_out_42, _8, _1);
  and and_30 (and_30_out, n17bit_adder_1_out_41, _8, _1);
  and and_31 (and_31_out, n17bit_adder_1_out_43, _8, _1);
  and and_32 (and_32_out, n17bit_adder_2_out_49, _2, not_6_out, _1);
  and and_33 (and_33_out, n17bit_adder_2_out_50, _2, not_6_out, _1);
  or or_2 (out_6, and_106_out, and_141_out, and_158_out, and_174_out, and_16_out, and_38_out, and_51_out, and_104_out, and_140_out);
  not not_36 (not_36_out, _2);
  not not_37 (not_37_out, _2);
  not not_38 (not_38_out, _2);
  not not_39 (not_39_out, _2);
  not not_40 (not_40_out, _2);
  not not_41 (not_41_out, _2);
  not not_42 (not_42_out, _2);
  not not_43 (not_43_out, _2);
  and and_34 (and_34_out, n17bit_adder_1_out_39, _8, _1);
  and and_35 (and_35_out, n17bit_adder_1_out_38, _8, _1);
  and and_36 (and_36_out, n17bit_adder_1_out_40, _8, _1);
  and and_37 (and_37_out, n17bit_adder_2_out_48, _2, not_6_out, _1);
  or or_3 (out_7, and_105_out, and_138_out, and_157_out, and_175_out, and_17_out, and_39_out, and_52_out, and_103_out, and_136_out);
  not not_44 (not_44_out, _2);
  not not_45 (not_45_out, _2);
  not not_46 (not_46_out, _2);
  not not_47 (not_47_out, _2);
  not not_48 (not_48_out, _2);
  not not_49 (not_49_out, _2);
  not not_50 (not_50_out, _2);
  and and_38 (and_38_out, n17bit_adder_1_out_36, _8, _1);
  and and_39 (and_39_out, n17bit_adder_1_out_37, _8, _1);
  and and_40 (and_40_out, n17bit_adder_2_out_47, _2, not_6_out, _1);
  and and_41 (and_41_out, n17bit_adder_2_out_46, _2, not_6_out, _1);
  not not_51 (not_51_out, _1);
  not not_52 (not_52_out, _1);
  not not_53 (not_53_out, _1);
  not not_54 (not_54_out, _1);
  not not_55 (not_55_out, _2);
  not not_56 (not_56_out, _1);
  not not_57 (not_57_out, _1);
  and and_42 (and_42_out, n17bit_adder_1_out_35, _8, _1);
  and and_43 (and_43_out, n17bit_adder_2_out_45, _2, not_6_out, _1);
  and and_44 (and_44_out, n17bit_adder_2_out_44, _2, not_6_out, _1);
  or or_4 (out_8, and_99_out, and_139_out, and_156_out, and_173_out, and_15_out, and_35_out, and_49_out, and_97_out, and_137_out);
  not not_58 (not_58_out, _1);
  not not_59 (not_59_out, _1);
  not not_60 (not_60_out, _1);
  not not_61 (not_61_out, _1);
  not not_62 (not_62_out, _1);
  not not_63 (not_63_out, _1);
  not not_64 (not_64_out, _1);
  not not_65 (not_65_out, _1);
  and and_45 (and_45_out, n17bit_adder_2_out_43, _2, not_6_out, _1);
  or or_5 (out_9, and_98_out, and_135_out, and_155_out, and_171_out, and_13_out, and_34_out, and_50_out, and_96_out, and_133_out);
  not not_66 (not_66_out, _1);
  not not_67 (not_67_out, _1);
  and and_46 (and_46_out, n17bit_adder_2_out_41, _2, not_6_out, _1);
  and and_47 (and_47_out, n17bit_adder_2_out_42, _2, not_6_out, _1);
  or or_6 (out_10, and_91_out, and_132_out, and_154_out, and_172_out, and_14_out, and_36_out, and_48_out, and_95_out, and_134_out);
  _17bit_Adder u_17bit_adder_2 (
    .in_1(not_55_out), .in_2(_2), .in_3(not_46_out), .in_4(not_47_out), .in_5(not_45_out), .in_6(not_48_out),
    .in_7(not_44_out), .in_8(not_50_out), .in_9(not_49_out), .in_10(not_39_out), .in_11(not_37_out),
    .in_12(not_42_out), .in_13(not_36_out), .in_14(not_40_out), .in_15(not_43_out), .in_16(not_41_out),
    .in_17(not_38_out), .in_18(_1), .in_19(not_67_out), .in_20(not_66_out), .in_21(not_63_out),
    .in_22(not_60_out), .in_23(not_62_out), .in_24(not_64_out), .in_25(not_61_out), .in_26(not_65_out),
    .in_27(not_59_out), .in_28(not_58_out), .in_29(not_51_out), .in_30(not_57_out), .in_31(not_56_out),
    .in_32(not_52_out), .in_33(not_53_out), .in_34(not_54_out), .out_35(n17bit_adder_2_out_35),
    .out_36(n17bit_adder_2_out_36), .out_37(n17bit_adder_2_out_37), .out_38(n17bit_adder_2_out_38),
    .out_39(n17bit_adder_2_out_39), .out_40(n17bit_adder_2_out_40), .out_41(n17bit_adder_2_out_41),
    .out_42(n17bit_adder_2_out_42), .out_43(n17bit_adder_2_out_43), .out_44(n17bit_adder_2_out_44),
    .out_45(n17bit_adder_2_out_45), .out_46(n17bit_adder_2_out_46), .out_47(n17bit_adder_2_out_47),
    .out_48(n17bit_adder_2_out_48), .out_49(n17bit_adder_2_out_49), .out_50(n17bit_adder_2_out_50),
    .out_51(n17bit_adder_2_out_51), .out_52(n17bit_adder_2_out_52));
  and and_48 (and_48_out, n17bit_adder_2_out_40, _2, not_6_out, _1);
  and and_49 (and_49_out, n17bit_adder_2_out_38, _2, not_6_out, _1);
  and and_50 (and_50_out, n17bit_adder_2_out_39, _2, not_6_out, _1);
  or or_7 (out_11, and_86_out, and_131_out, and_153_out, and_170_out, and_12_out, and_30_out, and_46_out, and_89_out, and_130_out);
  and and_51 (and_51_out, n17bit_adder_2_out_36, _2, not_6_out, _1);
  and and_52 (and_52_out, n17bit_adder_2_out_37, _2, not_6_out, _1);
  or or_8 (out_12, and_85_out, and_129_out, and_151_out, and_168_out, and_11_out, and_29_out, and_47_out, and_90_out, and_127_out);
  and and_53 (and_53_out, n17bit_adder_2_out_35, _2, not_6_out, _1);
  or or_9 (out_13, and_78_out, and_125_out, and_152_out, and_169_out, and_10_out, and_31_out, and_45_out, and_84_out, and_128_out);
  or or_10 (out_14, and_77_out, and_126_out, and_150_out, and_166_out, and_7_out, and_27_out, and_44_out, and_83_out, and_124_out);
  or or_11 (out_15, and_70_out, and_122_out, and_149_out, and_167_out, and_9_out, and_26_out, and_43_out, and_82_out, and_121_out);
  _17bit_Adder u_17bit_adder_3 (
    .in_1(_1), .in_2(not_67_out), .in_3(not_66_out), .in_4(not_63_out), .in_5(not_60_out), .in_6(not_62_out),
    .in_7(not_64_out), .in_8(not_61_out), .in_9(not_65_out), .in_10(not_59_out), .in_11(not_58_out),
    .in_12(not_51_out), .in_13(not_57_out), .in_14(not_56_out), .in_15(not_52_out), .in_16(not_53_out),
    .in_17(not_54_out), .in_18(not_32_out), .in_19(not_31_out), .in_20(_4), .in_21(not_30_out),
    .in_22(not_33_out), .in_23(not_35_out), .in_24(not_34_out), .in_25(not_29_out), .in_26(not_26_out),
    .in_27(not_25_out), .in_28(not_27_out), .in_29(not_22_out), .in_30(not_23_out), .in_31(not_28_out),
    .in_32(not_24_out), .in_33(not_20_out), .in_34(not_19_out), .out_35(n17bit_adder_3_out_35),
    .out_36(n17bit_adder_3_out_36), .out_37(n17bit_adder_3_out_37), .out_38(n17bit_adder_3_out_38),
    .out_39(n17bit_adder_3_out_39), .out_40(n17bit_adder_3_out_40), .out_41(n17bit_adder_3_out_41),
    .out_42(n17bit_adder_3_out_42), .out_43(n17bit_adder_3_out_43), .out_44(n17bit_adder_3_out_44),
    .out_45(n17bit_adder_3_out_45), .out_46(n17bit_adder_3_out_46), .out_47(n17bit_adder_3_out_47),
    .out_48(n17bit_adder_3_out_48), .out_49(n17bit_adder_3_out_49), .out_50(n17bit_adder_3_out_50),
    .out_51(n17bit_adder_3_out_51), .out_52(n17bit_adder_3_out_52));
  and and_54 (and_54_out, n17bit_adder_4_out_52, _4, _2, _1);
  and and_55 (and_55_out, n17bit_adder_4_out_51, _4, _2, _1);
  or or_12 (out_16, and_65_out, and_123_out, and_148_out, and_165_out, and_8_out, and_23_out, and_41_out, and_76_out, and_120_out);
  and and_56 (and_56_out, n17bit_adder_4_out_49, _4, _2, _1);
  and and_57 (and_57_out, n17bit_adder_4_out_50, _4, _2, _1);
  or or_13 (out_17, and_64_out, and_119_out, and_147_out, and_163_out, and_5_out, and_22_out, and_40_out, and_74_out, and_118_out);
  and and_58 (and_58_out, n17bit_adder_4_out_48, _4, _2, _1);
  or or_14 (out_18, and_58_out, and_115_out, and_146_out, and_164_out, and_6_out, and_24_out, and_37_out, and_75_out, and_117_out);
  and and_59 (and_59_out, n17bit_adder_5_out_50, _2, _4);
  and and_60 (and_60_out, n17bit_adder_5_out_52, _2, _4);
  and and_61 (and_61_out, n17bit_adder_5_out_51, _2, _4);
  and and_62 (and_62_out, and_60_out, not_7_out);
  and and_63 (and_63_out, and_61_out, not_7_out);
  and and_64 (and_64_out, n17bit_adder_4_out_47, _4, _2, _1);
  and and_65 (and_65_out, n17bit_adder_4_out_46, _4, _2, _1);
  and and_66 (and_66_out, n17bit_adder_5_out_49, _2, _4);
  and and_67 (and_67_out, n17bit_adder_5_out_48, _2, _4);
  and and_68 (and_68_out, and_66_out, not_7_out);
  and and_69 (and_69_out, and_59_out, not_7_out);
  _17bit_Adder u_17bit_adder_4 (
    .in_1(_1), .in_2(not_67_out), .in_3(not_66_out), .in_4(not_63_out), .in_5(not_60_out), .in_6(not_62_out),
    .in_7(not_64_out), .in_8(not_61_out), .in_9(not_65_out), .in_10(not_59_out), .in_11(not_58_out),
    .in_12(not_51_out), .in_13(not_57_out), .in_14(not_56_out), .in_15(not_52_out), .in_16(not_53_out),
    .in_17(not_54_out), .in_18(and_60_out), .in_19(and_61_out), .in_20(and_59_out), .in_21(and_66_out),
    .in_22(and_67_out), .in_23(and_71_out), .in_24(and_73_out), .in_25(and_72_out), .in_26(and_80_out),
    .in_27(and_81_out), .in_28(and_79_out), .in_29(and_88_out), .in_30(and_87_out), .in_31(and_92_out),
    .in_32(and_93_out), .in_33(and_94_out), .in_34(and_100_out), .out_35(n17bit_adder_4_out_35),
    .out_36(n17bit_adder_4_out_36), .out_37(n17bit_adder_4_out_37), .out_38(n17bit_adder_4_out_38),
    .out_39(n17bit_adder_4_out_39), .out_40(n17bit_adder_4_out_40), .out_41(n17bit_adder_4_out_41),
    .out_42(n17bit_adder_4_out_42), .out_43(n17bit_adder_4_out_43), .out_44(n17bit_adder_4_out_44),
    .out_45(n17bit_adder_4_out_45), .out_46(n17bit_adder_4_out_46), .out_47(n17bit_adder_4_out_47),
    .out_48(n17bit_adder_4_out_48), .out_49(n17bit_adder_4_out_49), .out_50(n17bit_adder_4_out_50),
    .out_51(n17bit_adder_4_out_51), .out_52(n17bit_adder_4_out_52));
  and and_70 (and_70_out, n17bit_adder_4_out_45, _4, _2, _1);
  or or_15 (out_19, and_56_out, and_116_out, and_145_out, and_162_out, and_4_out, and_19_out, and_32_out, and_68_out, and_114_out);
  and and_71 (and_71_out, n17bit_adder_5_out_47, _2, _4);
  and and_72 (and_72_out, n17bit_adder_5_out_45, _2, _4);
  and and_73 (and_73_out, n17bit_adder_5_out_46, _2, _4);
  and and_74 (and_74_out, and_71_out, not_7_out);
  and and_75 (and_75_out, and_67_out, not_7_out);
  and and_76 (and_76_out, and_73_out, not_7_out);
  and and_77 (and_77_out, n17bit_adder_4_out_44, _4, _2, _1);
  and and_78 (and_78_out, n17bit_adder_4_out_43, _4, _2, _1);
  or or_16 (out_20, and_57_out, and_113_out, and_143_out, and_161_out, and_2_out, and_20_out, and_33_out, and_69_out, and_112_out);
  _17bit_Adder u_17bit_adder_5 (
    .in_1(not_32_out), .in_2(not_31_out), .in_3(_4), .in_4(not_30_out), .in_5(not_33_out), .in_6(not_35_out),
    .in_7(not_34_out), .in_8(not_29_out), .in_9(not_26_out), .in_10(not_25_out), .in_11(not_27_out),
    .in_12(not_22_out), .in_13(not_23_out), .in_14(not_28_out), .in_15(not_24_out), .in_16(not_20_out),
    .in_17(not_19_out), .in_18(not_55_out), .in_19(_2), .in_20(not_46_out), .in_21(not_47_out),
    .in_22(not_45_out), .in_23(not_48_out), .in_24(not_44_out), .in_25(not_50_out), .in_26(not_49_out),
    .in_27(not_39_out), .in_28(not_37_out), .in_29(not_42_out), .in_30(not_36_out), .in_31(not_40_out),
    .in_32(not_43_out), .in_33(not_41_out), .in_34(not_38_out), .out_35(n17bit_adder_5_out_35),
    .out_36(n17bit_adder_5_out_36), .out_37(n17bit_adder_5_out_37), .out_38(n17bit_adder_5_out_38),
    .out_39(n17bit_adder_5_out_39), .out_40(n17bit_adder_5_out_40), .out_41(n17bit_adder_5_out_41),
    .out_42(n17bit_adder_5_out_42), .out_43(n17bit_adder_5_out_43), .out_44(n17bit_adder_5_out_44),
    .out_45(n17bit_adder_5_out_45), .out_46(n17bit_adder_5_out_46), .out_47(n17bit_adder_5_out_47),
    .out_48(n17bit_adder_5_out_48), .out_49(n17bit_adder_5_out_49), .out_50(n17bit_adder_5_out_50),
    .out_51(n17bit_adder_5_out_51), .out_52(n17bit_adder_5_out_52));
  and and_79 (and_79_out, n17bit_adder_5_out_42, _2, _4);
  and and_80 (and_80_out, n17bit_adder_5_out_44, _2, _4);
  and and_81 (and_81_out, n17bit_adder_5_out_43, _2, _4);
  and and_82 (and_82_out, and_72_out, not_7_out);
  and and_83 (and_83_out, and_80_out, not_7_out);
  and and_84 (and_84_out, and_81_out, not_7_out);
  and and_85 (and_85_out, n17bit_adder_4_out_42, _4, _2, _1);
  and and_86 (and_86_out, n17bit_adder_4_out_41, _4, _2, _1);
  or or_17 (out_21, and_55_out, and_110_out, and_144_out, and_160_out, and_3_out, and_21_out, and_28_out, and_63_out, and_109_out);
  and and_87 (and_87_out, n17bit_adder_5_out_40, _2, _4);
  and and_88 (and_88_out, n17bit_adder_5_out_41, _2, _4);
  and and_89 (and_89_out, and_88_out, not_7_out);
  and and_90 (and_90_out, and_79_out, not_7_out);
  and and_91 (and_91_out, n17bit_adder_4_out_40, _4, _2, _1);
  and and_92 (and_92_out, n17bit_adder_5_out_39, _2, _4);
  and and_93 (and_93_out, n17bit_adder_5_out_38, _2, _4);
  and and_94 (and_94_out, n17bit_adder_5_out_37, _2, _4);
  and and_95 (and_95_out, and_87_out, not_7_out);
  and and_96 (and_96_out, and_92_out, not_7_out);
  and and_97 (and_97_out, and_93_out, not_7_out);
  and and_98 (and_98_out, n17bit_adder_4_out_39, _4, _2, _1);
  and and_99 (and_99_out, n17bit_adder_4_out_38, _4, _2, _1);
  or or_18 (out_22, and_54_out, and_111_out, and_142_out, and_159_out, and_1_out, and_18_out, and_25_out, and_62_out, and_108_out);
  and and_100 (and_100_out, n17bit_adder_5_out_36, _2, _4);
  and and_101 (and_101_out, n17bit_adder_5_out_35, _2, _4);
  and and_102 (and_102_out, and_101_out, not_7_out);
  and and_103 (and_103_out, and_94_out, not_7_out);
  and and_104 (and_104_out, and_100_out, not_7_out);
  and and_105 (and_105_out, n17bit_adder_4_out_37, _4, _2, _1);
  and and_106 (and_106_out, n17bit_adder_4_out_36, _4, _2, _1);
  and and_107 (and_107_out, n17bit_adder_4_out_35, _4, _2, _1);
  and and_108 (and_108_out, not_32_out, not_72_out, not_71_out, _4);
  and and_109 (and_109_out, not_31_out, not_72_out, not_71_out, _4);
  not not_68 (not_68_out, _4);
  not not_69 (not_69_out, _2);
  not not_70 (not_70_out, _8);
  and and_110 (and_110_out, not_67_out, not_70_out, _1, not_68_out, not_69_out);
  and and_111 (and_111_out, _1, not_70_out, _1, not_68_out, not_69_out);
  and and_112 (and_112_out, _4, not_72_out, not_71_out, _4);
  and and_113 (and_113_out, not_66_out, not_70_out, _1, not_68_out, not_69_out);
  and and_114 (and_114_out, not_30_out, not_72_out, not_71_out, _4);
  and and_115 (and_115_out, not_60_out, not_70_out, _1, not_68_out, not_69_out);
  and and_116 (and_116_out, not_63_out, not_70_out, _1, not_68_out, not_69_out);
  and and_117 (and_117_out, not_33_out, not_72_out, not_71_out, _4);
  and and_118 (and_118_out, not_35_out, not_72_out, not_71_out, _4);
  and and_119 (and_119_out, not_62_out, not_70_out, _1, not_68_out, not_69_out);
  and and_120 (and_120_out, not_34_out, not_72_out, not_71_out, _4);
  and and_121 (and_121_out, not_29_out, not_72_out, not_71_out, _4);
  and and_122 (and_122_out, not_61_out, not_70_out, _1, not_68_out, not_69_out);
  and and_123 (and_123_out, not_64_out, not_70_out, _1, not_68_out, not_69_out);
  and and_124 (and_124_out, not_26_out, not_72_out, not_71_out, _4);
  and and_125 (and_125_out, not_59_out, not_70_out, _1, not_68_out, not_69_out);
  and and_126 (and_126_out, not_65_out, not_70_out, _1, not_68_out, not_69_out);
  not not_71 (not_71_out, _1);
  and and_127 (and_127_out, not_27_out, not_72_out, not_71_out, _4);
  and and_128 (and_128_out, not_25_out, not_72_out, not_71_out, _4);
  and and_129 (and_129_out, not_58_out, not_70_out, _1, not_68_out, not_69_out);
  not not_72 (not_72_out, _2);
  and and_130 (and_130_out, not_22_out, not_72_out, not_71_out, _4);
  and and_131 (and_131_out, not_51_out, not_70_out, _1, not_68_out, not_69_out);
  and and_132 (and_132_out, not_57_out, not_70_out, _1, not_68_out, not_69_out);
  and and_133 (and_133_out, not_28_out, not_72_out, not_71_out, _4);
  and and_134 (and_134_out, not_23_out, not_72_out, not_71_out, _4);
  and and_135 (and_135_out, not_56_out, not_70_out, _1, not_68_out, not_69_out);
  and and_136 (and_136_out, not_20_out, not_72_out, not_71_out, _4);
  and and_137 (and_137_out, not_24_out, not_72_out, not_71_out, _4);
  and and_138 (and_138_out, not_53_out, not_70_out, _1, not_68_out, not_69_out);
  and and_139 (and_139_out, not_52_out, not_70_out, _1, not_68_out, not_69_out);
  and and_140 (and_140_out, not_19_out, not_72_out, not_71_out, _4);
  and and_141 (and_141_out, not_54_out, not_70_out, _1, not_68_out, not_69_out);
  not not_73 (not_73_out, _4);
  and and_142 (and_142_out, not_55_out, _2, not_71_out, not_73_out);
  and and_143 (and_143_out, not_46_out, _2, not_71_out, not_73_out);
  and and_144 (and_144_out, _2, _2, not_71_out, not_73_out);
  and and_145 (and_145_out, not_47_out, _2, not_71_out, not_73_out);
  and and_146 (and_146_out, not_45_out, _2, not_71_out, not_73_out);
  and and_147 (and_147_out, not_48_out, _2, not_71_out, not_73_out);
  and and_148 (and_148_out, not_44_out, _2, not_71_out, not_73_out);
  and and_149 (and_149_out, not_50_out, _2, not_71_out, not_73_out);
  and and_150 (and_150_out, not_49_out, _2, not_71_out, not_73_out);
  and and_151 (and_151_out, not_37_out, _2, not_71_out, not_73_out);
  and and_152 (and_152_out, not_39_out, _2, not_71_out, not_73_out);
  and and_153 (and_153_out, not_42_out, _2, not_71_out, not_73_out);
  and and_154 (and_154_out, not_36_out, _2, not_71_out, not_73_out);
  and and_155 (and_155_out, not_40_out, _2, not_71_out, not_73_out);
  and and_156 (and_156_out, not_43_out, _2, not_71_out, not_73_out);
  and and_157 (and_157_out, not_41_out, _2, not_71_out, not_73_out);
  and and_158 (and_158_out, not_38_out, _2, not_71_out, not_73_out);
  not not_74 (not_74_out, _2);
  and and_159 (and_159_out, n17bit_adder_3_out_52, not_74_out, _4, _1);
  and and_160 (and_160_out, n17bit_adder_3_out_51, not_74_out, _4, _1);
  and and_161 (and_161_out, n17bit_adder_3_out_50, not_74_out, _4, _1);
  and and_162 (and_162_out, n17bit_adder_3_out_49, not_74_out, _4, _1);
  and and_163 (and_163_out, n17bit_adder_3_out_47, not_74_out, _4, _1);
  and and_164 (and_164_out, n17bit_adder_3_out_48, not_74_out, _4, _1);
  and and_165 (and_165_out, n17bit_adder_3_out_46, not_74_out, _4, _1);
  and and_166 (and_166_out, n17bit_adder_3_out_44, not_74_out, _4, _1);
  and and_167 (and_167_out, n17bit_adder_3_out_45, not_74_out, _4, _1);
  and and_168 (and_168_out, n17bit_adder_3_out_42, not_74_out, _4, _1);
  and and_169 (and_169_out, n17bit_adder_3_out_43, not_74_out, _4, _1);
  and and_170 (and_170_out, n17bit_adder_3_out_41, not_74_out, _4, _1);
  and and_171 (and_171_out, n17bit_adder_3_out_39, not_74_out, _4, _1);
  and and_172 (and_172_out, n17bit_adder_3_out_40, not_74_out, _4, _1);
  and and_173 (and_173_out, n17bit_adder_3_out_38, not_74_out, _4, _1);
  and and_174 (and_174_out, n17bit_adder_3_out_36, not_74_out, _4, _1);
  and and_175 (and_175_out, n17bit_adder_3_out_37, not_74_out, _4, _1);
  and and_176 (and_176_out, n17bit_adder_3_out_35, not_74_out, _4, _1);

  // Notes on the sheet:
  //   8
  //   9
  //   3
  //   5
  //   7
  //   RIGHT = LARGE SIDE
  //   6
  //   4
  //   1
  //   1
  //   2
  //   4
  //   2
endmodule
module BCD_Binary_10 (
  input  _80,
  input  _40,
  input  _20,
  input  _10,
  output out_5,
  output out_6,
  output out_7,
  output out_8,
  output out_9,
  output out_10,
  output out_11,
  output out_12,
  output out_13,
  output out_14,
  output out_15,
  output out_16,
  output out_17,
  output out_18,
  output out_19,
  output out_20,
  output out_21,
  output out_22
);

  wire and_1_out, and_2_out, and_3_out, and_4_out, and_5_out, and_6_out, and_7_out, and_8_out, and_9_out,
       and_10_out, and_11_out, and_12_out, and_13_out, and_14_out, and_15_out, and_16_out, and_17_out,
       and_18_out, and_19_out, and_20_out, and_21_out, and_22_out, and_23_out, and_24_out, and_25_out,
       and_26_out, and_27_out, and_28_out, and_29_out, and_30_out, and_31_out, and_32_out, and_33_out,
       and_34_out, and_35_out, and_36_out, and_37_out, and_38_out, and_39_out, and_40_out, and_41_out,
       and_42_out, and_43_out, and_44_out, and_45_out, and_46_out, and_47_out, and_48_out, and_49_out,
       and_50_out, and_51_out, and_52_out, and_53_out, and_54_out, and_55_out, and_56_out, and_57_out,
       and_58_out, and_59_out, and_60_out, and_61_out, and_62_out, and_63_out, and_64_out, and_65_out,
       and_66_out, and_67_out, and_68_out, and_69_out, and_70_out, and_71_out, and_72_out, and_73_out,
       and_74_out, and_75_out, and_76_out, and_77_out, and_78_out, and_79_out, and_80_out, and_81_out,
       and_82_out, and_83_out, and_84_out, and_85_out, and_86_out, and_87_out, and_88_out, and_89_out,
       and_90_out, and_91_out, and_92_out, and_93_out, and_94_out, and_95_out, and_96_out, and_97_out,
       and_98_out, and_99_out, and_100_out, and_101_out, and_102_out, and_103_out, and_104_out, and_105_out,
       and_106_out, and_107_out, and_108_out, and_109_out, and_110_out, and_111_out, and_112_out,
       and_113_out, and_114_out, and_115_out, and_116_out, and_117_out, and_118_out, and_119_out,
       and_120_out, and_121_out, and_122_out, and_123_out, and_124_out, and_125_out, and_126_out,
       and_127_out, and_128_out, and_129_out, and_130_out, and_131_out, and_132_out, and_133_out,
       and_134_out, and_135_out, and_136_out, and_137_out, and_138_out, and_139_out, and_140_out,
       and_141_out, and_142_out, and_143_out, and_144_out, and_145_out, and_146_out, and_147_out,
       and_148_out, and_149_out, and_150_out, and_151_out, and_152_out, and_153_out, and_154_out,
       and_155_out, and_156_out, and_157_out, and_158_out, and_159_out, and_160_out, and_161_out,
       and_162_out, and_163_out, and_164_out, and_165_out, and_166_out, and_167_out, and_168_out,
       and_169_out, and_170_out, and_171_out, and_172_out, and_173_out, and_174_out, and_175_out,
       and_176_out, n17bit_adder_1_out_35, n17bit_adder_1_out_36, n17bit_adder_1_out_37,
       n17bit_adder_1_out_38, n17bit_adder_1_out_39, n17bit_adder_1_out_40, n17bit_adder_1_out_41,
       n17bit_adder_1_out_42, n17bit_adder_1_out_43, n17bit_adder_1_out_44, n17bit_adder_1_out_45,
       n17bit_adder_1_out_46, n17bit_adder_1_out_47, n17bit_adder_1_out_48, n17bit_adder_1_out_49,
       n17bit_adder_1_out_50, n17bit_adder_1_out_51, n17bit_adder_1_out_52, n17bit_adder_2_out_35,
       n17bit_adder_2_out_36, n17bit_adder_2_out_37, n17bit_adder_2_out_38, n17bit_adder_2_out_39,
       n17bit_adder_2_out_40, n17bit_adder_2_out_41, n17bit_adder_2_out_42, n17bit_adder_2_out_43,
       n17bit_adder_2_out_44, n17bit_adder_2_out_45, n17bit_adder_2_out_46, n17bit_adder_2_out_47,
       n17bit_adder_2_out_48, n17bit_adder_2_out_49, n17bit_adder_2_out_50, n17bit_adder_2_out_51,
       n17bit_adder_2_out_52, n17bit_adder_3_out_35, n17bit_adder_3_out_36, n17bit_adder_3_out_37,
       n17bit_adder_3_out_38, n17bit_adder_3_out_39, n17bit_adder_3_out_40, n17bit_adder_3_out_41,
       n17bit_adder_3_out_42, n17bit_adder_3_out_43, n17bit_adder_3_out_44, n17bit_adder_3_out_45,
       n17bit_adder_3_out_46, n17bit_adder_3_out_47, n17bit_adder_3_out_48, n17bit_adder_3_out_49,
       n17bit_adder_3_out_50, n17bit_adder_3_out_51, n17bit_adder_3_out_52, n17bit_adder_4_out_35,
       n17bit_adder_4_out_36, n17bit_adder_4_out_37, n17bit_adder_4_out_38, n17bit_adder_4_out_39,
       n17bit_adder_4_out_40, n17bit_adder_4_out_41, n17bit_adder_4_out_42, n17bit_adder_4_out_43,
       n17bit_adder_4_out_44, n17bit_adder_4_out_45, n17bit_adder_4_out_46, n17bit_adder_4_out_47,
       n17bit_adder_4_out_48, n17bit_adder_4_out_49, n17bit_adder_4_out_50, n17bit_adder_4_out_51,
       n17bit_adder_4_out_52, n17bit_adder_5_out_35, n17bit_adder_5_out_36, n17bit_adder_5_out_37,
       n17bit_adder_5_out_38, n17bit_adder_5_out_39, n17bit_adder_5_out_40, n17bit_adder_5_out_41,
       n17bit_adder_5_out_42, n17bit_adder_5_out_43, n17bit_adder_5_out_44, n17bit_adder_5_out_45,
       n17bit_adder_5_out_46, n17bit_adder_5_out_47, n17bit_adder_5_out_48, n17bit_adder_5_out_49,
       n17bit_adder_5_out_50, n17bit_adder_5_out_51, n17bit_adder_5_out_52, not_1_out, not_2_out, not_3_out,
       not_4_out, not_5_out, not_6_out, not_7_out, not_8_out, not_9_out, not_10_out, not_11_out, not_12_out,
       not_13_out, not_14_out, not_15_out, not_16_out, not_17_out, not_18_out, not_19_out, not_20_out,
       not_21_out, not_22_out, not_23_out, not_24_out, not_25_out, not_26_out, not_27_out, not_28_out,
       not_29_out, not_30_out, not_31_out, not_32_out, not_33_out, not_34_out, not_35_out, not_36_out,
       not_37_out, not_38_out, not_39_out, not_40_out, not_41_out, not_42_out, not_43_out, not_44_out,
       not_45_out, not_46_out, not_47_out, not_48_out, not_49_out, not_50_out, not_51_out, not_52_out,
       not_53_out, not_54_out, not_55_out, not_56_out, not_57_out, not_58_out, not_59_out, not_60_out,
       not_61_out, not_62_out, not_63_out, not_64_out, not_65_out, not_66_out, not_67_out, not_68_out,
       not_69_out, not_70_out;

  and and_1 (and_1_out, not_1_out, _80, not_20_out);
  and and_2 (and_2_out, not_1_out, _80, not_17_out);
  and and_3 (and_3_out, not_1_out, _80, not_18_out);
  and and_4 (and_4_out, not_1_out, _80, not_19_out);
  and and_5 (and_5_out, not_1_out, _80, _80);
  and and_6 (and_6_out, not_1_out, _80, not_12_out);
  and and_7 (and_7_out, not_1_out, _80, not_8_out);
  and and_8 (and_8_out, not_1_out, _80, _80);
  and and_9 (and_9_out, not_1_out, _80, not_10_out);
  and and_10 (and_10_out, not_1_out, _80, not_11_out);
  and and_11 (and_11_out, not_1_out, _80, not_13_out);
  and and_12 (and_12_out, not_1_out, _80, not_9_out);
  and and_13 (and_13_out, not_1_out, _80, not_4_out);
  and and_14 (and_14_out, not_1_out, _80, not_14_out);
  and and_15 (and_15_out, not_1_out, _80, not_2_out);
  and and_16 (and_16_out, not_1_out, _80, not_3_out);
  and and_17 (and_17_out, not_1_out, _80, not_5_out);
  not not_1 (not_1_out, _10);
  not not_2 (not_2_out, _80);
  not not_3 (not_3_out, _80);
  not not_4 (not_4_out, _80);
  not not_5 (not_5_out, _80);
  and and_18 (and_18_out, n17bit_adder_1_out_52, _80, _10);
  not not_6 (not_6_out, _40);
  not not_7 (not_7_out, _10);
  not not_8 (not_8_out, _80);
  not not_9 (not_9_out, _80);
  not not_10 (not_10_out, _80);
  not not_11 (not_11_out, _80);
  not not_12 (not_12_out, _80);
  not not_13 (not_13_out, _80);
  not not_14 (not_14_out, _80);
  and and_19 (and_19_out, n17bit_adder_1_out_51, _80, _10);
  and and_20 (and_20_out, n17bit_adder_1_out_50, _80, _10);
  and and_21 (and_21_out, n17bit_adder_1_out_49, _80, _10);
  not not_15 (not_15_out, _40);
  not not_16 (not_16_out, _40);
  not not_17 (not_17_out, _80);
  not not_18 (not_18_out, _80);
  not not_19 (not_19_out, _80);
  not not_20 (not_20_out, _80);
  and and_22 (and_22_out, n17bit_adder_1_out_48, _80, _10);
  and and_23 (and_23_out, n17bit_adder_1_out_46, _80, _10);
  and and_24 (and_24_out, n17bit_adder_1_out_47, _80, _10);
  and and_25 (and_25_out, n17bit_adder_2_out_52, _20, not_6_out, _10);
  or or_1 (out_5, and_106_out, and_176_out, and_42_out, and_53_out, and_104_out);
  not not_21 (not_21_out, _40);
  not not_22 (not_22_out, _40);
  not not_23 (not_23_out, _40);
  not not_24 (not_24_out, _40);
  not not_25 (not_25_out, _40);
  not not_26 (not_26_out, _40);
  not not_27 (not_27_out, _40);
  not not_28 (not_28_out, _40);
  _17bit_Adder u_17bit_adder_1 (
    .in_1(not_63_out), .in_2(_10), .in_3(not_62_out), .in_4(_10), .in_5(not_57_out), .in_6(not_56_out),
    .in_7(not_61_out), .in_8(not_60_out), .in_9(not_58_out), .in_10(not_55_out), .in_11(not_59_out),
    .in_12(not_50_out), .in_13(not_54_out), .in_14(not_48_out), .in_15(not_53_out), .in_16(not_49_out),
    .in_17(not_51_out), .in_18(not_20_out), .in_19(not_18_out), .in_20(not_17_out), .in_21(not_19_out),
    .in_22(_80), .in_23(not_12_out), .in_24(_80), .in_25(not_10_out), .in_26(not_8_out), .in_27(not_13_out),
    .in_28(not_11_out), .in_29(not_9_out), .in_30(not_14_out), .in_31(not_4_out), .in_32(not_3_out),
    .in_33(not_2_out), .in_34(not_5_out), .out_35(n17bit_adder_1_out_35), .out_36(n17bit_adder_1_out_36),
    .out_37(n17bit_adder_1_out_37), .out_38(n17bit_adder_1_out_38), .out_39(n17bit_adder_1_out_39),
    .out_40(n17bit_adder_1_out_40), .out_41(n17bit_adder_1_out_41), .out_42(n17bit_adder_1_out_42),
    .out_43(n17bit_adder_1_out_43), .out_44(n17bit_adder_1_out_44), .out_45(n17bit_adder_1_out_45),
    .out_46(n17bit_adder_1_out_46), .out_47(n17bit_adder_1_out_47), .out_48(n17bit_adder_1_out_48),
    .out_49(n17bit_adder_1_out_49), .out_50(n17bit_adder_1_out_50), .out_51(n17bit_adder_1_out_51),
    .out_52(n17bit_adder_1_out_52));
  and and_26 (and_26_out, n17bit_adder_1_out_45, _80, _10);
  and and_27 (and_27_out, n17bit_adder_1_out_44, _80, _10);
  and and_28 (and_28_out, n17bit_adder_2_out_51, _20, not_6_out, _10);
  not not_29 (not_29_out, _40);
  not not_30 (not_30_out, _40);
  not not_31 (not_31_out, _40);
  not not_32 (not_32_out, _40);
  not not_33 (not_33_out, _40);
  and and_29 (and_29_out, n17bit_adder_1_out_43, _80, _10);
  and and_30 (and_30_out, n17bit_adder_1_out_41, _80, _10);
  and and_31 (and_31_out, n17bit_adder_1_out_42, _80, _10);
  and and_32 (and_32_out, n17bit_adder_2_out_49, _20, not_6_out, _10);
  and and_33 (and_33_out, n17bit_adder_2_out_50, _20, not_6_out, _10);
  or or_2 (out_6, and_107_out, and_141_out, and_158_out, and_175_out, and_17_out, and_38_out, and_51_out, and_102_out, and_140_out);
  not not_34 (not_34_out, _20);
  not not_35 (not_35_out, _20);
  not not_36 (not_36_out, _20);
  not not_37 (not_37_out, _20);
  not not_38 (not_38_out, _20);
  not not_39 (not_39_out, _20);
  not not_40 (not_40_out, _20);
  not not_41 (not_41_out, _20);
  and and_34 (and_34_out, n17bit_adder_1_out_40, _80, _10);
  and and_35 (and_35_out, n17bit_adder_1_out_39, _80, _10);
  and and_36 (and_36_out, n17bit_adder_1_out_38, _80, _10);
  and and_37 (and_37_out, n17bit_adder_2_out_48, _20, not_6_out, _10);
  or or_3 (out_7, and_105_out, and_138_out, and_156_out, and_174_out, and_15_out, and_39_out, and_52_out, and_103_out, and_136_out);
  not not_42 (not_42_out, _20);
  not not_43 (not_43_out, _20);
  not not_44 (not_44_out, _20);
  not not_45 (not_45_out, _20);
  not not_46 (not_46_out, _20);
  not not_47 (not_47_out, _20);
  and and_38 (and_38_out, n17bit_adder_1_out_36, _80, _10);
  and and_39 (and_39_out, n17bit_adder_1_out_37, _80, _10);
  and and_40 (and_40_out, n17bit_adder_2_out_46, _20, not_6_out, _10);
  and and_41 (and_41_out, n17bit_adder_2_out_47, _20, not_6_out, _10);
  not not_48 (not_48_out, _10);
  not not_49 (not_49_out, _10);
  not not_50 (not_50_out, _10);
  not not_51 (not_51_out, _10);
  not not_52 (not_52_out, _20);
  not not_53 (not_53_out, _10);
  not not_54 (not_54_out, _10);
  and and_42 (and_42_out, n17bit_adder_1_out_35, _80, _10);
  and and_43 (and_43_out, n17bit_adder_2_out_45, _20, not_6_out, _10);
  and and_44 (and_44_out, n17bit_adder_2_out_44, _20, not_6_out, _10);
  or or_4 (out_8, and_99_out, and_139_out, and_157_out, and_173_out, and_16_out, and_36_out, and_50_out, and_97_out, and_137_out);
  not not_55 (not_55_out, _10);
  not not_56 (not_56_out, _10);
  not not_57 (not_57_out, _10);
  not not_58 (not_58_out, _10);
  not not_59 (not_59_out, _10);
  not not_60 (not_60_out, _10);
  not not_61 (not_61_out, _10);
  and and_45 (and_45_out, n17bit_adder_2_out_43, _20, not_6_out, _10);
  or or_5 (out_9, and_98_out, and_135_out, and_154_out, and_172_out, and_13_out, and_35_out, and_49_out, and_95_out, and_134_out);
  not not_62 (not_62_out, _10);
  not not_63 (not_63_out, _10);
  and and_46 (and_46_out, n17bit_adder_2_out_41, _20, not_6_out, _10);
  and and_47 (and_47_out, n17bit_adder_2_out_42, _20, not_6_out, _10);
  or or_6 (out_10, and_91_out, and_131_out, and_155_out, and_171_out, and_14_out, and_34_out, and_48_out, and_96_out, and_133_out);
  _17bit_Adder u_17bit_adder_2 (
    .in_1(not_52_out), .in_2(not_47_out), .in_3(_20), .in_4(not_44_out), .in_5(_20), .in_6(not_43_out),
    .in_7(not_42_out), .in_8(not_46_out), .in_9(not_45_out), .in_10(not_34_out), .in_11(not_41_out),
    .in_12(not_37_out), .in_13(not_39_out), .in_14(not_38_out), .in_15(not_40_out), .in_16(not_35_out),
    .in_17(not_36_out), .in_18(not_63_out), .in_19(_10), .in_20(not_62_out), .in_21(_10), .in_22(not_57_out),
    .in_23(not_56_out), .in_24(not_61_out), .in_25(not_60_out), .in_26(not_58_out), .in_27(not_55_out),
    .in_28(not_59_out), .in_29(not_50_out), .in_30(not_54_out), .in_31(not_48_out), .in_32(not_53_out),
    .in_33(not_49_out), .in_34(not_51_out), .out_35(n17bit_adder_2_out_35), .out_36(n17bit_adder_2_out_36),
    .out_37(n17bit_adder_2_out_37), .out_38(n17bit_adder_2_out_38), .out_39(n17bit_adder_2_out_39),
    .out_40(n17bit_adder_2_out_40), .out_41(n17bit_adder_2_out_41), .out_42(n17bit_adder_2_out_42),
    .out_43(n17bit_adder_2_out_43), .out_44(n17bit_adder_2_out_44), .out_45(n17bit_adder_2_out_45),
    .out_46(n17bit_adder_2_out_46), .out_47(n17bit_adder_2_out_47), .out_48(n17bit_adder_2_out_48),
    .out_49(n17bit_adder_2_out_49), .out_50(n17bit_adder_2_out_50), .out_51(n17bit_adder_2_out_51),
    .out_52(n17bit_adder_2_out_52));
  and and_48 (and_48_out, n17bit_adder_2_out_40, _20, not_6_out, _10);
  and and_49 (and_49_out, n17bit_adder_2_out_39, _20, not_6_out, _10);
  and and_50 (and_50_out, n17bit_adder_2_out_38, _20, not_6_out, _10);
  or or_7 (out_11, and_86_out, and_132_out, and_153_out, and_170_out, and_12_out, and_30_out, and_46_out, and_90_out, and_130_out);
  and and_51 (and_51_out, n17bit_adder_2_out_36, _20, not_6_out, _10);
  and and_52 (and_52_out, n17bit_adder_2_out_37, _20, not_6_out, _10);
  or or_8 (out_12, and_85_out, and_129_out, and_151_out, and_169_out, and_10_out, and_31_out, and_47_out, and_89_out, and_127_out);
  and and_53 (and_53_out, n17bit_adder_2_out_35, _20, not_6_out, _10);
  or or_9 (out_13, and_77_out, and_125_out, and_152_out, and_168_out, and_11_out, and_29_out, and_45_out, and_82_out, and_128_out);
  or or_10 (out_14, and_78_out, and_126_out, and_150_out, and_166_out, and_7_out, and_27_out, and_44_out, and_83_out, and_124_out);
  or or_11 (out_15, and_70_out, and_123_out, and_149_out, and_167_out, and_9_out, and_26_out, and_43_out, and_84_out, and_120_out);
  _17bit_Adder u_17bit_adder_3 (
    .in_1(not_63_out), .in_2(_10), .in_3(not_62_out), .in_4(_10), .in_5(not_57_out), .in_6(not_56_out),
    .in_7(not_61_out), .in_8(not_60_out), .in_9(not_58_out), .in_10(not_55_out), .in_11(not_59_out),
    .in_12(not_50_out), .in_13(not_54_out), .in_14(not_48_out), .in_15(not_53_out), .in_16(not_49_out),
    .in_17(not_51_out), .in_18(not_32_out), .in_19(not_30_out), .in_20(not_31_out), .in_21(_40),
    .in_22(not_29_out), .in_23(_40), .in_24(not_33_out), .in_25(not_25_out), .in_26(not_23_out),
    .in_27(not_21_out), .in_28(not_26_out), .in_29(not_27_out), .in_30(not_28_out), .in_31(not_24_out),
    .in_32(not_22_out), .in_33(not_16_out), .in_34(not_15_out), .out_35(n17bit_adder_3_out_35),
    .out_36(n17bit_adder_3_out_36), .out_37(n17bit_adder_3_out_37), .out_38(n17bit_adder_3_out_38),
    .out_39(n17bit_adder_3_out_39), .out_40(n17bit_adder_3_out_40), .out_41(n17bit_adder_3_out_41),
    .out_42(n17bit_adder_3_out_42), .out_43(n17bit_adder_3_out_43), .out_44(n17bit_adder_3_out_44),
    .out_45(n17bit_adder_3_out_45), .out_46(n17bit_adder_3_out_46), .out_47(n17bit_adder_3_out_47),
    .out_48(n17bit_adder_3_out_48), .out_49(n17bit_adder_3_out_49), .out_50(n17bit_adder_3_out_50),
    .out_51(n17bit_adder_3_out_51), .out_52(n17bit_adder_3_out_52));
  and and_54 (and_54_out, n17bit_adder_4_out_52, _40, _20, _10);
  and and_55 (and_55_out, n17bit_adder_4_out_51, _40, _20, _10);
  or or_12 (out_16, and_65_out, and_122_out, and_148_out, and_165_out, and_8_out, and_23_out, and_40_out, and_76_out, and_121_out);
  and and_56 (and_56_out, n17bit_adder_4_out_50, _40, _20, _10);
  and and_57 (and_57_out, n17bit_adder_4_out_49, _40, _20, _10);
  or or_13 (out_17, and_64_out, and_119_out, and_146_out, and_163_out, and_6_out, and_24_out, and_41_out, and_74_out, and_117_out);
  and and_58 (and_58_out, n17bit_adder_4_out_48, _40, _20, _10);
  or or_14 (out_18, and_58_out, and_115_out, and_147_out, and_164_out, and_5_out, and_22_out, and_37_out, and_75_out, and_118_out);
  and and_59 (and_59_out, n17bit_adder_5_out_50, _20, _40);
  and and_60 (and_60_out, n17bit_adder_5_out_51, _20, _40);
  and and_61 (and_61_out, n17bit_adder_5_out_52, _20, _40);
  and and_62 (and_62_out, and_60_out, not_7_out);
  and and_63 (and_63_out, and_61_out, not_7_out);
  and and_64 (and_64_out, n17bit_adder_4_out_47, _40, _20, _10);
  and and_65 (and_65_out, n17bit_adder_4_out_46, _40, _20, _10);
  and and_66 (and_66_out, n17bit_adder_5_out_48, _20, _40);
  and and_67 (and_67_out, n17bit_adder_5_out_49, _20, _40);
  and and_68 (and_68_out, and_67_out, not_7_out);
  and and_69 (and_69_out, and_59_out, not_7_out);
  _17bit_Adder u_17bit_adder_4 (
    .in_1(not_63_out), .in_2(_10), .in_3(not_62_out), .in_4(_10), .in_5(not_57_out), .in_6(not_56_out),
    .in_7(not_61_out), .in_8(not_60_out), .in_9(not_58_out), .in_10(not_55_out), .in_11(not_59_out),
    .in_12(not_50_out), .in_13(not_54_out), .in_14(not_48_out), .in_15(not_53_out), .in_16(not_49_out),
    .in_17(not_51_out), .in_18(and_61_out), .in_19(and_60_out), .in_20(and_59_out), .in_21(and_67_out),
    .in_22(and_66_out), .in_23(and_71_out), .in_24(and_73_out), .in_25(and_72_out), .in_26(and_80_out),
    .in_27(and_81_out), .in_28(and_79_out), .in_29(and_87_out), .in_30(and_88_out), .in_31(and_92_out),
    .in_32(and_94_out), .in_33(and_93_out), .in_34(and_100_out), .out_35(n17bit_adder_4_out_35),
    .out_36(n17bit_adder_4_out_36), .out_37(n17bit_adder_4_out_37), .out_38(n17bit_adder_4_out_38),
    .out_39(n17bit_adder_4_out_39), .out_40(n17bit_adder_4_out_40), .out_41(n17bit_adder_4_out_41),
    .out_42(n17bit_adder_4_out_42), .out_43(n17bit_adder_4_out_43), .out_44(n17bit_adder_4_out_44),
    .out_45(n17bit_adder_4_out_45), .out_46(n17bit_adder_4_out_46), .out_47(n17bit_adder_4_out_47),
    .out_48(n17bit_adder_4_out_48), .out_49(n17bit_adder_4_out_49), .out_50(n17bit_adder_4_out_50),
    .out_51(n17bit_adder_4_out_51), .out_52(n17bit_adder_4_out_52));
  and and_70 (and_70_out, n17bit_adder_4_out_45, _40, _20, _10);
  or or_15 (out_19, and_57_out, and_116_out, and_145_out, and_162_out, and_4_out, and_21_out, and_32_out, and_68_out, and_114_out);
  and and_71 (and_71_out, n17bit_adder_5_out_47, _20, _40);
  and and_72 (and_72_out, n17bit_adder_5_out_45, _20, _40);
  and and_73 (and_73_out, n17bit_adder_5_out_46, _20, _40);
  and and_74 (and_74_out, and_71_out, not_7_out);
  and and_75 (and_75_out, and_66_out, not_7_out);
  and and_76 (and_76_out, and_73_out, not_7_out);
  and and_77 (and_77_out, n17bit_adder_4_out_43, _40, _20, _10);
  and and_78 (and_78_out, n17bit_adder_4_out_44, _40, _20, _10);
  or or_16 (out_20, and_56_out, and_113_out, and_144_out, and_160_out, and_2_out, and_20_out, and_33_out, and_69_out, and_112_out);
  _17bit_Adder u_17bit_adder_5 (
    .in_1(not_32_out), .in_2(not_30_out), .in_3(not_31_out), .in_4(_40), .in_5(not_29_out), .in_6(_40),
    .in_7(not_33_out), .in_8(not_25_out), .in_9(not_23_out), .in_10(not_21_out), .in_11(not_26_out),
    .in_12(not_27_out), .in_13(not_28_out), .in_14(not_24_out), .in_15(not_22_out), .in_16(not_16_out),
    .in_17(not_15_out), .in_18(not_52_out), .in_19(not_47_out), .in_20(_20), .in_21(not_44_out), .in_22(_20),
    .in_23(not_43_out), .in_24(not_42_out), .in_25(not_46_out), .in_26(not_45_out), .in_27(not_34_out),
    .in_28(not_41_out), .in_29(not_37_out), .in_30(not_39_out), .in_31(not_38_out), .in_32(not_40_out),
    .in_33(not_35_out), .in_34(not_36_out), .out_35(n17bit_adder_5_out_35), .out_36(n17bit_adder_5_out_36),
    .out_37(n17bit_adder_5_out_37), .out_38(n17bit_adder_5_out_38), .out_39(n17bit_adder_5_out_39),
    .out_40(n17bit_adder_5_out_40), .out_41(n17bit_adder_5_out_41), .out_42(n17bit_adder_5_out_42),
    .out_43(n17bit_adder_5_out_43), .out_44(n17bit_adder_5_out_44), .out_45(n17bit_adder_5_out_45),
    .out_46(n17bit_adder_5_out_46), .out_47(n17bit_adder_5_out_47), .out_48(n17bit_adder_5_out_48),
    .out_49(n17bit_adder_5_out_49), .out_50(n17bit_adder_5_out_50), .out_51(n17bit_adder_5_out_51),
    .out_52(n17bit_adder_5_out_52));
  and and_79 (and_79_out, n17bit_adder_5_out_42, _20, _40);
  and and_80 (and_80_out, n17bit_adder_5_out_44, _20, _40);
  and and_81 (and_81_out, n17bit_adder_5_out_43, _20, _40);
  and and_82 (and_82_out, and_81_out, not_7_out);
  and and_83 (and_83_out, and_80_out, not_7_out);
  and and_84 (and_84_out, and_72_out, not_7_out);
  and and_85 (and_85_out, n17bit_adder_4_out_42, _40, _20, _10);
  and and_86 (and_86_out, n17bit_adder_4_out_41, _40, _20, _10);
  or or_17 (out_21, and_55_out, and_111_out, and_143_out, and_161_out, and_3_out, and_19_out, and_28_out, and_62_out, and_109_out);
  and and_87 (and_87_out, n17bit_adder_5_out_41, _20, _40);
  and and_88 (and_88_out, n17bit_adder_5_out_40, _20, _40);
  and and_89 (and_89_out, and_79_out, not_7_out);
  and and_90 (and_90_out, and_87_out, not_7_out);
  and and_91 (and_91_out, n17bit_adder_4_out_40, _40, _20, _10);
  and and_92 (and_92_out, n17bit_adder_5_out_39, _20, _40);
  and and_93 (and_93_out, n17bit_adder_5_out_37, _20, _40);
  and and_94 (and_94_out, n17bit_adder_5_out_38, _20, _40);
  and and_95 (and_95_out, and_92_out, not_7_out);
  and and_96 (and_96_out, and_88_out, not_7_out);
  and and_97 (and_97_out, and_94_out, not_7_out);
  and and_98 (and_98_out, n17bit_adder_4_out_39, _40, _20, _10);
  and and_99 (and_99_out, n17bit_adder_4_out_38, _40, _20, _10);
  or or_18 (out_22, and_54_out, and_110_out, and_142_out, and_159_out, and_1_out, and_18_out, and_25_out, and_63_out, and_108_out);
  and and_100 (and_100_out, n17bit_adder_5_out_36, _20, _40);
  and and_101 (and_101_out, n17bit_adder_5_out_35, _20, _40);
  and and_102 (and_102_out, and_100_out, not_7_out);
  and and_103 (and_103_out, and_93_out, not_7_out);
  and and_104 (and_104_out, and_101_out, not_7_out);
  and and_105 (and_105_out, n17bit_adder_4_out_37, _40, _20, _10);
  and and_106 (and_106_out, n17bit_adder_4_out_35, _40, _20, _10);
  and and_107 (and_107_out, n17bit_adder_4_out_36, _40, _20, _10);
  and and_108 (and_108_out, not_32_out, not_68_out, not_67_out, _40);
  and and_109 (and_109_out, not_30_out, not_68_out, not_67_out, _40);
  not not_64 (not_64_out, _20);
  not not_65 (not_65_out, _80);
  not not_66 (not_66_out, _40);
  and and_110 (and_110_out, not_63_out, not_65_out, _10, not_66_out, not_64_out);
  and and_111 (and_111_out, _10, not_65_out, _10, not_66_out, not_64_out);
  and and_112 (and_112_out, not_31_out, not_68_out, not_67_out, _40);
  and and_113 (and_113_out, not_62_out, not_65_out, _10, not_66_out, not_64_out);
  and and_114 (and_114_out, _40, not_68_out, not_67_out, _40);
  and and_115 (and_115_out, not_57_out, not_65_out, _10, not_66_out, not_64_out);
  and and_116 (and_116_out, _10, not_65_out, _10, not_66_out, not_64_out);
  and and_117 (and_117_out, _40, not_68_out, not_67_out, _40);
  and and_118 (and_118_out, not_29_out, not_68_out, not_67_out, _40);
  and and_119 (and_119_out, not_56_out, not_65_out, _10, not_66_out, not_64_out);
  and and_120 (and_120_out, not_25_out, not_68_out, not_67_out, _40);
  and and_121 (and_121_out, not_33_out, not_68_out, not_67_out, _40);
  and and_122 (and_122_out, not_61_out, not_65_out, _10, not_66_out, not_64_out);
  and and_123 (and_123_out, not_60_out, not_65_out, _10, not_66_out, not_64_out);
  and and_124 (and_124_out, not_23_out, not_68_out, not_67_out, _40);
  and and_125 (and_125_out, not_55_out, not_65_out, _10, not_66_out, not_64_out);
  and and_126 (and_126_out, not_58_out, not_65_out, _10, not_66_out, not_64_out);
  not not_67 (not_67_out, _10);
  and and_127 (and_127_out, not_26_out, not_68_out, not_67_out, _40);
  and and_128 (and_128_out, not_21_out, not_68_out, not_67_out, _40);
  and and_129 (and_129_out, not_59_out, not_65_out, _10, not_66_out, not_64_out);
  not not_68 (not_68_out, _20);
  and and_130 (and_130_out, not_27_out, not_68_out, not_67_out, _40);
  and and_131 (and_131_out, not_54_out, not_65_out, _10, not_66_out, not_64_out);
  and and_132 (and_132_out, not_50_out, not_65_out, _10, not_66_out, not_64_out);
  and and_133 (and_133_out, not_28_out, not_68_out, not_67_out, _40);
  and and_134 (and_134_out, not_24_out, not_68_out, not_67_out, _40);
  and and_135 (and_135_out, not_48_out, not_65_out, _10, not_66_out, not_64_out);
  and and_136 (and_136_out, not_16_out, not_68_out, not_67_out, _40);
  and and_137 (and_137_out, not_22_out, not_68_out, not_67_out, _40);
  and and_138 (and_138_out, not_49_out, not_65_out, _10, not_66_out, not_64_out);
  and and_139 (and_139_out, not_53_out, not_65_out, _10, not_66_out, not_64_out);
  and and_140 (and_140_out, not_15_out, not_68_out, not_67_out, _40);
  and and_141 (and_141_out, not_51_out, not_65_out, _10, not_66_out, not_64_out);
  not not_69 (not_69_out, _40);
  and and_142 (and_142_out, not_52_out, _20, not_67_out, not_69_out);
  and and_143 (and_143_out, not_47_out, _20, not_67_out, not_69_out);
  and and_144 (and_144_out, _20, _20, not_67_out, not_69_out);
  and and_145 (and_145_out, not_44_out, _20, not_67_out, not_69_out);
  and and_146 (and_146_out, not_43_out, _20, not_67_out, not_69_out);
  and and_147 (and_147_out, _20, _20, not_67_out, not_69_out);
  and and_148 (and_148_out, not_42_out, _20, not_67_out, not_69_out);
  and and_149 (and_149_out, not_46_out, _20, not_67_out, not_69_out);
  and and_150 (and_150_out, not_45_out, _20, not_67_out, not_69_out);
  and and_151 (and_151_out, not_41_out, _20, not_67_out, not_69_out);
  and and_152 (and_152_out, not_34_out, _20, not_67_out, not_69_out);
  and and_153 (and_153_out, not_37_out, _20, not_67_out, not_69_out);
  and and_154 (and_154_out, not_38_out, _20, not_67_out, not_69_out);
  and and_155 (and_155_out, not_39_out, _20, not_67_out, not_69_out);
  and and_156 (and_156_out, not_35_out, _20, not_67_out, not_69_out);
  and and_157 (and_157_out, not_40_out, _20, not_67_out, not_69_out);
  and and_158 (and_158_out, not_36_out, _20, not_67_out, not_69_out);
  not not_70 (not_70_out, _20);
  and and_159 (and_159_out, n17bit_adder_3_out_52, not_70_out, _40, _10);
  and and_160 (and_160_out, n17bit_adder_3_out_50, not_70_out, _40, _10);
  and and_161 (and_161_out, n17bit_adder_3_out_51, not_70_out, _40, _10);
  and and_162 (and_162_out, n17bit_adder_3_out_49, not_70_out, _40, _10);
  and and_163 (and_163_out, n17bit_adder_3_out_47, not_70_out, _40, _10);
  and and_164 (and_164_out, n17bit_adder_3_out_48, not_70_out, _40, _10);
  and and_165 (and_165_out, n17bit_adder_3_out_46, not_70_out, _40, _10);
  and and_166 (and_166_out, n17bit_adder_3_out_44, not_70_out, _40, _10);
  and and_167 (and_167_out, n17bit_adder_3_out_45, not_70_out, _40, _10);
  and and_168 (and_168_out, n17bit_adder_3_out_43, not_70_out, _40, _10);
  and and_169 (and_169_out, n17bit_adder_3_out_42, not_70_out, _40, _10);
  and and_170 (and_170_out, n17bit_adder_3_out_41, not_70_out, _40, _10);
  and and_171 (and_171_out, n17bit_adder_3_out_40, not_70_out, _40, _10);
  and and_172 (and_172_out, n17bit_adder_3_out_39, not_70_out, _40, _10);
  and and_173 (and_173_out, n17bit_adder_3_out_38, not_70_out, _40, _10);
  and and_174 (and_174_out, n17bit_adder_3_out_37, not_70_out, _40, _10);
  and and_175 (and_175_out, n17bit_adder_3_out_36, not_70_out, _40, _10);
  and and_176 (and_176_out, n17bit_adder_3_out_35, not_70_out, _40, _10);

  // Notes on the sheet:
  //   8
  //   9
  //   3
  //   5
  //   7
  //   RIGHT = LARGE SIDE
  //   6
  //   4
  //   1
  //   1
  //   2
  //   4
  //   2
endmodule

module BCD_Binary_100 (
  input  _800,
  input  _400,
  input  _200,
  input  _100,
  output out_5,
  output out_6,
  output out_7,
  output out_8,
  output out_9,
  output out_10,
  output out_11,
  output out_12,
  output out_13,
  output out_14,
  output out_15,
  output out_16,
  output out_17,
  output out_18,
  output out_19,
  output out_20,
  output out_21,
  output out_22
);

  wire and_1_out, and_2_out, and_3_out, and_4_out, and_5_out, and_6_out, and_7_out, and_8_out, and_9_out,
       and_10_out, and_11_out, and_12_out, and_13_out, and_14_out, and_15_out, and_16_out, and_17_out,
       and_18_out, and_19_out, and_20_out, and_21_out, and_22_out, and_23_out, and_24_out, and_25_out,
       and_26_out, and_27_out, and_28_out, and_29_out, and_30_out, and_31_out, and_32_out, and_33_out,
       and_34_out, and_35_out, and_36_out, and_37_out, and_38_out, and_39_out, and_40_out, and_41_out,
       and_42_out, and_43_out, and_44_out, and_45_out, and_46_out, and_47_out, and_48_out, and_49_out,
       and_50_out, and_51_out, and_52_out, and_53_out, and_54_out, and_55_out, and_56_out, and_57_out,
       and_58_out, and_59_out, and_60_out, and_61_out, and_62_out, and_63_out, and_64_out, and_65_out,
       and_66_out, and_67_out, and_68_out, and_69_out, and_70_out, and_71_out, and_72_out, and_73_out,
       and_74_out, and_75_out, and_76_out, and_77_out, and_78_out, and_79_out, and_80_out, and_81_out,
       and_82_out, and_83_out, and_84_out, and_85_out, and_86_out, and_87_out, and_88_out, and_89_out,
       and_90_out, and_91_out, and_92_out, and_93_out, and_94_out, and_95_out, and_96_out, and_97_out,
       and_98_out, and_99_out, and_100_out, and_101_out, and_102_out, and_103_out, and_104_out, and_105_out,
       and_106_out, and_107_out, and_108_out, and_109_out, and_110_out, and_111_out, and_112_out,
       and_113_out, and_114_out, and_115_out, and_116_out, and_117_out, and_118_out, and_119_out,
       and_120_out, and_121_out, and_122_out, and_123_out, and_124_out, and_125_out, and_126_out,
       and_127_out, and_128_out, and_129_out, and_130_out, and_131_out, and_132_out, and_133_out,
       and_134_out, and_135_out, and_136_out, and_137_out, and_138_out, and_139_out, and_140_out,
       and_141_out, and_142_out, and_143_out, and_144_out, and_145_out, and_146_out, and_147_out,
       and_148_out, and_149_out, and_150_out, and_151_out, and_152_out, and_153_out, and_154_out,
       and_155_out, and_156_out, and_157_out, and_158_out, and_159_out, and_160_out, and_161_out,
       and_162_out, and_163_out, and_164_out, and_165_out, and_166_out, and_167_out, and_168_out,
       and_169_out, and_170_out, and_171_out, and_172_out, and_173_out, and_174_out, and_175_out,
       and_176_out, n17bit_adder_1_out_35, n17bit_adder_1_out_36, n17bit_adder_1_out_37,
       n17bit_adder_1_out_38, n17bit_adder_1_out_39, n17bit_adder_1_out_40, n17bit_adder_1_out_41,
       n17bit_adder_1_out_42, n17bit_adder_1_out_43, n17bit_adder_1_out_44, n17bit_adder_1_out_45,
       n17bit_adder_1_out_46, n17bit_adder_1_out_47, n17bit_adder_1_out_48, n17bit_adder_1_out_49,
       n17bit_adder_1_out_50, n17bit_adder_1_out_51, n17bit_adder_1_out_52, n17bit_adder_2_out_35,
       n17bit_adder_2_out_36, n17bit_adder_2_out_37, n17bit_adder_2_out_38, n17bit_adder_2_out_39,
       n17bit_adder_2_out_40, n17bit_adder_2_out_41, n17bit_adder_2_out_42, n17bit_adder_2_out_43,
       n17bit_adder_2_out_44, n17bit_adder_2_out_45, n17bit_adder_2_out_46, n17bit_adder_2_out_47,
       n17bit_adder_2_out_48, n17bit_adder_2_out_49, n17bit_adder_2_out_50, n17bit_adder_2_out_51,
       n17bit_adder_2_out_52, n17bit_adder_3_out_35, n17bit_adder_3_out_36, n17bit_adder_3_out_37,
       n17bit_adder_3_out_38, n17bit_adder_3_out_39, n17bit_adder_3_out_40, n17bit_adder_3_out_41,
       n17bit_adder_3_out_42, n17bit_adder_3_out_43, n17bit_adder_3_out_44, n17bit_adder_3_out_45,
       n17bit_adder_3_out_46, n17bit_adder_3_out_47, n17bit_adder_3_out_48, n17bit_adder_3_out_49,
       n17bit_adder_3_out_50, n17bit_adder_3_out_51, n17bit_adder_3_out_52, n17bit_adder_4_out_35,
       n17bit_adder_4_out_36, n17bit_adder_4_out_37, n17bit_adder_4_out_38, n17bit_adder_4_out_39,
       n17bit_adder_4_out_40, n17bit_adder_4_out_41, n17bit_adder_4_out_42, n17bit_adder_4_out_43,
       n17bit_adder_4_out_44, n17bit_adder_4_out_45, n17bit_adder_4_out_46, n17bit_adder_4_out_47,
       n17bit_adder_4_out_48, n17bit_adder_4_out_49, n17bit_adder_4_out_50, n17bit_adder_4_out_51,
       n17bit_adder_4_out_52, n17bit_adder_5_out_35, n17bit_adder_5_out_36, n17bit_adder_5_out_37,
       n17bit_adder_5_out_38, n17bit_adder_5_out_39, n17bit_adder_5_out_40, n17bit_adder_5_out_41,
       n17bit_adder_5_out_42, n17bit_adder_5_out_43, n17bit_adder_5_out_44, n17bit_adder_5_out_45,
       n17bit_adder_5_out_46, n17bit_adder_5_out_47, n17bit_adder_5_out_48, n17bit_adder_5_out_49,
       n17bit_adder_5_out_50, n17bit_adder_5_out_51, n17bit_adder_5_out_52, not_1_out, not_2_out, not_3_out,
       not_4_out, not_5_out, not_6_out, not_7_out, not_8_out, not_9_out, not_10_out, not_11_out, not_12_out,
       not_13_out, not_14_out, not_15_out, not_16_out, not_17_out, not_18_out, not_19_out, not_20_out,
       not_21_out, not_22_out, not_23_out, not_24_out, not_25_out, not_26_out, not_27_out, not_28_out,
       not_29_out, not_30_out, not_31_out, not_32_out, not_33_out, not_34_out, not_35_out, not_36_out,
       not_37_out, not_38_out, not_39_out, not_40_out, not_41_out, not_42_out, not_43_out, not_44_out,
       not_45_out, not_46_out, not_47_out, not_48_out, not_49_out, not_50_out, not_51_out, not_52_out,
       not_53_out, not_54_out, not_55_out, not_56_out, not_57_out, not_58_out, not_59_out, not_60_out,
       not_61_out, not_62_out, not_63_out, not_64_out, not_65_out, not_66_out;

  and and_1 (and_1_out, not_1_out, _800, not_15_out);
  and and_2 (and_2_out, not_1_out, _800, not_14_out);
  and and_3 (and_3_out, not_1_out, _800, not_17_out);
  and and_4 (and_4_out, not_1_out, _800, not_19_out);
  and and_5 (and_5_out, not_1_out, _800, _800);
  and and_6 (and_6_out, not_1_out, _800, not_16_out);
  and and_7 (and_7_out, not_1_out, _800, _800);
  and and_8 (and_8_out, not_1_out, _800, not_10_out);
  and and_9 (and_9_out, not_1_out, _800, not_8_out);
  and and_10 (and_10_out, not_1_out, _800, _800);
  and and_11 (and_11_out, not_1_out, _800, not_9_out);
  and and_12 (and_12_out, not_1_out, _800, not_12_out);
  and and_13 (and_13_out, not_1_out, _800, not_11_out);
  and and_14 (and_14_out, not_1_out, _800, not_2_out);
  and and_15 (and_15_out, not_1_out, _800, not_5_out);
  and and_16 (and_16_out, not_1_out, _800, not_4_out);
  and and_17 (and_17_out, not_1_out, _800, not_3_out);
  not not_1 (not_1_out, _100);
  not not_2 (not_2_out, _800);
  not not_3 (not_3_out, _800);
  not not_4 (not_4_out, _800);
  not not_5 (not_5_out, _800);
  and and_18 (and_18_out, n17bit_adder_1_out_52, _800, _100);
  not not_6 (not_6_out, _400);
  not not_7 (not_7_out, _100);
  not not_8 (not_8_out, _800);
  not not_9 (not_9_out, _800);
  not not_10 (not_10_out, _800);
  not not_11 (not_11_out, _800);
  not not_12 (not_12_out, _800);
  and and_19 (and_19_out, n17bit_adder_1_out_51, _800, _100);
  and and_20 (and_20_out, n17bit_adder_1_out_49, _800, _100);
  and and_21 (and_21_out, n17bit_adder_1_out_50, _800, _100);
  not not_13 (not_13_out, _400);
  not not_14 (not_14_out, _800);
  not not_15 (not_15_out, _800);
  not not_16 (not_16_out, _800);
  not not_17 (not_17_out, _800);
  not not_18 (not_18_out, _400);
  not not_19 (not_19_out, _800);
  and and_22 (and_22_out, n17bit_adder_1_out_48, _800, _100);
  and and_23 (and_23_out, n17bit_adder_1_out_47, _800, _100);
  and and_24 (and_24_out, n17bit_adder_1_out_46, _800, _100);
  and and_25 (and_25_out, n17bit_adder_2_out_52, _200, not_6_out, _100);
  or or_1 (out_5, and_107_out, and_176_out, and_42_out, and_53_out, and_104_out);
  not not_20 (not_20_out, _400);
  not not_21 (not_21_out, _400);
  not not_22 (not_22_out, _400);
  not not_23 (not_23_out, _400);
  not not_24 (not_24_out, _400);
  not not_25 (not_25_out, _400);
  _17bit_Adder u_17bit_adder_1 (
    .in_1(not_59_out), .in_2(not_58_out), .in_3(_100), .in_4(not_52_out), .in_5(not_56_out), .in_6(_100),
    .in_7(_100), .in_8(not_53_out), .in_9(not_57_out), .in_10(not_54_out), .in_11(not_55_out),
    .in_12(not_46_out), .in_13(not_51_out), .in_14(not_49_out), .in_15(not_48_out), .in_16(not_50_out),
    .in_17(not_45_out), .in_18(not_15_out), .in_19(not_19_out), .in_20(not_17_out), .in_21(not_14_out),
    .in_22(not_16_out), .in_23(_800), .in_24(not_8_out), .in_25(not_10_out), .in_26(_800), .in_27(_800),
    .in_28(not_12_out), .in_29(not_9_out), .in_30(not_11_out), .in_31(not_2_out), .in_32(not_4_out),
    .in_33(not_3_out), .in_34(not_5_out), .out_35(n17bit_adder_1_out_35), .out_36(n17bit_adder_1_out_36),
    .out_37(n17bit_adder_1_out_37), .out_38(n17bit_adder_1_out_38), .out_39(n17bit_adder_1_out_39),
    .out_40(n17bit_adder_1_out_40), .out_41(n17bit_adder_1_out_41), .out_42(n17bit_adder_1_out_42),
    .out_43(n17bit_adder_1_out_43), .out_44(n17bit_adder_1_out_44), .out_45(n17bit_adder_1_out_45),
    .out_46(n17bit_adder_1_out_46), .out_47(n17bit_adder_1_out_47), .out_48(n17bit_adder_1_out_48),
    .out_49(n17bit_adder_1_out_49), .out_50(n17bit_adder_1_out_50), .out_51(n17bit_adder_1_out_51),
    .out_52(n17bit_adder_1_out_52));
  and and_26 (and_26_out, n17bit_adder_1_out_44, _800, _100);
  and and_27 (and_27_out, n17bit_adder_1_out_45, _800, _100);
  and and_28 (and_28_out, n17bit_adder_2_out_51, _200, not_6_out, _100);
  not not_26 (not_26_out, _400);
  not not_27 (not_27_out, _400);
  not not_28 (not_28_out, _400);
  not not_29 (not_29_out, _400);
  not not_30 (not_30_out, _400);
  not not_31 (not_31_out, _400);
  and and_29 (and_29_out, n17bit_adder_1_out_42, _800, _100);
  and and_30 (and_30_out, n17bit_adder_1_out_41, _800, _100);
  and and_31 (and_31_out, n17bit_adder_1_out_43, _800, _100);
  and and_32 (and_32_out, n17bit_adder_2_out_50, _200, not_6_out, _100);
  and and_33 (and_33_out, n17bit_adder_2_out_49, _200, not_6_out, _100);
  or or_2 (out_6, and_106_out, and_141_out, and_158_out, and_175_out, and_15_out, and_38_out, and_52_out, and_103_out, and_140_out);
  not not_32 (not_32_out, _200);
  not not_33 (not_33_out, _200);
  not not_34 (not_34_out, _200);
  not not_35 (not_35_out, _200);
  not not_36 (not_36_out, _200);
  not not_37 (not_37_out, _200);
  not not_38 (not_38_out, _200);
  not not_39 (not_39_out, _200);
  and and_34 (and_34_out, n17bit_adder_1_out_38, _800, _100);
  and and_35 (and_35_out, n17bit_adder_1_out_39, _800, _100);
  and and_36 (and_36_out, n17bit_adder_1_out_40, _800, _100);
  and and_37 (and_37_out, n17bit_adder_2_out_48, _200, not_6_out, _100);
  or or_3 (out_7, and_105_out, and_139_out, and_156_out, and_174_out, and_17_out, and_39_out, and_51_out, and_102_out, and_136_out);
  not not_40 (not_40_out, _200);
  not not_41 (not_41_out, _200);
  not not_42 (not_42_out, _200);
  not not_43 (not_43_out, _200);
  not not_44 (not_44_out, _200);
  and and_38 (and_38_out, n17bit_adder_1_out_36, _800, _100);
  and and_39 (and_39_out, n17bit_adder_1_out_37, _800, _100);
  and and_40 (and_40_out, n17bit_adder_2_out_47, _200, not_6_out, _100);
  and and_41 (and_41_out, n17bit_adder_2_out_46, _200, not_6_out, _100);
  not not_45 (not_45_out, _100);
  not not_46 (not_46_out, _100);
  not not_47 (not_47_out, _200);
  not not_48 (not_48_out, _100);
  not not_49 (not_49_out, _100);
  not not_50 (not_50_out, _100);
  not not_51 (not_51_out, _100);
  and and_42 (and_42_out, n17bit_adder_1_out_35, _800, _100);
  and and_43 (and_43_out, n17bit_adder_2_out_45, _200, not_6_out, _100);
  and and_44 (and_44_out, n17bit_adder_2_out_44, _200, not_6_out, _100);
  or or_4 (out_8, and_98_out, and_138_out, and_157_out, and_173_out, and_16_out, and_34_out, and_49_out, and_97_out, and_137_out);
  not not_52 (not_52_out, _100);
  not not_53 (not_53_out, _100);
  not not_54 (not_54_out, _100);
  not not_55 (not_55_out, _100);
  not not_56 (not_56_out, _100);
  not not_57 (not_57_out, _100);
  and and_45 (and_45_out, n17bit_adder_2_out_43, _200, not_6_out, _100);
  or or_5 (out_9, and_99_out, and_135_out, and_155_out, and_172_out, and_14_out, and_35_out, and_50_out, and_95_out, and_133_out);
  not not_58 (not_58_out, _100);
  not not_59 (not_59_out, _100);
  and and_46 (and_46_out, n17bit_adder_2_out_41, _200, not_6_out, _100);
  and and_47 (and_47_out, n17bit_adder_2_out_42, _200, not_6_out, _100);
  or or_6 (out_10, and_91_out, and_131_out, and_154_out, and_171_out, and_13_out, and_36_out, and_48_out, and_96_out, and_134_out);
  _17bit_Adder u_17bit_adder_2 (
    .in_1(not_47_out), .in_2(not_44_out), .in_3(not_41_out), .in_4(_200), .in_5(not_43_out),
    .in_6(not_40_out), .in_7(_200), .in_8(_200), .in_9(not_42_out), .in_10(not_39_out), .in_11(not_36_out),
    .in_12(not_33_out), .in_13(not_34_out), .in_14(not_37_out), .in_15(not_32_out), .in_16(not_35_out),
    .in_17(not_38_out), .in_18(not_59_out), .in_19(not_58_out), .in_20(_100), .in_21(not_52_out),
    .in_22(not_56_out), .in_23(_100), .in_24(_100), .in_25(not_53_out), .in_26(not_57_out),
    .in_27(not_54_out), .in_28(not_55_out), .in_29(not_46_out), .in_30(not_51_out), .in_31(not_49_out),
    .in_32(not_48_out), .in_33(not_50_out), .in_34(not_45_out), .out_35(n17bit_adder_2_out_35),
    .out_36(n17bit_adder_2_out_36), .out_37(n17bit_adder_2_out_37), .out_38(n17bit_adder_2_out_38),
    .out_39(n17bit_adder_2_out_39), .out_40(n17bit_adder_2_out_40), .out_41(n17bit_adder_2_out_41),
    .out_42(n17bit_adder_2_out_42), .out_43(n17bit_adder_2_out_43), .out_44(n17bit_adder_2_out_44),
    .out_45(n17bit_adder_2_out_45), .out_46(n17bit_adder_2_out_46), .out_47(n17bit_adder_2_out_47),
    .out_48(n17bit_adder_2_out_48), .out_49(n17bit_adder_2_out_49), .out_50(n17bit_adder_2_out_50),
    .out_51(n17bit_adder_2_out_51), .out_52(n17bit_adder_2_out_52));
  and and_48 (and_48_out, n17bit_adder_2_out_40, _200, not_6_out, _100);
  and and_49 (and_49_out, n17bit_adder_2_out_38, _200, not_6_out, _100);
  and and_50 (and_50_out, n17bit_adder_2_out_39, _200, not_6_out, _100);
  or or_7 (out_11, and_85_out, and_132_out, and_153_out, and_170_out, and_11_out, and_30_out, and_46_out, and_90_out, and_130_out);
  and and_51 (and_51_out, n17bit_adder_2_out_37, _200, not_6_out, _100);
  and and_52 (and_52_out, n17bit_adder_2_out_36, _200, not_6_out, _100);
  or or_8 (out_12, and_86_out, and_129_out, and_152_out, and_168_out, and_12_out, and_29_out, and_47_out, and_89_out, and_128_out);
  and and_53 (and_53_out, n17bit_adder_2_out_35, _200, not_6_out, _100);
  or or_9 (out_13, and_78_out, and_125_out, and_151_out, and_169_out, and_10_out, and_31_out, and_45_out, and_82_out, and_127_out);
  or or_10 (out_14, and_77_out, and_126_out, and_150_out, and_167_out, and_7_out, and_26_out, and_44_out, and_83_out, and_124_out);
  or or_11 (out_15, and_70_out, and_123_out, and_149_out, and_166_out, and_8_out, and_27_out, and_43_out, and_84_out, and_121_out);
  _17bit_Adder u_17bit_adder_3 (
    .in_1(not_59_out), .in_2(not_58_out), .in_3(_100), .in_4(not_52_out), .in_5(not_56_out), .in_6(_100),
    .in_7(_100), .in_8(not_53_out), .in_9(not_57_out), .in_10(not_54_out), .in_11(not_55_out),
    .in_12(not_46_out), .in_13(not_51_out), .in_14(not_49_out), .in_15(not_48_out), .in_16(not_50_out),
    .in_17(not_45_out), .in_18(not_26_out), .in_19(not_28_out), .in_20(not_30_out), .in_21(not_27_out),
    .in_22(_400), .in_23(not_29_out), .in_24(not_31_out), .in_25(_400), .in_26(_400), .in_27(not_21_out),
    .in_28(not_24_out), .in_29(not_23_out), .in_30(not_20_out), .in_31(not_25_out), .in_32(not_22_out),
    .in_33(not_18_out), .in_34(not_13_out), .out_35(n17bit_adder_3_out_35), .out_36(n17bit_adder_3_out_36),
    .out_37(n17bit_adder_3_out_37), .out_38(n17bit_adder_3_out_38), .out_39(n17bit_adder_3_out_39),
    .out_40(n17bit_adder_3_out_40), .out_41(n17bit_adder_3_out_41), .out_42(n17bit_adder_3_out_42),
    .out_43(n17bit_adder_3_out_43), .out_44(n17bit_adder_3_out_44), .out_45(n17bit_adder_3_out_45),
    .out_46(n17bit_adder_3_out_46), .out_47(n17bit_adder_3_out_47), .out_48(n17bit_adder_3_out_48),
    .out_49(n17bit_adder_3_out_49), .out_50(n17bit_adder_3_out_50), .out_51(n17bit_adder_3_out_51),
    .out_52(n17bit_adder_3_out_52));
  and and_54 (and_54_out, n17bit_adder_4_out_51, _400, _200, _100);
  and and_55 (and_55_out, n17bit_adder_4_out_52, _400, _200, _100);
  or or_12 (out_16, and_64_out, and_122_out, and_148_out, and_165_out, and_9_out, and_24_out, and_41_out, and_75_out, and_120_out);
  and and_56 (and_56_out, n17bit_adder_4_out_49, _400, _200, _100);
  and and_57 (and_57_out, n17bit_adder_4_out_50, _400, _200, _100);
  or or_13 (out_17, and_65_out, and_119_out, and_146_out, and_163_out, and_5_out, and_23_out, and_40_out, and_76_out, and_118_out);
  and and_58 (and_58_out, n17bit_adder_4_out_48, _400, _200, _100);
  or or_14 (out_18, and_58_out, and_116_out, and_147_out, and_164_out, and_6_out, and_22_out, and_37_out, and_74_out, and_117_out);
  and and_59 (and_59_out, n17bit_adder_5_out_52, _200, _400);
  and and_60 (and_60_out, n17bit_adder_5_out_51, _200, _400);
  and and_61 (and_61_out, n17bit_adder_5_out_50, _200, _400);
  and and_62 (and_62_out, and_60_out, not_7_out);
  and and_63 (and_63_out, and_59_out, not_7_out);
  and and_64 (and_64_out, n17bit_adder_4_out_46, _400, _200, _100);
  and and_65 (and_65_out, n17bit_adder_4_out_47, _400, _200, _100);
  and and_66 (and_66_out, n17bit_adder_5_out_49, _200, _400);
  and and_67 (and_67_out, n17bit_adder_5_out_48, _200, _400);
  and and_68 (and_68_out, and_66_out, not_7_out);
  and and_69 (and_69_out, and_61_out, not_7_out);
  _17bit_Adder u_17bit_adder_4 (
    .in_1(not_59_out), .in_2(not_58_out), .in_3(_100), .in_4(not_52_out), .in_5(not_56_out), .in_6(_100),
    .in_7(_100), .in_8(not_53_out), .in_9(not_57_out), .in_10(not_54_out), .in_11(not_55_out),
    .in_12(not_46_out), .in_13(not_51_out), .in_14(not_49_out), .in_15(not_48_out), .in_16(not_50_out),
    .in_17(not_45_out), .in_18(and_59_out), .in_19(and_60_out), .in_20(and_61_out), .in_21(and_66_out),
    .in_22(and_67_out), .in_23(and_73_out), .in_24(and_71_out), .in_25(and_72_out), .in_26(and_79_out),
    .in_27(and_81_out), .in_28(and_80_out), .in_29(and_88_out), .in_30(and_87_out), .in_31(and_92_out),
    .in_32(and_94_out), .in_33(and_93_out), .in_34(and_100_out), .out_35(n17bit_adder_4_out_35),
    .out_36(n17bit_adder_4_out_36), .out_37(n17bit_adder_4_out_37), .out_38(n17bit_adder_4_out_38),
    .out_39(n17bit_adder_4_out_39), .out_40(n17bit_adder_4_out_40), .out_41(n17bit_adder_4_out_41),
    .out_42(n17bit_adder_4_out_42), .out_43(n17bit_adder_4_out_43), .out_44(n17bit_adder_4_out_44),
    .out_45(n17bit_adder_4_out_45), .out_46(n17bit_adder_4_out_46), .out_47(n17bit_adder_4_out_47),
    .out_48(n17bit_adder_4_out_48), .out_49(n17bit_adder_4_out_49), .out_50(n17bit_adder_4_out_50),
    .out_51(n17bit_adder_4_out_51), .out_52(n17bit_adder_4_out_52));
  and and_70 (and_70_out, n17bit_adder_4_out_45, _400, _200, _100);
  or or_15 (out_19, and_56_out, and_115_out, and_145_out, and_162_out, and_2_out, and_20_out, and_33_out, and_68_out, and_114_out);
  and and_71 (and_71_out, n17bit_adder_5_out_46, _200, _400);
  and and_72 (and_72_out, n17bit_adder_5_out_45, _200, _400);
  and and_73 (and_73_out, n17bit_adder_5_out_47, _200, _400);
  and and_74 (and_74_out, and_67_out, not_7_out);
  and and_75 (and_75_out, and_71_out, not_7_out);
  and and_76 (and_76_out, and_73_out, not_7_out);
  and and_77 (and_77_out, n17bit_adder_4_out_44, _400, _200, _100);
  and and_78 (and_78_out, n17bit_adder_4_out_43, _400, _200, _100);
  or or_16 (out_20, and_57_out, and_113_out, and_143_out, and_160_out, and_3_out, and_21_out, and_32_out, and_69_out, and_112_out);
  _17bit_Adder u_17bit_adder_5 (
    .in_1(not_26_out), .in_2(not_28_out), .in_3(not_30_out), .in_4(not_27_out), .in_5(_400),
    .in_6(not_29_out), .in_7(not_31_out), .in_8(_400), .in_9(_400), .in_10(not_21_out), .in_11(not_24_out),
    .in_12(not_23_out), .in_13(not_20_out), .in_14(not_25_out), .in_15(not_22_out), .in_16(not_18_out),
    .in_17(not_13_out), .in_18(not_47_out), .in_19(not_44_out), .in_20(not_41_out), .in_21(_200),
    .in_22(not_43_out), .in_23(not_40_out), .in_24(_200), .in_25(_200), .in_26(not_42_out),
    .in_27(not_39_out), .in_28(not_36_out), .in_29(not_33_out), .in_30(not_34_out), .in_31(not_37_out),
    .in_32(not_32_out), .in_33(not_35_out), .in_34(not_38_out), .out_35(n17bit_adder_5_out_35),
    .out_36(n17bit_adder_5_out_36), .out_37(n17bit_adder_5_out_37), .out_38(n17bit_adder_5_out_38),
    .out_39(n17bit_adder_5_out_39), .out_40(n17bit_adder_5_out_40), .out_41(n17bit_adder_5_out_41),
    .out_42(n17bit_adder_5_out_42), .out_43(n17bit_adder_5_out_43), .out_44(n17bit_adder_5_out_44),
    .out_45(n17bit_adder_5_out_45), .out_46(n17bit_adder_5_out_46), .out_47(n17bit_adder_5_out_47),
    .out_48(n17bit_adder_5_out_48), .out_49(n17bit_adder_5_out_49), .out_50(n17bit_adder_5_out_50),
    .out_51(n17bit_adder_5_out_51), .out_52(n17bit_adder_5_out_52));
  and and_79 (and_79_out, n17bit_adder_5_out_44, _200, _400);
  and and_80 (and_80_out, n17bit_adder_5_out_42, _200, _400);
  and and_81 (and_81_out, n17bit_adder_5_out_43, _200, _400);
  and and_82 (and_82_out, and_81_out, not_7_out);
  and and_83 (and_83_out, and_79_out, not_7_out);
  and and_84 (and_84_out, and_72_out, not_7_out);
  and and_85 (and_85_out, n17bit_adder_4_out_41, _400, _200, _100);
  and and_86 (and_86_out, n17bit_adder_4_out_42, _400, _200, _100);
  or or_17 (out_21, and_54_out, and_110_out, and_144_out, and_161_out, and_4_out, and_19_out, and_28_out, and_62_out, and_109_out);
  and and_87 (and_87_out, n17bit_adder_5_out_40, _200, _400);
  and and_88 (and_88_out, n17bit_adder_5_out_41, _200, _400);
  and and_89 (and_89_out, and_80_out, not_7_out);
  and and_90 (and_90_out, and_88_out, not_7_out);
  and and_91 (and_91_out, n17bit_adder_4_out_40, _400, _200, _100);
  and and_92 (and_92_out, n17bit_adder_5_out_39, _200, _400);
  and and_93 (and_93_out, n17bit_adder_5_out_37, _200, _400);
  and and_94 (and_94_out, n17bit_adder_5_out_38, _200, _400);
  and and_95 (and_95_out, and_92_out, not_7_out);
  and and_96 (and_96_out, and_87_out, not_7_out);
  and and_97 (and_97_out, and_94_out, not_7_out);
  and and_98 (and_98_out, n17bit_adder_4_out_38, _400, _200, _100);
  and and_99 (and_99_out, n17bit_adder_4_out_39, _400, _200, _100);
  or or_18 (out_22, and_55_out, and_111_out, and_142_out, and_159_out, and_1_out, and_18_out, and_25_out, and_63_out, and_108_out);
  and and_100 (and_100_out, n17bit_adder_5_out_36, _200, _400);
  and and_101 (and_101_out, n17bit_adder_5_out_35, _200, _400);
  and and_102 (and_102_out, and_93_out, not_7_out);
  and and_103 (and_103_out, and_100_out, not_7_out);
  and and_104 (and_104_out, and_101_out, not_7_out);
  and and_105 (and_105_out, n17bit_adder_4_out_37, _400, _200, _100);
  and and_106 (and_106_out, n17bit_adder_4_out_36, _400, _200, _100);
  and and_107 (and_107_out, n17bit_adder_4_out_35, _400, _200, _100);
  and and_108 (and_108_out, not_26_out, not_64_out, not_63_out, _400);
  and and_109 (and_109_out, not_28_out, not_64_out, not_63_out, _400);
  not not_60 (not_60_out, _400);
  not not_61 (not_61_out, _800);
  not not_62 (not_62_out, _200);
  and and_110 (and_110_out, not_58_out, not_61_out, _100, not_60_out, not_62_out);
  and and_111 (and_111_out, not_59_out, not_61_out, _100, not_60_out, not_62_out);
  and and_112 (and_112_out, not_30_out, not_64_out, not_63_out, _400);
  and and_113 (and_113_out, _100, not_61_out, _100, not_60_out, not_62_out);
  and and_114 (and_114_out, not_27_out, not_64_out, not_63_out, _400);
  and and_115 (and_115_out, not_52_out, not_61_out, _100, not_60_out, not_62_out);
  and and_116 (and_116_out, not_56_out, not_61_out, _100, not_60_out, not_62_out);
  and and_117 (and_117_out, _400, not_64_out, not_63_out, _400);
  and and_118 (and_118_out, not_29_out, not_64_out, not_63_out, _400);
  and and_119 (and_119_out, _100, not_61_out, _100, not_60_out, not_62_out);
  and and_120 (and_120_out, not_31_out, not_64_out, not_63_out, _400);
  and and_121 (and_121_out, _400, not_64_out, not_63_out, _400);
  and and_122 (and_122_out, _100, not_61_out, _100, not_60_out, not_62_out);
  and and_123 (and_123_out, not_53_out, not_61_out, _100, not_60_out, not_62_out);
  and and_124 (and_124_out, _400, not_64_out, not_63_out, _400);
  and and_125 (and_125_out, not_54_out, not_61_out, _100, not_60_out, not_62_out);
  and and_126 (and_126_out, not_57_out, not_61_out, _100, not_60_out, not_62_out);
  not not_63 (not_63_out, _100);
  and and_127 (and_127_out, not_21_out, not_64_out, not_63_out, _400);
  and and_128 (and_128_out, not_24_out, not_64_out, not_63_out, _400);
  and and_129 (and_129_out, not_55_out, not_61_out, _100, not_60_out, not_62_out);
  not not_64 (not_64_out, _200);
  and and_130 (and_130_out, not_23_out, not_64_out, not_63_out, _400);
  and and_131 (and_131_out, not_51_out, not_61_out, _100, not_60_out, not_62_out);
  and and_132 (and_132_out, not_46_out, not_61_out, _100, not_60_out, not_62_out);
  and and_133 (and_133_out, not_25_out, not_64_out, not_63_out, _400);
  and and_134 (and_134_out, not_20_out, not_64_out, not_63_out, _400);
  and and_135 (and_135_out, not_49_out, not_61_out, _100, not_60_out, not_62_out);
  and and_136 (and_136_out, not_18_out, not_64_out, not_63_out, _400);
  and and_137 (and_137_out, not_22_out, not_64_out, not_63_out, _400);
  and and_138 (and_138_out, not_48_out, not_61_out, _100, not_60_out, not_62_out);
  and and_139 (and_139_out, not_50_out, not_61_out, _100, not_60_out, not_62_out);
  and and_140 (and_140_out, not_13_out, not_64_out, not_63_out, _400);
  and and_141 (and_141_out, not_45_out, not_61_out, _100, not_60_out, not_62_out);
  not not_65 (not_65_out, _400);
  and and_142 (and_142_out, not_47_out, _200, not_63_out, not_65_out);
  and and_143 (and_143_out, not_41_out, _200, not_63_out, not_65_out);
  and and_144 (and_144_out, not_44_out, _200, not_63_out, not_65_out);
  and and_145 (and_145_out, _200, _200, not_63_out, not_65_out);
  and and_146 (and_146_out, not_40_out, _200, not_63_out, not_65_out);
  and and_147 (and_147_out, not_43_out, _200, not_63_out, not_65_out);
  and and_148 (and_148_out, _200, _200, not_63_out, not_65_out);
  and and_149 (and_149_out, _200, _200, not_63_out, not_65_out);
  and and_150 (and_150_out, not_42_out, _200, not_63_out, not_65_out);
  and and_151 (and_151_out, not_39_out, _200, not_63_out, not_65_out);
  and and_152 (and_152_out, not_36_out, _200, not_63_out, not_65_out);
  and and_153 (and_153_out, not_33_out, _200, not_63_out, not_65_out);
  and and_154 (and_154_out, not_34_out, _200, not_63_out, not_65_out);
  and and_155 (and_155_out, not_37_out, _200, not_63_out, not_65_out);
  and and_156 (and_156_out, not_35_out, _200, not_63_out, not_65_out);
  and and_157 (and_157_out, not_32_out, _200, not_63_out, not_65_out);
  and and_158 (and_158_out, not_38_out, _200, not_63_out, not_65_out);
  not not_66 (not_66_out, _200);
  and and_159 (and_159_out, n17bit_adder_3_out_52, not_66_out, _400, _100);
  and and_160 (and_160_out, n17bit_adder_3_out_50, not_66_out, _400, _100);
  and and_161 (and_161_out, n17bit_adder_3_out_51, not_66_out, _400, _100);
  and and_162 (and_162_out, n17bit_adder_3_out_49, not_66_out, _400, _100);
  and and_163 (and_163_out, n17bit_adder_3_out_47, not_66_out, _400, _100);
  and and_164 (and_164_out, n17bit_adder_3_out_48, not_66_out, _400, _100);
  and and_165 (and_165_out, n17bit_adder_3_out_46, not_66_out, _400, _100);
  and and_166 (and_166_out, n17bit_adder_3_out_45, not_66_out, _400, _100);
  and and_167 (and_167_out, n17bit_adder_3_out_44, not_66_out, _400, _100);
  and and_168 (and_168_out, n17bit_adder_3_out_42, not_66_out, _400, _100);
  and and_169 (and_169_out, n17bit_adder_3_out_43, not_66_out, _400, _100);
  and and_170 (and_170_out, n17bit_adder_3_out_41, not_66_out, _400, _100);
  and and_171 (and_171_out, n17bit_adder_3_out_40, not_66_out, _400, _100);
  and and_172 (and_172_out, n17bit_adder_3_out_39, not_66_out, _400, _100);
  and and_173 (and_173_out, n17bit_adder_3_out_38, not_66_out, _400, _100);
  and and_174 (and_174_out, n17bit_adder_3_out_37, not_66_out, _400, _100);
  and and_175 (and_175_out, n17bit_adder_3_out_36, not_66_out, _400, _100);
  and and_176 (and_176_out, n17bit_adder_3_out_35, not_66_out, _400, _100);

  // Notes on the sheet:
  //   8
  //   9
  //   3
  //   5
  //   7
  //   RIGHT = LARGE SIDE
  //   6
  //   4
  //   1
  //   1
  //   2
  //   4
  //   2
endmodule

module BCD_Binary_1k (
  input  _8000,
  input  _4000,
  input  _2000,
  input  _1000,
  output out_5,
  output out_6,
  output out_7,
  output out_8,
  output out_9,
  output out_10,
  output out_11,
  output out_12,
  output out_13,
  output out_14,
  output out_15,
  output out_16,
  output out_17,
  output out_18,
  output out_19,
  output out_20,
  output out_21,
  output out_22
);

  wire and_1_out, and_2_out, and_3_out, and_4_out, and_5_out, and_6_out, and_7_out, and_8_out, and_9_out,
       and_10_out, and_11_out, and_12_out, and_13_out, and_14_out, and_15_out, and_16_out, and_17_out,
       and_18_out, and_19_out, and_20_out, and_21_out, and_22_out, and_23_out, and_24_out, and_25_out,
       and_26_out, and_27_out, and_28_out, and_29_out, and_30_out, and_31_out, and_32_out, and_33_out,
       and_34_out, and_35_out, and_36_out, and_37_out, and_38_out, and_39_out, and_40_out, and_41_out,
       and_42_out, and_43_out, and_44_out, and_45_out, and_46_out, and_47_out, and_48_out, and_49_out,
       and_50_out, and_51_out, and_52_out, and_53_out, and_54_out, and_55_out, and_56_out, and_57_out,
       and_58_out, and_59_out, and_60_out, and_61_out, and_62_out, and_63_out, and_64_out, and_65_out,
       and_66_out, and_67_out, and_68_out, and_69_out, and_70_out, and_71_out, and_72_out, and_73_out,
       and_74_out, and_75_out, and_76_out, and_77_out, and_78_out, and_79_out, and_80_out, and_81_out,
       and_82_out, and_83_out, and_84_out, and_85_out, and_86_out, and_87_out, and_88_out, and_89_out,
       and_90_out, and_91_out, and_92_out, and_93_out, and_94_out, and_95_out, and_96_out, and_97_out,
       and_98_out, and_99_out, and_100_out, and_101_out, and_102_out, and_103_out, and_104_out, and_105_out,
       and_106_out, and_107_out, and_108_out, and_109_out, and_110_out, and_111_out, and_112_out,
       and_113_out, and_114_out, and_115_out, and_116_out, and_117_out, and_118_out, and_119_out,
       and_120_out, and_121_out, and_122_out, and_123_out, and_124_out, and_125_out, and_126_out,
       and_127_out, and_128_out, and_129_out, and_130_out, and_131_out, and_132_out, and_133_out,
       and_134_out, and_135_out, and_136_out, and_137_out, and_138_out, and_139_out, and_140_out,
       and_141_out, and_142_out, and_143_out, and_144_out, and_145_out, and_146_out, and_147_out,
       and_148_out, and_149_out, and_150_out, and_151_out, and_152_out, and_153_out, and_154_out,
       and_155_out, and_156_out, and_157_out, and_158_out, and_159_out, and_160_out, and_161_out,
       and_162_out, and_163_out, and_164_out, and_165_out, and_166_out, and_167_out, and_168_out,
       and_169_out, and_170_out, and_171_out, and_172_out, and_173_out, and_174_out, and_175_out,
       and_176_out, n17bit_adder_1_out_35, n17bit_adder_1_out_36, n17bit_adder_1_out_37,
       n17bit_adder_1_out_38, n17bit_adder_1_out_39, n17bit_adder_1_out_40, n17bit_adder_1_out_41,
       n17bit_adder_1_out_42, n17bit_adder_1_out_43, n17bit_adder_1_out_44, n17bit_adder_1_out_45,
       n17bit_adder_1_out_46, n17bit_adder_1_out_47, n17bit_adder_1_out_48, n17bit_adder_1_out_49,
       n17bit_adder_1_out_50, n17bit_adder_1_out_51, n17bit_adder_1_out_52, n17bit_adder_2_out_35,
       n17bit_adder_2_out_36, n17bit_adder_2_out_37, n17bit_adder_2_out_38, n17bit_adder_2_out_39,
       n17bit_adder_2_out_40, n17bit_adder_2_out_41, n17bit_adder_2_out_42, n17bit_adder_2_out_43,
       n17bit_adder_2_out_44, n17bit_adder_2_out_45, n17bit_adder_2_out_46, n17bit_adder_2_out_47,
       n17bit_adder_2_out_48, n17bit_adder_2_out_49, n17bit_adder_2_out_50, n17bit_adder_2_out_51,
       n17bit_adder_2_out_52, n17bit_adder_3_out_35, n17bit_adder_3_out_36, n17bit_adder_3_out_37,
       n17bit_adder_3_out_38, n17bit_adder_3_out_39, n17bit_adder_3_out_40, n17bit_adder_3_out_41,
       n17bit_adder_3_out_42, n17bit_adder_3_out_43, n17bit_adder_3_out_44, n17bit_adder_3_out_45,
       n17bit_adder_3_out_46, n17bit_adder_3_out_47, n17bit_adder_3_out_48, n17bit_adder_3_out_49,
       n17bit_adder_3_out_50, n17bit_adder_3_out_51, n17bit_adder_3_out_52, n17bit_adder_4_out_35,
       n17bit_adder_4_out_36, n17bit_adder_4_out_37, n17bit_adder_4_out_38, n17bit_adder_4_out_39,
       n17bit_adder_4_out_40, n17bit_adder_4_out_41, n17bit_adder_4_out_42, n17bit_adder_4_out_43,
       n17bit_adder_4_out_44, n17bit_adder_4_out_45, n17bit_adder_4_out_46, n17bit_adder_4_out_47,
       n17bit_adder_4_out_48, n17bit_adder_4_out_49, n17bit_adder_4_out_50, n17bit_adder_4_out_51,
       n17bit_adder_4_out_52, n17bit_adder_5_out_35, n17bit_adder_5_out_36, n17bit_adder_5_out_37,
       n17bit_adder_5_out_38, n17bit_adder_5_out_39, n17bit_adder_5_out_40, n17bit_adder_5_out_41,
       n17bit_adder_5_out_42, n17bit_adder_5_out_43, n17bit_adder_5_out_44, n17bit_adder_5_out_45,
       n17bit_adder_5_out_46, n17bit_adder_5_out_47, n17bit_adder_5_out_48, n17bit_adder_5_out_49,
       n17bit_adder_5_out_50, n17bit_adder_5_out_51, n17bit_adder_5_out_52, not_1_out, not_2_out, not_3_out,
       not_4_out, not_5_out, not_6_out, not_7_out, not_8_out, not_9_out, not_10_out, not_11_out, not_12_out,
       not_13_out, not_14_out, not_15_out, not_16_out, not_17_out, not_18_out, not_19_out, not_20_out,
       not_21_out, not_22_out, not_23_out, not_24_out, not_25_out, not_26_out, not_27_out, not_28_out,
       not_29_out, not_30_out, not_31_out, not_32_out, not_33_out, not_34_out, not_35_out, not_36_out,
       not_37_out, not_38_out, not_39_out, not_40_out, not_41_out, not_42_out, not_43_out, not_44_out,
       not_45_out, not_46_out, not_47_out, not_48_out, not_49_out, not_50_out, not_51_out, not_52_out,
       not_53_out, not_54_out;

  and and_1 (and_1_out, not_1_out, _8000, not_14_out);
  and and_2 (and_2_out, not_1_out, _8000, not_12_out);
  and and_3 (and_3_out, not_1_out, _8000, not_11_out);
  and and_4 (and_4_out, not_1_out, _8000, not_16_out);
  and and_5 (and_5_out, not_1_out, _8000, not_9_out);
  and and_6 (and_6_out, not_1_out, _8000, not_15_out);
  and and_7 (and_7_out, not_1_out, _8000, _8000);
  and and_8 (and_8_out, not_1_out, _8000, not_8_out);
  and and_9 (and_9_out, not_1_out, _8000, _8000);
  and and_10 (and_10_out, not_1_out, _8000, _8000);
  and and_11 (and_11_out, not_1_out, _8000, _8000);
  and and_12 (and_12_out, not_1_out, _8000, _8000);
  and and_13 (and_13_out, not_1_out, _8000, _8000);
  and and_14 (and_14_out, not_1_out, _8000, not_5_out);
  and and_15 (and_15_out, not_1_out, _8000, not_3_out);
  and and_16 (and_16_out, not_1_out, _8000, not_4_out);
  and and_17 (and_17_out, not_1_out, _8000, not_2_out);
  not not_1 (not_1_out, _1000);
  not not_2 (not_2_out, _8000);
  not not_3 (not_3_out, _8000);
  not not_4 (not_4_out, _8000);
  not not_5 (not_5_out, _8000);
  and and_18 (and_18_out, n17bit_adder_1_out_52, _8000, _1000);
  not not_6 (not_6_out, _4000);
  not not_7 (not_7_out, _1000);
  not not_8 (not_8_out, _8000);
  not not_9 (not_9_out, _8000);
  and and_19 (and_19_out, n17bit_adder_1_out_51, _8000, _1000);
  and and_20 (and_20_out, n17bit_adder_1_out_49, _8000, _1000);
  and and_21 (and_21_out, n17bit_adder_1_out_50, _8000, _1000);
  not not_10 (not_10_out, _4000);
  not not_11 (not_11_out, _8000);
  not not_12 (not_12_out, _8000);
  not not_13 (not_13_out, _4000);
  not not_14 (not_14_out, _8000);
  not not_15 (not_15_out, _8000);
  not not_16 (not_16_out, _8000);
  and and_22 (and_22_out, n17bit_adder_1_out_46, _8000, _1000);
  and and_23 (and_23_out, n17bit_adder_1_out_47, _8000, _1000);
  and and_24 (and_24_out, n17bit_adder_1_out_48, _8000, _1000);
  and and_25 (and_25_out, n17bit_adder_2_out_52, _2000, not_6_out, _1000);
  or or_1 (out_5, and_107_out, and_176_out, and_42_out, and_53_out, and_103_out);
  not not_17 (not_17_out, _4000);
  not not_18 (not_18_out, _4000);
  not not_19 (not_19_out, _4000);
  _17bit_Adder u_17bit_adder_1 (
    .in_1(not_47_out), .in_2(not_46_out), .in_3(not_45_out), .in_4(_1000), .in_5(not_43_out), .in_6(_1000),
    .in_7(_1000), .in_8(_1000), .in_9(_1000), .in_10(_1000), .in_11(not_44_out), .in_12(not_41_out),
    .in_13(not_42_out), .in_14(not_36_out), .in_15(not_39_out), .in_16(not_38_out), .in_17(not_40_out),
    .in_18(not_14_out), .in_19(not_12_out), .in_20(not_16_out), .in_21(not_11_out), .in_22(not_15_out),
    .in_23(not_9_out), .in_24(_8000), .in_25(not_8_out), .in_26(_8000), .in_27(_8000), .in_28(_8000),
    .in_29(_8000), .in_30(_8000), .in_31(not_5_out), .in_32(not_2_out), .in_33(not_3_out), .in_34(not_4_out),
    .out_35(n17bit_adder_1_out_35), .out_36(n17bit_adder_1_out_36), .out_37(n17bit_adder_1_out_37),
    .out_38(n17bit_adder_1_out_38), .out_39(n17bit_adder_1_out_39), .out_40(n17bit_adder_1_out_40),
    .out_41(n17bit_adder_1_out_41), .out_42(n17bit_adder_1_out_42), .out_43(n17bit_adder_1_out_43),
    .out_44(n17bit_adder_1_out_44), .out_45(n17bit_adder_1_out_45), .out_46(n17bit_adder_1_out_46),
    .out_47(n17bit_adder_1_out_47), .out_48(n17bit_adder_1_out_48), .out_49(n17bit_adder_1_out_49),
    .out_50(n17bit_adder_1_out_50), .out_51(n17bit_adder_1_out_51), .out_52(n17bit_adder_1_out_52));
  and and_26 (and_26_out, n17bit_adder_1_out_44, _8000, _1000);
  and and_27 (and_27_out, n17bit_adder_1_out_45, _8000, _1000);
  and and_28 (and_28_out, n17bit_adder_2_out_51, _2000, not_6_out, _1000);
  not not_20 (not_20_out, _4000);
  not not_21 (not_21_out, _4000);
  not not_22 (not_22_out, _4000);
  not not_23 (not_23_out, _4000);
  not not_24 (not_24_out, _4000);
  not not_25 (not_25_out, _4000);
  and and_29 (and_29_out, n17bit_adder_1_out_43, _8000, _1000);
  and and_30 (and_30_out, n17bit_adder_1_out_42, _8000, _1000);
  and and_31 (and_31_out, n17bit_adder_1_out_41, _8000, _1000);
  and and_32 (and_32_out, n17bit_adder_2_out_49, _2000, not_6_out, _1000);
  and and_33 (and_33_out, n17bit_adder_2_out_50, _2000, not_6_out, _1000);
  or or_2 (out_6, and_106_out, and_141_out, and_158_out, and_175_out, and_16_out, and_39_out, and_51_out, and_104_out, and_140_out);
  not not_26 (not_26_out, _2000);
  not not_27 (not_27_out, _2000);
  not not_28 (not_28_out, _2000);
  not not_29 (not_29_out, _2000);
  not not_30 (not_30_out, _2000);
  not not_31 (not_31_out, _2000);
  and and_34 (and_34_out, n17bit_adder_1_out_40, _8000, _1000);
  and and_35 (and_35_out, n17bit_adder_1_out_39, _8000, _1000);
  and and_36 (and_36_out, n17bit_adder_1_out_38, _8000, _1000);
  and and_37 (and_37_out, n17bit_adder_2_out_48, _2000, not_6_out, _1000);
  or or_3 (out_7, and_105_out, and_138_out, and_156_out, and_174_out, and_15_out, and_38_out, and_52_out, and_102_out, and_136_out);
  not not_32 (not_32_out, _2000);
  not not_33 (not_33_out, _2000);
  not not_34 (not_34_out, _2000);
  not not_35 (not_35_out, _2000);
  and and_38 (and_38_out, n17bit_adder_1_out_37, _8000, _1000);
  and and_39 (and_39_out, n17bit_adder_1_out_36, _8000, _1000);
  and and_40 (and_40_out, n17bit_adder_2_out_47, _2000, not_6_out, _1000);
  and and_41 (and_41_out, n17bit_adder_2_out_46, _2000, not_6_out, _1000);
  not not_36 (not_36_out, _1000);
  not not_37 (not_37_out, _2000);
  not not_38 (not_38_out, _1000);
  not not_39 (not_39_out, _1000);
  not not_40 (not_40_out, _1000);
  not not_41 (not_41_out, _1000);
  not not_42 (not_42_out, _1000);
  and and_42 (and_42_out, n17bit_adder_1_out_35, _8000, _1000);
  and and_43 (and_43_out, n17bit_adder_2_out_44, _2000, not_6_out, _1000);
  and and_44 (and_44_out, n17bit_adder_2_out_45, _2000, not_6_out, _1000);
  or or_4 (out_8, and_98_out, and_139_out, and_157_out, and_173_out, and_17_out, and_36_out, and_49_out, and_97_out, and_137_out);
  not not_43 (not_43_out, _1000);
  not not_44 (not_44_out, _1000);
  and and_45 (and_45_out, n17bit_adder_2_out_43, _2000, not_6_out, _1000);
  or or_5 (out_9, and_99_out, and_135_out, and_154_out, and_172_out, and_14_out, and_35_out, and_50_out, and_96_out, and_134_out);
  not not_45 (not_45_out, _1000);
  not not_46 (not_46_out, _1000);
  not not_47 (not_47_out, _1000);
  and and_46 (and_46_out, n17bit_adder_2_out_41, _2000, not_6_out, _1000);
  and and_47 (and_47_out, n17bit_adder_2_out_42, _2000, not_6_out, _1000);
  or or_6 (out_10, and_91_out, and_132_out, and_155_out, and_171_out, and_13_out, and_34_out, and_48_out, and_95_out, and_133_out);
  _17bit_Adder u_17bit_adder_2 (
    .in_1(not_37_out), .in_2(not_33_out), .in_3(not_32_out), .in_4(not_34_out), .in_5(_2000),
    .in_6(not_35_out), .in_7(_2000), .in_8(_2000), .in_9(_2000), .in_10(_2000), .in_11(_2000),
    .in_12(not_29_out), .in_13(not_30_out), .in_14(not_31_out), .in_15(not_26_out), .in_16(not_27_out),
    .in_17(not_28_out), .in_18(not_47_out), .in_19(not_46_out), .in_20(not_45_out), .in_21(_1000),
    .in_22(not_43_out), .in_23(_1000), .in_24(_1000), .in_25(_1000), .in_26(_1000), .in_27(_1000),
    .in_28(not_44_out), .in_29(not_41_out), .in_30(not_42_out), .in_31(not_36_out), .in_32(not_39_out),
    .in_33(not_38_out), .in_34(not_40_out), .out_35(n17bit_adder_2_out_35), .out_36(n17bit_adder_2_out_36),
    .out_37(n17bit_adder_2_out_37), .out_38(n17bit_adder_2_out_38), .out_39(n17bit_adder_2_out_39),
    .out_40(n17bit_adder_2_out_40), .out_41(n17bit_adder_2_out_41), .out_42(n17bit_adder_2_out_42),
    .out_43(n17bit_adder_2_out_43), .out_44(n17bit_adder_2_out_44), .out_45(n17bit_adder_2_out_45),
    .out_46(n17bit_adder_2_out_46), .out_47(n17bit_adder_2_out_47), .out_48(n17bit_adder_2_out_48),
    .out_49(n17bit_adder_2_out_49), .out_50(n17bit_adder_2_out_50), .out_51(n17bit_adder_2_out_51),
    .out_52(n17bit_adder_2_out_52));
  and and_48 (and_48_out, n17bit_adder_2_out_40, _2000, not_6_out, _1000);
  and and_49 (and_49_out, n17bit_adder_2_out_38, _2000, not_6_out, _1000);
  and and_50 (and_50_out, n17bit_adder_2_out_39, _2000, not_6_out, _1000);
  or or_7 (out_11, and_86_out, and_131_out, and_153_out, and_170_out, and_10_out, and_31_out, and_46_out, and_90_out, and_130_out);
  and and_51 (and_51_out, n17bit_adder_2_out_36, _2000, not_6_out, _1000);
  and and_52 (and_52_out, n17bit_adder_2_out_37, _2000, not_6_out, _1000);
  or or_8 (out_12, and_85_out, and_129_out, and_152_out, and_169_out, and_12_out, and_30_out, and_47_out, and_89_out, and_127_out);
  and and_53 (and_53_out, n17bit_adder_2_out_35, _2000, not_6_out, _1000);
  or or_9 (out_13, and_77_out, and_125_out, and_151_out, and_168_out, and_11_out, and_29_out, and_45_out, and_84_out, and_128_out);
  or or_10 (out_14, and_78_out, and_126_out, and_150_out, and_166_out, and_9_out, and_26_out, and_43_out, and_83_out, and_124_out);
  or or_11 (out_15, and_70_out, and_123_out, and_148_out, and_167_out, and_8_out, and_27_out, and_44_out, and_82_out, and_120_out);
  _17bit_Adder u_17bit_adder_3 (
    .in_1(not_47_out), .in_2(not_46_out), .in_3(not_45_out), .in_4(_1000), .in_5(not_43_out), .in_6(_1000),
    .in_7(_1000), .in_8(_1000), .in_9(_1000), .in_10(_1000), .in_11(not_44_out), .in_12(not_41_out),
    .in_13(not_42_out), .in_14(not_36_out), .in_15(not_39_out), .in_16(not_38_out), .in_17(not_40_out),
    .in_18(not_22_out), .in_19(not_25_out), .in_20(not_21_out), .in_21(not_24_out), .in_22(not_23_out),
    .in_23(_4000), .in_24(not_20_out), .in_25(_4000), .in_26(_4000), .in_27(_4000), .in_28(_4000),
    .in_29(_4000), .in_30(not_18_out), .in_31(not_17_out), .in_32(not_19_out), .in_33(not_13_out),
    .in_34(not_10_out), .out_35(n17bit_adder_3_out_35), .out_36(n17bit_adder_3_out_36),
    .out_37(n17bit_adder_3_out_37), .out_38(n17bit_adder_3_out_38), .out_39(n17bit_adder_3_out_39),
    .out_40(n17bit_adder_3_out_40), .out_41(n17bit_adder_3_out_41), .out_42(n17bit_adder_3_out_42),
    .out_43(n17bit_adder_3_out_43), .out_44(n17bit_adder_3_out_44), .out_45(n17bit_adder_3_out_45),
    .out_46(n17bit_adder_3_out_46), .out_47(n17bit_adder_3_out_47), .out_48(n17bit_adder_3_out_48),
    .out_49(n17bit_adder_3_out_49), .out_50(n17bit_adder_3_out_50), .out_51(n17bit_adder_3_out_51),
    .out_52(n17bit_adder_3_out_52));
  and and_54 (and_54_out, n17bit_adder_4_out_52, _4000, _2000, _1000);
  and and_55 (and_55_out, n17bit_adder_4_out_51, _4000, _2000, _1000);
  or or_12 (out_16, and_65_out, and_122_out, and_149_out, and_165_out, and_7_out, and_22_out, and_41_out, and_76_out, and_121_out);
  and and_56 (and_56_out, n17bit_adder_4_out_49, _4000, _2000, _1000);
  and and_57 (and_57_out, n17bit_adder_4_out_50, _4000, _2000, _1000);
  or or_13 (out_17, and_64_out, and_119_out, and_147_out, and_163_out, and_5_out, and_23_out, and_40_out, and_74_out, and_118_out);
  and and_58 (and_58_out, n17bit_adder_4_out_48, _4000, _2000, _1000);
  or or_14 (out_18, and_58_out, and_115_out, and_146_out, and_164_out, and_6_out, and_24_out, and_37_out, and_75_out, and_117_out);
  and and_59 (and_59_out, n17bit_adder_5_out_52, _2000, _4000);
  and and_60 (and_60_out, n17bit_adder_5_out_51, _2000, _4000);
  and and_61 (and_61_out, n17bit_adder_5_out_50, _2000, _4000);
  and and_62 (and_62_out, and_59_out, not_7_out);
  and and_63 (and_63_out, and_60_out, not_7_out);
  and and_64 (and_64_out, n17bit_adder_4_out_47, _4000, _2000, _1000);
  and and_65 (and_65_out, n17bit_adder_4_out_46, _4000, _2000, _1000);
  and and_66 (and_66_out, n17bit_adder_5_out_49, _2000, _4000);
  and and_67 (and_67_out, n17bit_adder_5_out_48, _2000, _4000);
  and and_68 (and_68_out, and_61_out, not_7_out);
  and and_69 (and_69_out, and_66_out, not_7_out);
  _17bit_Adder u_17bit_adder_4 (
    .in_1(not_47_out), .in_2(not_46_out), .in_3(not_45_out), .in_4(_1000), .in_5(not_43_out), .in_6(_1000),
    .in_7(_1000), .in_8(_1000), .in_9(_1000), .in_10(_1000), .in_11(not_44_out), .in_12(not_41_out),
    .in_13(not_42_out), .in_14(not_36_out), .in_15(not_39_out), .in_16(not_38_out), .in_17(not_40_out),
    .in_18(and_59_out), .in_19(and_60_out), .in_20(and_61_out), .in_21(and_66_out), .in_22(and_67_out),
    .in_23(and_71_out), .in_24(and_72_out), .in_25(and_73_out), .in_26(and_79_out), .in_27(and_81_out),
    .in_28(and_80_out), .in_29(and_87_out), .in_30(and_88_out), .in_31(and_94_out), .in_32(and_93_out),
    .in_33(and_92_out), .in_34(and_100_out), .out_35(n17bit_adder_4_out_35), .out_36(n17bit_adder_4_out_36),
    .out_37(n17bit_adder_4_out_37), .out_38(n17bit_adder_4_out_38), .out_39(n17bit_adder_4_out_39),
    .out_40(n17bit_adder_4_out_40), .out_41(n17bit_adder_4_out_41), .out_42(n17bit_adder_4_out_42),
    .out_43(n17bit_adder_4_out_43), .out_44(n17bit_adder_4_out_44), .out_45(n17bit_adder_4_out_45),
    .out_46(n17bit_adder_4_out_46), .out_47(n17bit_adder_4_out_47), .out_48(n17bit_adder_4_out_48),
    .out_49(n17bit_adder_4_out_49), .out_50(n17bit_adder_4_out_50), .out_51(n17bit_adder_4_out_51),
    .out_52(n17bit_adder_4_out_52));
  and and_70 (and_70_out, n17bit_adder_4_out_45, _4000, _2000, _1000);
  or or_15 (out_19, and_56_out, and_116_out, and_145_out, and_162_out, and_3_out, and_20_out, and_32_out, and_69_out, and_114_out);
  and and_71 (and_71_out, n17bit_adder_5_out_47, _2000, _4000);
  and and_72 (and_72_out, n17bit_adder_5_out_46, _2000, _4000);
  and and_73 (and_73_out, n17bit_adder_5_out_45, _2000, _4000);
  and and_74 (and_74_out, and_71_out, not_7_out);
  and and_75 (and_75_out, and_67_out, not_7_out);
  and and_76 (and_76_out, and_72_out, not_7_out);
  and and_77 (and_77_out, n17bit_adder_4_out_43, _4000, _2000, _1000);
  and and_78 (and_78_out, n17bit_adder_4_out_44, _4000, _2000, _1000);
  or or_16 (out_20, and_57_out, and_113_out, and_144_out, and_161_out, and_4_out, and_21_out, and_33_out, and_68_out, and_112_out);
  _17bit_Adder u_17bit_adder_5 (
    .in_1(not_22_out), .in_2(not_25_out), .in_3(not_21_out), .in_4(not_24_out), .in_5(not_23_out),
    .in_6(_4000), .in_7(not_20_out), .in_8(_4000), .in_9(_4000), .in_10(_4000), .in_11(_4000), .in_12(_4000),
    .in_13(not_18_out), .in_14(not_17_out), .in_15(not_19_out), .in_16(not_13_out), .in_17(not_10_out),
    .in_18(not_37_out), .in_19(not_33_out), .in_20(not_32_out), .in_21(not_34_out), .in_22(_2000),
    .in_23(not_35_out), .in_24(_2000), .in_25(_2000), .in_26(_2000), .in_27(_2000), .in_28(_2000),
    .in_29(not_29_out), .in_30(not_30_out), .in_31(not_31_out), .in_32(not_26_out), .in_33(not_27_out),
    .in_34(not_28_out), .out_35(n17bit_adder_5_out_35), .out_36(n17bit_adder_5_out_36),
    .out_37(n17bit_adder_5_out_37), .out_38(n17bit_adder_5_out_38), .out_39(n17bit_adder_5_out_39),
    .out_40(n17bit_adder_5_out_40), .out_41(n17bit_adder_5_out_41), .out_42(n17bit_adder_5_out_42),
    .out_43(n17bit_adder_5_out_43), .out_44(n17bit_adder_5_out_44), .out_45(n17bit_adder_5_out_45),
    .out_46(n17bit_adder_5_out_46), .out_47(n17bit_adder_5_out_47), .out_48(n17bit_adder_5_out_48),
    .out_49(n17bit_adder_5_out_49), .out_50(n17bit_adder_5_out_50), .out_51(n17bit_adder_5_out_51),
    .out_52(n17bit_adder_5_out_52));
  and and_79 (and_79_out, n17bit_adder_5_out_44, _2000, _4000);
  and and_80 (and_80_out, n17bit_adder_5_out_42, _2000, _4000);
  and and_81 (and_81_out, n17bit_adder_5_out_43, _2000, _4000);
  and and_82 (and_82_out, and_73_out, not_7_out);
  and and_83 (and_83_out, and_79_out, not_7_out);
  and and_84 (and_84_out, and_81_out, not_7_out);
  and and_85 (and_85_out, n17bit_adder_4_out_42, _4000, _2000, _1000);
  and and_86 (and_86_out, n17bit_adder_4_out_41, _4000, _2000, _1000);
  or or_17 (out_21, and_55_out, and_111_out, and_143_out, and_160_out, and_2_out, and_19_out, and_28_out, and_63_out, and_109_out);
  and and_87 (and_87_out, n17bit_adder_5_out_41, _2000, _4000);
  and and_88 (and_88_out, n17bit_adder_5_out_40, _2000, _4000);
  and and_89 (and_89_out, and_80_out, not_7_out);
  and and_90 (and_90_out, and_87_out, not_7_out);
  and and_91 (and_91_out, n17bit_adder_4_out_40, _4000, _2000, _1000);
  and and_92 (and_92_out, n17bit_adder_5_out_37, _2000, _4000);
  and and_93 (and_93_out, n17bit_adder_5_out_38, _2000, _4000);
  and and_94 (and_94_out, n17bit_adder_5_out_39, _2000, _4000);
  and and_95 (and_95_out, and_88_out, not_7_out);
  and and_96 (and_96_out, and_94_out, not_7_out);
  and and_97 (and_97_out, and_93_out, not_7_out);
  and and_98 (and_98_out, n17bit_adder_4_out_38, _4000, _2000, _1000);
  and and_99 (and_99_out, n17bit_adder_4_out_39, _4000, _2000, _1000);
  or or_18 (out_22, and_54_out, and_110_out, and_142_out, and_159_out, and_1_out, and_18_out, and_25_out, and_62_out, and_108_out);
  and and_100 (and_100_out, n17bit_adder_5_out_36, _2000, _4000);
  and and_101 (and_101_out, n17bit_adder_5_out_35, _2000, _4000);
  and and_102 (and_102_out, and_92_out, not_7_out);
  and and_103 (and_103_out, and_101_out, not_7_out);
  and and_104 (and_104_out, and_100_out, not_7_out);
  and and_105 (and_105_out, n17bit_adder_4_out_37, _4000, _2000, _1000);
  and and_106 (and_106_out, n17bit_adder_4_out_36, _4000, _2000, _1000);
  and and_107 (and_107_out, n17bit_adder_4_out_35, _4000, _2000, _1000);
  and and_108 (and_108_out, not_22_out, not_52_out, not_51_out, _4000);
  and and_109 (and_109_out, not_25_out, not_52_out, not_51_out, _4000);
  not not_48 (not_48_out, _4000);
  not not_49 (not_49_out, _2000);
  not not_50 (not_50_out, _8000);
  and and_110 (and_110_out, not_47_out, not_50_out, _1000, not_48_out, not_49_out);
  and and_111 (and_111_out, not_46_out, not_50_out, _1000, not_48_out, not_49_out);
  and and_112 (and_112_out, not_21_out, not_52_out, not_51_out, _4000);
  and and_113 (and_113_out, not_45_out, not_50_out, _1000, not_48_out, not_49_out);
  and and_114 (and_114_out, not_24_out, not_52_out, not_51_out, _4000);
  and and_115 (and_115_out, not_43_out, not_50_out, _1000, not_48_out, not_49_out);
  and and_116 (and_116_out, _1000, not_50_out, _1000, not_48_out, not_49_out);
  and and_117 (and_117_out, not_23_out, not_52_out, not_51_out, _4000);
  and and_118 (and_118_out, _4000, not_52_out, not_51_out, _4000);
  and and_119 (and_119_out, _1000, not_50_out, _1000, not_48_out, not_49_out);
  and and_120 (and_120_out, _4000, not_52_out, not_51_out, _4000);
  and and_121 (and_121_out, not_20_out, not_52_out, not_51_out, _4000);
  and and_122 (and_122_out, _1000, not_50_out, _1000, not_48_out, not_49_out);
  and and_123 (and_123_out, _1000, not_50_out, _1000, not_48_out, not_49_out);
  and and_124 (and_124_out, _4000, not_52_out, not_51_out, _4000);
  and and_125 (and_125_out, _1000, not_50_out, _1000, not_48_out, not_49_out);
  and and_126 (and_126_out, _1000, not_50_out, _1000, not_48_out, not_49_out);
  not not_51 (not_51_out, _1000);
  and and_127 (and_127_out, _4000, not_52_out, not_51_out, _4000);
  and and_128 (and_128_out, _4000, not_52_out, not_51_out, _4000);
  and and_129 (and_129_out, not_44_out, not_50_out, _1000, not_48_out, not_49_out);
  not not_52 (not_52_out, _2000);
  and and_130 (and_130_out, _4000, not_52_out, not_51_out, _4000);
  and and_131 (and_131_out, not_41_out, not_50_out, _1000, not_48_out, not_49_out);
  and and_132 (and_132_out, not_42_out, not_50_out, _1000, not_48_out, not_49_out);
  and and_133 (and_133_out, not_18_out, not_52_out, not_51_out, _4000);
  and and_134 (and_134_out, not_17_out, not_52_out, not_51_out, _4000);
  and and_135 (and_135_out, not_36_out, not_50_out, _1000, not_48_out, not_49_out);
  and and_136 (and_136_out, not_13_out, not_52_out, not_51_out, _4000);
  and and_137 (and_137_out, not_19_out, not_52_out, not_51_out, _4000);
  and and_138 (and_138_out, not_38_out, not_50_out, _1000, not_48_out, not_49_out);
  and and_139 (and_139_out, not_39_out, not_50_out, _1000, not_48_out, not_49_out);
  and and_140 (and_140_out, not_10_out, not_52_out, not_51_out, _4000);
  and and_141 (and_141_out, not_40_out, not_50_out, _1000, not_48_out, not_49_out);
  not not_53 (not_53_out, _4000);
  and and_142 (and_142_out, not_37_out, _2000, not_51_out, not_53_out);
  and and_143 (and_143_out, not_33_out, _2000, not_51_out, not_53_out);
  and and_144 (and_144_out, not_32_out, _2000, not_51_out, not_53_out);
  and and_145 (and_145_out, not_34_out, _2000, not_51_out, not_53_out);
  and and_146 (and_146_out, _2000, _2000, not_51_out, not_53_out);
  and and_147 (and_147_out, not_35_out, _2000, not_51_out, not_53_out);
  and and_148 (and_148_out, _2000, _2000, not_51_out, not_53_out);
  and and_149 (and_149_out, _2000, _2000, not_51_out, not_53_out);
  and and_150 (and_150_out, _2000, _2000, not_51_out, not_53_out);
  and and_151 (and_151_out, _2000, _2000, not_51_out, not_53_out);
  and and_152 (and_152_out, _2000, _2000, not_51_out, not_53_out);
  and and_153 (and_153_out, not_29_out, _2000, not_51_out, not_53_out);
  and and_154 (and_154_out, not_31_out, _2000, not_51_out, not_53_out);
  and and_155 (and_155_out, not_30_out, _2000, not_51_out, not_53_out);
  and and_156 (and_156_out, not_27_out, _2000, not_51_out, not_53_out);
  and and_157 (and_157_out, not_26_out, _2000, not_51_out, not_53_out);
  and and_158 (and_158_out, not_28_out, _2000, not_51_out, not_53_out);
  not not_54 (not_54_out, _2000);
  and and_159 (and_159_out, n17bit_adder_3_out_52, not_54_out, _4000, _1000);
  and and_160 (and_160_out, n17bit_adder_3_out_51, not_54_out, _4000, _1000);
  and and_161 (and_161_out, n17bit_adder_3_out_50, not_54_out, _4000, _1000);
  and and_162 (and_162_out, n17bit_adder_3_out_49, not_54_out, _4000, _1000);
  and and_163 (and_163_out, n17bit_adder_3_out_47, not_54_out, _4000, _1000);
  and and_164 (and_164_out, n17bit_adder_3_out_48, not_54_out, _4000, _1000);
  and and_165 (and_165_out, n17bit_adder_3_out_46, not_54_out, _4000, _1000);
  and and_166 (and_166_out, n17bit_adder_3_out_44, not_54_out, _4000, _1000);
  and and_167 (and_167_out, n17bit_adder_3_out_45, not_54_out, _4000, _1000);
  and and_168 (and_168_out, n17bit_adder_3_out_43, not_54_out, _4000, _1000);
  and and_169 (and_169_out, n17bit_adder_3_out_42, not_54_out, _4000, _1000);
  and and_170 (and_170_out, n17bit_adder_3_out_41, not_54_out, _4000, _1000);
  and and_171 (and_171_out, n17bit_adder_3_out_40, not_54_out, _4000, _1000);
  and and_172 (and_172_out, n17bit_adder_3_out_39, not_54_out, _4000, _1000);
  and and_173 (and_173_out, n17bit_adder_3_out_38, not_54_out, _4000, _1000);
  and and_174 (and_174_out, n17bit_adder_3_out_37, not_54_out, _4000, _1000);
  and and_175 (and_175_out, n17bit_adder_3_out_36, not_54_out, _4000, _1000);
  and and_176 (and_176_out, n17bit_adder_3_out_35, not_54_out, _4000, _1000);

  // Notes on the sheet:
  //   8
  //   9
  //   3
  //   5
  //   7
  //   RIGHT = LARGE SIDE
  //   6
  //   4
  //   1
  //   1
  //   2
  //   4
  //   2
endmodule
module BCD_Binary_10k (
  input  _80000,
  input  _40000,
  input  _20000,
  input  _10000,
  output out_5,
  output out_6,
  output out_7,
  output out_8,
  output out_9,
  output out_10,
  output out_11,
  output out_12,
  output out_13,
  output out_14,
  output out_15,
  output out_16,
  output out_17,
  output out_18,
  output out_19,
  output out_20,
  output out_21,
  output out_22
);

  wire and_1_out, and_2_out, and_3_out, and_4_out, and_5_out, and_6_out, and_7_out, and_8_out, and_9_out,
       and_10_out, and_11_out, and_12_out, and_13_out, and_14_out, and_15_out, and_16_out, and_17_out,
       and_18_out, and_19_out, and_20_out, and_21_out, and_22_out, and_23_out, and_24_out, and_25_out,
       and_26_out, and_27_out, and_28_out, and_29_out, and_30_out, and_31_out, and_32_out, and_33_out,
       and_34_out, and_35_out, and_36_out, and_37_out, and_38_out, and_39_out, and_40_out, and_41_out,
       and_42_out, and_43_out, and_44_out, and_45_out, and_46_out, and_47_out, and_48_out, and_49_out,
       and_50_out, and_51_out, and_52_out, and_53_out, and_54_out, and_55_out, and_56_out, and_57_out,
       and_58_out, and_59_out, and_60_out, and_61_out, and_62_out, and_63_out, and_64_out, and_65_out,
       and_66_out, and_67_out, and_68_out, and_69_out, and_70_out, and_71_out, and_72_out, and_73_out,
       and_74_out, and_75_out, and_76_out, and_77_out, and_78_out, and_79_out, and_80_out, and_81_out,
       and_82_out, and_83_out, and_84_out, and_85_out, and_86_out, and_87_out, and_88_out, and_89_out,
       and_90_out, and_91_out, and_92_out, and_93_out, and_94_out, and_95_out, and_96_out, and_97_out,
       and_98_out, and_99_out, and_100_out, and_101_out, and_102_out, and_103_out, and_104_out, and_105_out,
       and_106_out, and_107_out, and_108_out, and_109_out, and_110_out, and_111_out, and_112_out,
       and_113_out, and_114_out, and_115_out, and_116_out, and_117_out, and_118_out, and_119_out,
       and_120_out, and_121_out, and_122_out, and_123_out, and_124_out, and_125_out, and_126_out,
       and_127_out, and_128_out, and_129_out, and_130_out, and_131_out, and_132_out, and_133_out,
       and_134_out, and_135_out, and_136_out, and_137_out, and_138_out, and_139_out, and_140_out,
       and_141_out, and_142_out, and_143_out, and_144_out, and_145_out, and_146_out, and_147_out,
       and_148_out, and_149_out, and_150_out, and_151_out, and_152_out, and_153_out, and_154_out,
       and_155_out, and_156_out, and_157_out, and_158_out, and_159_out, and_160_out, and_161_out,
       and_162_out, and_163_out, and_164_out, and_165_out, and_166_out, and_167_out, and_168_out,
       and_169_out, and_170_out, and_171_out, and_172_out, and_173_out, and_174_out, and_175_out,
       and_176_out, n17bit_adder_1_out_35, n17bit_adder_1_out_36, n17bit_adder_1_out_37,
       n17bit_adder_1_out_38, n17bit_adder_1_out_39, n17bit_adder_1_out_40, n17bit_adder_1_out_41,
       n17bit_adder_1_out_42, n17bit_adder_1_out_43, n17bit_adder_1_out_44, n17bit_adder_1_out_45,
       n17bit_adder_1_out_46, n17bit_adder_1_out_47, n17bit_adder_1_out_48, n17bit_adder_1_out_49,
       n17bit_adder_1_out_50, n17bit_adder_1_out_51, n17bit_adder_1_out_52, n17bit_adder_2_out_35,
       n17bit_adder_2_out_36, n17bit_adder_2_out_37, n17bit_adder_2_out_38, n17bit_adder_2_out_39,
       n17bit_adder_2_out_40, n17bit_adder_2_out_41, n17bit_adder_2_out_42, n17bit_adder_2_out_43,
       n17bit_adder_2_out_44, n17bit_adder_2_out_45, n17bit_adder_2_out_46, n17bit_adder_2_out_47,
       n17bit_adder_2_out_48, n17bit_adder_2_out_49, n17bit_adder_2_out_50, n17bit_adder_2_out_51,
       n17bit_adder_2_out_52, n17bit_adder_3_out_35, n17bit_adder_3_out_36, n17bit_adder_3_out_37,
       n17bit_adder_3_out_38, n17bit_adder_3_out_39, n17bit_adder_3_out_40, n17bit_adder_3_out_41,
       n17bit_adder_3_out_42, n17bit_adder_3_out_43, n17bit_adder_3_out_44, n17bit_adder_3_out_45,
       n17bit_adder_3_out_46, n17bit_adder_3_out_47, n17bit_adder_3_out_48, n17bit_adder_3_out_49,
       n17bit_adder_3_out_50, n17bit_adder_3_out_51, n17bit_adder_3_out_52, n17bit_adder_4_out_35,
       n17bit_adder_4_out_36, n17bit_adder_4_out_37, n17bit_adder_4_out_38, n17bit_adder_4_out_39,
       n17bit_adder_4_out_40, n17bit_adder_4_out_41, n17bit_adder_4_out_42, n17bit_adder_4_out_43,
       n17bit_adder_4_out_44, n17bit_adder_4_out_45, n17bit_adder_4_out_46, n17bit_adder_4_out_47,
       n17bit_adder_4_out_48, n17bit_adder_4_out_49, n17bit_adder_4_out_50, n17bit_adder_4_out_51,
       n17bit_adder_4_out_52, n17bit_adder_5_out_35, n17bit_adder_5_out_36, n17bit_adder_5_out_37,
       n17bit_adder_5_out_38, n17bit_adder_5_out_39, n17bit_adder_5_out_40, n17bit_adder_5_out_41,
       n17bit_adder_5_out_42, n17bit_adder_5_out_43, n17bit_adder_5_out_44, n17bit_adder_5_out_45,
       n17bit_adder_5_out_46, n17bit_adder_5_out_47, n17bit_adder_5_out_48, n17bit_adder_5_out_49,
       n17bit_adder_5_out_50, n17bit_adder_5_out_51, n17bit_adder_5_out_52, not_1_out, not_2_out, not_3_out,
       not_4_out, not_5_out, not_6_out, not_7_out, not_8_out, not_9_out, not_10_out, not_11_out, not_12_out,
       not_13_out, not_14_out, not_15_out, not_16_out, not_17_out, not_18_out, not_19_out, not_20_out,
       not_21_out, not_22_out, not_23_out, not_24_out, not_25_out, not_26_out, not_27_out, not_28_out,
       not_29_out, not_30_out, not_31_out, not_32_out, not_33_out, not_34_out, not_35_out, not_36_out,
       not_37_out, not_38_out, not_39_out, not_40_out, not_41_out, not_42_out, not_43_out, not_44_out,
       not_45_out, not_46_out, not_47_out, not_48_out, not_49_out, not_50_out, not_51_out, not_52_out,
       not_53_out, not_54_out, not_55_out, not_56_out, not_57_out, not_58_out;

  and and_1 (and_1_out, not_1_out, _80000, not_12_out);
  and and_2 (and_2_out, not_1_out, _80000, not_14_out);
  and and_3 (and_3_out, not_1_out, _80000, not_11_out);
  and and_4 (and_4_out, not_1_out, _80000, not_15_out);
  and and_5 (and_5_out, not_1_out, _80000, not_16_out);
  and and_6 (and_6_out, not_1_out, _80000, not_9_out);
  and and_7 (and_7_out, not_1_out, _80000, not_8_out);
  and and_8 (and_8_out, not_1_out, _80000, _80000);
  and and_9 (and_9_out, not_1_out, _80000, not_10_out);
  and and_10 (and_10_out, not_1_out, _80000, _80000);
  and and_11 (and_11_out, not_1_out, _80000, not_7_out);
  and and_12 (and_12_out, not_1_out, _80000, not_6_out);
  and and_13 (and_13_out, not_1_out, _80000, _80000);
  and and_14 (and_14_out, not_1_out, _80000, _80000);
  and and_15 (and_15_out, not_1_out, _80000, not_3_out);
  and and_16 (and_16_out, not_1_out, _80000, _80000);
  and and_17 (and_17_out, not_1_out, _80000, not_2_out);
  not not_1 (not_1_out, _10000);
  not not_2 (not_2_out, _80000);
  not not_3 (not_3_out, _80000);
  and and_18 (and_18_out, n17bit_adder_1_out_52, _80000, _10000);
  not not_4 (not_4_out, _40000);
  not not_5 (not_5_out, _10000);
  not not_6 (not_6_out, _80000);
  not not_7 (not_7_out, _80000);
  not not_8 (not_8_out, _80000);
  not not_9 (not_9_out, _80000);
  not not_10 (not_10_out, _80000);
  and and_19 (and_19_out, n17bit_adder_1_out_51, _80000, _10000);
  and and_20 (and_20_out, n17bit_adder_1_out_49, _80000, _10000);
  and and_21 (and_21_out, n17bit_adder_1_out_50, _80000, _10000);
  not not_11 (not_11_out, _80000);
  not not_12 (not_12_out, _80000);
  not not_13 (not_13_out, _40000);
  not not_14 (not_14_out, _80000);
  not not_15 (not_15_out, _80000);
  not not_16 (not_16_out, _80000);
  and and_22 (and_22_out, n17bit_adder_1_out_47, _80000, _10000);
  and and_23 (and_23_out, n17bit_adder_1_out_46, _80000, _10000);
  and and_24 (and_24_out, n17bit_adder_1_out_48, _80000, _10000);
  and and_25 (and_25_out, n17bit_adder_2_out_52, _20000, not_4_out, _10000);
  or or_1 (out_5, and_106_out, and_176_out, and_42_out, and_53_out, and_102_out);
  not not_17 (not_17_out, _40000);
  not not_18 (not_18_out, _40000);
  not not_19 (not_19_out, _40000);
  not not_20 (not_20_out, _40000);
  not not_21 (not_21_out, _40000);
  _17bit_Adder u_17bit_adder_1 (
    .in_1(not_50_out), .in_2(not_49_out), .in_3(not_51_out), .in_4(not_46_out), .in_5(_10000),
    .in_6(not_48_out), .in_7(not_45_out), .in_8(not_47_out), .in_9(_10000), .in_10(_10000), .in_11(_10000),
    .in_12(not_41_out), .in_13(not_44_out), .in_14(_10000), .in_15(not_40_out), .in_16(not_42_out),
    .in_17(not_39_out), .in_18(not_12_out), .in_19(not_11_out), .in_20(not_14_out), .in_21(not_15_out),
    .in_22(not_16_out), .in_23(not_9_out), .in_24(not_10_out), .in_25(_80000), .in_26(not_8_out),
    .in_27(not_6_out), .in_28(not_7_out), .in_29(_80000), .in_30(_80000), .in_31(_80000), .in_32(not_3_out),
    .in_33(not_2_out), .in_34(_80000), .out_35(n17bit_adder_1_out_35), .out_36(n17bit_adder_1_out_36),
    .out_37(n17bit_adder_1_out_37), .out_38(n17bit_adder_1_out_38), .out_39(n17bit_adder_1_out_39),
    .out_40(n17bit_adder_1_out_40), .out_41(n17bit_adder_1_out_41), .out_42(n17bit_adder_1_out_42),
    .out_43(n17bit_adder_1_out_43), .out_44(n17bit_adder_1_out_44), .out_45(n17bit_adder_1_out_45),
    .out_46(n17bit_adder_1_out_46), .out_47(n17bit_adder_1_out_47), .out_48(n17bit_adder_1_out_48),
    .out_49(n17bit_adder_1_out_49), .out_50(n17bit_adder_1_out_50), .out_51(n17bit_adder_1_out_51),
    .out_52(n17bit_adder_1_out_52));
  and and_26 (and_26_out, n17bit_adder_1_out_44, _80000, _10000);
  and and_27 (and_27_out, n17bit_adder_1_out_45, _80000, _10000);
  and and_28 (and_28_out, n17bit_adder_2_out_51, _20000, not_4_out, _10000);
  not not_22 (not_22_out, _40000);
  not not_23 (not_23_out, _40000);
  not not_24 (not_24_out, _40000);
  not not_25 (not_25_out, _40000);
  not not_26 (not_26_out, _40000);
  not not_27 (not_27_out, _40000);
  and and_29 (and_29_out, n17bit_adder_1_out_42, _80000, _10000);
  and and_30 (and_30_out, n17bit_adder_1_out_41, _80000, _10000);
  and and_31 (and_31_out, n17bit_adder_1_out_43, _80000, _10000);
  and and_32 (and_32_out, n17bit_adder_2_out_50, _20000, not_4_out, _10000);
  and and_33 (and_33_out, n17bit_adder_2_out_49, _20000, not_4_out, _10000);
  or or_2 (out_6, and_107_out, and_141_out, and_158_out, and_175_out, and_16_out, and_38_out, and_52_out, and_103_out, and_140_out);
  not not_28 (not_28_out, _20000);
  not not_29 (not_29_out, _20000);
  not not_30 (not_30_out, _20000);
  not not_31 (not_31_out, _20000);
  and and_34 (and_34_out, n17bit_adder_1_out_39, _80000, _10000);
  and and_35 (and_35_out, n17bit_adder_1_out_40, _80000, _10000);
  and and_36 (and_36_out, n17bit_adder_1_out_38, _80000, _10000);
  and and_37 (and_37_out, n17bit_adder_2_out_48, _20000, not_4_out, _10000);
  or or_3 (out_7, and_105_out, and_139_out, and_157_out, and_174_out, and_17_out, and_39_out, and_51_out, and_104_out, and_137_out);
  not not_32 (not_32_out, _20000);
  not not_33 (not_33_out, _20000);
  not not_34 (not_34_out, _20000);
  not not_35 (not_35_out, _20000);
  not not_36 (not_36_out, _20000);
  not not_37 (not_37_out, _20000);
  not not_38 (not_38_out, _20000);
  and and_38 (and_38_out, n17bit_adder_1_out_36, _80000, _10000);
  and and_39 (and_39_out, n17bit_adder_1_out_37, _80000, _10000);
  and and_40 (and_40_out, n17bit_adder_2_out_47, _20000, not_4_out, _10000);
  and and_41 (and_41_out, n17bit_adder_2_out_46, _20000, not_4_out, _10000);
  not not_39 (not_39_out, _10000);
  not not_40 (not_40_out, _10000);
  not not_41 (not_41_out, _10000);
  not not_42 (not_42_out, _10000);
  not not_43 (not_43_out, _20000);
  not not_44 (not_44_out, _10000);
  and and_42 (and_42_out, n17bit_adder_1_out_35, _80000, _10000);
  and and_43 (and_43_out, n17bit_adder_2_out_45, _20000, not_4_out, _10000);
  and and_44 (and_44_out, n17bit_adder_2_out_44, _20000, not_4_out, _10000);
  or or_4 (out_8, and_99_out, and_138_out, and_156_out, and_173_out, and_15_out, and_36_out, and_49_out, and_96_out, and_136_out);
  not not_45 (not_45_out, _10000);
  not not_46 (not_46_out, _10000);
  not not_47 (not_47_out, _10000);
  not not_48 (not_48_out, _10000);
  and and_45 (and_45_out, n17bit_adder_2_out_43, _20000, not_4_out, _10000);
  or or_5 (out_9, and_98_out, and_135_out, and_154_out, and_172_out, and_14_out, and_34_out, and_50_out, and_95_out, and_134_out);
  not not_49 (not_49_out, _10000);
  not not_50 (not_50_out, _10000);
  not not_51 (not_51_out, _10000);
  and and_46 (and_46_out, n17bit_adder_2_out_41, _20000, not_4_out, _10000);
  and and_47 (and_47_out, n17bit_adder_2_out_42, _20000, not_4_out, _10000);
  or or_6 (out_10, and_91_out, and_132_out, and_155_out, and_171_out, and_13_out, and_35_out, and_48_out, and_97_out, and_133_out);
  _17bit_Adder u_17bit_adder_2 (
    .in_1(not_43_out), .in_2(not_32_out), .in_3(not_33_out), .in_4(not_34_out), .in_5(not_36_out),
    .in_6(_20000), .in_7(not_37_out), .in_8(not_35_out), .in_9(not_38_out), .in_10(_20000), .in_11(_20000),
    .in_12(_20000), .in_13(not_29_out), .in_14(not_31_out), .in_15(_20000), .in_16(not_28_out),
    .in_17(not_30_out), .in_18(not_50_out), .in_19(not_49_out), .in_20(not_51_out), .in_21(not_46_out),
    .in_22(_10000), .in_23(not_48_out), .in_24(not_45_out), .in_25(not_47_out), .in_26(_10000),
    .in_27(_10000), .in_28(_10000), .in_29(not_41_out), .in_30(not_44_out), .in_31(_10000),
    .in_32(not_40_out), .in_33(not_42_out), .in_34(not_39_out), .out_35(n17bit_adder_2_out_35),
    .out_36(n17bit_adder_2_out_36), .out_37(n17bit_adder_2_out_37), .out_38(n17bit_adder_2_out_38),
    .out_39(n17bit_adder_2_out_39), .out_40(n17bit_adder_2_out_40), .out_41(n17bit_adder_2_out_41),
    .out_42(n17bit_adder_2_out_42), .out_43(n17bit_adder_2_out_43), .out_44(n17bit_adder_2_out_44),
    .out_45(n17bit_adder_2_out_45), .out_46(n17bit_adder_2_out_46), .out_47(n17bit_adder_2_out_47),
    .out_48(n17bit_adder_2_out_48), .out_49(n17bit_adder_2_out_49), .out_50(n17bit_adder_2_out_50),
    .out_51(n17bit_adder_2_out_51), .out_52(n17bit_adder_2_out_52));
  and and_48 (and_48_out, n17bit_adder_2_out_40, _20000, not_4_out, _10000);
  and and_49 (and_49_out, n17bit_adder_2_out_38, _20000, not_4_out, _10000);
  and and_50 (and_50_out, n17bit_adder_2_out_39, _20000, not_4_out, _10000);
  or or_7 (out_11, and_86_out, and_131_out, and_153_out, and_170_out, and_10_out, and_30_out, and_46_out, and_89_out, and_130_out);
  and and_51 (and_51_out, n17bit_adder_2_out_37, _20000, not_4_out, _10000);
  and and_52 (and_52_out, n17bit_adder_2_out_36, _20000, not_4_out, _10000);
  or or_8 (out_12, and_85_out, and_129_out, and_152_out, and_168_out, and_11_out, and_29_out, and_47_out, and_90_out, and_127_out);
  and and_53 (and_53_out, n17bit_adder_2_out_35, _20000, not_4_out, _10000);
  or or_9 (out_13, and_77_out, and_125_out, and_151_out, and_169_out, and_12_out, and_31_out, and_45_out, and_82_out, and_128_out);
  or or_10 (out_14, and_78_out, and_126_out, and_150_out, and_166_out, and_7_out, and_26_out, and_44_out, and_83_out, and_124_out);
  or or_11 (out_15, and_70_out, and_122_out, and_148_out, and_167_out, and_8_out, and_27_out, and_43_out, and_84_out, and_121_out);
  _17bit_Adder u_17bit_adder_3 (
    .in_1(not_50_out), .in_2(not_49_out), .in_3(not_51_out), .in_4(not_46_out), .in_5(_10000),
    .in_6(not_48_out), .in_7(not_45_out), .in_8(not_47_out), .in_9(_10000), .in_10(_10000), .in_11(_10000),
    .in_12(not_41_out), .in_13(not_44_out), .in_14(_10000), .in_15(not_40_out), .in_16(not_42_out),
    .in_17(not_39_out), .in_18(not_22_out), .in_19(not_27_out), .in_20(not_25_out), .in_21(not_24_out),
    .in_22(not_26_out), .in_23(not_23_out), .in_24(_40000), .in_25(not_18_out), .in_26(not_19_out),
    .in_27(not_20_out), .in_28(_40000), .in_29(_40000), .in_30(_40000), .in_31(not_17_out),
    .in_32(not_21_out), .in_33(_40000), .in_34(not_13_out), .out_35(n17bit_adder_3_out_35),
    .out_36(n17bit_adder_3_out_36), .out_37(n17bit_adder_3_out_37), .out_38(n17bit_adder_3_out_38),
    .out_39(n17bit_adder_3_out_39), .out_40(n17bit_adder_3_out_40), .out_41(n17bit_adder_3_out_41),
    .out_42(n17bit_adder_3_out_42), .out_43(n17bit_adder_3_out_43), .out_44(n17bit_adder_3_out_44),
    .out_45(n17bit_adder_3_out_45), .out_46(n17bit_adder_3_out_46), .out_47(n17bit_adder_3_out_47),
    .out_48(n17bit_adder_3_out_48), .out_49(n17bit_adder_3_out_49), .out_50(n17bit_adder_3_out_50),
    .out_51(n17bit_adder_3_out_51), .out_52(n17bit_adder_3_out_52));
  and and_54 (and_54_out, n17bit_adder_4_out_52, _40000, _20000, _10000);
  and and_55 (and_55_out, n17bit_adder_4_out_51, _40000, _20000, _10000);
  or or_12 (out_16, and_64_out, and_123_out, and_149_out, and_165_out, and_9_out, and_23_out, and_41_out, and_75_out, and_120_out);
  and and_56 (and_56_out, n17bit_adder_4_out_49, _40000, _20000, _10000);
  and and_57 (and_57_out, n17bit_adder_4_out_50, _40000, _20000, _10000);
  or or_13 (out_17, and_65_out, and_119_out, and_146_out, and_163_out, and_6_out, and_22_out, and_40_out, and_74_out, and_117_out);
  and and_58 (and_58_out, n17bit_adder_4_out_48, _40000, _20000, _10000);
  or or_14 (out_18, and_58_out, and_116_out, and_147_out, and_164_out, and_5_out, and_24_out, and_37_out, and_76_out, and_118_out);
  and and_59 (and_59_out, n17bit_adder_5_out_51, _20000, _40000);
  and and_60 (and_60_out, n17bit_adder_5_out_50, _20000, _40000);
  and and_61 (and_61_out, n17bit_adder_5_out_52, _20000, _40000);
  and and_62 (and_62_out, and_61_out, not_5_out);
  and and_63 (and_63_out, and_59_out, not_5_out);
  and and_64 (and_64_out, n17bit_adder_4_out_46, _40000, _20000, _10000);
  and and_65 (and_65_out, n17bit_adder_4_out_47, _40000, _20000, _10000);
  and and_66 (and_66_out, n17bit_adder_5_out_49, _20000, _40000);
  and and_67 (and_67_out, n17bit_adder_5_out_48, _20000, _40000);
  and and_68 (and_68_out, and_66_out, not_5_out);
  and and_69 (and_69_out, and_60_out, not_5_out);
  _17bit_Adder u_17bit_adder_4 (
    .in_1(not_50_out), .in_2(not_49_out), .in_3(not_51_out), .in_4(not_46_out), .in_5(_10000),
    .in_6(not_48_out), .in_7(not_45_out), .in_8(not_47_out), .in_9(_10000), .in_10(_10000), .in_11(_10000),
    .in_12(not_41_out), .in_13(not_44_out), .in_14(_10000), .in_15(not_40_out), .in_16(not_42_out),
    .in_17(not_39_out), .in_18(and_61_out), .in_19(and_59_out), .in_20(and_60_out), .in_21(and_66_out),
    .in_22(and_67_out), .in_23(and_73_out), .in_24(and_71_out), .in_25(and_72_out), .in_26(and_79_out),
    .in_27(and_81_out), .in_28(and_80_out), .in_29(and_87_out), .in_30(and_88_out), .in_31(and_93_out),
    .in_32(and_94_out), .in_33(and_92_out), .in_34(and_100_out), .out_35(n17bit_adder_4_out_35),
    .out_36(n17bit_adder_4_out_36), .out_37(n17bit_adder_4_out_37), .out_38(n17bit_adder_4_out_38),
    .out_39(n17bit_adder_4_out_39), .out_40(n17bit_adder_4_out_40), .out_41(n17bit_adder_4_out_41),
    .out_42(n17bit_adder_4_out_42), .out_43(n17bit_adder_4_out_43), .out_44(n17bit_adder_4_out_44),
    .out_45(n17bit_adder_4_out_45), .out_46(n17bit_adder_4_out_46), .out_47(n17bit_adder_4_out_47),
    .out_48(n17bit_adder_4_out_48), .out_49(n17bit_adder_4_out_49), .out_50(n17bit_adder_4_out_50),
    .out_51(n17bit_adder_4_out_51), .out_52(n17bit_adder_4_out_52));
  and and_70 (and_70_out, n17bit_adder_4_out_45, _40000, _20000, _10000);
  or or_15 (out_19, and_56_out, and_115_out, and_145_out, and_162_out, and_4_out, and_20_out, and_33_out, and_68_out, and_114_out);
  and and_71 (and_71_out, n17bit_adder_5_out_46, _20000, _40000);
  and and_72 (and_72_out, n17bit_adder_5_out_45, _20000, _40000);
  and and_73 (and_73_out, n17bit_adder_5_out_47, _20000, _40000);
  and and_74 (and_74_out, and_73_out, not_5_out);
  and and_75 (and_75_out, and_71_out, not_5_out);
  and and_76 (and_76_out, and_67_out, not_5_out);
  and and_77 (and_77_out, n17bit_adder_4_out_43, _40000, _20000, _10000);
  and and_78 (and_78_out, n17bit_adder_4_out_44, _40000, _20000, _10000);
  or or_16 (out_20, and_57_out, and_113_out, and_144_out, and_161_out, and_2_out, and_21_out, and_32_out, and_69_out, and_112_out);
  _17bit_Adder u_17bit_adder_5 (
    .in_1(not_22_out), .in_2(not_27_out), .in_3(not_25_out), .in_4(not_24_out), .in_5(not_26_out),
    .in_6(not_23_out), .in_7(_40000), .in_8(not_18_out), .in_9(not_19_out), .in_10(not_20_out),
    .in_11(_40000), .in_12(_40000), .in_13(_40000), .in_14(not_17_out), .in_15(not_21_out), .in_16(_40000),
    .in_17(not_13_out), .in_18(not_43_out), .in_19(not_32_out), .in_20(not_33_out), .in_21(not_34_out),
    .in_22(not_36_out), .in_23(_20000), .in_24(not_37_out), .in_25(not_35_out), .in_26(not_38_out),
    .in_27(_20000), .in_28(_20000), .in_29(_20000), .in_30(not_29_out), .in_31(not_31_out), .in_32(_20000),
    .in_33(not_28_out), .in_34(not_30_out), .out_35(n17bit_adder_5_out_35), .out_36(n17bit_adder_5_out_36),
    .out_37(n17bit_adder_5_out_37), .out_38(n17bit_adder_5_out_38), .out_39(n17bit_adder_5_out_39),
    .out_40(n17bit_adder_5_out_40), .out_41(n17bit_adder_5_out_41), .out_42(n17bit_adder_5_out_42),
    .out_43(n17bit_adder_5_out_43), .out_44(n17bit_adder_5_out_44), .out_45(n17bit_adder_5_out_45),
    .out_46(n17bit_adder_5_out_46), .out_47(n17bit_adder_5_out_47), .out_48(n17bit_adder_5_out_48),
    .out_49(n17bit_adder_5_out_49), .out_50(n17bit_adder_5_out_50), .out_51(n17bit_adder_5_out_51),
    .out_52(n17bit_adder_5_out_52));
  and and_79 (and_79_out, n17bit_adder_5_out_44, _20000, _40000);
  and and_80 (and_80_out, n17bit_adder_5_out_42, _20000, _40000);
  and and_81 (and_81_out, n17bit_adder_5_out_43, _20000, _40000);
  and and_82 (and_82_out, and_81_out, not_5_out);
  and and_83 (and_83_out, and_79_out, not_5_out);
  and and_84 (and_84_out, and_72_out, not_5_out);
  and and_85 (and_85_out, n17bit_adder_4_out_42, _40000, _20000, _10000);
  and and_86 (and_86_out, n17bit_adder_4_out_41, _40000, _20000, _10000);
  or or_17 (out_21, and_55_out, and_110_out, and_143_out, and_160_out, and_3_out, and_19_out, and_28_out, and_63_out, and_109_out);
  and and_87 (and_87_out, n17bit_adder_5_out_41, _20000, _40000);
  and and_88 (and_88_out, n17bit_adder_5_out_40, _20000, _40000);
  and and_89 (and_89_out, and_87_out, not_5_out);
  and and_90 (and_90_out, and_80_out, not_5_out);
  and and_91 (and_91_out, n17bit_adder_4_out_40, _40000, _20000, _10000);
  and and_92 (and_92_out, n17bit_adder_5_out_37, _20000, _40000);
  and and_93 (and_93_out, n17bit_adder_5_out_39, _20000, _40000);
  and and_94 (and_94_out, n17bit_adder_5_out_38, _20000, _40000);
  and and_95 (and_95_out, and_93_out, not_5_out);
  and and_96 (and_96_out, and_94_out, not_5_out);
  and and_97 (and_97_out, and_88_out, not_5_out);
  and and_98 (and_98_out, n17bit_adder_4_out_39, _40000, _20000, _10000);
  and and_99 (and_99_out, n17bit_adder_4_out_38, _40000, _20000, _10000);
  or or_18 (out_22, and_54_out, and_111_out, and_142_out, and_159_out, and_1_out, and_18_out, and_25_out, and_62_out, and_108_out);
  and and_100 (and_100_out, n17bit_adder_5_out_36, _20000, _40000);
  and and_101 (and_101_out, n17bit_adder_5_out_35, _20000, _40000);
  and and_102 (and_102_out, and_101_out, not_5_out);
  and and_103 (and_103_out, and_100_out, not_5_out);
  and and_104 (and_104_out, and_92_out, not_5_out);
  and and_105 (and_105_out, n17bit_adder_4_out_37, _40000, _20000, _10000);
  and and_106 (and_106_out, n17bit_adder_4_out_35, _40000, _20000, _10000);
  and and_107 (and_107_out, n17bit_adder_4_out_36, _40000, _20000, _10000);
  and and_108 (and_108_out, not_22_out, not_56_out, not_55_out, _40000);
  and and_109 (and_109_out, not_27_out, not_56_out, not_55_out, _40000);
  not not_52 (not_52_out, _80000);
  not not_53 (not_53_out, _40000);
  not not_54 (not_54_out, _20000);
  and and_110 (and_110_out, not_49_out, not_52_out, _10000, not_53_out, not_54_out);
  and and_111 (and_111_out, not_50_out, not_52_out, _10000, not_53_out, not_54_out);
  and and_112 (and_112_out, not_25_out, not_56_out, not_55_out, _40000);
  and and_113 (and_113_out, not_51_out, not_52_out, _10000, not_53_out, not_54_out);
  and and_114 (and_114_out, not_24_out, not_56_out, not_55_out, _40000);
  and and_115 (and_115_out, not_46_out, not_52_out, _10000, not_53_out, not_54_out);
  and and_116 (and_116_out, _10000, not_52_out, _10000, not_53_out, not_54_out);
  and and_117 (and_117_out, not_23_out, not_56_out, not_55_out, _40000);
  and and_118 (and_118_out, not_26_out, not_56_out, not_55_out, _40000);
  and and_119 (and_119_out, not_48_out, not_52_out, _10000, not_53_out, not_54_out);
  and and_120 (and_120_out, _40000, not_56_out, not_55_out, _40000);
  and and_121 (and_121_out, not_18_out, not_56_out, not_55_out, _40000);
  and and_122 (and_122_out, not_47_out, not_52_out, _10000, not_53_out, not_54_out);
  and and_123 (and_123_out, not_45_out, not_52_out, _10000, not_53_out, not_54_out);
  and and_124 (and_124_out, not_19_out, not_56_out, not_55_out, _40000);
  and and_125 (and_125_out, _10000, not_52_out, _10000, not_53_out, not_54_out);
  and and_126 (and_126_out, _10000, not_52_out, _10000, not_53_out, not_54_out);
  not not_55 (not_55_out, _10000);
  and and_127 (and_127_out, _40000, not_56_out, not_55_out, _40000);
  and and_128 (and_128_out, not_20_out, not_56_out, not_55_out, _40000);
  and and_129 (and_129_out, _10000, not_52_out, _10000, not_53_out, not_54_out);
  not not_56 (not_56_out, _20000);
  and and_130 (and_130_out, _40000, not_56_out, not_55_out, _40000);
  and and_131 (and_131_out, not_41_out, not_52_out, _10000, not_53_out, not_54_out);
  and and_132 (and_132_out, not_44_out, not_52_out, _10000, not_53_out, not_54_out);
  and and_133 (and_133_out, _40000, not_56_out, not_55_out, _40000);
  and and_134 (and_134_out, not_17_out, not_56_out, not_55_out, _40000);
  and and_135 (and_135_out, _10000, not_52_out, _10000, not_53_out, not_54_out);
  and and_136 (and_136_out, not_21_out, not_56_out, not_55_out, _40000);
  and and_137 (and_137_out, _40000, not_56_out, not_55_out, _40000);
  and and_138 (and_138_out, not_40_out, not_52_out, _10000, not_53_out, not_54_out);
  and and_139 (and_139_out, not_42_out, not_52_out, _10000, not_53_out, not_54_out);
  and and_140 (and_140_out, not_13_out, not_56_out, not_55_out, _40000);
  and and_141 (and_141_out, not_39_out, not_52_out, _10000, not_53_out, not_54_out);
  not not_57 (not_57_out, _40000);
  and and_142 (and_142_out, not_43_out, _20000, not_55_out, not_57_out);
  and and_143 (and_143_out, not_32_out, _20000, not_55_out, not_57_out);
  and and_144 (and_144_out, not_33_out, _20000, not_55_out, not_57_out);
  and and_145 (and_145_out, not_34_out, _20000, not_55_out, not_57_out);
  and and_146 (and_146_out, _20000, _20000, not_55_out, not_57_out);
  and and_147 (and_147_out, not_36_out, _20000, not_55_out, not_57_out);
  and and_148 (and_148_out, not_35_out, _20000, not_55_out, not_57_out);
  and and_149 (and_149_out, not_37_out, _20000, not_55_out, not_57_out);
  and and_150 (and_150_out, not_38_out, _20000, not_55_out, not_57_out);
  and and_151 (and_151_out, _20000, _20000, not_55_out, not_57_out);
  and and_152 (and_152_out, _20000, _20000, not_55_out, not_57_out);
  and and_153 (and_153_out, _20000, _20000, not_55_out, not_57_out);
  and and_154 (and_154_out, not_31_out, _20000, not_55_out, not_57_out);
  and and_155 (and_155_out, not_29_out, _20000, not_55_out, not_57_out);
  and and_156 (and_156_out, _20000, _20000, not_55_out, not_57_out);
  and and_157 (and_157_out, not_28_out, _20000, not_55_out, not_57_out);
  and and_158 (and_158_out, not_30_out, _20000, not_55_out, not_57_out);
  not not_58 (not_58_out, _20000);
  and and_159 (and_159_out, n17bit_adder_3_out_52, not_58_out, _40000, _10000);
  and and_160 (and_160_out, n17bit_adder_3_out_51, not_58_out, _40000, _10000);
  and and_161 (and_161_out, n17bit_adder_3_out_50, not_58_out, _40000, _10000);
  and and_162 (and_162_out, n17bit_adder_3_out_49, not_58_out, _40000, _10000);
  and and_163 (and_163_out, n17bit_adder_3_out_47, not_58_out, _40000, _10000);
  and and_164 (and_164_out, n17bit_adder_3_out_48, not_58_out, _40000, _10000);
  and and_165 (and_165_out, n17bit_adder_3_out_46, not_58_out, _40000, _10000);
  and and_166 (and_166_out, n17bit_adder_3_out_44, not_58_out, _40000, _10000);
  and and_167 (and_167_out, n17bit_adder_3_out_45, not_58_out, _40000, _10000);
  and and_168 (and_168_out, n17bit_adder_3_out_42, not_58_out, _40000, _10000);
  and and_169 (and_169_out, n17bit_adder_3_out_43, not_58_out, _40000, _10000);
  and and_170 (and_170_out, n17bit_adder_3_out_41, not_58_out, _40000, _10000);
  and and_171 (and_171_out, n17bit_adder_3_out_40, not_58_out, _40000, _10000);
  and and_172 (and_172_out, n17bit_adder_3_out_39, not_58_out, _40000, _10000);
  and and_173 (and_173_out, n17bit_adder_3_out_38, not_58_out, _40000, _10000);
  and and_174 (and_174_out, n17bit_adder_3_out_37, not_58_out, _40000, _10000);
  and and_175 (and_175_out, n17bit_adder_3_out_36, not_58_out, _40000, _10000);
  and and_176 (and_176_out, n17bit_adder_3_out_35, not_58_out, _40000, _10000);

  // Notes on the sheet:
  //   8
  //   9
  //   3
  //   5
  //   7
  //   RIGHT = LARGE SIDE
  //   6
  //   4
  //   1
  //   1
  //   2
  //   4
  //   2
endmodule

module BCD_to_Binary (
  input  in_1,
  input  _10_000s,
  input  in_3,
  input  in_4,
  input  in_5,
  input  _1_000s,
  input  in_7,
  input  in_8,
  input  in_9,
  input  _100s,
  input  in_11,
  input  in_12,
  input  in_13,
  input  _10s,
  input  in_15,
  input  in_16,
  input  in_17,
  input  _1s,
  input  in_19,
  input  in_20,
  output out_21,
  output out_22,
  output out_23,
  output out_24,
  output out_25,
  output out_26,
  output out_27,
  output out_28,
  output out_29,
  output out_30,
  output out_31,
  output out_32,
  output out_33,
  output out_34,
  output out_35,
  output out_36,
  output out_37,
  output out_38
);

  wire bcd_binary_1_1_out_5, bcd_binary_1_1_out_6, bcd_binary_1_1_out_7, bcd_binary_1_1_out_8,
       bcd_binary_1_1_out_9, bcd_binary_1_1_out_10, bcd_binary_1_1_out_11, bcd_binary_1_1_out_12,
       bcd_binary_1_1_out_13, bcd_binary_1_1_out_14, bcd_binary_1_1_out_15, bcd_binary_1_1_out_16,
       bcd_binary_1_1_out_17, bcd_binary_1_1_out_18, bcd_binary_1_1_out_19, bcd_binary_1_1_out_20,
       bcd_binary_1_1_out_21, bcd_binary_1_1_out_22, bcd_binary_1k_1_out_5, bcd_binary_1k_1_out_6,
       bcd_binary_1k_1_out_7, bcd_binary_1k_1_out_8, bcd_binary_1k_1_out_9, bcd_binary_1k_1_out_10,
       bcd_binary_1k_1_out_11, bcd_binary_1k_1_out_12, bcd_binary_1k_1_out_13, bcd_binary_1k_1_out_14,
       bcd_binary_1k_1_out_15, bcd_binary_1k_1_out_16, bcd_binary_1k_1_out_17, bcd_binary_1k_1_out_18,
       bcd_binary_1k_1_out_19, bcd_binary_1k_1_out_20, bcd_binary_1k_1_out_21, bcd_binary_1k_1_out_22,
       bcd_binary_10_1_out_5, bcd_binary_10_1_out_6, bcd_binary_10_1_out_7, bcd_binary_10_1_out_8,
       bcd_binary_10_1_out_9, bcd_binary_10_1_out_10, bcd_binary_10_1_out_11, bcd_binary_10_1_out_12,
       bcd_binary_10_1_out_13, bcd_binary_10_1_out_14, bcd_binary_10_1_out_15, bcd_binary_10_1_out_16,
       bcd_binary_10_1_out_17, bcd_binary_10_1_out_18, bcd_binary_10_1_out_19, bcd_binary_10_1_out_20,
       bcd_binary_10_1_out_21, bcd_binary_10_1_out_22, bcd_binary_10k_1_out_5, bcd_binary_10k_1_out_6,
       bcd_binary_10k_1_out_7, bcd_binary_10k_1_out_8, bcd_binary_10k_1_out_9, bcd_binary_10k_1_out_10,
       bcd_binary_10k_1_out_11, bcd_binary_10k_1_out_12, bcd_binary_10k_1_out_13, bcd_binary_10k_1_out_14,
       bcd_binary_10k_1_out_15, bcd_binary_10k_1_out_16, bcd_binary_10k_1_out_17, bcd_binary_10k_1_out_18,
       bcd_binary_10k_1_out_19, bcd_binary_10k_1_out_20, bcd_binary_10k_1_out_21, bcd_binary_10k_1_out_22,
       bcd_binary_100_1_out_5, bcd_binary_100_1_out_6, bcd_binary_100_1_out_7, bcd_binary_100_1_out_8,
       bcd_binary_100_1_out_9, bcd_binary_100_1_out_10, bcd_binary_100_1_out_11, bcd_binary_100_1_out_12,
       bcd_binary_100_1_out_13, bcd_binary_100_1_out_14, bcd_binary_100_1_out_15, bcd_binary_100_1_out_16,
       bcd_binary_100_1_out_17, bcd_binary_100_1_out_18, bcd_binary_100_1_out_19, bcd_binary_100_1_out_20,
       bcd_binary_100_1_out_21, bcd_binary_100_1_out_22, n18bit_adder_1_out_38, n18bit_adder_1_out_39,
       n18bit_adder_1_out_40, n18bit_adder_1_out_41, n18bit_adder_1_out_42, n18bit_adder_1_out_43,
       n18bit_adder_1_out_44, n18bit_adder_1_out_45, n18bit_adder_1_out_46, n18bit_adder_1_out_47,
       n18bit_adder_1_out_48, n18bit_adder_1_out_49, n18bit_adder_1_out_50, n18bit_adder_1_out_51,
       n18bit_adder_1_out_52, n18bit_adder_1_out_53, n18bit_adder_1_out_54, n18bit_adder_1_out_55,
       n18bit_adder_2_out_38, n18bit_adder_2_out_39, n18bit_adder_2_out_40, n18bit_adder_2_out_41,
       n18bit_adder_2_out_42, n18bit_adder_2_out_43, n18bit_adder_2_out_44, n18bit_adder_2_out_45,
       n18bit_adder_2_out_46, n18bit_adder_2_out_47, n18bit_adder_2_out_48, n18bit_adder_2_out_49,
       n18bit_adder_2_out_50, n18bit_adder_2_out_51, n18bit_adder_2_out_52, n18bit_adder_2_out_53,
       n18bit_adder_2_out_54, n18bit_adder_2_out_55, n18bit_adder_4_out_38, n18bit_adder_4_out_39,
       n18bit_adder_4_out_40, n18bit_adder_4_out_41, n18bit_adder_4_out_42, n18bit_adder_4_out_43,
       n18bit_adder_4_out_44, n18bit_adder_4_out_45, n18bit_adder_4_out_46, n18bit_adder_4_out_47,
       n18bit_adder_4_out_48, n18bit_adder_4_out_49, n18bit_adder_4_out_50, n18bit_adder_4_out_51,
       n18bit_adder_4_out_52, n18bit_adder_4_out_53, n18bit_adder_4_out_54, n18bit_adder_4_out_55;

  BCD_Binary_10k bcd_binary_10k_1 (
    ._80000(in_1), ._40000(_10_000s), ._20000(in_3), ._10000(in_4), .out_5(bcd_binary_10k_1_out_5),
    .out_6(bcd_binary_10k_1_out_6), .out_7(bcd_binary_10k_1_out_7), .out_8(bcd_binary_10k_1_out_8),
    .out_9(bcd_binary_10k_1_out_9), .out_10(bcd_binary_10k_1_out_10), .out_11(bcd_binary_10k_1_out_11),
    .out_12(bcd_binary_10k_1_out_12), .out_13(bcd_binary_10k_1_out_13), .out_14(bcd_binary_10k_1_out_14),
    .out_15(bcd_binary_10k_1_out_15), .out_16(bcd_binary_10k_1_out_16), .out_17(bcd_binary_10k_1_out_17),
    .out_18(bcd_binary_10k_1_out_18), .out_19(bcd_binary_10k_1_out_19), .out_20(bcd_binary_10k_1_out_20),
    .out_21(bcd_binary_10k_1_out_21), .out_22(bcd_binary_10k_1_out_22));
  _18bit_Adder u_18bit_adder_1 (
    .in_1(n18bit_adder_2_out_55), .in_2(n18bit_adder_2_out_54), .in_3(n18bit_adder_2_out_53),
    .in_4(n18bit_adder_2_out_52), .in_5(n18bit_adder_2_out_51), .in_6(n18bit_adder_2_out_50),
    .in_7(n18bit_adder_2_out_49), .in_8(n18bit_adder_2_out_48), .in_9(n18bit_adder_2_out_47),
    .in_10(n18bit_adder_2_out_46), .in_11(n18bit_adder_2_out_45), .in_12(n18bit_adder_2_out_44),
    .in_13(n18bit_adder_2_out_43), .in_14(n18bit_adder_2_out_42), .in_15(n18bit_adder_2_out_41),
    .in_16(n18bit_adder_2_out_40), .in_17(n18bit_adder_2_out_39), .in_18(n18bit_adder_2_out_38),
    .in_19(bcd_binary_10k_1_out_22), .in_20(bcd_binary_10k_1_out_21), .in_21(bcd_binary_10k_1_out_20),
    .in_22(bcd_binary_10k_1_out_19), .in_23(bcd_binary_10k_1_out_18), .in_24(bcd_binary_10k_1_out_17),
    .in_25(bcd_binary_10k_1_out_16), .in_26(bcd_binary_10k_1_out_15), .in_27(bcd_binary_10k_1_out_14),
    .in_28(bcd_binary_10k_1_out_13), .in_29(bcd_binary_10k_1_out_12), .in_30(bcd_binary_10k_1_out_11),
    .in_31(bcd_binary_10k_1_out_10), .in_32(bcd_binary_10k_1_out_9), .in_33(bcd_binary_10k_1_out_8),
    .in_34(bcd_binary_10k_1_out_7), .in_35(bcd_binary_10k_1_out_6), .in_36(bcd_binary_10k_1_out_5),
    .out_38(n18bit_adder_1_out_38), .out_39(n18bit_adder_1_out_39), .out_40(n18bit_adder_1_out_40),
    .out_41(n18bit_adder_1_out_41), .out_42(n18bit_adder_1_out_42), .out_43(n18bit_adder_1_out_43),
    .out_44(n18bit_adder_1_out_44), .out_45(n18bit_adder_1_out_45), .out_46(n18bit_adder_1_out_46),
    .out_47(n18bit_adder_1_out_47), .out_48(n18bit_adder_1_out_48), .out_49(n18bit_adder_1_out_49),
    .out_50(n18bit_adder_1_out_50), .out_51(n18bit_adder_1_out_51), .out_52(n18bit_adder_1_out_52),
    .out_53(n18bit_adder_1_out_53), .out_54(n18bit_adder_1_out_54), .out_55(n18bit_adder_1_out_55));  // open: out_37
  BCD_Binary_1k bcd_binary_1k_1 (
    ._8000(in_5), ._4000(_1_000s), ._2000(in_7), ._1000(in_8), .out_5(bcd_binary_1k_1_out_5),
    .out_6(bcd_binary_1k_1_out_6), .out_7(bcd_binary_1k_1_out_7), .out_8(bcd_binary_1k_1_out_8),
    .out_9(bcd_binary_1k_1_out_9), .out_10(bcd_binary_1k_1_out_10), .out_11(bcd_binary_1k_1_out_11),
    .out_12(bcd_binary_1k_1_out_12), .out_13(bcd_binary_1k_1_out_13), .out_14(bcd_binary_1k_1_out_14),
    .out_15(bcd_binary_1k_1_out_15), .out_16(bcd_binary_1k_1_out_16), .out_17(bcd_binary_1k_1_out_17),
    .out_18(bcd_binary_1k_1_out_18), .out_19(bcd_binary_1k_1_out_19), .out_20(bcd_binary_1k_1_out_20),
    .out_21(bcd_binary_1k_1_out_21), .out_22(bcd_binary_1k_1_out_22));
  BCD_Binary_100 bcd_binary_100_1 (
    ._800(in_9), ._400(_100s), ._200(in_11), ._100(in_12), .out_5(bcd_binary_100_1_out_5),
    .out_6(bcd_binary_100_1_out_6), .out_7(bcd_binary_100_1_out_7), .out_8(bcd_binary_100_1_out_8),
    .out_9(bcd_binary_100_1_out_9), .out_10(bcd_binary_100_1_out_10), .out_11(bcd_binary_100_1_out_11),
    .out_12(bcd_binary_100_1_out_12), .out_13(bcd_binary_100_1_out_13), .out_14(bcd_binary_100_1_out_14),
    .out_15(bcd_binary_100_1_out_15), .out_16(bcd_binary_100_1_out_16), .out_17(bcd_binary_100_1_out_17),
    .out_18(bcd_binary_100_1_out_18), .out_19(bcd_binary_100_1_out_19), .out_20(bcd_binary_100_1_out_20),
    .out_21(bcd_binary_100_1_out_21), .out_22(bcd_binary_100_1_out_22));
  _18bit_Adder u_18bit_adder_2 (
    .in_1(bcd_binary_100_1_out_22), .in_2(bcd_binary_100_1_out_21), .in_3(bcd_binary_100_1_out_20),
    .in_4(bcd_binary_100_1_out_19), .in_5(bcd_binary_100_1_out_18), .in_6(bcd_binary_100_1_out_17),
    .in_7(bcd_binary_100_1_out_16), .in_8(bcd_binary_100_1_out_15), .in_9(bcd_binary_100_1_out_14),
    .in_10(bcd_binary_100_1_out_13), .in_11(bcd_binary_100_1_out_12), .in_12(bcd_binary_100_1_out_11),
    .in_13(bcd_binary_100_1_out_10), .in_14(bcd_binary_100_1_out_9), .in_15(bcd_binary_100_1_out_8),
    .in_16(bcd_binary_100_1_out_7), .in_17(bcd_binary_100_1_out_6), .in_18(bcd_binary_100_1_out_5),
    .in_19(bcd_binary_1k_1_out_22), .in_20(bcd_binary_1k_1_out_21), .in_21(bcd_binary_1k_1_out_20),
    .in_22(bcd_binary_1k_1_out_19), .in_23(bcd_binary_1k_1_out_18), .in_24(bcd_binary_1k_1_out_17),
    .in_25(bcd_binary_1k_1_out_16), .in_26(bcd_binary_1k_1_out_15), .in_27(bcd_binary_1k_1_out_14),
    .in_28(bcd_binary_1k_1_out_13), .in_29(bcd_binary_1k_1_out_12), .in_30(bcd_binary_1k_1_out_11),
    .in_31(bcd_binary_1k_1_out_10), .in_32(bcd_binary_1k_1_out_9), .in_33(bcd_binary_1k_1_out_8),
    .in_34(bcd_binary_1k_1_out_7), .in_35(bcd_binary_1k_1_out_6), .in_36(bcd_binary_1k_1_out_5),
    .out_38(n18bit_adder_2_out_38), .out_39(n18bit_adder_2_out_39), .out_40(n18bit_adder_2_out_40),
    .out_41(n18bit_adder_2_out_41), .out_42(n18bit_adder_2_out_42), .out_43(n18bit_adder_2_out_43),
    .out_44(n18bit_adder_2_out_44), .out_45(n18bit_adder_2_out_45), .out_46(n18bit_adder_2_out_46),
    .out_47(n18bit_adder_2_out_47), .out_48(n18bit_adder_2_out_48), .out_49(n18bit_adder_2_out_49),
    .out_50(n18bit_adder_2_out_50), .out_51(n18bit_adder_2_out_51), .out_52(n18bit_adder_2_out_52),
    .out_53(n18bit_adder_2_out_53), .out_54(n18bit_adder_2_out_54), .out_55(n18bit_adder_2_out_55));  // open: out_37
  _18bit_Adder u_18bit_adder_3 (
    .in_1(n18bit_adder_4_out_55), .in_2(n18bit_adder_4_out_54), .in_3(n18bit_adder_4_out_53),
    .in_4(n18bit_adder_4_out_52), .in_5(n18bit_adder_4_out_51), .in_6(n18bit_adder_4_out_50),
    .in_7(n18bit_adder_4_out_49), .in_8(n18bit_adder_4_out_48), .in_9(n18bit_adder_4_out_47),
    .in_10(n18bit_adder_4_out_46), .in_11(n18bit_adder_4_out_45), .in_12(n18bit_adder_4_out_44),
    .in_13(n18bit_adder_4_out_43), .in_14(n18bit_adder_4_out_42), .in_15(n18bit_adder_4_out_41),
    .in_16(n18bit_adder_4_out_40), .in_17(n18bit_adder_4_out_39), .in_18(n18bit_adder_4_out_38),
    .in_19(n18bit_adder_1_out_55), .in_20(n18bit_adder_1_out_54), .in_21(n18bit_adder_1_out_53),
    .in_22(n18bit_adder_1_out_52), .in_23(n18bit_adder_1_out_51), .in_24(n18bit_adder_1_out_50),
    .in_25(n18bit_adder_1_out_49), .in_26(n18bit_adder_1_out_48), .in_27(n18bit_adder_1_out_47),
    .in_28(n18bit_adder_1_out_46), .in_29(n18bit_adder_1_out_45), .in_30(n18bit_adder_1_out_44),
    .in_31(n18bit_adder_1_out_43), .in_32(n18bit_adder_1_out_42), .in_33(n18bit_adder_1_out_41),
    .in_34(n18bit_adder_1_out_40), .in_35(n18bit_adder_1_out_39), .in_36(n18bit_adder_1_out_38),
    .out_38(out_21), .out_39(out_22), .out_40(out_23), .out_41(out_24), .out_42(out_25), .out_43(out_26),
    .out_44(out_27), .out_45(out_28), .out_46(out_29), .out_47(out_30), .out_48(out_31), .out_49(out_32),
    .out_50(out_33), .out_51(out_34), .out_52(out_35), .out_53(out_36), .out_54(out_37), .out_55(out_38));  // open: out_37
  BCD_Binary_10 bcd_binary_10_1 (
    ._80(in_13), ._40(_10s), ._20(in_15), ._10(in_16), .out_5(bcd_binary_10_1_out_5),
    .out_6(bcd_binary_10_1_out_6), .out_7(bcd_binary_10_1_out_7), .out_8(bcd_binary_10_1_out_8),
    .out_9(bcd_binary_10_1_out_9), .out_10(bcd_binary_10_1_out_10), .out_11(bcd_binary_10_1_out_11),
    .out_12(bcd_binary_10_1_out_12), .out_13(bcd_binary_10_1_out_13), .out_14(bcd_binary_10_1_out_14),
    .out_15(bcd_binary_10_1_out_15), .out_16(bcd_binary_10_1_out_16), .out_17(bcd_binary_10_1_out_17),
    .out_18(bcd_binary_10_1_out_18), .out_19(bcd_binary_10_1_out_19), .out_20(bcd_binary_10_1_out_20),
    .out_21(bcd_binary_10_1_out_21), .out_22(bcd_binary_10_1_out_22));
  BCD_Binary_1 bcd_binary_1_1 (
    ._8(in_17), ._4(_1s), ._2(in_19), ._1(in_20), .out_5(bcd_binary_1_1_out_5), .out_6(bcd_binary_1_1_out_6),
    .out_7(bcd_binary_1_1_out_7), .out_8(bcd_binary_1_1_out_8), .out_9(bcd_binary_1_1_out_9),
    .out_10(bcd_binary_1_1_out_10), .out_11(bcd_binary_1_1_out_11), .out_12(bcd_binary_1_1_out_12),
    .out_13(bcd_binary_1_1_out_13), .out_14(bcd_binary_1_1_out_14), .out_15(bcd_binary_1_1_out_15),
    .out_16(bcd_binary_1_1_out_16), .out_17(bcd_binary_1_1_out_17), .out_18(bcd_binary_1_1_out_18),
    .out_19(bcd_binary_1_1_out_19), .out_20(bcd_binary_1_1_out_20), .out_21(bcd_binary_1_1_out_21),
    .out_22(bcd_binary_1_1_out_22));
  _18bit_Adder u_18bit_adder_4 (
    .in_1(bcd_binary_1_1_out_22), .in_2(bcd_binary_1_1_out_21), .in_3(bcd_binary_1_1_out_20),
    .in_4(bcd_binary_1_1_out_19), .in_5(bcd_binary_1_1_out_18), .in_6(bcd_binary_1_1_out_17),
    .in_7(bcd_binary_1_1_out_16), .in_8(bcd_binary_1_1_out_15), .in_9(bcd_binary_1_1_out_14),
    .in_10(bcd_binary_1_1_out_13), .in_11(bcd_binary_1_1_out_12), .in_12(bcd_binary_1_1_out_11),
    .in_13(bcd_binary_1_1_out_10), .in_14(bcd_binary_1_1_out_9), .in_15(bcd_binary_1_1_out_8),
    .in_16(bcd_binary_1_1_out_7), .in_17(bcd_binary_1_1_out_6), .in_18(bcd_binary_1_1_out_5),
    .in_19(bcd_binary_10_1_out_22), .in_20(bcd_binary_10_1_out_21), .in_21(bcd_binary_10_1_out_20),
    .in_22(bcd_binary_10_1_out_19), .in_23(bcd_binary_10_1_out_18), .in_24(bcd_binary_10_1_out_17),
    .in_25(bcd_binary_10_1_out_16), .in_26(bcd_binary_10_1_out_15), .in_27(bcd_binary_10_1_out_14),
    .in_28(bcd_binary_10_1_out_13), .in_29(bcd_binary_10_1_out_12), .in_30(bcd_binary_10_1_out_11),
    .in_31(bcd_binary_10_1_out_10), .in_32(bcd_binary_10_1_out_9), .in_33(bcd_binary_10_1_out_8),
    .in_34(bcd_binary_10_1_out_7), .in_35(bcd_binary_10_1_out_6), .in_36(bcd_binary_10_1_out_5),
    .out_38(n18bit_adder_4_out_38), .out_39(n18bit_adder_4_out_39), .out_40(n18bit_adder_4_out_40),
    .out_41(n18bit_adder_4_out_41), .out_42(n18bit_adder_4_out_42), .out_43(n18bit_adder_4_out_43),
    .out_44(n18bit_adder_4_out_44), .out_45(n18bit_adder_4_out_45), .out_46(n18bit_adder_4_out_46),
    .out_47(n18bit_adder_4_out_47), .out_48(n18bit_adder_4_out_48), .out_49(n18bit_adder_4_out_49),
    .out_50(n18bit_adder_4_out_50), .out_51(n18bit_adder_4_out_51), .out_52(n18bit_adder_4_out_52),
    .out_53(n18bit_adder_4_out_53), .out_54(n18bit_adder_4_out_54), .out_55(n18bit_adder_4_out_55));  // open: out_37

  // Other names for the same wires on the sheet: _1 = out_38; _1a = out_29; _2 = out_37; _2a = out_28; _3 = out_36;
  //   _3a = out_27; _4 = out_35; _4a = out_26; _5 = out_34; _5a = out_25; _6 = out_33; _6a = out_24; _7 = out_32;
  //   _7a = out_23; _8 = out_31; _8a = out_22; _9 = out_30; _9a = out_21

  // Notes on the sheet:
  //   L
  //   L
  //   H
  //   L
  //   H
  //   H
  //   l
  //   h
endmodule
