// Logisim project Hardware coursework 2016.circ as structural Verilog: 4 circuits, main circuit main
module main (
  input  DATA,
  output out_2,
  output out_3
);

  wire button_1_out, d0_1_q0_2, d1_1_q1_2, d2_1_q2_2, d_ff_1_q, d_ff_2_q, RESET_out;

  Button button_1 (.out(button_1_out));
  Button RESET (.out(RESET_out));
  D2 d2_1 (.DATA(DATA), .Q2(d_ff_1_q), .Q1(d_ff_2_q), .Q0(d_ff_2_q), .Q2_2(d2_1_q2_2));
  D1 d1_1 (.DATA(DATA), .Q2(d_ff_1_q), .Q1(d_ff_2_q), .Q0(d_ff_2_q), .Q1_2(d1_1_q1_2));
  D0 d0_1 (.DATA(DATA), .Q2(d_ff_1_q), .Q1(d_ff_2_q), .Q0(d_ff_2_q), .Q0_2(d0_1_q0_2));
  D_Flip_Flop d_ff_1 (.clk(button_1_out), .D(d2_1_q2_2), .Q(d_ff_1_q), .reset(RESET_out));  // open: Qn, preset, en
  D_Flip_Flop d_ff_2 (.clk(button_1_out), .D(d1_1_q1_2), .Q(d_ff_2_q), .reset(RESET_out));  // open: Qn, preset, en
  D_Flip_Flop d_ff_3 (.clk(button_1_out), .D(d0_1_q0_2), .Q(d_ff_2_q), .reset(RESET_out));  // open: Qn, preset, en
  nor nor_1 (out_2, ~d_ff_1_q, ~d_ff_2_q, d_ff_2_q);  // NOR_Gate
  nand nand_1 (out_3, d_ff_1_q, ~d_ff_2_q, d_ff_2_q);  // NAND_Gate
endmodule

module D2 (
  input  DATA,
  input  Q2,
  input  Q1,
  input  Q0,
  output Q2_2
);

  wire nand_1_out, nand_2_out, xnor_1_out;

  xnor xnor_1 (xnor_1_out, DATA, Q1);
  nand nand_1 (nand_1_out, DATA, Q0);
  nand nand_2 (nand_2_out, ~Q0, Q2);  // NAND_Gate
  nand nand_3 (Q2_2, xnor_1_out, nand_1_out, nand_2_out);
endmodule

module D1 (
  input  DATA,
  input  Q2,
  input  Q1,
  input  Q0,
  output Q1_2
);

  wire nand_1_out, nand_2_out, nand_3_out;

  nand nand_1 (nand_1_out, Q0, ~Q1, ~Q2);  // NAND_Gate
  nand nand_2 (nand_2_out, ~DATA, Q1);  // NAND_Gate
  nand nand_3 (nand_3_out, ~Q0, DATA);  // NAND_Gate
  nand nand_4 (Q1_2, nand_1_out, nand_2_out, nand_3_out);
endmodule

module D0 (
  input  DATA,
  input  Q2,
  input  Q1,
  input  Q0,
  output Q0_2
);

  wire nand_1_out, nand_2_out, nand_3_out, nand_4_out, nand_5_out;

  nand nand_1 (nand_1_out, ~DATA, ~Q1, ~Q0);  // NAND_Gate
  nand nand_2 (nand_2_out, Q2, Q0);
  nand nand_3 (nand_3_out, Q1, ~Q0, ~Q2);  // NAND_Gate
  nand nand_4 (nand_4_out, nand_2_out, nand_3_out);
  nand nand_5 (nand_5_out, DATA, nand_4_out);
  nand nand_6 (Q0_2, nand_1_out, nand_5_out);
endmodule
