// Logisim project Hardware coursework.circ as structural Verilog: 2 circuits, main circuit main
module main (
  input  C1,
  input  C0,
  input  A,
  input  B,
  output out_5
);

  wire nand_1_out, nand_2_out, nand_3_out, nand_4_out, nand_6_out, nor_1_out, not_1_out, or_1_out, xnor_1_out;

  not not_1 (not_1_out, A);
  nor nor_1 (nor_1_out, C1, C0);
  or or_1 (or_1_out, C0, xnor_1_out);
  xnor xnor_1 (xnor_1_out, C1, B);
  nand nand_1 (nand_1_out, nor_1_out, A);
  nand nand_2 (nand_2_out, nand_1_out, nand_3_out);
  nand nand_3 (nand_3_out, C1, C0);
  nand nand_4 (nand_4_out, not_1_out, or_1_out);
  nand nand_5 (out_5, nand_4_out, nand_6_out);
  nand nand_6 (nand_6_out, B, nand_2_out);
endmodule

module Test (
  input  in_1,
  input  in_2,
  output out_3
);

  and and_1 (out_3, ~in_1, ~in_2);  // AND_Gate
endmodule
