// Logisim project Hardware1-2015.circ as structural Verilog: 2 circuits, main circuit main
module main (
  input  C1,
  input  C0,
  input  A,
  input  B,
  output out_5
);

  wire and_1_out, nand_1_out, nand_2_out, nand_3_out, nand_4_out, nand_5_out, nand_6_out, nor_1_out,
       nor_2_out, nor_3_out, nor_4_out, not_1_out, not_2_out, not_3_out, not_4_out;

  not not_1 (not_1_out, C1);
  not not_2 (not_2_out, C0);
  not not_3 (not_3_out, A);
  not not_4 (not_4_out, B);
  nor nor_1 (nor_1_out, C1, B);
  nand nand_1 (nand_1_out, C1, B);
  nor nor_2 (nor_2_out, C0, nor_1_out);
  nand nand_2 (nand_2_out, nor_2_out, nand_1_out);
  nor nor_3 (nor_3_out, not_2_out, not_1_out);
  nand nand_3 (nand_3_out, nor_3_out, not_4_out);
  nand nand_4 (nand_4_out, not_2_out, not_1_out);
  nor nor_4 (nor_4_out, nand_4_out, not_4_out);
  nand nand_5 (nand_5_out, nand_2_out, not_3_out);
  nand nand_6 (nand_6_out, nor_4_out, A);
  and and_1 (and_1_out, nand_5_out, nand_3_out);
  nand nand_7 (out_5, and_1_out, nand_6_out);
endmodule

module TEST (
  input  C1,
  input  C0,
  input  B,
  output out_4
);

  wire and_1_out, and_2_out, not_1_out, not_2_out, not_3_out;

  not not_1 (not_1_out, C1);
  not not_2 (not_2_out, C0);
  not not_3 (not_3_out, B);
  and and_1 (and_1_out, not_1_out, not_2_out, B);
  and and_2 (and_2_out, C1, C0, not_3_out);
  or or_1 (out_4, and_1_out, and_2_out);
endmodule
