// Logisim project dlock.circ as structural Verilog: 6 circuits, main circuit main
module main (
  input  DATA,
  input  CLOCK,
  input  RESET,
  output LOCK,
  output ALARM
);

  wire d0_1_d0, d1_1_d1, d2_1_d2, flip_flops_1_q0, flip_flops_1_q1, flip_flops_1_q2;

  Flip_Flops flip_flops_1 (
    .CLOCK(CLOCK), .RESET(RESET), .D0(d0_1_d0), .D1(d1_1_d1), .D2(d2_1_d2), .Q0(flip_flops_1_q0),
    .Q1(flip_flops_1_q1), .Q2(flip_flops_1_q2));
  D0 d0_1 (.DATA(DATA), .Q2(flip_flops_1_q2), .Q1(flip_flops_1_q1), .Q0(flip_flops_1_q0), .D0(d0_1_d0));
  D1 d1_1 (.DATA(DATA), .Q2(flip_flops_1_q2), .Q1(flip_flops_1_q1), .Q0(flip_flops_1_q0), .D1(d1_1_d1));
  D2 d2_1 (.DATA(DATA), .Q2(flip_flops_1_q2), .Q1(flip_flops_1_q1), .Q0(flip_flops_1_q0), .D2(d2_1_d2));
  Output output_1 (.Q0(flip_flops_1_q0), .Q1(flip_flops_1_q1), .Q2(flip_flops_1_q2), .LOCK(LOCK), .ALARM(ALARM));
endmodule

module D0 (
  input  DATA,
  input  Q2,
  input  Q1,
  input  Q0,
  output D0
);

  wire and_1_out, and_2_out, and_3_out, and_4_out, not_1_out, not_2_out, not_3_out, not_4_out, or_1_out;

  not not_1 (not_1_out, DATA);
  not not_2 (not_2_out, Q2);
  not not_3 (not_3_out, Q1);
  not not_4 (not_4_out, Q0);
  and and_1 (and_1_out, not_4_out, Q1, not_2_out);
  and and_2 (and_2_out, Q2, Q0);
  and and_3 (and_3_out, DATA, or_1_out);
  or or_1 (or_1_out, and_1_out, and_2_out);
  and and_4 (and_4_out, not_1_out, not_3_out, not_4_out);
  or or_2 (D0, and_3_out, and_4_out);
endmodule

module D1 (
  input  DATA,
  input  Q2,
  input  Q1,
  input  Q0,
  output D1
);

  wire and_1_out, and_2_out, and_3_out, and_4_out, not_1_out, not_2_out, not_3_out, or_1_out, or_2_out;

  not not_1 (not_1_out, Q2);
  not not_2 (not_2_out, Q1);
  not not_3 (not_3_out, Q0);
  or or_1 (or_1_out, DATA, and_1_out);
  and and_1 (and_1_out, not_2_out, Q0);
  and and_2 (and_2_out, DATA, not_2_out);
  or or_2 (or_2_out, and_2_out, Q1);
  and and_3 (and_3_out, not_1_out, or_1_out);
  or or_3 (D1, and_3_out, and_4_out);
  and and_4 (and_4_out, or_2_out, not_3_out);
endmodule

module D2 (
  input  DATA,
  input  Q2,
  input  Q1,
  input  Q0,
  output D2
);

  wire and_1_out, and_2_out, and_3_out, and_4_out, not_1_out, not_2_out, not_3_out, or_1_out, or_2_out;

  not not_1 (not_1_out, DATA);
  or or_1 (or_1_out, Q2, not_2_out);
  not not_2 (not_2_out, Q1);
  not not_3 (not_3_out, Q0);
  and and_1 (and_1_out, Q2, not_3_out);
  or or_2 (or_2_out, and_1_out, Q1);
  and and_2 (and_2_out, DATA, or_1_out);
  and and_3 (and_3_out, Q1, Q0);
  and and_4 (and_4_out, not_1_out, or_2_out);
  or or_3 (D2, and_4_out, and_2_out, and_3_out);
endmodule

module Flip_Flops (
  input  CLOCK,
  input  RESET,
  input  D0,
  input  D1,
  input  D2,
  output Q0,
  output Q1,
  output Q2
);

  D_Flip_Flop d_ff_1 (.clk(CLOCK), .D(D0), .Q(Q0), .reset(RESET));  // open: Qn, preset, en
  D_Flip_Flop d_ff_2 (.clk(CLOCK), .D(D1), .Q(Q1), .reset(RESET));  // open: Qn, preset, en
  D_Flip_Flop d_ff_3 (.clk(CLOCK), .D(D2), .Q(Q2), .reset(RESET));  // open: Qn, preset, en
endmodule

module Output (
  input  Q0,
  input  Q1,
  input  Q2,
  output LOCK,
  output ALARM
);

  wire not_1_out, not_2_out;

  not not_1 (not_1_out, Q0);
  not not_2 (not_2_out, Q2);
  or or_1 (LOCK, not_1_out, Q1, not_2_out);
  and and_1 (ALARM, Q2, Q1, not_1_out);
endmodule
